// Logisim project 8-Bit-CPU-INS-ROM.circ as structural Verilog: 15 circuits, main circuit INS_ROM_0
module INS_ROM_0 (
  input  [7:0] in_1,
  input  CLK,
  output IP_inc,
  output IP_read,
  output IP_write,
  output SP_inc,
  output SP_dec,
  output SP_read,
  output SP_write,
  output MAR_read,
  output MAR_write,
  output MDR0_read,
  output MDR0_write,
  output MDR0_zero,
  output MDR1_read,
  output MDR1_write,
  output MDR1_zero,
  output MDR2_read,
  output MDR2_write,
  output MDR2_zero,
  output MEM_read,
  output MEM_read2,
  output MEM_write,
  output MDR0_MEM_IN,
  output MDR1_MEM_IN,
  output MDR2_MEM_IN,
  output MDR0_REG_IN,
  output MDR1_REG_IN,
  output MDR2_REG_IN,
  output MAR_REG_ID,
  output MDR0_REG_ID,
  output MDR1_REG_ID,
  output MDR2_REG_ID,
  output REG_OUT_MAR,
  output REG_OUT_MDR0,
  output REG_OUT_MDR1,
  output REG_OUT_MDR2,
  output REG_read,
  output REG_write,
  output MAR_MDR0,
  output MAR_MDR1,
  output MAR_MDR2,
  output MDR0_MAR,
  output MDR0_MDR1,
  output MDR0_MDR2,
  output MDR1_MAR,
  output MDR1_MDR0,
  output MDR1_MDR2,
  output MDR2_MAR,
  output MDR2_MDR0,
  output MDR2_MDR1,
  output MAR_ALU_IN0,
  output MDR0_ALU_IN0,
  output MDR1_ALU_IN0,
  output MDR2_ALU_IN0,
  output MAR_ALU_IN1,
  output MDR0_ALU_IN1,
  output MDR1_ALU_IN1,
  output MDR2_ALU_IN1,
  output [7:0] ALU_SELECT,
  output ALU_read,
  output ALU_write,
  output ALU_readFlags,
  output ALU_OUT_MAR,
  output ALU_OUT_MDR0,
  output ALU_OUT_MDR1,
  output ALU_OUT_MDR2,
  output ALU_REMAINDER_MAR,
  output ALU_REMAINDER_MDR0,
  output ALU_REMAINDER_MDR1,
  output ALU_REMAINDER_MDR2,
  output CU_endInstruction
);

  wire [12:0] rom_2_data;
  wire [63:0] rom_1_data;

  ROM #(.dataWidth(64)) rom_1 (.addr(in_1), .data(rom_1_data));
  ROM #(.dataWidth(13)) rom_2 (.addr(in_1), .data(rom_2_data));
  INS_ROM_AND ins_rom_and_1 (
    .in_1(rom_1_data[0]), .in_2(rom_1_data[1]), .in_3(rom_1_data[2]), .in_4(rom_1_data[3]),
    .in_5(rom_1_data[4]), .in_6(rom_1_data[5]), .in_7(rom_1_data[6]), .in_8(rom_1_data[7]),
    .in_9(rom_1_data[8]), .in_10(rom_1_data[9]), .in_11(rom_1_data[10]), .in_12(rom_1_data[11]),
    .in_13(rom_1_data[12]), .in_14(rom_1_data[13]), .in_15(rom_1_data[14]), .in_16(rom_1_data[15]),
    .in_17(rom_1_data[16]), .in_18(rom_1_data[17]), .in_19(rom_1_data[18]), .in_20(rom_1_data[19]),
    .in_21(rom_1_data[20]), .in_22(rom_1_data[21]), .in_23(rom_1_data[22]), .in_24(rom_1_data[23]),
    .in_25(rom_1_data[24]), .in_26(rom_1_data[25]), .in_27(rom_1_data[26]), .in_28(rom_1_data[27]),
    .in_29(rom_1_data[28]), .in_30(rom_1_data[29]), .in_31(rom_1_data[30]), .in_32(rom_1_data[31]),
    .in_33(rom_1_data[32]), .in_34(rom_1_data[33]), .in_35(rom_1_data[34]), .in_36(rom_1_data[35]),
    .in_37(rom_1_data[36]), .in_38(rom_1_data[37]), .in_39(rom_1_data[38]), .in_40(rom_1_data[39]),
    .in_41(rom_1_data[40]), .in_42(rom_1_data[41]), .in_43(rom_1_data[42]), .in_44(rom_1_data[43]),
    .in_45(rom_1_data[44]), .in_46(rom_1_data[45]), .in_47(rom_1_data[46]), .in_48(rom_1_data[47]),
    .in_49(rom_1_data[48]), .in_50(rom_1_data[49]), .in_51(rom_1_data[50]), .in_52(rom_1_data[51]),
    .in_53(rom_1_data[52]), .in_54(rom_1_data[53]), .in_55(rom_1_data[54]), .in_56(rom_1_data[55]),
    .in_57(rom_1_data[56]), .in_58({rom_2_data[0], rom_1_data[63:57]}), .in_59(rom_2_data[1]),
    .in_60(rom_2_data[2]), .in_61(rom_2_data[3]), .in_62(rom_2_data[4]), .in_63(rom_2_data[5]),
    .in_64(rom_2_data[6]), .in_65(rom_2_data[7]), .in_66(rom_2_data[8]), .in_67(rom_2_data[9]),
    .in_68(rom_2_data[10]), .in_69(rom_2_data[11]), .in_70(rom_2_data[12]), .CLK(CLK), .IP_inc(IP_inc),
    .IP_read(IP_read), .IP_write(IP_write), .SP_inc(SP_inc), .SP_dec(SP_dec), .SP_read(SP_read),
    .SP_write(SP_write), .MAR_read(MAR_read), .MAR_write(MAR_write), .MDR0_read(MDR0_read),
    .MDR0_write(MDR0_write), .MDR0_zero(MDR0_zero), .MDR1_read(MDR1_read), .MDR1_write(MDR1_write),
    .MDR1_zero(MDR1_zero), .MDR2_read(MDR2_read), .MDR2_write(MDR2_write), .MDR2_zero(MDR2_zero),
    .MEM_read(MEM_read), .MEM_read2(MEM_read2), .MEM_write(MEM_write), .MDR0_MEM_IN(MDR0_MEM_IN),
    .MDR1_MEM_IN(MDR1_MEM_IN), .MDR2_MEM_IN(MDR2_MEM_IN), .MDR0_REG_IN(MDR0_REG_IN),
    .MDR1_REG_IN(MDR1_REG_IN), .MDR2_REG_IN(MDR2_REG_IN), .MAR_REG_ID(MAR_REG_ID), .MDR0_REG_ID(MDR0_REG_ID),
    .MDR1_REG_ID(MDR1_REG_ID), .MDR2_REG_ID(MDR2_REG_ID), .REG_OUT_MAR(REG_OUT_MAR),
    .REG_OUT_MDR0(REG_OUT_MDR0), .REG_OUT_MDR1(REG_OUT_MDR1), .REG_OUT_MDR2(REG_OUT_MDR2),
    .REG_read(REG_read), .REG_write(REG_write), .MAR_MDR0(MAR_MDR0), .MAR_MDR1(MAR_MDR1),
    .MAR_MDR2(MAR_MDR2), .MDR0_MAR(MDR0_MAR), .MDR0_MDR1(MDR0_MDR1), .MDR0_MDR2(MDR0_MDR2),
    .MDR1_MAR(MDR1_MAR), .MDR1_MDR0(MDR1_MDR0), .MDR1_MDR2(MDR1_MDR2), .MDR2_MAR(MDR2_MAR),
    .MDR2_MDR0(MDR2_MDR0), .MDR2_MDR1(MDR2_MDR1), .MAR_ALU_IN0(MAR_ALU_IN0), .MDR0_ALU_IN0(MDR0_ALU_IN0),
    .MDR1_ALU_IN0(MDR1_ALU_IN0), .MDR2_ALU_IN0(MDR2_ALU_IN0), .MAR_ALU_IN1(MAR_ALU_IN1),
    .MDR0_ALU_IN1(MDR0_ALU_IN1), .MDR1_ALU_IN1(MDR1_ALU_IN1), .MDR2_ALU_IN1(MDR2_ALU_IN1),
    .ALU_SELECT(ALU_SELECT), .ALU_read(ALU_read), .ALU_write(ALU_write), .ALU_readFlags(ALU_readFlags),
    .ALU_OUT_MAR(ALU_OUT_MAR), .ALU_OUT_MDR0(ALU_OUT_MDR0), .ALU_OUT_MDR1(ALU_OUT_MDR1),
    .ALU_OUT_MDR2(ALU_OUT_MDR2), .ALU_REMAINDER_MAR(ALU_REMAINDER_MAR),
    .ALU_REMAINDER_MDR0(ALU_REMAINDER_MDR0), .ALU_REMAINDER_MDR1(ALU_REMAINDER_MDR1),
    .ALU_REMAINDER_MDR2(ALU_REMAINDER_MDR2), .CU_endInstruction(CU_endInstruction));

  // Notes on the sheet:
  //   contents of rom_1 (hex, n*v repeats v):
  //   40183 10120c3783 c200d3583 400000d2783 c2583 c200d3583 400000d2783 90000c100db783 c200d3583
  //   400000d2783 400000d2783 c200d3583 400000d2783 290000c100db783 c200d3583 400000d2783 400000d2783
  //   c200d3583 400000d2783 490000c100db783 c200d3583 400000d2783 400000d2783 c200d3583 400000d2783
  //   690000c100db783 c200d3583 400000d2783 400000d2783 c200d3583 400000d2783 40593 a10042593 20000040793
  //   20000042783 20000042783 890000c100db783 c200d3583 a90000c100db783 c200d3583 c90000c100db783
  //   c200d3583 400000c2783 400000d2783 c200d3583 400000d2783 1090000c100db783 c200d3583 400000c2783
  //   400000d2783 c200d3583 400000d2783 1290000c100db783 c200d3583 400000c2783 400000d2783 c200d3583
  //   400000d2783 e10000c10058783 40000050783 290000c100db783 c200d3583 400000d2783 400000d2783 c200d3583
  //   400000d2783 c100d2783 c2583 400000d2783 40583 a10042783 40583 a10042783 40583 a10042783 40583
  //   a10042783 40583 a10042783 40583 a10042783 40583 a10042783 40583 a10042783 40583 a10042783 40583
  //   a10042783 40583 a10042783 40583 a10042783 40583 a10042783 40583 a10042783 40583 a10042783 40583
  //   a10042783 40583 a10042783
  //   contents of rom_2 (hex, n*v repeats v):
  //   1000 6*0 4 5*0 4 5*0 4 5*0 4 10*0 4 0 4 0 4 5*0 4 5*0 4 5*0 4 0 4
endmodule

module INS_ROM_1 (
  input  [7:0] Instruc,
  input  [7:0] Flags,
  input  CLK,
  output IP_inc,
  output IP_read,
  output IP_write,
  output SP_inc,
  output SP_dec,
  output SP_read,
  output SP_write,
  output MAR_read,
  output MAR_write,
  output MDR0_read,
  output MDR0_write,
  output MDR0_zero,
  output MDR1_read,
  output MDR1_write,
  output MDR1_zero,
  output MDR2_read,
  output MDR2_write,
  output MDR2_zero,
  output MEM_read,
  output MEM_read2,
  output MEM_write,
  output MDR0_MEM_IN,
  output MDR1_MEM_IN,
  output MDR2_MEM_IN,
  output MDR0_REG_IN,
  output MDR1_REG_IN,
  output MDR2_REG_IN,
  output MAR_REG_ID,
  output MDR0_REG_ID,
  output MDR1_REG_ID,
  output MDR2_REG_ID,
  output REG_OUT_MAR,
  output REG_OUT_MDR0,
  output REG_OUT_MDR1,
  output REG_OUT_MDR2,
  output REG_read,
  output REG_write,
  output MAR_MDR0,
  output MAR_MDR1,
  output MAR_MDR2,
  output MDR0_MAR,
  output MDR0_MDR1,
  output MDR0_MDR2,
  output MDR1_MAR,
  output MDR1_MDR0,
  output MDR1_MDR2,
  output MDR2_MAR,
  output MDR2_MDR0,
  output MDR2_MDR1,
  output MAR_ALU_IN0,
  output MDR0_ALU_IN0,
  output MDR1_ALU_IN0,
  output MDR2_ALU_IN0,
  output MAR_ALU_IN1,
  output MDR0_ALU_IN1,
  output MDR1_ALU_IN1,
  output MDR2_ALU_IN1,
  output [7:0] ALU_SELECT,
  output ALU_read,
  output ALU_write,
  output ALU_readFlags,
  output ALU_OUT_MAR,
  output ALU_OUT_MDR0,
  output ALU_OUT_MDR1,
  output ALU_OUT_MDR2,
  output ALU_REMAINDER_MAR,
  output ALU_REMAINDER_MDR0,
  output ALU_REMAINDER_MDR1,
  output ALU_REMAINDER_MDR2,
  output CU_endInstruction
);

  wire ins_rom_jumps_1_out_3, not_1_out, or_1_out, or_2_out;
  wire [12:0] rom_2_data;
  wire [63:0] rom_1_data;

  ROM #(.dataWidth(64)) rom_1 (.addr(Instruc), .data(rom_1_data));
  ROM #(.dataWidth(13)) rom_2 (.addr(Instruc), .data(rom_2_data));
  INS_ROM_JUMPS ins_rom_jumps_1 (.in_1(Instruc), .Flags(Flags), .out_3(ins_rom_jumps_1_out_3));
  not not_1 (not_1_out, ins_rom_jumps_1_out_3);
  or or_1 (or_1_out, not_1_out, rom_1_data[0]);
  or or_2 (or_2_out, ins_rom_jumps_1_out_3, rom_1_data[2]);
  INS_ROM_AND ins_rom_and_1 (
    .in_1(or_1_out), .in_2(rom_1_data[1]), .in_3(or_2_out), .in_4(rom_1_data[3]), .in_5(rom_1_data[4]),
    .in_6(rom_1_data[5]), .in_7(rom_1_data[6]), .in_8(rom_1_data[7]), .in_9(rom_1_data[8]),
    .in_10(rom_1_data[9]), .in_11(rom_1_data[10]), .in_12(rom_1_data[11]), .in_13(rom_1_data[12]),
    .in_14(rom_1_data[13]), .in_15(rom_1_data[14]), .in_16(rom_1_data[15]), .in_17(rom_1_data[16]),
    .in_18(rom_1_data[17]), .in_19(rom_1_data[18]), .in_20(rom_1_data[19]), .in_21(rom_1_data[20]),
    .in_22(rom_1_data[21]), .in_23(rom_1_data[22]), .in_24(rom_1_data[23]), .in_25(rom_1_data[24]),
    .in_26(rom_1_data[25]), .in_27(rom_1_data[26]), .in_28(rom_1_data[27]), .in_29(rom_1_data[28]),
    .in_30(rom_1_data[29]), .in_31(rom_1_data[30]), .in_32(rom_1_data[31]), .in_33(rom_1_data[32]),
    .in_34(rom_1_data[33]), .in_35(rom_1_data[34]), .in_36(rom_1_data[35]), .in_37(rom_1_data[36]),
    .in_38(rom_1_data[37]), .in_39(rom_1_data[38]), .in_40(rom_1_data[39]), .in_41(rom_1_data[40]),
    .in_42(rom_1_data[41]), .in_43(rom_1_data[42]), .in_44(rom_1_data[43]), .in_45(rom_1_data[44]),
    .in_46(rom_1_data[45]), .in_47(rom_1_data[46]), .in_48(rom_1_data[47]), .in_49(rom_1_data[48]),
    .in_50(rom_1_data[49]), .in_51(rom_1_data[50]), .in_52(rom_1_data[51]), .in_53(rom_1_data[52]),
    .in_54(rom_1_data[53]), .in_55(rom_1_data[54]), .in_56(rom_1_data[55]), .in_57(rom_1_data[56]),
    .in_58({rom_2_data[0], rom_1_data[63:57]}), .in_59(rom_2_data[1]), .in_60(rom_2_data[2]),
    .in_61(rom_2_data[3]), .in_62(rom_2_data[4]), .in_63(rom_2_data[5]), .in_64(rom_2_data[6]),
    .in_65(rom_2_data[7]), .in_66(rom_2_data[8]), .in_67(rom_2_data[9]), .in_68(rom_2_data[10]),
    .in_69(rom_2_data[11]), .in_70(rom_2_data[12]), .CLK(CLK), .IP_inc(IP_inc), .IP_read(IP_read),
    .IP_write(IP_write), .SP_inc(SP_inc), .SP_dec(SP_dec), .SP_read(SP_read), .SP_write(SP_write),
    .MAR_read(MAR_read), .MAR_write(MAR_write), .MDR0_read(MDR0_read), .MDR0_write(MDR0_write),
    .MDR0_zero(MDR0_zero), .MDR1_read(MDR1_read), .MDR1_write(MDR1_write), .MDR1_zero(MDR1_zero),
    .MDR2_read(MDR2_read), .MDR2_write(MDR2_write), .MDR2_zero(MDR2_zero), .MEM_read(MEM_read),
    .MEM_read2(MEM_read2), .MEM_write(MEM_write), .MDR0_MEM_IN(MDR0_MEM_IN), .MDR1_MEM_IN(MDR1_MEM_IN),
    .MDR2_MEM_IN(MDR2_MEM_IN), .MDR0_REG_IN(MDR0_REG_IN), .MDR1_REG_IN(MDR1_REG_IN),
    .MDR2_REG_IN(MDR2_REG_IN), .MAR_REG_ID(MAR_REG_ID), .MDR0_REG_ID(MDR0_REG_ID), .MDR1_REG_ID(MDR1_REG_ID),
    .MDR2_REG_ID(MDR2_REG_ID), .REG_OUT_MAR(REG_OUT_MAR), .REG_OUT_MDR0(REG_OUT_MDR0),
    .REG_OUT_MDR1(REG_OUT_MDR1), .REG_OUT_MDR2(REG_OUT_MDR2), .REG_read(REG_read), .REG_write(REG_write),
    .MAR_MDR0(MAR_MDR0), .MAR_MDR1(MAR_MDR1), .MAR_MDR2(MAR_MDR2), .MDR0_MAR(MDR0_MAR),
    .MDR0_MDR1(MDR0_MDR1), .MDR0_MDR2(MDR0_MDR2), .MDR1_MAR(MDR1_MAR), .MDR1_MDR0(MDR1_MDR0),
    .MDR1_MDR2(MDR1_MDR2), .MDR2_MAR(MDR2_MAR), .MDR2_MDR0(MDR2_MDR0), .MDR2_MDR1(MDR2_MDR1),
    .MAR_ALU_IN0(MAR_ALU_IN0), .MDR0_ALU_IN0(MDR0_ALU_IN0), .MDR1_ALU_IN0(MDR1_ALU_IN0),
    .MDR2_ALU_IN0(MDR2_ALU_IN0), .MAR_ALU_IN1(MAR_ALU_IN1), .MDR0_ALU_IN1(MDR0_ALU_IN1),
    .MDR1_ALU_IN1(MDR1_ALU_IN1), .MDR2_ALU_IN1(MDR2_ALU_IN1), .ALU_SELECT(ALU_SELECT), .ALU_read(ALU_read),
    .ALU_write(ALU_write), .ALU_readFlags(ALU_readFlags), .ALU_OUT_MAR(ALU_OUT_MAR),
    .ALU_OUT_MDR0(ALU_OUT_MDR0), .ALU_OUT_MDR1(ALU_OUT_MDR1), .ALU_OUT_MDR2(ALU_OUT_MDR2),
    .ALU_REMAINDER_MAR(ALU_REMAINDER_MAR), .ALU_REMAINDER_MDR0(ALU_REMAINDER_MDR0),
    .ALU_REMAINDER_MDR1(ALU_REMAINDER_MDR1), .ALU_REMAINDER_MDR2(ALU_REMAINDER_MDR2),
    .CU_endInstruction(CU_endInstruction));

  // Notes on the sheet:
  //   contents of rom_1 (hex, n*v repeats v):
  //   0 1 1014008201 81041049781 10000501381 10000908381 80000041581 1014018201 108000a1000b201
  //   808c0049681 84400000049781 10000000301 80000041581 1014018201 308000a1000b201 808c0049681
  //   284400000049781 10000000301 80000041581 1014018201 508000a1000b201 808c0049681 484400000049781
  //   10000000301 80000041581 1012003201 708000a1000b201 808c0049681 684400000049781 10000000301
  //   80000041581 3003a1 5011a1 80000041581 10210417a1 405a1 1012003201 908000a1000b201 1012003201
  //   b08000a1000b201 1014018201 d08000a1000b201 80000041581 c84400000049781 10000000301 80000041581
  //   1014018201 1108000a1000b201 80000041581 1084400000049781 10000000301 80000041581 1014018201
  //   1308000a1000b201 80000041581 1284400000049781 10000000301 80000041581 1014018201 e04400000048781 1
  //   308000a1000b201 80000041581 284400000049781 10000000301 80000041581 8a0001101 10c20011301
  //   80000041581 40386 41186 40382 41182 40382 41182 40382 41182 40382 41182 40382 41182 40382 41182
  //   40382 41182 40382 41182 40382 41182 40382 41182 40382 41182 40382 41182 40382 41182 40382 41182
  //   40382 41182 40382 41182
  //   contents of rom_2 (hex, n*v repeats v):
  //   7*0 82 4 0 4 0 0 82 4 0 4 0 0 82 4 0 4 0 0 42 4 0 4 7*0 42 4 42 4 82 4 0 4 0 0 82 4 0 4 0 0 82 4 0 4
  //   0 0 82 4 0 4 0 4 5*0 34*1008
endmodule

module INS_ROM_2 (
  input  [7:0] in_1,
  input  CLK,
  output IP_inc,
  output IP_read,
  output IP_write,
  output SP_inc,
  output SP_dec,
  output SP_read,
  output SP_write,
  output MAR_read,
  output MAR_write,
  output MDR0_read,
  output MDR0_write,
  output MDR0_zero,
  output MDR1_read,
  output MDR1_write,
  output MDR1_zero,
  output MDR2_read,
  output MDR2_write,
  output MDR2_zero,
  output MEM_read,
  output MEM_read2,
  output MEM_write,
  output MDR0_MEM_IN,
  output MDR1_MEM_IN,
  output MDR2_MEM_IN,
  output MDR0_REG_IN,
  output MDR1_REG_IN,
  output MDR2_REG_IN,
  output MAR_REG_ID,
  output MDR0_REG_ID,
  output MDR1_REG_ID,
  output MDR2_REG_ID,
  output REG_OUT_MAR,
  output REG_OUT_MDR0,
  output REG_OUT_MDR1,
  output REG_OUT_MDR2,
  output REG_read,
  output REG_write,
  output MAR_MDR0,
  output MAR_MDR1,
  output MAR_MDR2,
  output MDR0_MAR,
  output MDR0_MDR1,
  output MDR0_MDR2,
  output MDR1_MAR,
  output MDR1_MDR0,
  output MDR1_MDR2,
  output MDR2_MAR,
  output MDR2_MDR0,
  output MDR2_MDR1,
  output MAR_ALU_IN0,
  output MDR0_ALU_IN0,
  output MDR1_ALU_IN0,
  output MDR2_ALU_IN0,
  output MAR_ALU_IN1,
  output MDR0_ALU_IN1,
  output MDR1_ALU_IN1,
  output MDR2_ALU_IN1,
  output [7:0] ALU_SELECT,
  output ALU_read,
  output ALU_write,
  output ALU_readFlags,
  output ALU_OUT_MAR,
  output ALU_OUT_MDR0,
  output ALU_OUT_MDR1,
  output ALU_OUT_MDR2,
  output ALU_REMAINDER_MAR,
  output ALU_REMAINDER_MDR0,
  output ALU_REMAINDER_MDR1,
  output ALU_REMAINDER_MDR2,
  output CU_endInstruction
);

  wire [12:0] rom_2_data;
  wire [63:0] rom_1_data;

  ROM #(.dataWidth(64)) rom_1 (.addr(in_1), .data(rom_1_data));
  ROM #(.dataWidth(13)) rom_2 (.addr(in_1), .data(rom_2_data));
  INS_ROM_AND ins_rom_and_1 (
    .in_1(rom_1_data[0]), .in_2(rom_1_data[1]), .in_3(rom_1_data[2]), .in_4(rom_1_data[3]),
    .in_5(rom_1_data[4]), .in_6(rom_1_data[5]), .in_7(rom_1_data[6]), .in_8(rom_1_data[7]),
    .in_9(rom_1_data[8]), .in_10(rom_1_data[9]), .in_11(rom_1_data[10]), .in_12(rom_1_data[11]),
    .in_13(rom_1_data[12]), .in_14(rom_1_data[13]), .in_15(rom_1_data[14]), .in_16(rom_1_data[15]),
    .in_17(rom_1_data[16]), .in_18(rom_1_data[17]), .in_19(rom_1_data[18]), .in_20(rom_1_data[19]),
    .in_21(rom_1_data[20]), .in_22(rom_1_data[21]), .in_23(rom_1_data[22]), .in_24(rom_1_data[23]),
    .in_25(rom_1_data[24]), .in_26(rom_1_data[25]), .in_27(rom_1_data[26]), .in_28(rom_1_data[27]),
    .in_29(rom_1_data[28]), .in_30(rom_1_data[29]), .in_31(rom_1_data[30]), .in_32(rom_1_data[31]),
    .in_33(rom_1_data[32]), .in_34(rom_1_data[33]), .in_35(rom_1_data[34]), .in_36(rom_1_data[35]),
    .in_37(rom_1_data[36]), .in_38(rom_1_data[37]), .in_39(rom_1_data[38]), .in_40(rom_1_data[39]),
    .in_41(rom_1_data[40]), .in_42(rom_1_data[41]), .in_43(rom_1_data[42]), .in_44(rom_1_data[43]),
    .in_45(rom_1_data[44]), .in_46(rom_1_data[45]), .in_47(rom_1_data[46]), .in_48(rom_1_data[47]),
    .in_49(rom_1_data[48]), .in_50(rom_1_data[49]), .in_51(rom_1_data[50]), .in_52(rom_1_data[51]),
    .in_53(rom_1_data[52]), .in_54(rom_1_data[53]), .in_55(rom_1_data[54]), .in_56(rom_1_data[55]),
    .in_57(rom_1_data[56]), .in_58({rom_2_data[0], rom_1_data[63:57]}), .in_59(rom_2_data[1]),
    .in_60(rom_2_data[2]), .in_61(rom_2_data[3]), .in_62(rom_2_data[4]), .in_63(rom_2_data[5]),
    .in_64(rom_2_data[6]), .in_65(rom_2_data[7]), .in_66(rom_2_data[8]), .in_67(rom_2_data[9]),
    .in_68(rom_2_data[10]), .in_69(rom_2_data[11]), .in_70(rom_2_data[12]), .CLK(CLK), .IP_inc(IP_inc),
    .IP_read(IP_read), .IP_write(IP_write), .SP_inc(SP_inc), .SP_dec(SP_dec), .SP_read(SP_read),
    .SP_write(SP_write), .MAR_read(MAR_read), .MAR_write(MAR_write), .MDR0_read(MDR0_read),
    .MDR0_write(MDR0_write), .MDR0_zero(MDR0_zero), .MDR1_read(MDR1_read), .MDR1_write(MDR1_write),
    .MDR1_zero(MDR1_zero), .MDR2_read(MDR2_read), .MDR2_write(MDR2_write), .MDR2_zero(MDR2_zero),
    .MEM_read(MEM_read), .MEM_read2(MEM_read2), .MEM_write(MEM_write), .MDR0_MEM_IN(MDR0_MEM_IN),
    .MDR1_MEM_IN(MDR1_MEM_IN), .MDR2_MEM_IN(MDR2_MEM_IN), .MDR0_REG_IN(MDR0_REG_IN),
    .MDR1_REG_IN(MDR1_REG_IN), .MDR2_REG_IN(MDR2_REG_IN), .MAR_REG_ID(MAR_REG_ID), .MDR0_REG_ID(MDR0_REG_ID),
    .MDR1_REG_ID(MDR1_REG_ID), .MDR2_REG_ID(MDR2_REG_ID), .REG_OUT_MAR(REG_OUT_MAR),
    .REG_OUT_MDR0(REG_OUT_MDR0), .REG_OUT_MDR1(REG_OUT_MDR1), .REG_OUT_MDR2(REG_OUT_MDR2),
    .REG_read(REG_read), .REG_write(REG_write), .MAR_MDR0(MAR_MDR0), .MAR_MDR1(MAR_MDR1),
    .MAR_MDR2(MAR_MDR2), .MDR0_MAR(MDR0_MAR), .MDR0_MDR1(MDR0_MDR1), .MDR0_MDR2(MDR0_MDR2),
    .MDR1_MAR(MDR1_MAR), .MDR1_MDR0(MDR1_MDR0), .MDR1_MDR2(MDR1_MDR2), .MDR2_MAR(MDR2_MAR),
    .MDR2_MDR0(MDR2_MDR0), .MDR2_MDR1(MDR2_MDR1), .MAR_ALU_IN0(MAR_ALU_IN0), .MDR0_ALU_IN0(MDR0_ALU_IN0),
    .MDR1_ALU_IN0(MDR1_ALU_IN0), .MDR2_ALU_IN0(MDR2_ALU_IN0), .MAR_ALU_IN1(MAR_ALU_IN1),
    .MDR0_ALU_IN1(MDR0_ALU_IN1), .MDR1_ALU_IN1(MDR1_ALU_IN1), .MDR2_ALU_IN1(MDR2_ALU_IN1),
    .ALU_SELECT(ALU_SELECT), .ALU_read(ALU_read), .ALU_write(ALU_write), .ALU_readFlags(ALU_readFlags),
    .ALU_OUT_MAR(ALU_OUT_MAR), .ALU_OUT_MDR0(ALU_OUT_MDR0), .ALU_OUT_MDR1(ALU_OUT_MDR1),
    .ALU_OUT_MDR2(ALU_OUT_MDR2), .ALU_REMAINDER_MAR(ALU_REMAINDER_MAR),
    .ALU_REMAINDER_MDR0(ALU_REMAINDER_MDR0), .ALU_REMAINDER_MDR1(ALU_REMAINDER_MDR1),
    .ALU_REMAINDER_MDR2(ALU_REMAINDER_MDR2), .CU_endInstruction(CU_endInstruction));

  // Notes on the sheet:
  //   contents of rom_1 (hex, n*v repeats v):
  //   0 5*40183 400000308381 40183 1012003201 42001041008881 300681 104000000048681 42000000a301 40183
  //   1012003201 24200104200b281 300681 304000000048681 42000000a301 40183 1012003201 44200104200b281
  //   300681 504000000048681 42000000a301 1002003001 1012003201 64200104200b281 300681 704000000048681
  //   42000000a301 40182 40182 3003a0 100088 100090 40183 1012003201 40183 1012003201 40183 1012003201
  //   c48000a4000b201 300681 d04000000048681 42000000a301 40183 1012003201 1048000a4000b201 300681
  //   1104000000048681 42000000a301 40183 1012003201 1248000a4000b201 300681 1304000000048681 42000000a301
  //   40182 100680 40183 40183 308000a40013001 40183 104000000048681 42000000a301 1024009001 1021041681
  //   400000008101
  //   contents of rom_2 (hex, n*v repeats v):
  //   0 5*1000 0 1000 42 26 22 4 0 1000 42 46 22 4 0 1000 42 46 22 4 0 402 42 46 22 4 0 1000 1000 0 0 0
  //   1000 42 1000 42 1000 42 4 22 4 0 1000 42 4 22 4 0 1000 42 4 22 4 0 1000 42 1000 1000 4 1000 4
endmodule

module INS_ROM_3 (
  input  [7:0] in_1,
  input  CLK,
  output IP_inc,
  output IP_read,
  output IP_write,
  output SP_inc,
  output SP_dec,
  output SP_read,
  output SP_write,
  output MAR_read,
  output MAR_write,
  output MDR0_read,
  output MDR0_write,
  output MDR0_zero,
  output MDR1_read,
  output MDR1_write,
  output MDR1_zero,
  output MDR2_read,
  output MDR2_write,
  output MDR2_zero,
  output MEM_read,
  output MEM_read2,
  output MEM_write,
  output MDR0_MEM_IN,
  output MDR1_MEM_IN,
  output MDR2_MEM_IN,
  output MDR0_REG_IN,
  output MDR1_REG_IN,
  output MDR2_REG_IN,
  output MAR_REG_ID,
  output MDR0_REG_ID,
  output MDR1_REG_ID,
  output MDR2_REG_ID,
  output REG_OUT_MAR,
  output REG_OUT_MDR0,
  output REG_OUT_MDR1,
  output REG_OUT_MDR2,
  output REG_read,
  output REG_write,
  output MAR_MDR0,
  output MAR_MDR1,
  output MAR_MDR2,
  output MDR0_MAR,
  output MDR0_MDR1,
  output MDR0_MDR2,
  output MDR1_MAR,
  output MDR1_MDR0,
  output MDR1_MDR2,
  output MDR2_MAR,
  output MDR2_MDR0,
  output MDR2_MDR1,
  output MAR_ALU_IN0,
  output MDR0_ALU_IN0,
  output MDR1_ALU_IN0,
  output MDR2_ALU_IN0,
  output MAR_ALU_IN1,
  output MDR0_ALU_IN1,
  output MDR1_ALU_IN1,
  output MDR2_ALU_IN1,
  output [7:0] ALU_SELECT,
  output ALU_read,
  output ALU_write,
  output ALU_readFlags,
  output ALU_OUT_MAR,
  output ALU_OUT_MDR0,
  output ALU_OUT_MDR1,
  output ALU_OUT_MDR2,
  output ALU_REMAINDER_MAR,
  output ALU_REMAINDER_MDR0,
  output ALU_REMAINDER_MDR1,
  output ALU_REMAINDER_MDR2,
  output CU_endInstruction
);

  wire [12:0] rom_2_data;
  wire [63:0] rom_1_data;

  ROM #(.dataWidth(64)) rom_1 (.addr(in_1), .data(rom_1_data));
  ROM #(.dataWidth(13)) rom_2 (.addr(in_1), .data(rom_2_data));
  INS_ROM_AND ins_rom_and_1 (
    .in_1(rom_1_data[0]), .in_2(rom_1_data[1]), .in_3(rom_1_data[2]), .in_4(rom_1_data[3]),
    .in_5(rom_1_data[4]), .in_6(rom_1_data[5]), .in_7(rom_1_data[6]), .in_8(rom_1_data[7]),
    .in_9(rom_1_data[8]), .in_10(rom_1_data[9]), .in_11(rom_1_data[10]), .in_12(rom_1_data[11]),
    .in_13(rom_1_data[12]), .in_14(rom_1_data[13]), .in_15(rom_1_data[14]), .in_16(rom_1_data[15]),
    .in_17(rom_1_data[16]), .in_18(rom_1_data[17]), .in_19(rom_1_data[18]), .in_20(rom_1_data[19]),
    .in_21(rom_1_data[20]), .in_22(rom_1_data[21]), .in_23(rom_1_data[22]), .in_24(rom_1_data[23]),
    .in_25(rom_1_data[24]), .in_26(rom_1_data[25]), .in_27(rom_1_data[26]), .in_28(rom_1_data[27]),
    .in_29(rom_1_data[28]), .in_30(rom_1_data[29]), .in_31(rom_1_data[30]), .in_32(rom_1_data[31]),
    .in_33(rom_1_data[32]), .in_34(rom_1_data[33]), .in_35(rom_1_data[34]), .in_36(rom_1_data[35]),
    .in_37(rom_1_data[36]), .in_38(rom_1_data[37]), .in_39(rom_1_data[38]), .in_40(rom_1_data[39]),
    .in_41(rom_1_data[40]), .in_42(rom_1_data[41]), .in_43(rom_1_data[42]), .in_44(rom_1_data[43]),
    .in_45(rom_1_data[44]), .in_46(rom_1_data[45]), .in_47(rom_1_data[46]), .in_48(rom_1_data[47]),
    .in_49(rom_1_data[48]), .in_50(rom_1_data[49]), .in_51(rom_1_data[50]), .in_52(rom_1_data[51]),
    .in_53(rom_1_data[52]), .in_54(rom_1_data[53]), .in_55(rom_1_data[54]), .in_56(rom_1_data[55]),
    .in_57(rom_1_data[56]), .in_58({rom_2_data[0], rom_1_data[63:57]}), .in_59(rom_2_data[1]),
    .in_60(rom_2_data[2]), .in_61(rom_2_data[3]), .in_62(rom_2_data[4]), .in_63(rom_2_data[5]),
    .in_64(rom_2_data[6]), .in_65(rom_2_data[7]), .in_66(rom_2_data[8]), .in_67(rom_2_data[9]),
    .in_68(rom_2_data[10]), .in_69(rom_2_data[11]), .in_70(rom_2_data[12]), .CLK(CLK), .IP_inc(IP_inc),
    .IP_read(IP_read), .IP_write(IP_write), .SP_inc(SP_inc), .SP_dec(SP_dec), .SP_read(SP_read),
    .SP_write(SP_write), .MAR_read(MAR_read), .MAR_write(MAR_write), .MDR0_read(MDR0_read),
    .MDR0_write(MDR0_write), .MDR0_zero(MDR0_zero), .MDR1_read(MDR1_read), .MDR1_write(MDR1_write),
    .MDR1_zero(MDR1_zero), .MDR2_read(MDR2_read), .MDR2_write(MDR2_write), .MDR2_zero(MDR2_zero),
    .MEM_read(MEM_read), .MEM_read2(MEM_read2), .MEM_write(MEM_write), .MDR0_MEM_IN(MDR0_MEM_IN),
    .MDR1_MEM_IN(MDR1_MEM_IN), .MDR2_MEM_IN(MDR2_MEM_IN), .MDR0_REG_IN(MDR0_REG_IN),
    .MDR1_REG_IN(MDR1_REG_IN), .MDR2_REG_IN(MDR2_REG_IN), .MAR_REG_ID(MAR_REG_ID), .MDR0_REG_ID(MDR0_REG_ID),
    .MDR1_REG_ID(MDR1_REG_ID), .MDR2_REG_ID(MDR2_REG_ID), .REG_OUT_MAR(REG_OUT_MAR),
    .REG_OUT_MDR0(REG_OUT_MDR0), .REG_OUT_MDR1(REG_OUT_MDR1), .REG_OUT_MDR2(REG_OUT_MDR2),
    .REG_read(REG_read), .REG_write(REG_write), .MAR_MDR0(MAR_MDR0), .MAR_MDR1(MAR_MDR1),
    .MAR_MDR2(MAR_MDR2), .MDR0_MAR(MDR0_MAR), .MDR0_MDR1(MDR0_MDR1), .MDR0_MDR2(MDR0_MDR2),
    .MDR1_MAR(MDR1_MAR), .MDR1_MDR0(MDR1_MDR0), .MDR1_MDR2(MDR1_MDR2), .MDR2_MAR(MDR2_MAR),
    .MDR2_MDR0(MDR2_MDR0), .MDR2_MDR1(MDR2_MDR1), .MAR_ALU_IN0(MAR_ALU_IN0), .MDR0_ALU_IN0(MDR0_ALU_IN0),
    .MDR1_ALU_IN0(MDR1_ALU_IN0), .MDR2_ALU_IN0(MDR2_ALU_IN0), .MAR_ALU_IN1(MAR_ALU_IN1),
    .MDR0_ALU_IN1(MDR0_ALU_IN1), .MDR1_ALU_IN1(MDR1_ALU_IN1), .MDR2_ALU_IN1(MDR2_ALU_IN1),
    .ALU_SELECT(ALU_SELECT), .ALU_read(ALU_read), .ALU_write(ALU_write), .ALU_readFlags(ALU_readFlags),
    .ALU_OUT_MAR(ALU_OUT_MAR), .ALU_OUT_MDR0(ALU_OUT_MDR0), .ALU_OUT_MDR1(ALU_OUT_MDR1),
    .ALU_OUT_MDR2(ALU_OUT_MDR2), .ALU_REMAINDER_MAR(ALU_REMAINDER_MAR),
    .ALU_REMAINDER_MDR0(ALU_REMAINDER_MDR0), .ALU_REMAINDER_MDR1(ALU_REMAINDER_MDR1),
    .ALU_REMAINDER_MDR2(ALU_REMAINDER_MDR2), .CU_endInstruction(CU_endInstruction));

  // Notes on the sheet:
  //   contents of rom_1 (hex, n*v repeats v):
  //   6*0 40182 0 40182 40182 40182 300680 48000000041680 0 40182 40182 40182 300680 284000000041680 0
  //   40182 40182 40182 300680 484000000041680 40182 1002003000 1001000600 40182 300680 684000000051680 0
  //   0 40182 40182 80000301380 0 40182 0 40182 0 40182 104200b000 40182 300680 c84000000041680 0 40182
  //   104200b000 40182 300680 1084000000041680 0 40182 104200b000 40182 300680 1284000000041680 0 40182 0
  //   0 40182 0 40182 1284000000041680 5012003280 908080 40000010200
  //   contents of rom_2 (hex, n*v repeats v):
  //   6*0 1000 0 1000 1000 1000 22 4 0 1000 1000 1000 22 4 0 1000 1000 1000 22 4 1000 402 202 1000 22 86 0
  //   0 1000 1000 0 0 1000 0 1000 0 1000 42 1000 22 4 0 1000 42 1000 22 4 0 1000 42 1000 22 4 0 1000 0 0
  //   1000 0 1000 4
endmodule

module INS_ROM_4 (
  input  [7:0] in_1,
  input  CLK,
  output IP_inc,
  output IP_read,
  output IP_write,
  output SP_inc,
  output SP_dec,
  output SP_read,
  output SP_write,
  output MAR_read,
  output MAR_write,
  output MDR0_read,
  output MDR0_write,
  output MDR0_zero,
  output MDR1_read,
  output MDR1_write,
  output MDR1_zero,
  output MDR2_read,
  output MDR2_write,
  output MDR2_zero,
  output MEM_read,
  output MEM_read2,
  output MEM_write,
  output MDR0_MEM_IN,
  output MDR1_MEM_IN,
  output MDR2_MEM_IN,
  output MDR0_REG_IN,
  output MDR1_REG_IN,
  output MDR2_REG_IN,
  output MAR_REG_ID,
  output MDR0_REG_ID,
  output MDR1_REG_ID,
  output MDR2_REG_ID,
  output REG_OUT_MAR,
  output REG_OUT_MDR0,
  output REG_OUT_MDR1,
  output REG_OUT_MDR2,
  output REG_read,
  output REG_write,
  output MAR_MDR0,
  output MAR_MDR1,
  output MAR_MDR2,
  output MDR0_MAR,
  output MDR0_MDR1,
  output MDR0_MDR2,
  output MDR1_MAR,
  output MDR1_MDR0,
  output MDR1_MDR2,
  output MDR2_MAR,
  output MDR2_MDR0,
  output MDR2_MDR1,
  output MAR_ALU_IN0,
  output MDR0_ALU_IN0,
  output MDR1_ALU_IN0,
  output MDR2_ALU_IN0,
  output MAR_ALU_IN1,
  output MDR0_ALU_IN1,
  output MDR1_ALU_IN1,
  output MDR2_ALU_IN1,
  output [7:0] ALU_SELECT,
  output ALU_read,
  output ALU_write,
  output ALU_readFlags,
  output ALU_OUT_MAR,
  output ALU_OUT_MDR0,
  output ALU_OUT_MDR1,
  output ALU_OUT_MDR2,
  output ALU_REMAINDER_MAR,
  output ALU_REMAINDER_MDR0,
  output ALU_REMAINDER_MDR1,
  output ALU_REMAINDER_MDR2,
  output CU_endInstruction
);

  wire [12:0] rom_2_data;
  wire [63:0] rom_1_data;

  ROM #(.dataWidth(64)) rom_1 (.addr(in_1), .data(rom_1_data));
  ROM #(.dataWidth(13)) rom_2 (.addr(in_1), .data(rom_2_data));
  INS_ROM_AND ins_rom_and_1 (
    .in_1(rom_1_data[0]), .in_2(rom_1_data[1]), .in_3(rom_1_data[2]), .in_4(rom_1_data[3]),
    .in_5(rom_1_data[4]), .in_6(rom_1_data[5]), .in_7(rom_1_data[6]), .in_8(rom_1_data[7]),
    .in_9(rom_1_data[8]), .in_10(rom_1_data[9]), .in_11(rom_1_data[10]), .in_12(rom_1_data[11]),
    .in_13(rom_1_data[12]), .in_14(rom_1_data[13]), .in_15(rom_1_data[14]), .in_16(rom_1_data[15]),
    .in_17(rom_1_data[16]), .in_18(rom_1_data[17]), .in_19(rom_1_data[18]), .in_20(rom_1_data[19]),
    .in_21(rom_1_data[20]), .in_22(rom_1_data[21]), .in_23(rom_1_data[22]), .in_24(rom_1_data[23]),
    .in_25(rom_1_data[24]), .in_26(rom_1_data[25]), .in_27(rom_1_data[26]), .in_28(rom_1_data[27]),
    .in_29(rom_1_data[28]), .in_30(rom_1_data[29]), .in_31(rom_1_data[30]), .in_32(rom_1_data[31]),
    .in_33(rom_1_data[32]), .in_34(rom_1_data[33]), .in_35(rom_1_data[34]), .in_36(rom_1_data[35]),
    .in_37(rom_1_data[36]), .in_38(rom_1_data[37]), .in_39(rom_1_data[38]), .in_40(rom_1_data[39]),
    .in_41(rom_1_data[40]), .in_42(rom_1_data[41]), .in_43(rom_1_data[42]), .in_44(rom_1_data[43]),
    .in_45(rom_1_data[44]), .in_46(rom_1_data[45]), .in_47(rom_1_data[46]), .in_48(rom_1_data[47]),
    .in_49(rom_1_data[48]), .in_50(rom_1_data[49]), .in_51(rom_1_data[50]), .in_52(rom_1_data[51]),
    .in_53(rom_1_data[52]), .in_54(rom_1_data[53]), .in_55(rom_1_data[54]), .in_56(rom_1_data[55]),
    .in_57(rom_1_data[56]), .in_58({rom_2_data[0], rom_1_data[63:57]}), .in_59(rom_2_data[1]),
    .in_60(rom_2_data[2]), .in_61(rom_2_data[3]), .in_62(rom_2_data[4]), .in_63(rom_2_data[5]),
    .in_64(rom_2_data[6]), .in_65(rom_2_data[7]), .in_66(rom_2_data[8]), .in_67(rom_2_data[9]),
    .in_68(rom_2_data[10]), .in_69(rom_2_data[11]), .in_70(rom_2_data[12]), .CLK(CLK), .IP_inc(IP_inc),
    .IP_read(IP_read), .IP_write(IP_write), .SP_inc(SP_inc), .SP_dec(SP_dec), .SP_read(SP_read),
    .SP_write(SP_write), .MAR_read(MAR_read), .MAR_write(MAR_write), .MDR0_read(MDR0_read),
    .MDR0_write(MDR0_write), .MDR0_zero(MDR0_zero), .MDR1_read(MDR1_read), .MDR1_write(MDR1_write),
    .MDR1_zero(MDR1_zero), .MDR2_read(MDR2_read), .MDR2_write(MDR2_write), .MDR2_zero(MDR2_zero),
    .MEM_read(MEM_read), .MEM_read2(MEM_read2), .MEM_write(MEM_write), .MDR0_MEM_IN(MDR0_MEM_IN),
    .MDR1_MEM_IN(MDR1_MEM_IN), .MDR2_MEM_IN(MDR2_MEM_IN), .MDR0_REG_IN(MDR0_REG_IN),
    .MDR1_REG_IN(MDR1_REG_IN), .MDR2_REG_IN(MDR2_REG_IN), .MAR_REG_ID(MAR_REG_ID), .MDR0_REG_ID(MDR0_REG_ID),
    .MDR1_REG_ID(MDR1_REG_ID), .MDR2_REG_ID(MDR2_REG_ID), .REG_OUT_MAR(REG_OUT_MAR),
    .REG_OUT_MDR0(REG_OUT_MDR0), .REG_OUT_MDR1(REG_OUT_MDR1), .REG_OUT_MDR2(REG_OUT_MDR2),
    .REG_read(REG_read), .REG_write(REG_write), .MAR_MDR0(MAR_MDR0), .MAR_MDR1(MAR_MDR1),
    .MAR_MDR2(MAR_MDR2), .MDR0_MAR(MDR0_MAR), .MDR0_MDR1(MDR0_MDR1), .MDR0_MDR2(MDR0_MDR2),
    .MDR1_MAR(MDR1_MAR), .MDR1_MDR0(MDR1_MDR0), .MDR1_MDR2(MDR1_MDR2), .MDR2_MAR(MDR2_MAR),
    .MDR2_MDR0(MDR2_MDR0), .MDR2_MDR1(MDR2_MDR1), .MAR_ALU_IN0(MAR_ALU_IN0), .MDR0_ALU_IN0(MDR0_ALU_IN0),
    .MDR1_ALU_IN0(MDR1_ALU_IN0), .MDR2_ALU_IN0(MDR2_ALU_IN0), .MAR_ALU_IN1(MAR_ALU_IN1),
    .MDR0_ALU_IN1(MDR0_ALU_IN1), .MDR1_ALU_IN1(MDR1_ALU_IN1), .MDR2_ALU_IN1(MDR2_ALU_IN1),
    .ALU_SELECT(ALU_SELECT), .ALU_read(ALU_read), .ALU_write(ALU_write), .ALU_readFlags(ALU_readFlags),
    .ALU_OUT_MAR(ALU_OUT_MAR), .ALU_OUT_MDR0(ALU_OUT_MDR0), .ALU_OUT_MDR1(ALU_OUT_MDR1),
    .ALU_OUT_MDR2(ALU_OUT_MDR2), .ALU_REMAINDER_MAR(ALU_REMAINDER_MAR),
    .ALU_REMAINDER_MDR0(ALU_REMAINDER_MDR0), .ALU_REMAINDER_MDR1(ALU_REMAINDER_MDR1),
    .ALU_REMAINDER_MDR2(ALU_REMAINDER_MDR2), .CU_endInstruction(CU_endInstruction));

  // Notes on the sheet:
  //   contents of rom_1 (hex, n*v repeats v):
  //   11*0 40182 300680 4*0 40182 300680 4*0 40182 300680 0 40182 40182 0 40182 908080 4*0 40182 6*0 40182
  //   0 40182 300680 0 0 40182 0 40182 300680 0 0 40182 0 40182 300680 7*0 40182 40182 40182 40480
  //   contents of rom_2 (hex, n*v repeats v):
  //   11*0 1000 22 4*0 1000 22 4*0 1000 42 0 1000 1000 0 1000 5*0 1000 6*0 1000 0 1000 22 0 0 1000 0 1000
  //   22 0 0 1000 0 1000 22 7*0 1000 1000 1000
endmodule

module INS_ROM_5 (
  input  [7:0] in_1,
  input  CLK,
  output IP_inc,
  output IP_read,
  output IP_write,
  output SP_inc,
  output SP_dec,
  output SP_read,
  output SP_write,
  output MAR_read,
  output MAR_write,
  output MDR0_read,
  output MDR0_write,
  output MDR0_zero,
  output MDR1_read,
  output MDR1_write,
  output MDR1_zero,
  output MDR2_read,
  output MDR2_write,
  output MDR2_zero,
  output MEM_read,
  output MEM_read2,
  output MEM_write,
  output MDR0_MEM_IN,
  output MDR1_MEM_IN,
  output MDR2_MEM_IN,
  output MDR0_REG_IN,
  output MDR1_REG_IN,
  output MDR2_REG_IN,
  output MAR_REG_ID,
  output MDR0_REG_ID,
  output MDR1_REG_ID,
  output MDR2_REG_ID,
  output REG_OUT_MAR,
  output REG_OUT_MDR0,
  output REG_OUT_MDR1,
  output REG_OUT_MDR2,
  output REG_read,
  output REG_write,
  output MAR_MDR0,
  output MAR_MDR1,
  output MAR_MDR2,
  output MDR0_MAR,
  output MDR0_MDR1,
  output MDR0_MDR2,
  output MDR1_MAR,
  output MDR1_MDR0,
  output MDR1_MDR2,
  output MDR2_MAR,
  output MDR2_MDR0,
  output MDR2_MDR1,
  output MAR_ALU_IN0,
  output MDR0_ALU_IN0,
  output MDR1_ALU_IN0,
  output MDR2_ALU_IN0,
  output MAR_ALU_IN1,
  output MDR0_ALU_IN1,
  output MDR1_ALU_IN1,
  output MDR2_ALU_IN1,
  output [7:0] ALU_SELECT,
  output ALU_read,
  output ALU_write,
  output ALU_readFlags,
  output ALU_OUT_MAR,
  output ALU_OUT_MDR0,
  output ALU_OUT_MDR1,
  output ALU_OUT_MDR2,
  output ALU_REMAINDER_MAR,
  output ALU_REMAINDER_MDR0,
  output ALU_REMAINDER_MDR1,
  output ALU_REMAINDER_MDR2,
  output CU_endInstruction
);

  wire [12:0] rom_2_data;
  wire [63:0] rom_1_data;

  ROM #(.dataWidth(64)) rom_1 (.addr(in_1), .data(rom_1_data));
  ROM #(.dataWidth(13)) rom_2 (.addr(in_1), .data(rom_2_data));
  INS_ROM_AND ins_rom_and_1 (
    .in_1(rom_1_data[0]), .in_2(rom_1_data[1]), .in_3(rom_1_data[2]), .in_4(rom_1_data[3]),
    .in_5(rom_1_data[4]), .in_6(rom_1_data[5]), .in_7(rom_1_data[6]), .in_8(rom_1_data[7]),
    .in_9(rom_1_data[8]), .in_10(rom_1_data[9]), .in_11(rom_1_data[10]), .in_12(rom_1_data[11]),
    .in_13(rom_1_data[12]), .in_14(rom_1_data[13]), .in_15(rom_1_data[14]), .in_16(rom_1_data[15]),
    .in_17(rom_1_data[16]), .in_18(rom_1_data[17]), .in_19(rom_1_data[18]), .in_20(rom_1_data[19]),
    .in_21(rom_1_data[20]), .in_22(rom_1_data[21]), .in_23(rom_1_data[22]), .in_24(rom_1_data[23]),
    .in_25(rom_1_data[24]), .in_26(rom_1_data[25]), .in_27(rom_1_data[26]), .in_28(rom_1_data[27]),
    .in_29(rom_1_data[28]), .in_30(rom_1_data[29]), .in_31(rom_1_data[30]), .in_32(rom_1_data[31]),
    .in_33(rom_1_data[32]), .in_34(rom_1_data[33]), .in_35(rom_1_data[34]), .in_36(rom_1_data[35]),
    .in_37(rom_1_data[36]), .in_38(rom_1_data[37]), .in_39(rom_1_data[38]), .in_40(rom_1_data[39]),
    .in_41(rom_1_data[40]), .in_42(rom_1_data[41]), .in_43(rom_1_data[42]), .in_44(rom_1_data[43]),
    .in_45(rom_1_data[44]), .in_46(rom_1_data[45]), .in_47(rom_1_data[46]), .in_48(rom_1_data[47]),
    .in_49(rom_1_data[48]), .in_50(rom_1_data[49]), .in_51(rom_1_data[50]), .in_52(rom_1_data[51]),
    .in_53(rom_1_data[52]), .in_54(rom_1_data[53]), .in_55(rom_1_data[54]), .in_56(rom_1_data[55]),
    .in_57(rom_1_data[56]), .in_58({rom_2_data[0], rom_1_data[63:57]}), .in_59(rom_2_data[1]),
    .in_60(rom_2_data[2]), .in_61(rom_2_data[3]), .in_62(rom_2_data[4]), .in_63(rom_2_data[5]),
    .in_64(rom_2_data[6]), .in_65(rom_2_data[7]), .in_66(rom_2_data[8]), .in_67(rom_2_data[9]),
    .in_68(rom_2_data[10]), .in_69(rom_2_data[11]), .in_70(rom_2_data[12]), .CLK(CLK), .IP_inc(IP_inc),
    .IP_read(IP_read), .IP_write(IP_write), .SP_inc(SP_inc), .SP_dec(SP_dec), .SP_read(SP_read),
    .SP_write(SP_write), .MAR_read(MAR_read), .MAR_write(MAR_write), .MDR0_read(MDR0_read),
    .MDR0_write(MDR0_write), .MDR0_zero(MDR0_zero), .MDR1_read(MDR1_read), .MDR1_write(MDR1_write),
    .MDR1_zero(MDR1_zero), .MDR2_read(MDR2_read), .MDR2_write(MDR2_write), .MDR2_zero(MDR2_zero),
    .MEM_read(MEM_read), .MEM_read2(MEM_read2), .MEM_write(MEM_write), .MDR0_MEM_IN(MDR0_MEM_IN),
    .MDR1_MEM_IN(MDR1_MEM_IN), .MDR2_MEM_IN(MDR2_MEM_IN), .MDR0_REG_IN(MDR0_REG_IN),
    .MDR1_REG_IN(MDR1_REG_IN), .MDR2_REG_IN(MDR2_REG_IN), .MAR_REG_ID(MAR_REG_ID), .MDR0_REG_ID(MDR0_REG_ID),
    .MDR1_REG_ID(MDR1_REG_ID), .MDR2_REG_ID(MDR2_REG_ID), .REG_OUT_MAR(REG_OUT_MAR),
    .REG_OUT_MDR0(REG_OUT_MDR0), .REG_OUT_MDR1(REG_OUT_MDR1), .REG_OUT_MDR2(REG_OUT_MDR2),
    .REG_read(REG_read), .REG_write(REG_write), .MAR_MDR0(MAR_MDR0), .MAR_MDR1(MAR_MDR1),
    .MAR_MDR2(MAR_MDR2), .MDR0_MAR(MDR0_MAR), .MDR0_MDR1(MDR0_MDR1), .MDR0_MDR2(MDR0_MDR2),
    .MDR1_MAR(MDR1_MAR), .MDR1_MDR0(MDR1_MDR0), .MDR1_MDR2(MDR1_MDR2), .MDR2_MAR(MDR2_MAR),
    .MDR2_MDR0(MDR2_MDR0), .MDR2_MDR1(MDR2_MDR1), .MAR_ALU_IN0(MAR_ALU_IN0), .MDR0_ALU_IN0(MDR0_ALU_IN0),
    .MDR1_ALU_IN0(MDR1_ALU_IN0), .MDR2_ALU_IN0(MDR2_ALU_IN0), .MAR_ALU_IN1(MAR_ALU_IN1),
    .MDR0_ALU_IN1(MDR0_ALU_IN1), .MDR1_ALU_IN1(MDR1_ALU_IN1), .MDR2_ALU_IN1(MDR2_ALU_IN1),
    .ALU_SELECT(ALU_SELECT), .ALU_read(ALU_read), .ALU_write(ALU_write), .ALU_readFlags(ALU_readFlags),
    .ALU_OUT_MAR(ALU_OUT_MAR), .ALU_OUT_MDR0(ALU_OUT_MDR0), .ALU_OUT_MDR1(ALU_OUT_MDR1),
    .ALU_OUT_MDR2(ALU_OUT_MDR2), .ALU_REMAINDER_MAR(ALU_REMAINDER_MAR),
    .ALU_REMAINDER_MDR0(ALU_REMAINDER_MDR0), .ALU_REMAINDER_MDR1(ALU_REMAINDER_MDR1),
    .ALU_REMAINDER_MDR2(ALU_REMAINDER_MDR2), .CU_endInstruction(CU_endInstruction));

  // Notes on the sheet:
  //   contents of rom_1 (hex, n*v repeats v):
  //   12*0 40182 5*0 40182 5*0 40182 5*0 40182 14*0 40182 5*0 40182 5*0 40182 10*0 908080
  //   contents of rom_2 (hex, n*v repeats v):
  //   11*0 1000 22 4*0 1000 22 4*0 1000 42 0 1000 1000 0 1000 5*0 1000 6*0 1000 0 1000 22 0 0 1000 0 1000
  //   22 0 0 1000 0 1000 22 7*0 1000 1000 1000
endmodule

module INS_ROM_6 (
  input  [7:0] in_1,
  input  CLK,
  output IP_inc,
  output IP_read,
  output IP_write,
  output SP_inc,
  output SP_dec,
  output SP_read,
  output SP_write,
  output MAR_read,
  output MAR_write,
  output MDR0_read,
  output MDR0_write,
  output MDR0_zero,
  output MDR1_read,
  output MDR1_write,
  output MDR1_zero,
  output MDR2_read,
  output MDR2_write,
  output MDR2_zero,
  output MEM_read,
  output MEM_read2,
  output MEM_write,
  output MDR0_MEM_IN,
  output MDR1_MEM_IN,
  output MDR2_MEM_IN,
  output MDR0_REG_IN,
  output MDR1_REG_IN,
  output MDR2_REG_IN,
  output MAR_REG_ID,
  output MDR0_REG_ID,
  output MDR1_REG_ID,
  output MDR2_REG_ID,
  output REG_OUT_MAR,
  output REG_OUT_MDR0,
  output REG_OUT_MDR1,
  output REG_OUT_MDR2,
  output REG_read,
  output REG_write,
  output MAR_MDR0,
  output MAR_MDR1,
  output MAR_MDR2,
  output MDR0_MAR,
  output MDR0_MDR1,
  output MDR0_MDR2,
  output MDR1_MAR,
  output MDR1_MDR0,
  output MDR1_MDR2,
  output MDR2_MAR,
  output MDR2_MDR0,
  output MDR2_MDR1,
  output MAR_ALU_IN0,
  output MDR0_ALU_IN0,
  output MDR1_ALU_IN0,
  output MDR2_ALU_IN0,
  output MAR_ALU_IN1,
  output MDR0_ALU_IN1,
  output MDR1_ALU_IN1,
  output MDR2_ALU_IN1,
  output [7:0] ALU_SELECT,
  output ALU_read,
  output ALU_write,
  output ALU_readFlags,
  output ALU_OUT_MAR,
  output ALU_OUT_MDR0,
  output ALU_OUT_MDR1,
  output ALU_OUT_MDR2,
  output ALU_REMAINDER_MAR,
  output ALU_REMAINDER_MDR0,
  output ALU_REMAINDER_MDR1,
  output ALU_REMAINDER_MDR2,
  output CU_endInstruction
);

  wire [12:0] rom_2_data;
  wire [63:0] rom_1_data;

  ROM #(.dataWidth(64)) rom_1 (.addr(in_1), .data(rom_1_data));
  ROM #(.dataWidth(13)) rom_2 (.addr(in_1), .data(rom_2_data));
  INS_ROM_AND ins_rom_and_1 (
    .in_1(rom_1_data[0]), .in_2(rom_1_data[1]), .in_3(rom_1_data[2]), .in_4(rom_1_data[3]),
    .in_5(rom_1_data[4]), .in_6(rom_1_data[5]), .in_7(rom_1_data[6]), .in_8(rom_1_data[7]),
    .in_9(rom_1_data[8]), .in_10(rom_1_data[9]), .in_11(rom_1_data[10]), .in_12(rom_1_data[11]),
    .in_13(rom_1_data[12]), .in_14(rom_1_data[13]), .in_15(rom_1_data[14]), .in_16(rom_1_data[15]),
    .in_17(rom_1_data[16]), .in_18(rom_1_data[17]), .in_19(rom_1_data[18]), .in_20(rom_1_data[19]),
    .in_21(rom_1_data[20]), .in_22(rom_1_data[21]), .in_23(rom_1_data[22]), .in_24(rom_1_data[23]),
    .in_25(rom_1_data[24]), .in_26(rom_1_data[25]), .in_27(rom_1_data[26]), .in_28(rom_1_data[27]),
    .in_29(rom_1_data[28]), .in_30(rom_1_data[29]), .in_31(rom_1_data[30]), .in_32(rom_1_data[31]),
    .in_33(rom_1_data[32]), .in_34(rom_1_data[33]), .in_35(rom_1_data[34]), .in_36(rom_1_data[35]),
    .in_37(rom_1_data[36]), .in_38(rom_1_data[37]), .in_39(rom_1_data[38]), .in_40(rom_1_data[39]),
    .in_41(rom_1_data[40]), .in_42(rom_1_data[41]), .in_43(rom_1_data[42]), .in_44(rom_1_data[43]),
    .in_45(rom_1_data[44]), .in_46(rom_1_data[45]), .in_47(rom_1_data[46]), .in_48(rom_1_data[47]),
    .in_49(rom_1_data[48]), .in_50(rom_1_data[49]), .in_51(rom_1_data[50]), .in_52(rom_1_data[51]),
    .in_53(rom_1_data[52]), .in_54(rom_1_data[53]), .in_55(rom_1_data[54]), .in_56(rom_1_data[55]),
    .in_57(rom_1_data[56]), .in_58({rom_2_data[0], rom_1_data[63:57]}), .in_59(rom_2_data[1]),
    .in_60(rom_2_data[2]), .in_61(rom_2_data[3]), .in_62(rom_2_data[4]), .in_63(rom_2_data[5]),
    .in_64(rom_2_data[6]), .in_65(rom_2_data[7]), .in_66(rom_2_data[8]), .in_67(rom_2_data[9]),
    .in_68(rom_2_data[10]), .in_69(rom_2_data[11]), .in_70(rom_2_data[12]), .CLK(CLK), .IP_inc(IP_inc),
    .IP_read(IP_read), .IP_write(IP_write), .SP_inc(SP_inc), .SP_dec(SP_dec), .SP_read(SP_read),
    .SP_write(SP_write), .MAR_read(MAR_read), .MAR_write(MAR_write), .MDR0_read(MDR0_read),
    .MDR0_write(MDR0_write), .MDR0_zero(MDR0_zero), .MDR1_read(MDR1_read), .MDR1_write(MDR1_write),
    .MDR1_zero(MDR1_zero), .MDR2_read(MDR2_read), .MDR2_write(MDR2_write), .MDR2_zero(MDR2_zero),
    .MEM_read(MEM_read), .MEM_read2(MEM_read2), .MEM_write(MEM_write), .MDR0_MEM_IN(MDR0_MEM_IN),
    .MDR1_MEM_IN(MDR1_MEM_IN), .MDR2_MEM_IN(MDR2_MEM_IN), .MDR0_REG_IN(MDR0_REG_IN),
    .MDR1_REG_IN(MDR1_REG_IN), .MDR2_REG_IN(MDR2_REG_IN), .MAR_REG_ID(MAR_REG_ID), .MDR0_REG_ID(MDR0_REG_ID),
    .MDR1_REG_ID(MDR1_REG_ID), .MDR2_REG_ID(MDR2_REG_ID), .REG_OUT_MAR(REG_OUT_MAR),
    .REG_OUT_MDR0(REG_OUT_MDR0), .REG_OUT_MDR1(REG_OUT_MDR1), .REG_OUT_MDR2(REG_OUT_MDR2),
    .REG_read(REG_read), .REG_write(REG_write), .MAR_MDR0(MAR_MDR0), .MAR_MDR1(MAR_MDR1),
    .MAR_MDR2(MAR_MDR2), .MDR0_MAR(MDR0_MAR), .MDR0_MDR1(MDR0_MDR1), .MDR0_MDR2(MDR0_MDR2),
    .MDR1_MAR(MDR1_MAR), .MDR1_MDR0(MDR1_MDR0), .MDR1_MDR2(MDR1_MDR2), .MDR2_MAR(MDR2_MAR),
    .MDR2_MDR0(MDR2_MDR0), .MDR2_MDR1(MDR2_MDR1), .MAR_ALU_IN0(MAR_ALU_IN0), .MDR0_ALU_IN0(MDR0_ALU_IN0),
    .MDR1_ALU_IN0(MDR1_ALU_IN0), .MDR2_ALU_IN0(MDR2_ALU_IN0), .MAR_ALU_IN1(MAR_ALU_IN1),
    .MDR0_ALU_IN1(MDR0_ALU_IN1), .MDR1_ALU_IN1(MDR1_ALU_IN1), .MDR2_ALU_IN1(MDR2_ALU_IN1),
    .ALU_SELECT(ALU_SELECT), .ALU_read(ALU_read), .ALU_write(ALU_write), .ALU_readFlags(ALU_readFlags),
    .ALU_OUT_MAR(ALU_OUT_MAR), .ALU_OUT_MDR0(ALU_OUT_MDR0), .ALU_OUT_MDR1(ALU_OUT_MDR1),
    .ALU_OUT_MDR2(ALU_OUT_MDR2), .ALU_REMAINDER_MAR(ALU_REMAINDER_MAR),
    .ALU_REMAINDER_MDR0(ALU_REMAINDER_MDR0), .ALU_REMAINDER_MDR1(ALU_REMAINDER_MDR1),
    .ALU_REMAINDER_MDR2(ALU_REMAINDER_MDR2), .CU_endInstruction(CU_endInstruction));

  // Notes on the sheet:
  //   contents of rom_1 (hex, n*v repeats v):
  //   68*0 80000301380
endmodule

module INS_ROM_7 (
  input  [7:0] in_1,
  input  CLK,
  output IP_inc,
  output IP_read,
  output IP_write,
  output SP_inc,
  output SP_dec,
  output SP_read,
  output SP_write,
  output MAR_read,
  output MAR_write,
  output MDR0_read,
  output MDR0_write,
  output MDR0_zero,
  output MDR1_read,
  output MDR1_write,
  output MDR1_zero,
  output MDR2_read,
  output MDR2_write,
  output MDR2_zero,
  output MEM_read,
  output MEM_read2,
  output MEM_write,
  output MDR0_MEM_IN,
  output MDR1_MEM_IN,
  output MDR2_MEM_IN,
  output MDR0_REG_IN,
  output MDR1_REG_IN,
  output MDR2_REG_IN,
  output MAR_REG_ID,
  output MDR0_REG_ID,
  output MDR1_REG_ID,
  output MDR2_REG_ID,
  output REG_OUT_MAR,
  output REG_OUT_MDR0,
  output REG_OUT_MDR1,
  output REG_OUT_MDR2,
  output REG_read,
  output REG_write,
  output MAR_MDR0,
  output MAR_MDR1,
  output MAR_MDR2,
  output MDR0_MAR,
  output MDR0_MDR1,
  output MDR0_MDR2,
  output MDR1_MAR,
  output MDR1_MDR0,
  output MDR1_MDR2,
  output MDR2_MAR,
  output MDR2_MDR0,
  output MDR2_MDR1,
  output MAR_ALU_IN0,
  output MDR0_ALU_IN0,
  output MDR1_ALU_IN0,
  output MDR2_ALU_IN0,
  output MAR_ALU_IN1,
  output MDR0_ALU_IN1,
  output MDR1_ALU_IN1,
  output MDR2_ALU_IN1,
  output [7:0] ALU_SELECT,
  output ALU_read,
  output ALU_write,
  output ALU_readFlags,
  output ALU_OUT_MAR,
  output ALU_OUT_MDR0,
  output ALU_OUT_MDR1,
  output ALU_OUT_MDR2,
  output ALU_REMAINDER_MAR,
  output ALU_REMAINDER_MDR0,
  output ALU_REMAINDER_MDR1,
  output ALU_REMAINDER_MDR2,
  output CU_endInstruction
);

  wire [12:0] rom_2_data;
  wire [63:0] rom_1_data;

  ROM #(.dataWidth(64)) rom_1 (.addr(in_1), .data(rom_1_data));
  ROM #(.dataWidth(13)) rom_2 (.addr(in_1), .data(rom_2_data));
  INS_ROM_AND ins_rom_and_1 (
    .in_1(rom_1_data[0]), .in_2(rom_1_data[1]), .in_3(rom_1_data[2]), .in_4(rom_1_data[3]),
    .in_5(rom_1_data[4]), .in_6(rom_1_data[5]), .in_7(rom_1_data[6]), .in_8(rom_1_data[7]),
    .in_9(rom_1_data[8]), .in_10(rom_1_data[9]), .in_11(rom_1_data[10]), .in_12(rom_1_data[11]),
    .in_13(rom_1_data[12]), .in_14(rom_1_data[13]), .in_15(rom_1_data[14]), .in_16(rom_1_data[15]),
    .in_17(rom_1_data[16]), .in_18(rom_1_data[17]), .in_19(rom_1_data[18]), .in_20(rom_1_data[19]),
    .in_21(rom_1_data[20]), .in_22(rom_1_data[21]), .in_23(rom_1_data[22]), .in_24(rom_1_data[23]),
    .in_25(rom_1_data[24]), .in_26(rom_1_data[25]), .in_27(rom_1_data[26]), .in_28(rom_1_data[27]),
    .in_29(rom_1_data[28]), .in_30(rom_1_data[29]), .in_31(rom_1_data[30]), .in_32(rom_1_data[31]),
    .in_33(rom_1_data[32]), .in_34(rom_1_data[33]), .in_35(rom_1_data[34]), .in_36(rom_1_data[35]),
    .in_37(rom_1_data[36]), .in_38(rom_1_data[37]), .in_39(rom_1_data[38]), .in_40(rom_1_data[39]),
    .in_41(rom_1_data[40]), .in_42(rom_1_data[41]), .in_43(rom_1_data[42]), .in_44(rom_1_data[43]),
    .in_45(rom_1_data[44]), .in_46(rom_1_data[45]), .in_47(rom_1_data[46]), .in_48(rom_1_data[47]),
    .in_49(rom_1_data[48]), .in_50(rom_1_data[49]), .in_51(rom_1_data[50]), .in_52(rom_1_data[51]),
    .in_53(rom_1_data[52]), .in_54(rom_1_data[53]), .in_55(rom_1_data[54]), .in_56(rom_1_data[55]),
    .in_57(rom_1_data[56]), .in_58({rom_2_data[0], rom_1_data[63:57]}), .in_59(rom_2_data[1]),
    .in_60(rom_2_data[2]), .in_61(rom_2_data[3]), .in_62(rom_2_data[4]), .in_63(rom_2_data[5]),
    .in_64(rom_2_data[6]), .in_65(rom_2_data[7]), .in_66(rom_2_data[8]), .in_67(rom_2_data[9]),
    .in_68(rom_2_data[10]), .in_69(rom_2_data[11]), .in_70(rom_2_data[12]), .CLK(CLK), .IP_inc(IP_inc),
    .IP_read(IP_read), .IP_write(IP_write), .SP_inc(SP_inc), .SP_dec(SP_dec), .SP_read(SP_read),
    .SP_write(SP_write), .MAR_read(MAR_read), .MAR_write(MAR_write), .MDR0_read(MDR0_read),
    .MDR0_write(MDR0_write), .MDR0_zero(MDR0_zero), .MDR1_read(MDR1_read), .MDR1_write(MDR1_write),
    .MDR1_zero(MDR1_zero), .MDR2_read(MDR2_read), .MDR2_write(MDR2_write), .MDR2_zero(MDR2_zero),
    .MEM_read(MEM_read), .MEM_read2(MEM_read2), .MEM_write(MEM_write), .MDR0_MEM_IN(MDR0_MEM_IN),
    .MDR1_MEM_IN(MDR1_MEM_IN), .MDR2_MEM_IN(MDR2_MEM_IN), .MDR0_REG_IN(MDR0_REG_IN),
    .MDR1_REG_IN(MDR1_REG_IN), .MDR2_REG_IN(MDR2_REG_IN), .MAR_REG_ID(MAR_REG_ID), .MDR0_REG_ID(MDR0_REG_ID),
    .MDR1_REG_ID(MDR1_REG_ID), .MDR2_REG_ID(MDR2_REG_ID), .REG_OUT_MAR(REG_OUT_MAR),
    .REG_OUT_MDR0(REG_OUT_MDR0), .REG_OUT_MDR1(REG_OUT_MDR1), .REG_OUT_MDR2(REG_OUT_MDR2),
    .REG_read(REG_read), .REG_write(REG_write), .MAR_MDR0(MAR_MDR0), .MAR_MDR1(MAR_MDR1),
    .MAR_MDR2(MAR_MDR2), .MDR0_MAR(MDR0_MAR), .MDR0_MDR1(MDR0_MDR1), .MDR0_MDR2(MDR0_MDR2),
    .MDR1_MAR(MDR1_MAR), .MDR1_MDR0(MDR1_MDR0), .MDR1_MDR2(MDR1_MDR2), .MDR2_MAR(MDR2_MAR),
    .MDR2_MDR0(MDR2_MDR0), .MDR2_MDR1(MDR2_MDR1), .MAR_ALU_IN0(MAR_ALU_IN0), .MDR0_ALU_IN0(MDR0_ALU_IN0),
    .MDR1_ALU_IN0(MDR1_ALU_IN0), .MDR2_ALU_IN0(MDR2_ALU_IN0), .MAR_ALU_IN1(MAR_ALU_IN1),
    .MDR0_ALU_IN1(MDR0_ALU_IN1), .MDR1_ALU_IN1(MDR1_ALU_IN1), .MDR2_ALU_IN1(MDR2_ALU_IN1),
    .ALU_SELECT(ALU_SELECT), .ALU_read(ALU_read), .ALU_write(ALU_write), .ALU_readFlags(ALU_readFlags),
    .ALU_OUT_MAR(ALU_OUT_MAR), .ALU_OUT_MDR0(ALU_OUT_MDR0), .ALU_OUT_MDR1(ALU_OUT_MDR1),
    .ALU_OUT_MDR2(ALU_OUT_MDR2), .ALU_REMAINDER_MAR(ALU_REMAINDER_MAR),
    .ALU_REMAINDER_MDR0(ALU_REMAINDER_MDR0), .ALU_REMAINDER_MDR1(ALU_REMAINDER_MDR1),
    .ALU_REMAINDER_MDR2(ALU_REMAINDER_MDR2), .CU_endInstruction(CU_endInstruction));

  // Notes on the sheet:
  //   contents of rom_1 (hex, n*v repeats v):
  //   68*0 40182
  //   contents of rom_2 (hex, n*v repeats v):
  //   68*0 1000
endmodule

module INS_ROM_8 (
  input  [7:0] in_1,
  input  CLK,
  output IP_inc,
  output IP_read,
  output IP_write,
  output SP_inc,
  output SP_dec,
  output SP_read,
  output SP_write,
  output MAR_read,
  output MAR_write,
  output MDR0_read,
  output MDR0_write,
  output MDR0_zero,
  output MDR1_read,
  output MDR1_write,
  output MDR1_zero,
  output MDR2_read,
  output MDR2_write,
  output MDR2_zero,
  output MEM_read,
  output MEM_read2,
  output MEM_write,
  output MDR0_MEM_IN,
  output MDR1_MEM_IN,
  output MDR2_MEM_IN,
  output MDR0_REG_IN,
  output MDR1_REG_IN,
  output MDR2_REG_IN,
  output MAR_REG_ID,
  output MDR0_REG_ID,
  output MDR1_REG_ID,
  output MDR2_REG_ID,
  output REG_OUT_MAR,
  output REG_OUT_MDR0,
  output REG_OUT_MDR1,
  output REG_OUT_MDR2,
  output REG_read,
  output REG_write,
  output MAR_MDR0,
  output MAR_MDR1,
  output MAR_MDR2,
  output MDR0_MAR,
  output MDR0_MDR1,
  output MDR0_MDR2,
  output MDR1_MAR,
  output MDR1_MDR0,
  output MDR1_MDR2,
  output MDR2_MAR,
  output MDR2_MDR0,
  output MDR2_MDR1,
  output MAR_ALU_IN0,
  output MDR0_ALU_IN0,
  output MDR1_ALU_IN0,
  output MDR2_ALU_IN0,
  output MAR_ALU_IN1,
  output MDR0_ALU_IN1,
  output MDR1_ALU_IN1,
  output MDR2_ALU_IN1,
  output [7:0] ALU_SELECT,
  output ALU_read,
  output ALU_write,
  output ALU_readFlags,
  output ALU_OUT_MAR,
  output ALU_OUT_MDR0,
  output ALU_OUT_MDR1,
  output ALU_OUT_MDR2,
  output ALU_REMAINDER_MAR,
  output ALU_REMAINDER_MDR0,
  output ALU_REMAINDER_MDR1,
  output ALU_REMAINDER_MDR2,
  output CU_endInstruction
);

  wire [12:0] rom_2_data;
  wire [63:0] rom_1_data;

  ROM #(.dataWidth(64)) rom_1 (.addr(in_1), .data(rom_1_data));
  ROM #(.dataWidth(13)) rom_2 (.addr(in_1), .data(rom_2_data));
  INS_ROM_AND ins_rom_and_1 (
    .in_1(rom_1_data[0]), .in_2(rom_1_data[1]), .in_3(rom_1_data[2]), .in_4(rom_1_data[3]),
    .in_5(rom_1_data[4]), .in_6(rom_1_data[5]), .in_7(rom_1_data[6]), .in_8(rom_1_data[7]),
    .in_9(rom_1_data[8]), .in_10(rom_1_data[9]), .in_11(rom_1_data[10]), .in_12(rom_1_data[11]),
    .in_13(rom_1_data[12]), .in_14(rom_1_data[13]), .in_15(rom_1_data[14]), .in_16(rom_1_data[15]),
    .in_17(rom_1_data[16]), .in_18(rom_1_data[17]), .in_19(rom_1_data[18]), .in_20(rom_1_data[19]),
    .in_21(rom_1_data[20]), .in_22(rom_1_data[21]), .in_23(rom_1_data[22]), .in_24(rom_1_data[23]),
    .in_25(rom_1_data[24]), .in_26(rom_1_data[25]), .in_27(rom_1_data[26]), .in_28(rom_1_data[27]),
    .in_29(rom_1_data[28]), .in_30(rom_1_data[29]), .in_31(rom_1_data[30]), .in_32(rom_1_data[31]),
    .in_33(rom_1_data[32]), .in_34(rom_1_data[33]), .in_35(rom_1_data[34]), .in_36(rom_1_data[35]),
    .in_37(rom_1_data[36]), .in_38(rom_1_data[37]), .in_39(rom_1_data[38]), .in_40(rom_1_data[39]),
    .in_41(rom_1_data[40]), .in_42(rom_1_data[41]), .in_43(rom_1_data[42]), .in_44(rom_1_data[43]),
    .in_45(rom_1_data[44]), .in_46(rom_1_data[45]), .in_47(rom_1_data[46]), .in_48(rom_1_data[47]),
    .in_49(rom_1_data[48]), .in_50(rom_1_data[49]), .in_51(rom_1_data[50]), .in_52(rom_1_data[51]),
    .in_53(rom_1_data[52]), .in_54(rom_1_data[53]), .in_55(rom_1_data[54]), .in_56(rom_1_data[55]),
    .in_57(rom_1_data[56]), .in_58({rom_2_data[0], rom_1_data[63:57]}), .in_59(rom_2_data[1]),
    .in_60(rom_2_data[2]), .in_61(rom_2_data[3]), .in_62(rom_2_data[4]), .in_63(rom_2_data[5]),
    .in_64(rom_2_data[6]), .in_65(rom_2_data[7]), .in_66(rom_2_data[8]), .in_67(rom_2_data[9]),
    .in_68(rom_2_data[10]), .in_69(rom_2_data[11]), .in_70(rom_2_data[12]), .CLK(CLK), .IP_inc(IP_inc),
    .IP_read(IP_read), .IP_write(IP_write), .SP_inc(SP_inc), .SP_dec(SP_dec), .SP_read(SP_read),
    .SP_write(SP_write), .MAR_read(MAR_read), .MAR_write(MAR_write), .MDR0_read(MDR0_read),
    .MDR0_write(MDR0_write), .MDR0_zero(MDR0_zero), .MDR1_read(MDR1_read), .MDR1_write(MDR1_write),
    .MDR1_zero(MDR1_zero), .MDR2_read(MDR2_read), .MDR2_write(MDR2_write), .MDR2_zero(MDR2_zero),
    .MEM_read(MEM_read), .MEM_read2(MEM_read2), .MEM_write(MEM_write), .MDR0_MEM_IN(MDR0_MEM_IN),
    .MDR1_MEM_IN(MDR1_MEM_IN), .MDR2_MEM_IN(MDR2_MEM_IN), .MDR0_REG_IN(MDR0_REG_IN),
    .MDR1_REG_IN(MDR1_REG_IN), .MDR2_REG_IN(MDR2_REG_IN), .MAR_REG_ID(MAR_REG_ID), .MDR0_REG_ID(MDR0_REG_ID),
    .MDR1_REG_ID(MDR1_REG_ID), .MDR2_REG_ID(MDR2_REG_ID), .REG_OUT_MAR(REG_OUT_MAR),
    .REG_OUT_MDR0(REG_OUT_MDR0), .REG_OUT_MDR1(REG_OUT_MDR1), .REG_OUT_MDR2(REG_OUT_MDR2),
    .REG_read(REG_read), .REG_write(REG_write), .MAR_MDR0(MAR_MDR0), .MAR_MDR1(MAR_MDR1),
    .MAR_MDR2(MAR_MDR2), .MDR0_MAR(MDR0_MAR), .MDR0_MDR1(MDR0_MDR1), .MDR0_MDR2(MDR0_MDR2),
    .MDR1_MAR(MDR1_MAR), .MDR1_MDR0(MDR1_MDR0), .MDR1_MDR2(MDR1_MDR2), .MDR2_MAR(MDR2_MAR),
    .MDR2_MDR0(MDR2_MDR0), .MDR2_MDR1(MDR2_MDR1), .MAR_ALU_IN0(MAR_ALU_IN0), .MDR0_ALU_IN0(MDR0_ALU_IN0),
    .MDR1_ALU_IN0(MDR1_ALU_IN0), .MDR2_ALU_IN0(MDR2_ALU_IN0), .MAR_ALU_IN1(MAR_ALU_IN1),
    .MDR0_ALU_IN1(MDR0_ALU_IN1), .MDR1_ALU_IN1(MDR1_ALU_IN1), .MDR2_ALU_IN1(MDR2_ALU_IN1),
    .ALU_SELECT(ALU_SELECT), .ALU_read(ALU_read), .ALU_write(ALU_write), .ALU_readFlags(ALU_readFlags),
    .ALU_OUT_MAR(ALU_OUT_MAR), .ALU_OUT_MDR0(ALU_OUT_MDR0), .ALU_OUT_MDR1(ALU_OUT_MDR1),
    .ALU_OUT_MDR2(ALU_OUT_MDR2), .ALU_REMAINDER_MAR(ALU_REMAINDER_MAR),
    .ALU_REMAINDER_MDR0(ALU_REMAINDER_MDR0), .ALU_REMAINDER_MDR1(ALU_REMAINDER_MDR1),
    .ALU_REMAINDER_MDR2(ALU_REMAINDER_MDR2), .CU_endInstruction(CU_endInstruction));
endmodule

module INS_ROM_9 (
  input  [7:0] in_1,
  input  CLK,
  output IP_inc,
  output IP_read,
  output IP_write,
  output SP_inc,
  output SP_dec,
  output SP_read,
  output SP_write,
  output MAR_read,
  output MAR_write,
  output MDR0_read,
  output MDR0_write,
  output MDR0_zero,
  output MDR1_read,
  output MDR1_write,
  output MDR1_zero,
  output MDR2_read,
  output MDR2_write,
  output MDR2_zero,
  output MEM_read,
  output MEM_read2,
  output MEM_write,
  output MDR0_MEM_IN,
  output MDR1_MEM_IN,
  output MDR2_MEM_IN,
  output MDR0_REG_IN,
  output MDR1_REG_IN,
  output MDR2_REG_IN,
  output MAR_REG_ID,
  output MDR0_REG_ID,
  output MDR1_REG_ID,
  output MDR2_REG_ID,
  output REG_OUT_MAR,
  output REG_OUT_MDR0,
  output REG_OUT_MDR1,
  output REG_OUT_MDR2,
  output REG_read,
  output REG_write,
  output MAR_MDR0,
  output MAR_MDR1,
  output MAR_MDR2,
  output MDR0_MAR,
  output MDR0_MDR1,
  output MDR0_MDR2,
  output MDR1_MAR,
  output MDR1_MDR0,
  output MDR1_MDR2,
  output MDR2_MAR,
  output MDR2_MDR0,
  output MDR2_MDR1,
  output MAR_ALU_IN0,
  output MDR0_ALU_IN0,
  output MDR1_ALU_IN0,
  output MDR2_ALU_IN0,
  output MAR_ALU_IN1,
  output MDR0_ALU_IN1,
  output MDR1_ALU_IN1,
  output MDR2_ALU_IN1,
  output [7:0] ALU_SELECT,
  output ALU_read,
  output ALU_write,
  output ALU_readFlags,
  output ALU_OUT_MAR,
  output ALU_OUT_MDR0,
  output ALU_OUT_MDR1,
  output ALU_OUT_MDR2,
  output ALU_REMAINDER_MAR,
  output ALU_REMAINDER_MDR0,
  output ALU_REMAINDER_MDR1,
  output ALU_REMAINDER_MDR2,
  output CU_endInstruction
);

  wire [12:0] rom_2_data;
  wire [63:0] rom_1_data;

  ROM #(.dataWidth(64)) rom_1 (.addr(in_1), .data(rom_1_data));
  ROM #(.dataWidth(13)) rom_2 (.addr(in_1), .data(rom_2_data));
  INS_ROM_AND ins_rom_and_1 (
    .in_1(rom_1_data[0]), .in_2(rom_1_data[1]), .in_3(rom_1_data[2]), .in_4(rom_1_data[3]),
    .in_5(rom_1_data[4]), .in_6(rom_1_data[5]), .in_7(rom_1_data[6]), .in_8(rom_1_data[7]),
    .in_9(rom_1_data[8]), .in_10(rom_1_data[9]), .in_11(rom_1_data[10]), .in_12(rom_1_data[11]),
    .in_13(rom_1_data[12]), .in_14(rom_1_data[13]), .in_15(rom_1_data[14]), .in_16(rom_1_data[15]),
    .in_17(rom_1_data[16]), .in_18(rom_1_data[17]), .in_19(rom_1_data[18]), .in_20(rom_1_data[19]),
    .in_21(rom_1_data[20]), .in_22(rom_1_data[21]), .in_23(rom_1_data[22]), .in_24(rom_1_data[23]),
    .in_25(rom_1_data[24]), .in_26(rom_1_data[25]), .in_27(rom_1_data[26]), .in_28(rom_1_data[27]),
    .in_29(rom_1_data[28]), .in_30(rom_1_data[29]), .in_31(rom_1_data[30]), .in_32(rom_1_data[31]),
    .in_33(rom_1_data[32]), .in_34(rom_1_data[33]), .in_35(rom_1_data[34]), .in_36(rom_1_data[35]),
    .in_37(rom_1_data[36]), .in_38(rom_1_data[37]), .in_39(rom_1_data[38]), .in_40(rom_1_data[39]),
    .in_41(rom_1_data[40]), .in_42(rom_1_data[41]), .in_43(rom_1_data[42]), .in_44(rom_1_data[43]),
    .in_45(rom_1_data[44]), .in_46(rom_1_data[45]), .in_47(rom_1_data[46]), .in_48(rom_1_data[47]),
    .in_49(rom_1_data[48]), .in_50(rom_1_data[49]), .in_51(rom_1_data[50]), .in_52(rom_1_data[51]),
    .in_53(rom_1_data[52]), .in_54(rom_1_data[53]), .in_55(rom_1_data[54]), .in_56(rom_1_data[55]),
    .in_57(rom_1_data[56]), .in_58({rom_2_data[0], rom_1_data[63:57]}), .in_59(rom_2_data[1]),
    .in_60(rom_2_data[2]), .in_61(rom_2_data[3]), .in_62(rom_2_data[4]), .in_63(rom_2_data[5]),
    .in_64(rom_2_data[6]), .in_65(rom_2_data[7]), .in_66(rom_2_data[8]), .in_67(rom_2_data[9]),
    .in_68(rom_2_data[10]), .in_69(rom_2_data[11]), .in_70(rom_2_data[12]), .CLK(CLK), .IP_inc(IP_inc),
    .IP_read(IP_read), .IP_write(IP_write), .SP_inc(SP_inc), .SP_dec(SP_dec), .SP_read(SP_read),
    .SP_write(SP_write), .MAR_read(MAR_read), .MAR_write(MAR_write), .MDR0_read(MDR0_read),
    .MDR0_write(MDR0_write), .MDR0_zero(MDR0_zero), .MDR1_read(MDR1_read), .MDR1_write(MDR1_write),
    .MDR1_zero(MDR1_zero), .MDR2_read(MDR2_read), .MDR2_write(MDR2_write), .MDR2_zero(MDR2_zero),
    .MEM_read(MEM_read), .MEM_read2(MEM_read2), .MEM_write(MEM_write), .MDR0_MEM_IN(MDR0_MEM_IN),
    .MDR1_MEM_IN(MDR1_MEM_IN), .MDR2_MEM_IN(MDR2_MEM_IN), .MDR0_REG_IN(MDR0_REG_IN),
    .MDR1_REG_IN(MDR1_REG_IN), .MDR2_REG_IN(MDR2_REG_IN), .MAR_REG_ID(MAR_REG_ID), .MDR0_REG_ID(MDR0_REG_ID),
    .MDR1_REG_ID(MDR1_REG_ID), .MDR2_REG_ID(MDR2_REG_ID), .REG_OUT_MAR(REG_OUT_MAR),
    .REG_OUT_MDR0(REG_OUT_MDR0), .REG_OUT_MDR1(REG_OUT_MDR1), .REG_OUT_MDR2(REG_OUT_MDR2),
    .REG_read(REG_read), .REG_write(REG_write), .MAR_MDR0(MAR_MDR0), .MAR_MDR1(MAR_MDR1),
    .MAR_MDR2(MAR_MDR2), .MDR0_MAR(MDR0_MAR), .MDR0_MDR1(MDR0_MDR1), .MDR0_MDR2(MDR0_MDR2),
    .MDR1_MAR(MDR1_MAR), .MDR1_MDR0(MDR1_MDR0), .MDR1_MDR2(MDR1_MDR2), .MDR2_MAR(MDR2_MAR),
    .MDR2_MDR0(MDR2_MDR0), .MDR2_MDR1(MDR2_MDR1), .MAR_ALU_IN0(MAR_ALU_IN0), .MDR0_ALU_IN0(MDR0_ALU_IN0),
    .MDR1_ALU_IN0(MDR1_ALU_IN0), .MDR2_ALU_IN0(MDR2_ALU_IN0), .MAR_ALU_IN1(MAR_ALU_IN1),
    .MDR0_ALU_IN1(MDR0_ALU_IN1), .MDR1_ALU_IN1(MDR1_ALU_IN1), .MDR2_ALU_IN1(MDR2_ALU_IN1),
    .ALU_SELECT(ALU_SELECT), .ALU_read(ALU_read), .ALU_write(ALU_write), .ALU_readFlags(ALU_readFlags),
    .ALU_OUT_MAR(ALU_OUT_MAR), .ALU_OUT_MDR0(ALU_OUT_MDR0), .ALU_OUT_MDR1(ALU_OUT_MDR1),
    .ALU_OUT_MDR2(ALU_OUT_MDR2), .ALU_REMAINDER_MAR(ALU_REMAINDER_MAR),
    .ALU_REMAINDER_MDR0(ALU_REMAINDER_MDR0), .ALU_REMAINDER_MDR1(ALU_REMAINDER_MDR1),
    .ALU_REMAINDER_MDR2(ALU_REMAINDER_MDR2), .CU_endInstruction(CU_endInstruction));
endmodule
module INS_ROM (
  input  [7:0] Instruction,
  input  [7:0] Cycle,
  input  CLK,
  input  [7:0] Flags,
  output IP_inc,
  output IP_read,
  output IP_write,
  output SP_inc,
  output SP_dec,
  output SP_read,
  output SP_write,
  output MAR_read,
  output MAR_write,
  output MDR0_read,
  output MDR0_write,
  output MDR0_zero,
  output MDR1_read,
  output MDR1_write,
  output MDR1_zero,
  output MDR2_read,
  output MDR2_write,
  output MDR2_zero,
  output MEM_read,
  output MEM_read2,
  output MEM_write,
  output MDR0_MEM_IN,
  output MDR1_MEM_IN,
  output MDR2_MEM_IN,
  output MDR0_REG_IN,
  output MDR1_REG_IN,
  output MDR2_REG_IN,
  output MAR_REG_ID,
  output MDR0_REG_ID,
  output MDR1_REG_ID,
  output MDR2_REG_ID,
  output REG_OUT_MAR,
  output REG_OUT_MDR0,
  output REG_OUT_MDR1,
  output REG_OUT_MDR2,
  output REG_read,
  output REG_write,
  output MAR_MDR0,
  output MAR_MDR1,
  output MAR_MDR2,
  output MDR0_MAR,
  output MDR0_MDR1,
  output MDR0_MDR2,
  output MDR1_MAR,
  output MDR1_MDR0,
  output MDR1_MDR2,
  output MDR2_MAR,
  output MDR2_MDR0,
  output MDR2_MDR1,
  output MAR_ALU_IN0,
  output MDR0_ALU_IN0,
  output MDR1_ALU_IN0,
  output MDR2_ALU_IN0,
  output MAR_ALU_IN1,
  output MDR0_ALU_IN1,
  output MDR1_ALU_IN1,
  output MDR2_ALU_IN1,
  output [7:0] ALU_SELECT,
  output ALU_read,
  output ALU_write,
  output ALU_readFlags,
  output ALU_OUT_MAR,
  output ALU_OUT_MDR0,
  output ALU_OUT_MDR1,
  output ALU_OUT_MDR2,
  output ALU_REMAINDER_MAR,
  output ALU_REMAINDER_MDR0,
  output ALU_REMAINDER_MDR1,
  output ALU_REMAINDER_MDR2,
  output CU_endInstruction
);

  wire demultiplexer_1_out0, demultiplexer_1_out1, demultiplexer_1_out2, demultiplexer_1_out3,
       demultiplexer_1_out4, demultiplexer_1_out5, demultiplexer_1_out6, demultiplexer_1_out7,
       demultiplexer_1_out8, demultiplexer_1_out9, ins_rom_0_1_alu_out_mar, ins_rom_0_1_alu_out_mdr0,
       ins_rom_0_1_alu_out_mdr1, ins_rom_0_1_alu_out_mdr2, ins_rom_0_1_alu_read, ins_rom_0_1_alu_readflags,
       ins_rom_0_1_alu_remainder_mar, ins_rom_0_1_alu_remainder_mdr0, ins_rom_0_1_alu_remainder_mdr1,
       ins_rom_0_1_alu_remainder_mdr2, ins_rom_0_1_alu_write, ins_rom_0_1_cu_endinstruction,
       ins_rom_0_1_ip_inc, ins_rom_0_1_ip_read, ins_rom_0_1_ip_write, ins_rom_0_1_mar_alu_in0,
       ins_rom_0_1_mar_alu_in1, ins_rom_0_1_mar_mdr0, ins_rom_0_1_mar_mdr1, ins_rom_0_1_mar_mdr2,
       ins_rom_0_1_mar_read, ins_rom_0_1_mar_reg_id, ins_rom_0_1_mar_write, ins_rom_0_1_mdr0_alu_in0,
       ins_rom_0_1_mdr0_alu_in1, ins_rom_0_1_mdr0_mar, ins_rom_0_1_mdr0_mdr1, ins_rom_0_1_mdr0_mdr2,
       ins_rom_0_1_mdr0_mem_in, ins_rom_0_1_mdr0_read, ins_rom_0_1_mdr0_reg_id, ins_rom_0_1_mdr0_reg_in,
       ins_rom_0_1_mdr0_write, ins_rom_0_1_mdr0_zero, ins_rom_0_1_mdr1_alu_in0, ins_rom_0_1_mdr1_alu_in1,
       ins_rom_0_1_mdr1_mar, ins_rom_0_1_mdr1_mdr0, ins_rom_0_1_mdr1_mdr2, ins_rom_0_1_mdr1_mem_in,
       ins_rom_0_1_mdr1_read, ins_rom_0_1_mdr1_reg_id, ins_rom_0_1_mdr1_reg_in, ins_rom_0_1_mdr1_write,
       ins_rom_0_1_mdr1_zero, ins_rom_0_1_mdr2_alu_in0, ins_rom_0_1_mdr2_alu_in1, ins_rom_0_1_mdr2_mar,
       ins_rom_0_1_mdr2_mdr0, ins_rom_0_1_mdr2_mdr1, ins_rom_0_1_mdr2_mem_in, ins_rom_0_1_mdr2_read,
       ins_rom_0_1_mdr2_reg_id, ins_rom_0_1_mdr2_reg_in, ins_rom_0_1_mdr2_write, ins_rom_0_1_mdr2_zero,
       ins_rom_0_1_mem_read, ins_rom_0_1_mem_read2, ins_rom_0_1_mem_write, ins_rom_0_1_reg_out_mar,
       ins_rom_0_1_reg_out_mdr0, ins_rom_0_1_reg_out_mdr1, ins_rom_0_1_reg_out_mdr2, ins_rom_0_1_reg_read,
       ins_rom_0_1_reg_write, ins_rom_0_1_sp_dec, ins_rom_0_1_sp_inc, ins_rom_0_1_sp_read,
       ins_rom_0_1_sp_write, ins_rom_1_1_alu_out_mar, ins_rom_1_1_alu_out_mdr0, ins_rom_1_1_alu_out_mdr1,
       ins_rom_1_1_alu_out_mdr2, ins_rom_1_1_alu_read, ins_rom_1_1_alu_readflags,
       ins_rom_1_1_alu_remainder_mar, ins_rom_1_1_alu_remainder_mdr0, ins_rom_1_1_alu_remainder_mdr1,
       ins_rom_1_1_alu_remainder_mdr2, ins_rom_1_1_alu_write, ins_rom_1_1_cu_endinstruction,
       ins_rom_1_1_ip_inc, ins_rom_1_1_ip_read, ins_rom_1_1_ip_write, ins_rom_1_1_mar_alu_in0,
       ins_rom_1_1_mar_alu_in1, ins_rom_1_1_mar_mdr0, ins_rom_1_1_mar_mdr1, ins_rom_1_1_mar_mdr2,
       ins_rom_1_1_mar_read, ins_rom_1_1_mar_reg_id, ins_rom_1_1_mar_write, ins_rom_1_1_mdr0_alu_in0,
       ins_rom_1_1_mdr0_alu_in1, ins_rom_1_1_mdr0_mar, ins_rom_1_1_mdr0_mdr1, ins_rom_1_1_mdr0_mdr2,
       ins_rom_1_1_mdr0_mem_in, ins_rom_1_1_mdr0_read, ins_rom_1_1_mdr0_reg_id, ins_rom_1_1_mdr0_reg_in,
       ins_rom_1_1_mdr0_write, ins_rom_1_1_mdr0_zero, ins_rom_1_1_mdr1_alu_in0, ins_rom_1_1_mdr1_alu_in1,
       ins_rom_1_1_mdr1_mar, ins_rom_1_1_mdr1_mdr0, ins_rom_1_1_mdr1_mdr2, ins_rom_1_1_mdr1_mem_in,
       ins_rom_1_1_mdr1_read, ins_rom_1_1_mdr1_reg_id, ins_rom_1_1_mdr1_reg_in, ins_rom_1_1_mdr1_write,
       ins_rom_1_1_mdr1_zero, ins_rom_1_1_mdr2_alu_in0, ins_rom_1_1_mdr2_alu_in1, ins_rom_1_1_mdr2_mar,
       ins_rom_1_1_mdr2_mdr0, ins_rom_1_1_mdr2_mdr1, ins_rom_1_1_mdr2_mem_in, ins_rom_1_1_mdr2_read,
       ins_rom_1_1_mdr2_reg_id, ins_rom_1_1_mdr2_reg_in, ins_rom_1_1_mdr2_write, ins_rom_1_1_mdr2_zero,
       ins_rom_1_1_mem_read, ins_rom_1_1_mem_read2, ins_rom_1_1_mem_write, ins_rom_1_1_reg_out_mar,
       ins_rom_1_1_reg_out_mdr0, ins_rom_1_1_reg_out_mdr1, ins_rom_1_1_reg_out_mdr2, ins_rom_1_1_reg_read,
       ins_rom_1_1_reg_write, ins_rom_1_1_sp_dec, ins_rom_1_1_sp_inc, ins_rom_1_1_sp_read,
       ins_rom_1_1_sp_write, ins_rom_2_1_alu_out_mar, ins_rom_2_1_alu_out_mdr0, ins_rom_2_1_alu_out_mdr1,
       ins_rom_2_1_alu_out_mdr2, ins_rom_2_1_alu_read, ins_rom_2_1_alu_readflags,
       ins_rom_2_1_alu_remainder_mar, ins_rom_2_1_alu_remainder_mdr0, ins_rom_2_1_alu_remainder_mdr1,
       ins_rom_2_1_alu_remainder_mdr2, ins_rom_2_1_alu_write, ins_rom_2_1_cu_endinstruction,
       ins_rom_2_1_ip_inc, ins_rom_2_1_ip_read, ins_rom_2_1_ip_write, ins_rom_2_1_mar_alu_in0,
       ins_rom_2_1_mar_alu_in1, ins_rom_2_1_mar_mdr0, ins_rom_2_1_mar_mdr1, ins_rom_2_1_mar_mdr2,
       ins_rom_2_1_mar_read, ins_rom_2_1_mar_reg_id, ins_rom_2_1_mar_write, ins_rom_2_1_mdr0_alu_in0,
       ins_rom_2_1_mdr0_alu_in1, ins_rom_2_1_mdr0_mar, ins_rom_2_1_mdr0_mdr1, ins_rom_2_1_mdr0_mdr2,
       ins_rom_2_1_mdr0_mem_in, ins_rom_2_1_mdr0_read, ins_rom_2_1_mdr0_reg_id, ins_rom_2_1_mdr0_reg_in,
       ins_rom_2_1_mdr0_write, ins_rom_2_1_mdr0_zero, ins_rom_2_1_mdr1_alu_in0, ins_rom_2_1_mdr1_alu_in1,
       ins_rom_2_1_mdr1_mar, ins_rom_2_1_mdr1_mdr0, ins_rom_2_1_mdr1_mdr2, ins_rom_2_1_mdr1_mem_in,
       ins_rom_2_1_mdr1_read, ins_rom_2_1_mdr1_reg_id, ins_rom_2_1_mdr1_reg_in, ins_rom_2_1_mdr1_write,
       ins_rom_2_1_mdr1_zero, ins_rom_2_1_mdr2_alu_in0, ins_rom_2_1_mdr2_alu_in1, ins_rom_2_1_mdr2_mar,
       ins_rom_2_1_mdr2_mdr0, ins_rom_2_1_mdr2_mdr1, ins_rom_2_1_mdr2_mem_in, ins_rom_2_1_mdr2_read,
       ins_rom_2_1_mdr2_reg_id, ins_rom_2_1_mdr2_reg_in, ins_rom_2_1_mdr2_write, ins_rom_2_1_mdr2_zero,
       ins_rom_2_1_mem_read, ins_rom_2_1_mem_read2, ins_rom_2_1_mem_write, ins_rom_2_1_reg_out_mar,
       ins_rom_2_1_reg_out_mdr0, ins_rom_2_1_reg_out_mdr1, ins_rom_2_1_reg_out_mdr2, ins_rom_2_1_reg_read,
       ins_rom_2_1_reg_write, ins_rom_2_1_sp_dec, ins_rom_2_1_sp_inc, ins_rom_2_1_sp_read,
       ins_rom_2_1_sp_write, ins_rom_3_1_alu_out_mar, ins_rom_3_1_alu_out_mdr0, ins_rom_3_1_alu_out_mdr1,
       ins_rom_3_1_alu_out_mdr2, ins_rom_3_1_alu_read, ins_rom_3_1_alu_readflags,
       ins_rom_3_1_alu_remainder_mar, ins_rom_3_1_alu_remainder_mdr0, ins_rom_3_1_alu_remainder_mdr1,
       ins_rom_3_1_alu_remainder_mdr2, ins_rom_3_1_alu_write, ins_rom_3_1_cu_endinstruction,
       ins_rom_3_1_ip_inc, ins_rom_3_1_ip_read, ins_rom_3_1_ip_write, ins_rom_3_1_mar_alu_in0,
       ins_rom_3_1_mar_alu_in1, ins_rom_3_1_mar_mdr0, ins_rom_3_1_mar_mdr1, ins_rom_3_1_mar_mdr2,
       ins_rom_3_1_mar_read, ins_rom_3_1_mar_reg_id, ins_rom_3_1_mar_write, ins_rom_3_1_mdr0_alu_in0,
       ins_rom_3_1_mdr0_alu_in1, ins_rom_3_1_mdr0_mar, ins_rom_3_1_mdr0_mdr1, ins_rom_3_1_mdr0_mdr2,
       ins_rom_3_1_mdr0_mem_in, ins_rom_3_1_mdr0_read, ins_rom_3_1_mdr0_reg_id, ins_rom_3_1_mdr0_reg_in,
       ins_rom_3_1_mdr0_write, ins_rom_3_1_mdr0_zero, ins_rom_3_1_mdr1_alu_in0, ins_rom_3_1_mdr1_alu_in1,
       ins_rom_3_1_mdr1_mar, ins_rom_3_1_mdr1_mdr0, ins_rom_3_1_mdr1_mdr2, ins_rom_3_1_mdr1_mem_in,
       ins_rom_3_1_mdr1_read, ins_rom_3_1_mdr1_reg_id, ins_rom_3_1_mdr1_reg_in, ins_rom_3_1_mdr1_write,
       ins_rom_3_1_mdr1_zero, ins_rom_3_1_mdr2_alu_in0, ins_rom_3_1_mdr2_alu_in1, ins_rom_3_1_mdr2_mar,
       ins_rom_3_1_mdr2_mdr0, ins_rom_3_1_mdr2_mdr1, ins_rom_3_1_mdr2_mem_in, ins_rom_3_1_mdr2_read,
       ins_rom_3_1_mdr2_reg_id, ins_rom_3_1_mdr2_reg_in, ins_rom_3_1_mdr2_write, ins_rom_3_1_mdr2_zero,
       ins_rom_3_1_mem_read, ins_rom_3_1_mem_read2, ins_rom_3_1_mem_write, ins_rom_3_1_reg_out_mar,
       ins_rom_3_1_reg_out_mdr0, ins_rom_3_1_reg_out_mdr1, ins_rom_3_1_reg_out_mdr2, ins_rom_3_1_reg_read,
       ins_rom_3_1_reg_write, ins_rom_3_1_sp_dec, ins_rom_3_1_sp_inc, ins_rom_3_1_sp_read,
       ins_rom_3_1_sp_write, ins_rom_4_1_alu_out_mar, ins_rom_4_1_alu_out_mdr0, ins_rom_4_1_alu_out_mdr1,
       ins_rom_4_1_alu_out_mdr2, ins_rom_4_1_alu_read, ins_rom_4_1_alu_readflags,
       ins_rom_4_1_alu_remainder_mar, ins_rom_4_1_alu_remainder_mdr0, ins_rom_4_1_alu_remainder_mdr1,
       ins_rom_4_1_alu_remainder_mdr2, ins_rom_4_1_alu_write, ins_rom_4_1_cu_endinstruction,
       ins_rom_4_1_ip_inc, ins_rom_4_1_ip_read, ins_rom_4_1_ip_write, ins_rom_4_1_mar_alu_in0,
       ins_rom_4_1_mar_alu_in1, ins_rom_4_1_mar_mdr0, ins_rom_4_1_mar_mdr1, ins_rom_4_1_mar_mdr2,
       ins_rom_4_1_mar_read, ins_rom_4_1_mar_reg_id, ins_rom_4_1_mar_write, ins_rom_4_1_mdr0_alu_in0,
       ins_rom_4_1_mdr0_alu_in1, ins_rom_4_1_mdr0_mar, ins_rom_4_1_mdr0_mdr1, ins_rom_4_1_mdr0_mdr2,
       ins_rom_4_1_mdr0_mem_in, ins_rom_4_1_mdr0_read, ins_rom_4_1_mdr0_reg_id, ins_rom_4_1_mdr0_reg_in,
       ins_rom_4_1_mdr0_write, ins_rom_4_1_mdr0_zero, ins_rom_4_1_mdr1_alu_in0, ins_rom_4_1_mdr1_alu_in1,
       ins_rom_4_1_mdr1_mar, ins_rom_4_1_mdr1_mdr0, ins_rom_4_1_mdr1_mdr2, ins_rom_4_1_mdr1_mem_in,
       ins_rom_4_1_mdr1_read, ins_rom_4_1_mdr1_reg_id, ins_rom_4_1_mdr1_reg_in, ins_rom_4_1_mdr1_write,
       ins_rom_4_1_mdr1_zero, ins_rom_4_1_mdr2_alu_in0, ins_rom_4_1_mdr2_alu_in1, ins_rom_4_1_mdr2_mar,
       ins_rom_4_1_mdr2_mdr0, ins_rom_4_1_mdr2_mdr1, ins_rom_4_1_mdr2_mem_in, ins_rom_4_1_mdr2_read,
       ins_rom_4_1_mdr2_reg_id, ins_rom_4_1_mdr2_reg_in, ins_rom_4_1_mdr2_write, ins_rom_4_1_mdr2_zero,
       ins_rom_4_1_mem_read, ins_rom_4_1_mem_read2, ins_rom_4_1_mem_write, ins_rom_4_1_reg_out_mar,
       ins_rom_4_1_reg_out_mdr0, ins_rom_4_1_reg_out_mdr1, ins_rom_4_1_reg_out_mdr2, ins_rom_4_1_reg_read,
       ins_rom_4_1_reg_write, ins_rom_4_1_sp_dec, ins_rom_4_1_sp_inc, ins_rom_4_1_sp_read,
       ins_rom_4_1_sp_write, ins_rom_5_1_alu_out_mar, ins_rom_5_1_alu_out_mdr0, ins_rom_5_1_alu_out_mdr1,
       ins_rom_5_1_alu_out_mdr2, ins_rom_5_1_alu_read, ins_rom_5_1_alu_readflags,
       ins_rom_5_1_alu_remainder_mar, ins_rom_5_1_alu_remainder_mdr0, ins_rom_5_1_alu_remainder_mdr1,
       ins_rom_5_1_alu_remainder_mdr2, ins_rom_5_1_alu_write, ins_rom_5_1_cu_endinstruction,
       ins_rom_5_1_ip_inc, ins_rom_5_1_ip_read, ins_rom_5_1_ip_write, ins_rom_5_1_mar_alu_in0,
       ins_rom_5_1_mar_alu_in1, ins_rom_5_1_mar_mdr0, ins_rom_5_1_mar_mdr1, ins_rom_5_1_mar_mdr2,
       ins_rom_5_1_mar_read, ins_rom_5_1_mar_reg_id, ins_rom_5_1_mar_write, ins_rom_5_1_mdr0_alu_in0,
       ins_rom_5_1_mdr0_alu_in1, ins_rom_5_1_mdr0_mar, ins_rom_5_1_mdr0_mdr1, ins_rom_5_1_mdr0_mdr2,
       ins_rom_5_1_mdr0_mem_in, ins_rom_5_1_mdr0_read, ins_rom_5_1_mdr0_reg_id, ins_rom_5_1_mdr0_reg_in,
       ins_rom_5_1_mdr0_write, ins_rom_5_1_mdr0_zero, ins_rom_5_1_mdr1_alu_in0, ins_rom_5_1_mdr1_alu_in1,
       ins_rom_5_1_mdr1_mar, ins_rom_5_1_mdr1_mdr0, ins_rom_5_1_mdr1_mdr2, ins_rom_5_1_mdr1_mem_in,
       ins_rom_5_1_mdr1_read, ins_rom_5_1_mdr1_reg_id, ins_rom_5_1_mdr1_reg_in, ins_rom_5_1_mdr1_write,
       ins_rom_5_1_mdr1_zero, ins_rom_5_1_mdr2_alu_in0, ins_rom_5_1_mdr2_alu_in1, ins_rom_5_1_mdr2_mar,
       ins_rom_5_1_mdr2_mdr0, ins_rom_5_1_mdr2_mdr1, ins_rom_5_1_mdr2_mem_in, ins_rom_5_1_mdr2_read,
       ins_rom_5_1_mdr2_reg_id, ins_rom_5_1_mdr2_reg_in, ins_rom_5_1_mdr2_write, ins_rom_5_1_mdr2_zero,
       ins_rom_5_1_mem_read, ins_rom_5_1_mem_read2, ins_rom_5_1_mem_write, ins_rom_5_1_reg_out_mar,
       ins_rom_5_1_reg_out_mdr0, ins_rom_5_1_reg_out_mdr1, ins_rom_5_1_reg_out_mdr2, ins_rom_5_1_reg_read,
       ins_rom_5_1_reg_write, ins_rom_5_1_sp_dec, ins_rom_5_1_sp_inc, ins_rom_5_1_sp_read,
       ins_rom_5_1_sp_write, ins_rom_6_1_alu_out_mar, ins_rom_6_1_alu_out_mdr0, ins_rom_6_1_alu_out_mdr1,
       ins_rom_6_1_alu_out_mdr2, ins_rom_6_1_alu_read, ins_rom_6_1_alu_readflags,
       ins_rom_6_1_alu_remainder_mar, ins_rom_6_1_alu_remainder_mdr0, ins_rom_6_1_alu_remainder_mdr1,
       ins_rom_6_1_alu_remainder_mdr2, ins_rom_6_1_alu_write, ins_rom_6_1_cu_endinstruction,
       ins_rom_6_1_ip_inc, ins_rom_6_1_ip_read, ins_rom_6_1_ip_write, ins_rom_6_1_mar_alu_in0,
       ins_rom_6_1_mar_alu_in1, ins_rom_6_1_mar_mdr0, ins_rom_6_1_mar_mdr1, ins_rom_6_1_mar_mdr2,
       ins_rom_6_1_mar_read, ins_rom_6_1_mar_reg_id, ins_rom_6_1_mar_write, ins_rom_6_1_mdr0_alu_in0,
       ins_rom_6_1_mdr0_alu_in1, ins_rom_6_1_mdr0_mar, ins_rom_6_1_mdr0_mdr1, ins_rom_6_1_mdr0_mdr2,
       ins_rom_6_1_mdr0_mem_in, ins_rom_6_1_mdr0_read, ins_rom_6_1_mdr0_reg_id, ins_rom_6_1_mdr0_reg_in,
       ins_rom_6_1_mdr0_write, ins_rom_6_1_mdr0_zero, ins_rom_6_1_mdr1_alu_in0, ins_rom_6_1_mdr1_alu_in1,
       ins_rom_6_1_mdr1_mar, ins_rom_6_1_mdr1_mdr0, ins_rom_6_1_mdr1_mdr2, ins_rom_6_1_mdr1_mem_in,
       ins_rom_6_1_mdr1_read, ins_rom_6_1_mdr1_reg_id, ins_rom_6_1_mdr1_reg_in, ins_rom_6_1_mdr1_write,
       ins_rom_6_1_mdr1_zero, ins_rom_6_1_mdr2_alu_in0, ins_rom_6_1_mdr2_alu_in1, ins_rom_6_1_mdr2_mar,
       ins_rom_6_1_mdr2_mdr0, ins_rom_6_1_mdr2_mdr1, ins_rom_6_1_mdr2_mem_in, ins_rom_6_1_mdr2_read,
       ins_rom_6_1_mdr2_reg_id, ins_rom_6_1_mdr2_reg_in, ins_rom_6_1_mdr2_write, ins_rom_6_1_mdr2_zero,
       ins_rom_6_1_mem_read, ins_rom_6_1_mem_read2, ins_rom_6_1_mem_write, ins_rom_6_1_reg_out_mar,
       ins_rom_6_1_reg_out_mdr0, ins_rom_6_1_reg_out_mdr1, ins_rom_6_1_reg_out_mdr2, ins_rom_6_1_reg_read,
       ins_rom_6_1_reg_write, ins_rom_6_1_sp_dec, ins_rom_6_1_sp_inc, ins_rom_6_1_sp_read,
       ins_rom_6_1_sp_write, ins_rom_7_1_alu_out_mar, ins_rom_7_1_alu_out_mdr0, ins_rom_7_1_alu_out_mdr1,
       ins_rom_7_1_alu_out_mdr2, ins_rom_7_1_alu_read, ins_rom_7_1_alu_readflags,
       ins_rom_7_1_alu_remainder_mar, ins_rom_7_1_alu_remainder_mdr0, ins_rom_7_1_alu_remainder_mdr1,
       ins_rom_7_1_alu_remainder_mdr2, ins_rom_7_1_alu_write, ins_rom_7_1_cu_endinstruction,
       ins_rom_7_1_ip_inc, ins_rom_7_1_ip_read, ins_rom_7_1_ip_write, ins_rom_7_1_mar_alu_in0,
       ins_rom_7_1_mar_alu_in1, ins_rom_7_1_mar_mdr0, ins_rom_7_1_mar_mdr1, ins_rom_7_1_mar_mdr2,
       ins_rom_7_1_mar_read, ins_rom_7_1_mar_reg_id, ins_rom_7_1_mar_write, ins_rom_7_1_mdr0_alu_in0,
       ins_rom_7_1_mdr0_alu_in1, ins_rom_7_1_mdr0_mar, ins_rom_7_1_mdr0_mdr1, ins_rom_7_1_mdr0_mdr2,
       ins_rom_7_1_mdr0_mem_in, ins_rom_7_1_mdr0_read, ins_rom_7_1_mdr0_reg_id, ins_rom_7_1_mdr0_reg_in,
       ins_rom_7_1_mdr0_write, ins_rom_7_1_mdr0_zero, ins_rom_7_1_mdr1_alu_in0, ins_rom_7_1_mdr1_alu_in1,
       ins_rom_7_1_mdr1_mar, ins_rom_7_1_mdr1_mdr0, ins_rom_7_1_mdr1_mdr2, ins_rom_7_1_mdr1_mem_in,
       ins_rom_7_1_mdr1_read, ins_rom_7_1_mdr1_reg_id, ins_rom_7_1_mdr1_reg_in, ins_rom_7_1_mdr1_write,
       ins_rom_7_1_mdr1_zero, ins_rom_7_1_mdr2_alu_in0, ins_rom_7_1_mdr2_alu_in1, ins_rom_7_1_mdr2_mar,
       ins_rom_7_1_mdr2_mdr0, ins_rom_7_1_mdr2_mdr1, ins_rom_7_1_mdr2_mem_in, ins_rom_7_1_mdr2_read,
       ins_rom_7_1_mdr2_reg_id, ins_rom_7_1_mdr2_reg_in, ins_rom_7_1_mdr2_write, ins_rom_7_1_mdr2_zero,
       ins_rom_7_1_mem_read, ins_rom_7_1_mem_read2, ins_rom_7_1_mem_write, ins_rom_7_1_reg_out_mar,
       ins_rom_7_1_reg_out_mdr0, ins_rom_7_1_reg_out_mdr1, ins_rom_7_1_reg_out_mdr2, ins_rom_7_1_reg_read,
       ins_rom_7_1_reg_write, ins_rom_7_1_sp_dec, ins_rom_7_1_sp_inc, ins_rom_7_1_sp_read,
       ins_rom_7_1_sp_write, ins_rom_8_1_alu_out_mar, ins_rom_8_1_alu_out_mdr0, ins_rom_8_1_alu_out_mdr1,
       ins_rom_8_1_alu_out_mdr2, ins_rom_8_1_alu_read, ins_rom_8_1_alu_readflags,
       ins_rom_8_1_alu_remainder_mar, ins_rom_8_1_alu_remainder_mdr0, ins_rom_8_1_alu_remainder_mdr1,
       ins_rom_8_1_alu_remainder_mdr2, ins_rom_8_1_alu_write, ins_rom_8_1_cu_endinstruction,
       ins_rom_8_1_ip_inc, ins_rom_8_1_ip_read, ins_rom_8_1_ip_write, ins_rom_8_1_mar_alu_in0,
       ins_rom_8_1_mar_alu_in1, ins_rom_8_1_mar_mdr0, ins_rom_8_1_mar_mdr1, ins_rom_8_1_mar_mdr2,
       ins_rom_8_1_mar_read, ins_rom_8_1_mar_reg_id, ins_rom_8_1_mar_write, ins_rom_8_1_mdr0_alu_in0,
       ins_rom_8_1_mdr0_alu_in1, ins_rom_8_1_mdr0_mar, ins_rom_8_1_mdr0_mdr1, ins_rom_8_1_mdr0_mdr2,
       ins_rom_8_1_mdr0_mem_in, ins_rom_8_1_mdr0_read, ins_rom_8_1_mdr0_reg_id, ins_rom_8_1_mdr0_reg_in,
       ins_rom_8_1_mdr0_write, ins_rom_8_1_mdr0_zero, ins_rom_8_1_mdr1_alu_in0, ins_rom_8_1_mdr1_alu_in1,
       ins_rom_8_1_mdr1_mar, ins_rom_8_1_mdr1_mdr0, ins_rom_8_1_mdr1_mdr2, ins_rom_8_1_mdr1_mem_in,
       ins_rom_8_1_mdr1_read, ins_rom_8_1_mdr1_reg_id, ins_rom_8_1_mdr1_reg_in, ins_rom_8_1_mdr1_write,
       ins_rom_8_1_mdr1_zero, ins_rom_8_1_mdr2_alu_in0, ins_rom_8_1_mdr2_alu_in1, ins_rom_8_1_mdr2_mar,
       ins_rom_8_1_mdr2_mdr0, ins_rom_8_1_mdr2_mdr1, ins_rom_8_1_mdr2_mem_in, ins_rom_8_1_mdr2_read,
       ins_rom_8_1_mdr2_reg_id, ins_rom_8_1_mdr2_reg_in, ins_rom_8_1_mdr2_write, ins_rom_8_1_mdr2_zero,
       ins_rom_8_1_mem_read, ins_rom_8_1_mem_read2, ins_rom_8_1_mem_write, ins_rom_8_1_reg_out_mar,
       ins_rom_8_1_reg_out_mdr0, ins_rom_8_1_reg_out_mdr1, ins_rom_8_1_reg_out_mdr2, ins_rom_8_1_reg_read,
       ins_rom_8_1_reg_write, ins_rom_8_1_sp_dec, ins_rom_8_1_sp_inc, ins_rom_8_1_sp_read,
       ins_rom_8_1_sp_write, ins_rom_9_1_alu_out_mar, ins_rom_9_1_alu_out_mdr0, ins_rom_9_1_alu_out_mdr1,
       ins_rom_9_1_alu_out_mdr2, ins_rom_9_1_alu_read, ins_rom_9_1_alu_readflags,
       ins_rom_9_1_alu_remainder_mar, ins_rom_9_1_alu_remainder_mdr0, ins_rom_9_1_alu_remainder_mdr1,
       ins_rom_9_1_alu_remainder_mdr2, ins_rom_9_1_alu_write, ins_rom_9_1_cu_endinstruction,
       ins_rom_9_1_ip_inc, ins_rom_9_1_ip_read, ins_rom_9_1_ip_write, ins_rom_9_1_mar_alu_in0,
       ins_rom_9_1_mar_alu_in1, ins_rom_9_1_mar_mdr0, ins_rom_9_1_mar_mdr1, ins_rom_9_1_mar_mdr2,
       ins_rom_9_1_mar_read, ins_rom_9_1_mar_reg_id, ins_rom_9_1_mar_write, ins_rom_9_1_mdr0_alu_in0,
       ins_rom_9_1_mdr0_alu_in1, ins_rom_9_1_mdr0_mar, ins_rom_9_1_mdr0_mdr1, ins_rom_9_1_mdr0_mdr2,
       ins_rom_9_1_mdr0_mem_in, ins_rom_9_1_mdr0_read, ins_rom_9_1_mdr0_reg_id, ins_rom_9_1_mdr0_reg_in,
       ins_rom_9_1_mdr0_write, ins_rom_9_1_mdr0_zero, ins_rom_9_1_mdr1_alu_in0, ins_rom_9_1_mdr1_alu_in1,
       ins_rom_9_1_mdr1_mar, ins_rom_9_1_mdr1_mdr0, ins_rom_9_1_mdr1_mdr2, ins_rom_9_1_mdr1_mem_in,
       ins_rom_9_1_mdr1_read, ins_rom_9_1_mdr1_reg_id, ins_rom_9_1_mdr1_reg_in, ins_rom_9_1_mdr1_write,
       ins_rom_9_1_mdr1_zero, ins_rom_9_1_mdr2_alu_in0, ins_rom_9_1_mdr2_alu_in1, ins_rom_9_1_mdr2_mar,
       ins_rom_9_1_mdr2_mdr0, ins_rom_9_1_mdr2_mdr1, ins_rom_9_1_mdr2_mem_in, ins_rom_9_1_mdr2_read,
       ins_rom_9_1_mdr2_reg_id, ins_rom_9_1_mdr2_reg_in, ins_rom_9_1_mdr2_write, ins_rom_9_1_mdr2_zero,
       ins_rom_9_1_mem_read, ins_rom_9_1_mem_read2, ins_rom_9_1_mem_write, ins_rom_9_1_reg_out_mar,
       ins_rom_9_1_reg_out_mdr0, ins_rom_9_1_reg_out_mdr1, ins_rom_9_1_reg_out_mdr2, ins_rom_9_1_reg_read,
       ins_rom_9_1_reg_write, ins_rom_9_1_sp_dec, ins_rom_9_1_sp_inc, ins_rom_9_1_sp_read,
       ins_rom_9_1_sp_write, ins_rom_weaver_1_alu_out_mar, ins_rom_weaver_1_alu_out_mdr0,
       ins_rom_weaver_1_alu_out_mdr1, ins_rom_weaver_1_alu_out_mdr2, ins_rom_weaver_1_alu_read,
       ins_rom_weaver_1_alu_readflags, ins_rom_weaver_1_alu_remainder_mar,
       ins_rom_weaver_1_alu_remainder_mdr0, ins_rom_weaver_1_alu_remainder_mdr1,
       ins_rom_weaver_1_alu_remainder_mdr2, ins_rom_weaver_1_alu_write, ins_rom_weaver_1_cu_endinstruction,
       ins_rom_weaver_1_ip_inc, ins_rom_weaver_1_ip_read, ins_rom_weaver_1_ip_write,
       ins_rom_weaver_1_mar_alu_in0, ins_rom_weaver_1_mar_alu_in1, ins_rom_weaver_1_mar_mdr0,
       ins_rom_weaver_1_mar_mdr1, ins_rom_weaver_1_mar_mdr2, ins_rom_weaver_1_mar_read,
       ins_rom_weaver_1_mar_reg_id, ins_rom_weaver_1_mar_write, ins_rom_weaver_1_mdr0_alu_in0,
       ins_rom_weaver_1_mdr0_alu_in1, ins_rom_weaver_1_mdr0_mar, ins_rom_weaver_1_mdr0_mdr1,
       ins_rom_weaver_1_mdr0_mdr2, ins_rom_weaver_1_mdr0_mem_in, ins_rom_weaver_1_mdr0_read,
       ins_rom_weaver_1_mdr0_reg_id, ins_rom_weaver_1_mdr0_reg_in, ins_rom_weaver_1_mdr0_write,
       ins_rom_weaver_1_mdr0_zero, ins_rom_weaver_1_mdr1_alu_in0, ins_rom_weaver_1_mdr1_alu_in1,
       ins_rom_weaver_1_mdr1_mar, ins_rom_weaver_1_mdr1_mdr0, ins_rom_weaver_1_mdr1_mdr2,
       ins_rom_weaver_1_mdr1_mem_in, ins_rom_weaver_1_mdr1_read, ins_rom_weaver_1_mdr1_reg_id,
       ins_rom_weaver_1_mdr1_reg_in, ins_rom_weaver_1_mdr1_write, ins_rom_weaver_1_mdr1_zero,
       ins_rom_weaver_1_mdr2_alu_in0, ins_rom_weaver_1_mdr2_alu_in1, ins_rom_weaver_1_mdr2_mar,
       ins_rom_weaver_1_mdr2_mdr0, ins_rom_weaver_1_mdr2_mdr1, ins_rom_weaver_1_mdr2_mem_in,
       ins_rom_weaver_1_mdr2_read, ins_rom_weaver_1_mdr2_reg_id, ins_rom_weaver_1_mdr2_reg_in,
       ins_rom_weaver_1_mdr2_write, ins_rom_weaver_1_mdr2_zero, ins_rom_weaver_1_mem_read,
       ins_rom_weaver_1_mem_read2, ins_rom_weaver_1_mem_write, ins_rom_weaver_1_reg_out_mar,
       ins_rom_weaver_1_reg_out_mdr0, ins_rom_weaver_1_reg_out_mdr1, ins_rom_weaver_1_reg_out_mdr2,
       ins_rom_weaver_1_reg_read, ins_rom_weaver_1_reg_write, ins_rom_weaver_1_sp_dec,
       ins_rom_weaver_1_sp_inc, ins_rom_weaver_1_sp_read, ins_rom_weaver_1_sp_write,
       ins_rom_weaver_2_alu_out_mar, ins_rom_weaver_2_alu_out_mdr0, ins_rom_weaver_2_alu_out_mdr1,
       ins_rom_weaver_2_alu_out_mdr2, ins_rom_weaver_2_alu_read, ins_rom_weaver_2_alu_readflags,
       ins_rom_weaver_2_alu_remainder_mar, ins_rom_weaver_2_alu_remainder_mdr0,
       ins_rom_weaver_2_alu_remainder_mdr1, ins_rom_weaver_2_alu_remainder_mdr2, ins_rom_weaver_2_alu_write,
       ins_rom_weaver_2_cu_endinstruction, ins_rom_weaver_2_ip_inc, ins_rom_weaver_2_ip_read,
       ins_rom_weaver_2_ip_write, ins_rom_weaver_2_mar_alu_in0, ins_rom_weaver_2_mar_alu_in1,
       ins_rom_weaver_2_mar_mdr0, ins_rom_weaver_2_mar_mdr1, ins_rom_weaver_2_mar_mdr2,
       ins_rom_weaver_2_mar_read, ins_rom_weaver_2_mar_reg_id, ins_rom_weaver_2_mar_write,
       ins_rom_weaver_2_mdr0_alu_in0, ins_rom_weaver_2_mdr0_alu_in1, ins_rom_weaver_2_mdr0_mar,
       ins_rom_weaver_2_mdr0_mdr1, ins_rom_weaver_2_mdr0_mdr2, ins_rom_weaver_2_mdr0_mem_in,
       ins_rom_weaver_2_mdr0_read, ins_rom_weaver_2_mdr0_reg_id, ins_rom_weaver_2_mdr0_reg_in,
       ins_rom_weaver_2_mdr0_write, ins_rom_weaver_2_mdr0_zero, ins_rom_weaver_2_mdr1_alu_in0,
       ins_rom_weaver_2_mdr1_alu_in1, ins_rom_weaver_2_mdr1_mar, ins_rom_weaver_2_mdr1_mdr0,
       ins_rom_weaver_2_mdr1_mdr2, ins_rom_weaver_2_mdr1_mem_in, ins_rom_weaver_2_mdr1_read,
       ins_rom_weaver_2_mdr1_reg_id, ins_rom_weaver_2_mdr1_reg_in, ins_rom_weaver_2_mdr1_write,
       ins_rom_weaver_2_mdr1_zero, ins_rom_weaver_2_mdr2_alu_in0, ins_rom_weaver_2_mdr2_alu_in1,
       ins_rom_weaver_2_mdr2_mar, ins_rom_weaver_2_mdr2_mdr0, ins_rom_weaver_2_mdr2_mdr1,
       ins_rom_weaver_2_mdr2_mem_in, ins_rom_weaver_2_mdr2_read, ins_rom_weaver_2_mdr2_reg_id,
       ins_rom_weaver_2_mdr2_reg_in, ins_rom_weaver_2_mdr2_write, ins_rom_weaver_2_mdr2_zero,
       ins_rom_weaver_2_mem_read, ins_rom_weaver_2_mem_read2, ins_rom_weaver_2_mem_write,
       ins_rom_weaver_2_reg_out_mar, ins_rom_weaver_2_reg_out_mdr0, ins_rom_weaver_2_reg_out_mdr1,
       ins_rom_weaver_2_reg_out_mdr2, ins_rom_weaver_2_reg_read, ins_rom_weaver_2_reg_write,
       ins_rom_weaver_2_sp_dec, ins_rom_weaver_2_sp_inc, ins_rom_weaver_2_sp_read, ins_rom_weaver_2_sp_write,
       ins_rom_weaver_3_alu_out_mar, ins_rom_weaver_3_alu_out_mdr0, ins_rom_weaver_3_alu_out_mdr1,
       ins_rom_weaver_3_alu_out_mdr2, ins_rom_weaver_3_alu_read, ins_rom_weaver_3_alu_readflags,
       ins_rom_weaver_3_alu_remainder_mar, ins_rom_weaver_3_alu_remainder_mdr0,
       ins_rom_weaver_3_alu_remainder_mdr1, ins_rom_weaver_3_alu_remainder_mdr2, ins_rom_weaver_3_alu_write,
       ins_rom_weaver_3_cu_endinstruction, ins_rom_weaver_3_ip_inc, ins_rom_weaver_3_ip_read,
       ins_rom_weaver_3_ip_write, ins_rom_weaver_3_mar_alu_in0, ins_rom_weaver_3_mar_alu_in1,
       ins_rom_weaver_3_mar_mdr0, ins_rom_weaver_3_mar_mdr1, ins_rom_weaver_3_mar_mdr2,
       ins_rom_weaver_3_mar_read, ins_rom_weaver_3_mar_reg_id, ins_rom_weaver_3_mar_write,
       ins_rom_weaver_3_mdr0_alu_in0, ins_rom_weaver_3_mdr0_alu_in1, ins_rom_weaver_3_mdr0_mar,
       ins_rom_weaver_3_mdr0_mdr1, ins_rom_weaver_3_mdr0_mdr2, ins_rom_weaver_3_mdr0_mem_in,
       ins_rom_weaver_3_mdr0_read, ins_rom_weaver_3_mdr0_reg_id, ins_rom_weaver_3_mdr0_reg_in,
       ins_rom_weaver_3_mdr0_write, ins_rom_weaver_3_mdr0_zero, ins_rom_weaver_3_mdr1_alu_in0,
       ins_rom_weaver_3_mdr1_alu_in1, ins_rom_weaver_3_mdr1_mar, ins_rom_weaver_3_mdr1_mdr0,
       ins_rom_weaver_3_mdr1_mdr2, ins_rom_weaver_3_mdr1_mem_in, ins_rom_weaver_3_mdr1_read,
       ins_rom_weaver_3_mdr1_reg_id, ins_rom_weaver_3_mdr1_reg_in, ins_rom_weaver_3_mdr1_write,
       ins_rom_weaver_3_mdr1_zero, ins_rom_weaver_3_mdr2_alu_in0, ins_rom_weaver_3_mdr2_alu_in1,
       ins_rom_weaver_3_mdr2_mar, ins_rom_weaver_3_mdr2_mdr0, ins_rom_weaver_3_mdr2_mdr1,
       ins_rom_weaver_3_mdr2_mem_in, ins_rom_weaver_3_mdr2_read, ins_rom_weaver_3_mdr2_reg_id,
       ins_rom_weaver_3_mdr2_reg_in, ins_rom_weaver_3_mdr2_write, ins_rom_weaver_3_mdr2_zero,
       ins_rom_weaver_3_mem_read, ins_rom_weaver_3_mem_read2, ins_rom_weaver_3_mem_write,
       ins_rom_weaver_3_reg_out_mar, ins_rom_weaver_3_reg_out_mdr0, ins_rom_weaver_3_reg_out_mdr1,
       ins_rom_weaver_3_reg_out_mdr2, ins_rom_weaver_3_reg_read, ins_rom_weaver_3_reg_write,
       ins_rom_weaver_3_sp_dec, ins_rom_weaver_3_sp_inc, ins_rom_weaver_3_sp_read, ins_rom_weaver_3_sp_write,
       ins_rom_weaver_4_alu_out_mar, ins_rom_weaver_4_alu_out_mdr0, ins_rom_weaver_4_alu_out_mdr1,
       ins_rom_weaver_4_alu_out_mdr2, ins_rom_weaver_4_alu_read, ins_rom_weaver_4_alu_readflags,
       ins_rom_weaver_4_alu_remainder_mar, ins_rom_weaver_4_alu_remainder_mdr0,
       ins_rom_weaver_4_alu_remainder_mdr1, ins_rom_weaver_4_alu_remainder_mdr2, ins_rom_weaver_4_alu_write,
       ins_rom_weaver_4_cu_endinstruction, ins_rom_weaver_4_ip_inc, ins_rom_weaver_4_ip_read,
       ins_rom_weaver_4_ip_write, ins_rom_weaver_4_mar_alu_in0, ins_rom_weaver_4_mar_alu_in1,
       ins_rom_weaver_4_mar_mdr0, ins_rom_weaver_4_mar_mdr1, ins_rom_weaver_4_mar_mdr2,
       ins_rom_weaver_4_mar_read, ins_rom_weaver_4_mar_reg_id, ins_rom_weaver_4_mar_write,
       ins_rom_weaver_4_mdr0_alu_in0, ins_rom_weaver_4_mdr0_alu_in1, ins_rom_weaver_4_mdr0_mar,
       ins_rom_weaver_4_mdr0_mdr1, ins_rom_weaver_4_mdr0_mdr2, ins_rom_weaver_4_mdr0_mem_in,
       ins_rom_weaver_4_mdr0_read, ins_rom_weaver_4_mdr0_reg_id, ins_rom_weaver_4_mdr0_reg_in,
       ins_rom_weaver_4_mdr0_write, ins_rom_weaver_4_mdr0_zero, ins_rom_weaver_4_mdr1_alu_in0,
       ins_rom_weaver_4_mdr1_alu_in1, ins_rom_weaver_4_mdr1_mar, ins_rom_weaver_4_mdr1_mdr0,
       ins_rom_weaver_4_mdr1_mdr2, ins_rom_weaver_4_mdr1_mem_in, ins_rom_weaver_4_mdr1_read,
       ins_rom_weaver_4_mdr1_reg_id, ins_rom_weaver_4_mdr1_reg_in, ins_rom_weaver_4_mdr1_write,
       ins_rom_weaver_4_mdr1_zero, ins_rom_weaver_4_mdr2_alu_in0, ins_rom_weaver_4_mdr2_alu_in1,
       ins_rom_weaver_4_mdr2_mar, ins_rom_weaver_4_mdr2_mdr0, ins_rom_weaver_4_mdr2_mdr1,
       ins_rom_weaver_4_mdr2_mem_in, ins_rom_weaver_4_mdr2_read, ins_rom_weaver_4_mdr2_reg_id,
       ins_rom_weaver_4_mdr2_reg_in, ins_rom_weaver_4_mdr2_write, ins_rom_weaver_4_mdr2_zero,
       ins_rom_weaver_4_mem_read, ins_rom_weaver_4_mem_read2, ins_rom_weaver_4_mem_write,
       ins_rom_weaver_4_reg_out_mar, ins_rom_weaver_4_reg_out_mdr0, ins_rom_weaver_4_reg_out_mdr1,
       ins_rom_weaver_4_reg_out_mdr2, ins_rom_weaver_4_reg_read, ins_rom_weaver_4_reg_write,
       ins_rom_weaver_4_sp_dec, ins_rom_weaver_4_sp_inc, ins_rom_weaver_4_sp_read, ins_rom_weaver_4_sp_write,
       ins_rom_weaver_5_alu_out_mar, ins_rom_weaver_5_alu_out_mdr0, ins_rom_weaver_5_alu_out_mdr1,
       ins_rom_weaver_5_alu_out_mdr2, ins_rom_weaver_5_alu_read, ins_rom_weaver_5_alu_readflags,
       ins_rom_weaver_5_alu_remainder_mar, ins_rom_weaver_5_alu_remainder_mdr0,
       ins_rom_weaver_5_alu_remainder_mdr1, ins_rom_weaver_5_alu_remainder_mdr2, ins_rom_weaver_5_alu_write,
       ins_rom_weaver_5_cu_endinstruction, ins_rom_weaver_5_ip_inc, ins_rom_weaver_5_ip_read,
       ins_rom_weaver_5_ip_write, ins_rom_weaver_5_mar_alu_in0, ins_rom_weaver_5_mar_alu_in1,
       ins_rom_weaver_5_mar_mdr0, ins_rom_weaver_5_mar_mdr1, ins_rom_weaver_5_mar_mdr2,
       ins_rom_weaver_5_mar_read, ins_rom_weaver_5_mar_reg_id, ins_rom_weaver_5_mar_write,
       ins_rom_weaver_5_mdr0_alu_in0, ins_rom_weaver_5_mdr0_alu_in1, ins_rom_weaver_5_mdr0_mar,
       ins_rom_weaver_5_mdr0_mdr1, ins_rom_weaver_5_mdr0_mdr2, ins_rom_weaver_5_mdr0_mem_in,
       ins_rom_weaver_5_mdr0_read, ins_rom_weaver_5_mdr0_reg_id, ins_rom_weaver_5_mdr0_reg_in,
       ins_rom_weaver_5_mdr0_write, ins_rom_weaver_5_mdr0_zero, ins_rom_weaver_5_mdr1_alu_in0,
       ins_rom_weaver_5_mdr1_alu_in1, ins_rom_weaver_5_mdr1_mar, ins_rom_weaver_5_mdr1_mdr0,
       ins_rom_weaver_5_mdr1_mdr2, ins_rom_weaver_5_mdr1_mem_in, ins_rom_weaver_5_mdr1_read,
       ins_rom_weaver_5_mdr1_reg_id, ins_rom_weaver_5_mdr1_reg_in, ins_rom_weaver_5_mdr1_write,
       ins_rom_weaver_5_mdr1_zero, ins_rom_weaver_5_mdr2_alu_in0, ins_rom_weaver_5_mdr2_alu_in1,
       ins_rom_weaver_5_mdr2_mar, ins_rom_weaver_5_mdr2_mdr0, ins_rom_weaver_5_mdr2_mdr1,
       ins_rom_weaver_5_mdr2_mem_in, ins_rom_weaver_5_mdr2_read, ins_rom_weaver_5_mdr2_reg_id,
       ins_rom_weaver_5_mdr2_reg_in, ins_rom_weaver_5_mdr2_write, ins_rom_weaver_5_mdr2_zero,
       ins_rom_weaver_5_mem_read, ins_rom_weaver_5_mem_read2, ins_rom_weaver_5_mem_write,
       ins_rom_weaver_5_reg_out_mar, ins_rom_weaver_5_reg_out_mdr0, ins_rom_weaver_5_reg_out_mdr1,
       ins_rom_weaver_5_reg_out_mdr2, ins_rom_weaver_5_reg_read, ins_rom_weaver_5_reg_write,
       ins_rom_weaver_5_sp_dec, ins_rom_weaver_5_sp_inc, ins_rom_weaver_5_sp_read, ins_rom_weaver_5_sp_write,
       ins_rom_weaver_6_alu_out_mar, ins_rom_weaver_6_alu_out_mdr0, ins_rom_weaver_6_alu_out_mdr1,
       ins_rom_weaver_6_alu_out_mdr2, ins_rom_weaver_6_alu_read, ins_rom_weaver_6_alu_readflags,
       ins_rom_weaver_6_alu_remainder_mar, ins_rom_weaver_6_alu_remainder_mdr0,
       ins_rom_weaver_6_alu_remainder_mdr1, ins_rom_weaver_6_alu_remainder_mdr2, ins_rom_weaver_6_alu_write,
       ins_rom_weaver_6_cu_endinstruction, ins_rom_weaver_6_ip_inc, ins_rom_weaver_6_ip_read,
       ins_rom_weaver_6_ip_write, ins_rom_weaver_6_mar_alu_in0, ins_rom_weaver_6_mar_alu_in1,
       ins_rom_weaver_6_mar_mdr0, ins_rom_weaver_6_mar_mdr1, ins_rom_weaver_6_mar_mdr2,
       ins_rom_weaver_6_mar_read, ins_rom_weaver_6_mar_reg_id, ins_rom_weaver_6_mar_write,
       ins_rom_weaver_6_mdr0_alu_in0, ins_rom_weaver_6_mdr0_alu_in1, ins_rom_weaver_6_mdr0_mar,
       ins_rom_weaver_6_mdr0_mdr1, ins_rom_weaver_6_mdr0_mdr2, ins_rom_weaver_6_mdr0_mem_in,
       ins_rom_weaver_6_mdr0_read, ins_rom_weaver_6_mdr0_reg_id, ins_rom_weaver_6_mdr0_reg_in,
       ins_rom_weaver_6_mdr0_write, ins_rom_weaver_6_mdr0_zero, ins_rom_weaver_6_mdr1_alu_in0,
       ins_rom_weaver_6_mdr1_alu_in1, ins_rom_weaver_6_mdr1_mar, ins_rom_weaver_6_mdr1_mdr0,
       ins_rom_weaver_6_mdr1_mdr2, ins_rom_weaver_6_mdr1_mem_in, ins_rom_weaver_6_mdr1_read,
       ins_rom_weaver_6_mdr1_reg_id, ins_rom_weaver_6_mdr1_reg_in, ins_rom_weaver_6_mdr1_write,
       ins_rom_weaver_6_mdr1_zero, ins_rom_weaver_6_mdr2_alu_in0, ins_rom_weaver_6_mdr2_alu_in1,
       ins_rom_weaver_6_mdr2_mar, ins_rom_weaver_6_mdr2_mdr0, ins_rom_weaver_6_mdr2_mdr1,
       ins_rom_weaver_6_mdr2_mem_in, ins_rom_weaver_6_mdr2_read, ins_rom_weaver_6_mdr2_reg_id,
       ins_rom_weaver_6_mdr2_reg_in, ins_rom_weaver_6_mdr2_write, ins_rom_weaver_6_mdr2_zero,
       ins_rom_weaver_6_mem_read, ins_rom_weaver_6_mem_read2, ins_rom_weaver_6_mem_write,
       ins_rom_weaver_6_reg_out_mar, ins_rom_weaver_6_reg_out_mdr0, ins_rom_weaver_6_reg_out_mdr1,
       ins_rom_weaver_6_reg_out_mdr2, ins_rom_weaver_6_reg_read, ins_rom_weaver_6_reg_write,
       ins_rom_weaver_6_sp_dec, ins_rom_weaver_6_sp_inc, ins_rom_weaver_6_sp_read, ins_rom_weaver_6_sp_write,
       ins_rom_weaver_7_alu_out_mar, ins_rom_weaver_7_alu_out_mdr0, ins_rom_weaver_7_alu_out_mdr1,
       ins_rom_weaver_7_alu_out_mdr2, ins_rom_weaver_7_alu_read, ins_rom_weaver_7_alu_readflags,
       ins_rom_weaver_7_alu_remainder_mar, ins_rom_weaver_7_alu_remainder_mdr0,
       ins_rom_weaver_7_alu_remainder_mdr1, ins_rom_weaver_7_alu_remainder_mdr2, ins_rom_weaver_7_alu_write,
       ins_rom_weaver_7_cu_endinstruction, ins_rom_weaver_7_ip_inc, ins_rom_weaver_7_ip_read,
       ins_rom_weaver_7_ip_write, ins_rom_weaver_7_mar_alu_in0, ins_rom_weaver_7_mar_alu_in1,
       ins_rom_weaver_7_mar_mdr0, ins_rom_weaver_7_mar_mdr1, ins_rom_weaver_7_mar_mdr2,
       ins_rom_weaver_7_mar_read, ins_rom_weaver_7_mar_reg_id, ins_rom_weaver_7_mar_write,
       ins_rom_weaver_7_mdr0_alu_in0, ins_rom_weaver_7_mdr0_alu_in1, ins_rom_weaver_7_mdr0_mar,
       ins_rom_weaver_7_mdr0_mdr1, ins_rom_weaver_7_mdr0_mdr2, ins_rom_weaver_7_mdr0_mem_in,
       ins_rom_weaver_7_mdr0_read, ins_rom_weaver_7_mdr0_reg_id, ins_rom_weaver_7_mdr0_reg_in,
       ins_rom_weaver_7_mdr0_write, ins_rom_weaver_7_mdr0_zero, ins_rom_weaver_7_mdr1_alu_in0,
       ins_rom_weaver_7_mdr1_alu_in1, ins_rom_weaver_7_mdr1_mar, ins_rom_weaver_7_mdr1_mdr0,
       ins_rom_weaver_7_mdr1_mdr2, ins_rom_weaver_7_mdr1_mem_in, ins_rom_weaver_7_mdr1_read,
       ins_rom_weaver_7_mdr1_reg_id, ins_rom_weaver_7_mdr1_reg_in, ins_rom_weaver_7_mdr1_write,
       ins_rom_weaver_7_mdr1_zero, ins_rom_weaver_7_mdr2_alu_in0, ins_rom_weaver_7_mdr2_alu_in1,
       ins_rom_weaver_7_mdr2_mar, ins_rom_weaver_7_mdr2_mdr0, ins_rom_weaver_7_mdr2_mdr1,
       ins_rom_weaver_7_mdr2_mem_in, ins_rom_weaver_7_mdr2_read, ins_rom_weaver_7_mdr2_reg_id,
       ins_rom_weaver_7_mdr2_reg_in, ins_rom_weaver_7_mdr2_write, ins_rom_weaver_7_mdr2_zero,
       ins_rom_weaver_7_mem_read, ins_rom_weaver_7_mem_read2, ins_rom_weaver_7_mem_write,
       ins_rom_weaver_7_reg_out_mar, ins_rom_weaver_7_reg_out_mdr0, ins_rom_weaver_7_reg_out_mdr1,
       ins_rom_weaver_7_reg_out_mdr2, ins_rom_weaver_7_reg_read, ins_rom_weaver_7_reg_write,
       ins_rom_weaver_7_sp_dec, ins_rom_weaver_7_sp_inc, ins_rom_weaver_7_sp_read, ins_rom_weaver_7_sp_write,
       ins_rom_weaver_8_alu_out_mar, ins_rom_weaver_8_alu_out_mdr0, ins_rom_weaver_8_alu_out_mdr1,
       ins_rom_weaver_8_alu_out_mdr2, ins_rom_weaver_8_alu_read, ins_rom_weaver_8_alu_readflags,
       ins_rom_weaver_8_alu_remainder_mar, ins_rom_weaver_8_alu_remainder_mdr0,
       ins_rom_weaver_8_alu_remainder_mdr1, ins_rom_weaver_8_alu_remainder_mdr2, ins_rom_weaver_8_alu_write,
       ins_rom_weaver_8_cu_endinstruction, ins_rom_weaver_8_ip_inc, ins_rom_weaver_8_ip_read,
       ins_rom_weaver_8_ip_write, ins_rom_weaver_8_mar_alu_in0, ins_rom_weaver_8_mar_alu_in1,
       ins_rom_weaver_8_mar_mdr0, ins_rom_weaver_8_mar_mdr1, ins_rom_weaver_8_mar_mdr2,
       ins_rom_weaver_8_mar_read, ins_rom_weaver_8_mar_reg_id, ins_rom_weaver_8_mar_write,
       ins_rom_weaver_8_mdr0_alu_in0, ins_rom_weaver_8_mdr0_alu_in1, ins_rom_weaver_8_mdr0_mar,
       ins_rom_weaver_8_mdr0_mdr1, ins_rom_weaver_8_mdr0_mdr2, ins_rom_weaver_8_mdr0_mem_in,
       ins_rom_weaver_8_mdr0_read, ins_rom_weaver_8_mdr0_reg_id, ins_rom_weaver_8_mdr0_reg_in,
       ins_rom_weaver_8_mdr0_write, ins_rom_weaver_8_mdr0_zero, ins_rom_weaver_8_mdr1_alu_in0,
       ins_rom_weaver_8_mdr1_alu_in1, ins_rom_weaver_8_mdr1_mar, ins_rom_weaver_8_mdr1_mdr0,
       ins_rom_weaver_8_mdr1_mdr2, ins_rom_weaver_8_mdr1_mem_in, ins_rom_weaver_8_mdr1_read,
       ins_rom_weaver_8_mdr1_reg_id, ins_rom_weaver_8_mdr1_reg_in, ins_rom_weaver_8_mdr1_write,
       ins_rom_weaver_8_mdr1_zero, ins_rom_weaver_8_mdr2_alu_in0, ins_rom_weaver_8_mdr2_alu_in1,
       ins_rom_weaver_8_mdr2_mar, ins_rom_weaver_8_mdr2_mdr0, ins_rom_weaver_8_mdr2_mdr1,
       ins_rom_weaver_8_mdr2_mem_in, ins_rom_weaver_8_mdr2_read, ins_rom_weaver_8_mdr2_reg_id,
       ins_rom_weaver_8_mdr2_reg_in, ins_rom_weaver_8_mdr2_write, ins_rom_weaver_8_mdr2_zero,
       ins_rom_weaver_8_mem_read, ins_rom_weaver_8_mem_read2, ins_rom_weaver_8_mem_write,
       ins_rom_weaver_8_reg_out_mar, ins_rom_weaver_8_reg_out_mdr0, ins_rom_weaver_8_reg_out_mdr1,
       ins_rom_weaver_8_reg_out_mdr2, ins_rom_weaver_8_reg_read, ins_rom_weaver_8_reg_write,
       ins_rom_weaver_8_sp_dec, ins_rom_weaver_8_sp_inc, ins_rom_weaver_8_sp_read, ins_rom_weaver_8_sp_write;
  wire [7:0] ins_rom_0_1_alu_select, ins_rom_1_1_alu_select, ins_rom_2_1_alu_select, ins_rom_3_1_alu_select,
       ins_rom_4_1_alu_select, ins_rom_5_1_alu_select, ins_rom_6_1_alu_select, ins_rom_7_1_alu_select,
       ins_rom_8_1_alu_select, ins_rom_9_1_alu_select, ins_rom_weaver_1_alu_select,
       ins_rom_weaver_2_alu_select, ins_rom_weaver_3_alu_select, ins_rom_weaver_4_alu_select,
       ins_rom_weaver_5_alu_select, ins_rom_weaver_6_alu_select, ins_rom_weaver_7_alu_select,
       ins_rom_weaver_8_alu_select;

  Demultiplexer #(.select(4)) demultiplexer_1 (
    .out0(demultiplexer_1_out0), .out1(demultiplexer_1_out1), .out2(demultiplexer_1_out2),
    .out3(demultiplexer_1_out3), .out4(demultiplexer_1_out4), .out5(demultiplexer_1_out5),
    .out6(demultiplexer_1_out6), .out7(demultiplexer_1_out7), .out8(demultiplexer_1_out8),
    .out9(demultiplexer_1_out9), .in(CLK), .sel(Cycle[3:0]));  // open: out10, out11, out12, out13, out14, out15
  INS_ROM_0 ins_rom_0_1 (
    .in_1(Instruction), .CLK(demultiplexer_1_out0), .IP_inc(ins_rom_0_1_ip_inc),
    .IP_read(ins_rom_0_1_ip_read), .IP_write(ins_rom_0_1_ip_write), .SP_inc(ins_rom_0_1_sp_inc),
    .SP_dec(ins_rom_0_1_sp_dec), .SP_read(ins_rom_0_1_sp_read), .SP_write(ins_rom_0_1_sp_write),
    .MAR_read(ins_rom_0_1_mar_read), .MAR_write(ins_rom_0_1_mar_write), .MDR0_read(ins_rom_0_1_mdr0_read),
    .MDR0_write(ins_rom_0_1_mdr0_write), .MDR0_zero(ins_rom_0_1_mdr0_zero),
    .MDR1_read(ins_rom_0_1_mdr1_read), .MDR1_write(ins_rom_0_1_mdr1_write),
    .MDR1_zero(ins_rom_0_1_mdr1_zero), .MDR2_read(ins_rom_0_1_mdr2_read),
    .MDR2_write(ins_rom_0_1_mdr2_write), .MDR2_zero(ins_rom_0_1_mdr2_zero), .MEM_read(ins_rom_0_1_mem_read),
    .MEM_read2(ins_rom_0_1_mem_read2), .MEM_write(ins_rom_0_1_mem_write),
    .MDR0_MEM_IN(ins_rom_0_1_mdr0_mem_in), .MDR1_MEM_IN(ins_rom_0_1_mdr1_mem_in),
    .MDR2_MEM_IN(ins_rom_0_1_mdr2_mem_in), .MDR0_REG_IN(ins_rom_0_1_mdr0_reg_in),
    .MDR1_REG_IN(ins_rom_0_1_mdr1_reg_in), .MDR2_REG_IN(ins_rom_0_1_mdr2_reg_in),
    .MAR_REG_ID(ins_rom_0_1_mar_reg_id), .MDR0_REG_ID(ins_rom_0_1_mdr0_reg_id),
    .MDR1_REG_ID(ins_rom_0_1_mdr1_reg_id), .MDR2_REG_ID(ins_rom_0_1_mdr2_reg_id),
    .REG_OUT_MAR(ins_rom_0_1_reg_out_mar), .REG_OUT_MDR0(ins_rom_0_1_reg_out_mdr0),
    .REG_OUT_MDR1(ins_rom_0_1_reg_out_mdr1), .REG_OUT_MDR2(ins_rom_0_1_reg_out_mdr2),
    .REG_read(ins_rom_0_1_reg_read), .REG_write(ins_rom_0_1_reg_write), .MAR_MDR0(ins_rom_0_1_mar_mdr0),
    .MAR_MDR1(ins_rom_0_1_mar_mdr1), .MAR_MDR2(ins_rom_0_1_mar_mdr2), .MDR0_MAR(ins_rom_0_1_mdr0_mar),
    .MDR0_MDR1(ins_rom_0_1_mdr0_mdr1), .MDR0_MDR2(ins_rom_0_1_mdr0_mdr2), .MDR1_MAR(ins_rom_0_1_mdr1_mar),
    .MDR1_MDR0(ins_rom_0_1_mdr1_mdr0), .MDR1_MDR2(ins_rom_0_1_mdr1_mdr2), .MDR2_MAR(ins_rom_0_1_mdr2_mar),
    .MDR2_MDR0(ins_rom_0_1_mdr2_mdr0), .MDR2_MDR1(ins_rom_0_1_mdr2_mdr1),
    .MAR_ALU_IN0(ins_rom_0_1_mar_alu_in0), .MDR0_ALU_IN0(ins_rom_0_1_mdr0_alu_in0),
    .MDR1_ALU_IN0(ins_rom_0_1_mdr1_alu_in0), .MDR2_ALU_IN0(ins_rom_0_1_mdr2_alu_in0),
    .MAR_ALU_IN1(ins_rom_0_1_mar_alu_in1), .MDR0_ALU_IN1(ins_rom_0_1_mdr0_alu_in1),
    .MDR1_ALU_IN1(ins_rom_0_1_mdr1_alu_in1), .MDR2_ALU_IN1(ins_rom_0_1_mdr2_alu_in1),
    .ALU_SELECT(ins_rom_0_1_alu_select), .ALU_read(ins_rom_0_1_alu_read), .ALU_write(ins_rom_0_1_alu_write),
    .ALU_readFlags(ins_rom_0_1_alu_readflags), .ALU_OUT_MAR(ins_rom_0_1_alu_out_mar),
    .ALU_OUT_MDR0(ins_rom_0_1_alu_out_mdr0), .ALU_OUT_MDR1(ins_rom_0_1_alu_out_mdr1),
    .ALU_OUT_MDR2(ins_rom_0_1_alu_out_mdr2), .ALU_REMAINDER_MAR(ins_rom_0_1_alu_remainder_mar),
    .ALU_REMAINDER_MDR0(ins_rom_0_1_alu_remainder_mdr0), .ALU_REMAINDER_MDR1(ins_rom_0_1_alu_remainder_mdr1),
    .ALU_REMAINDER_MDR2(ins_rom_0_1_alu_remainder_mdr2), .CU_endInstruction(ins_rom_0_1_cu_endinstruction));
  INS_ROM_1 ins_rom_1_1 (
    .Instruc(Instruction), .Flags(Flags), .CLK(demultiplexer_1_out1), .IP_inc(ins_rom_1_1_ip_inc),
    .IP_read(ins_rom_1_1_ip_read), .IP_write(ins_rom_1_1_ip_write), .SP_inc(ins_rom_1_1_sp_inc),
    .SP_dec(ins_rom_1_1_sp_dec), .SP_read(ins_rom_1_1_sp_read), .SP_write(ins_rom_1_1_sp_write),
    .MAR_read(ins_rom_1_1_mar_read), .MAR_write(ins_rom_1_1_mar_write), .MDR0_read(ins_rom_1_1_mdr0_read),
    .MDR0_write(ins_rom_1_1_mdr0_write), .MDR0_zero(ins_rom_1_1_mdr0_zero),
    .MDR1_read(ins_rom_1_1_mdr1_read), .MDR1_write(ins_rom_1_1_mdr1_write),
    .MDR1_zero(ins_rom_1_1_mdr1_zero), .MDR2_read(ins_rom_1_1_mdr2_read),
    .MDR2_write(ins_rom_1_1_mdr2_write), .MDR2_zero(ins_rom_1_1_mdr2_zero), .MEM_read(ins_rom_1_1_mem_read),
    .MEM_read2(ins_rom_1_1_mem_read2), .MEM_write(ins_rom_1_1_mem_write),
    .MDR0_MEM_IN(ins_rom_1_1_mdr0_mem_in), .MDR1_MEM_IN(ins_rom_1_1_mdr1_mem_in),
    .MDR2_MEM_IN(ins_rom_1_1_mdr2_mem_in), .MDR0_REG_IN(ins_rom_1_1_mdr0_reg_in),
    .MDR1_REG_IN(ins_rom_1_1_mdr1_reg_in), .MDR2_REG_IN(ins_rom_1_1_mdr2_reg_in),
    .MAR_REG_ID(ins_rom_1_1_mar_reg_id), .MDR0_REG_ID(ins_rom_1_1_mdr0_reg_id),
    .MDR1_REG_ID(ins_rom_1_1_mdr1_reg_id), .MDR2_REG_ID(ins_rom_1_1_mdr2_reg_id),
    .REG_OUT_MAR(ins_rom_1_1_reg_out_mar), .REG_OUT_MDR0(ins_rom_1_1_reg_out_mdr0),
    .REG_OUT_MDR1(ins_rom_1_1_reg_out_mdr1), .REG_OUT_MDR2(ins_rom_1_1_reg_out_mdr2),
    .REG_read(ins_rom_1_1_reg_read), .REG_write(ins_rom_1_1_reg_write), .MAR_MDR0(ins_rom_1_1_mar_mdr0),
    .MAR_MDR1(ins_rom_1_1_mar_mdr1), .MAR_MDR2(ins_rom_1_1_mar_mdr2), .MDR0_MAR(ins_rom_1_1_mdr0_mar),
    .MDR0_MDR1(ins_rom_1_1_mdr0_mdr1), .MDR0_MDR2(ins_rom_1_1_mdr0_mdr2), .MDR1_MAR(ins_rom_1_1_mdr1_mar),
    .MDR1_MDR0(ins_rom_1_1_mdr1_mdr0), .MDR1_MDR2(ins_rom_1_1_mdr1_mdr2), .MDR2_MAR(ins_rom_1_1_mdr2_mar),
    .MDR2_MDR0(ins_rom_1_1_mdr2_mdr0), .MDR2_MDR1(ins_rom_1_1_mdr2_mdr1),
    .MAR_ALU_IN0(ins_rom_1_1_mar_alu_in0), .MDR0_ALU_IN0(ins_rom_1_1_mdr0_alu_in0),
    .MDR1_ALU_IN0(ins_rom_1_1_mdr1_alu_in0), .MDR2_ALU_IN0(ins_rom_1_1_mdr2_alu_in0),
    .MAR_ALU_IN1(ins_rom_1_1_mar_alu_in1), .MDR0_ALU_IN1(ins_rom_1_1_mdr0_alu_in1),
    .MDR1_ALU_IN1(ins_rom_1_1_mdr1_alu_in1), .MDR2_ALU_IN1(ins_rom_1_1_mdr2_alu_in1),
    .ALU_SELECT(ins_rom_1_1_alu_select), .ALU_read(ins_rom_1_1_alu_read), .ALU_write(ins_rom_1_1_alu_write),
    .ALU_readFlags(ins_rom_1_1_alu_readflags), .ALU_OUT_MAR(ins_rom_1_1_alu_out_mar),
    .ALU_OUT_MDR0(ins_rom_1_1_alu_out_mdr0), .ALU_OUT_MDR1(ins_rom_1_1_alu_out_mdr1),
    .ALU_OUT_MDR2(ins_rom_1_1_alu_out_mdr2), .ALU_REMAINDER_MAR(ins_rom_1_1_alu_remainder_mar),
    .ALU_REMAINDER_MDR0(ins_rom_1_1_alu_remainder_mdr0), .ALU_REMAINDER_MDR1(ins_rom_1_1_alu_remainder_mdr1),
    .ALU_REMAINDER_MDR2(ins_rom_1_1_alu_remainder_mdr2), .CU_endInstruction(ins_rom_1_1_cu_endinstruction));
  INS_ROM_WEAVER ins_rom_weaver_1 (
    .in_1(ins_rom_0_1_ip_inc), .in_2(ins_rom_0_1_ip_read), .in_3(ins_rom_0_1_ip_write),
    .in_4(ins_rom_0_1_sp_inc), .in_5(ins_rom_0_1_sp_dec), .in_6(ins_rom_0_1_sp_read),
    .in_7(ins_rom_0_1_sp_write), .in_8(ins_rom_0_1_mar_read), .in_9(ins_rom_0_1_mar_write),
    .in_10(ins_rom_0_1_mdr0_read), .in_11(ins_rom_0_1_mdr0_write), .in_12(ins_rom_0_1_mdr0_zero),
    .in_13(ins_rom_0_1_mdr1_read), .in_14(ins_rom_0_1_mdr1_write), .in_15(ins_rom_0_1_mdr1_zero),
    .in_16(ins_rom_0_1_mdr2_read), .in_17(ins_rom_0_1_mdr2_write), .in_18(ins_rom_0_1_mdr2_zero),
    .in_19(ins_rom_0_1_mem_read), .in_20(ins_rom_0_1_mem_read2), .in_21(ins_rom_0_1_mem_write),
    .in_22(ins_rom_0_1_mdr0_mem_in), .in_23(ins_rom_0_1_mdr1_mem_in), .in_24(ins_rom_0_1_mdr2_mem_in),
    .in_25(ins_rom_0_1_mdr0_reg_in), .in_26(ins_rom_0_1_mdr1_reg_in), .in_27(ins_rom_0_1_mdr2_reg_in),
    .in_28(ins_rom_0_1_mar_reg_id), .in_29(ins_rom_0_1_mdr0_reg_id), .in_30(ins_rom_0_1_mdr1_reg_id),
    .in_31(ins_rom_0_1_mdr2_reg_id), .in_32(ins_rom_0_1_reg_out_mar), .in_33(ins_rom_0_1_reg_out_mdr0),
    .in_34(ins_rom_0_1_reg_out_mdr1), .in_35(ins_rom_0_1_reg_out_mdr2), .in_36(ins_rom_0_1_reg_read),
    .in_37(ins_rom_0_1_reg_write), .in_38(ins_rom_0_1_mar_mdr0), .in_39(ins_rom_0_1_mar_mdr1),
    .in_40(ins_rom_0_1_mar_mdr2), .in_41(ins_rom_0_1_mdr0_mar), .in_42(ins_rom_0_1_mdr0_mdr1),
    .in_43(ins_rom_0_1_mdr0_mdr2), .in_44(ins_rom_0_1_mdr1_mar), .in_45(ins_rom_0_1_mdr1_mdr0),
    .in_46(ins_rom_0_1_mdr1_mdr2), .in_47(ins_rom_0_1_mdr2_mar), .in_48(ins_rom_0_1_mdr2_mdr0),
    .in_49(ins_rom_0_1_mdr2_mdr1), .in_50(ins_rom_0_1_mar_alu_in0), .in_51(ins_rom_0_1_mdr0_alu_in0),
    .in_52(ins_rom_0_1_mdr1_alu_in0), .in_53(ins_rom_0_1_mdr2_alu_in0), .in_54(ins_rom_0_1_mar_alu_in1),
    .in_55(ins_rom_0_1_mdr0_alu_in1), .in_56(ins_rom_0_1_mdr1_alu_in1), .in_57(ins_rom_0_1_mdr2_alu_in1),
    .in_58(ins_rom_0_1_alu_select), .in_59(ins_rom_0_1_alu_read), .in_60(ins_rom_0_1_alu_write),
    .in_61(ins_rom_0_1_alu_readflags), .in_62(ins_rom_0_1_alu_out_mar), .in_63(ins_rom_0_1_alu_out_mdr0),
    .in_64(ins_rom_0_1_alu_out_mdr1), .in_65(ins_rom_0_1_alu_out_mdr2),
    .in_66(ins_rom_0_1_alu_remainder_mar), .in_67(ins_rom_0_1_alu_remainder_mdr0),
    .in_68(ins_rom_0_1_alu_remainder_mdr1), .in_69(ins_rom_0_1_alu_remainder_mdr2),
    .in_70(ins_rom_0_1_cu_endinstruction), .in_71(ins_rom_1_1_ip_inc), .in_72(ins_rom_1_1_ip_read),
    .in_73(ins_rom_1_1_ip_write), .in_74(ins_rom_1_1_sp_inc), .in_75(ins_rom_1_1_sp_dec),
    .in_76(ins_rom_1_1_sp_read), .in_77(ins_rom_1_1_sp_write), .in_78(ins_rom_1_1_mar_read),
    .in_79(ins_rom_1_1_mar_write), .in_80(ins_rom_1_1_mdr0_read), .in_81(ins_rom_1_1_mdr0_write),
    .in_82(ins_rom_1_1_mdr0_zero), .in_83(ins_rom_1_1_mdr1_read), .in_84(ins_rom_1_1_mdr1_write),
    .in_85(ins_rom_1_1_mdr1_zero), .in_86(ins_rom_1_1_mdr2_read), .in_87(ins_rom_1_1_mdr2_write),
    .in_88(ins_rom_1_1_mdr2_zero), .in_89(ins_rom_1_1_mem_read), .in_90(ins_rom_1_1_mem_read2),
    .in_91(ins_rom_1_1_mem_write), .in_92(ins_rom_1_1_mdr0_mem_in), .in_93(ins_rom_1_1_mdr1_mem_in),
    .in_94(ins_rom_1_1_mdr2_mem_in), .in_95(ins_rom_1_1_mdr0_reg_in), .in_96(ins_rom_1_1_mdr1_reg_in),
    .in_97(ins_rom_1_1_mdr2_reg_in), .in_98(ins_rom_1_1_mar_reg_id), .in_99(ins_rom_1_1_mdr0_reg_id),
    .in_100(ins_rom_1_1_mdr1_reg_id), .in_101(ins_rom_1_1_mdr2_reg_id), .in_102(ins_rom_1_1_reg_out_mar),
    .in_103(ins_rom_1_1_reg_out_mdr0), .in_104(ins_rom_1_1_reg_out_mdr1), .in_105(ins_rom_1_1_reg_out_mdr2),
    .in_106(ins_rom_1_1_reg_read), .in_107(ins_rom_1_1_reg_write), .in_108(ins_rom_1_1_mar_mdr0),
    .in_109(ins_rom_1_1_mar_mdr1), .in_110(ins_rom_1_1_mar_mdr2), .in_111(ins_rom_1_1_mdr0_mar),
    .in_112(ins_rom_1_1_mdr0_mdr1), .in_113(ins_rom_1_1_mdr0_mdr2), .in_114(ins_rom_1_1_mdr1_mar),
    .in_115(ins_rom_1_1_mdr1_mdr0), .in_116(ins_rom_1_1_mdr1_mdr2), .in_117(ins_rom_1_1_mdr2_mar),
    .in_118(ins_rom_1_1_mdr2_mdr0), .in_119(ins_rom_1_1_mdr2_mdr1), .in_120(ins_rom_1_1_mar_alu_in0),
    .in_121(ins_rom_1_1_mdr0_alu_in0), .in_122(ins_rom_1_1_mdr1_alu_in0), .in_123(ins_rom_1_1_mdr2_alu_in0),
    .in_124(ins_rom_1_1_mar_alu_in1), .in_125(ins_rom_1_1_mdr0_alu_in1), .in_126(ins_rom_1_1_mdr1_alu_in1),
    .in_127(ins_rom_1_1_mdr2_alu_in1), .in_128(ins_rom_1_1_alu_select), .in_129(ins_rom_1_1_alu_read),
    .in_130(ins_rom_1_1_alu_write), .in_131(ins_rom_1_1_alu_readflags), .in_132(ins_rom_1_1_alu_out_mar),
    .in_133(ins_rom_1_1_alu_out_mdr0), .in_134(ins_rom_1_1_alu_out_mdr1), .in_135(ins_rom_1_1_alu_out_mdr2),
    .in_136(ins_rom_1_1_alu_remainder_mar), .in_137(ins_rom_1_1_alu_remainder_mdr0),
    .in_138(ins_rom_1_1_alu_remainder_mdr1), .in_139(ins_rom_1_1_alu_remainder_mdr2),
    .in_140(ins_rom_1_1_cu_endinstruction), .IP_inc(ins_rom_weaver_1_ip_inc),
    .IP_read(ins_rom_weaver_1_ip_read), .IP_write(ins_rom_weaver_1_ip_write),
    .SP_inc(ins_rom_weaver_1_sp_inc), .SP_dec(ins_rom_weaver_1_sp_dec), .SP_read(ins_rom_weaver_1_sp_read),
    .SP_write(ins_rom_weaver_1_sp_write), .MAR_read(ins_rom_weaver_1_mar_read),
    .MAR_write(ins_rom_weaver_1_mar_write), .MDR0_read(ins_rom_weaver_1_mdr0_read),
    .MDR0_write(ins_rom_weaver_1_mdr0_write), .MDR0_zero(ins_rom_weaver_1_mdr0_zero),
    .MDR1_read(ins_rom_weaver_1_mdr1_read), .MDR1_write(ins_rom_weaver_1_mdr1_write),
    .MDR1_zero(ins_rom_weaver_1_mdr1_zero), .MDR2_read(ins_rom_weaver_1_mdr2_read),
    .MDR2_write(ins_rom_weaver_1_mdr2_write), .MDR2_zero(ins_rom_weaver_1_mdr2_zero),
    .MEM_read(ins_rom_weaver_1_mem_read), .MEM_read2(ins_rom_weaver_1_mem_read2),
    .MEM_write(ins_rom_weaver_1_mem_write), .MDR0_MEM_IN(ins_rom_weaver_1_mdr0_mem_in),
    .MDR1_MEM_IN(ins_rom_weaver_1_mdr1_mem_in), .MDR2_MEM_IN(ins_rom_weaver_1_mdr2_mem_in),
    .MDR0_REG_IN(ins_rom_weaver_1_mdr0_reg_in), .MDR1_REG_IN(ins_rom_weaver_1_mdr1_reg_in),
    .MDR2_REG_IN(ins_rom_weaver_1_mdr2_reg_in), .MAR_REG_ID(ins_rom_weaver_1_mar_reg_id),
    .MDR0_REG_ID(ins_rom_weaver_1_mdr0_reg_id), .MDR1_REG_ID(ins_rom_weaver_1_mdr1_reg_id),
    .MDR2_REG_ID(ins_rom_weaver_1_mdr2_reg_id), .REG_OUT_MAR(ins_rom_weaver_1_reg_out_mar),
    .REG_OUT_MDR0(ins_rom_weaver_1_reg_out_mdr0), .REG_OUT_MDR1(ins_rom_weaver_1_reg_out_mdr1),
    .REG_OUT_MDR2(ins_rom_weaver_1_reg_out_mdr2), .REG_read(ins_rom_weaver_1_reg_read),
    .REG_write(ins_rom_weaver_1_reg_write), .MAR_MDR0(ins_rom_weaver_1_mar_mdr0),
    .MAR_MDR1(ins_rom_weaver_1_mar_mdr1), .MAR_MDR2(ins_rom_weaver_1_mar_mdr2),
    .MDR0_MAR(ins_rom_weaver_1_mdr0_mar), .MDR0_MDR1(ins_rom_weaver_1_mdr0_mdr1),
    .MDR0_MDR2(ins_rom_weaver_1_mdr0_mdr2), .MDR1_MAR(ins_rom_weaver_1_mdr1_mar),
    .MDR1_MDR0(ins_rom_weaver_1_mdr1_mdr0), .MDR1_MDR2(ins_rom_weaver_1_mdr1_mdr2),
    .MDR2_MAR(ins_rom_weaver_1_mdr2_mar), .MDR2_MDR0(ins_rom_weaver_1_mdr2_mdr0),
    .MDR2_MDR1(ins_rom_weaver_1_mdr2_mdr1), .MAR_ALU_IN0(ins_rom_weaver_1_mar_alu_in0),
    .MDR0_ALU_IN0(ins_rom_weaver_1_mdr0_alu_in0), .MDR1_ALU_IN0(ins_rom_weaver_1_mdr1_alu_in0),
    .MDR2_ALU_IN0(ins_rom_weaver_1_mdr2_alu_in0), .MAR_ALU_IN1(ins_rom_weaver_1_mar_alu_in1),
    .MDR0_ALU_IN1(ins_rom_weaver_1_mdr0_alu_in1), .MDR1_ALU_IN1(ins_rom_weaver_1_mdr1_alu_in1),
    .MDR2_ALU_IN1(ins_rom_weaver_1_mdr2_alu_in1), .ALU_SELECT(ins_rom_weaver_1_alu_select),
    .ALU_read(ins_rom_weaver_1_alu_read), .ALU_write(ins_rom_weaver_1_alu_write),
    .ALU_readFlags(ins_rom_weaver_1_alu_readflags), .ALU_OUT_MAR(ins_rom_weaver_1_alu_out_mar),
    .ALU_OUT_MDR0(ins_rom_weaver_1_alu_out_mdr0), .ALU_OUT_MDR1(ins_rom_weaver_1_alu_out_mdr1),
    .ALU_OUT_MDR2(ins_rom_weaver_1_alu_out_mdr2), .ALU_REMAINDER_MAR(ins_rom_weaver_1_alu_remainder_mar),
    .ALU_REMAINDER_MDR0(ins_rom_weaver_1_alu_remainder_mdr0),
    .ALU_REMAINDER_MDR1(ins_rom_weaver_1_alu_remainder_mdr1),
    .ALU_REMAINDER_MDR2(ins_rom_weaver_1_alu_remainder_mdr2),
    .CU_endInstruction(ins_rom_weaver_1_cu_endinstruction));
  INS_ROM_2 ins_rom_2_1 (
    .in_1(Instruction), .CLK(demultiplexer_1_out2), .IP_inc(ins_rom_2_1_ip_inc),
    .IP_read(ins_rom_2_1_ip_read), .IP_write(ins_rom_2_1_ip_write), .SP_inc(ins_rom_2_1_sp_inc),
    .SP_dec(ins_rom_2_1_sp_dec), .SP_read(ins_rom_2_1_sp_read), .SP_write(ins_rom_2_1_sp_write),
    .MAR_read(ins_rom_2_1_mar_read), .MAR_write(ins_rom_2_1_mar_write), .MDR0_read(ins_rom_2_1_mdr0_read),
    .MDR0_write(ins_rom_2_1_mdr0_write), .MDR0_zero(ins_rom_2_1_mdr0_zero),
    .MDR1_read(ins_rom_2_1_mdr1_read), .MDR1_write(ins_rom_2_1_mdr1_write),
    .MDR1_zero(ins_rom_2_1_mdr1_zero), .MDR2_read(ins_rom_2_1_mdr2_read),
    .MDR2_write(ins_rom_2_1_mdr2_write), .MDR2_zero(ins_rom_2_1_mdr2_zero), .MEM_read(ins_rom_2_1_mem_read),
    .MEM_read2(ins_rom_2_1_mem_read2), .MEM_write(ins_rom_2_1_mem_write),
    .MDR0_MEM_IN(ins_rom_2_1_mdr0_mem_in), .MDR1_MEM_IN(ins_rom_2_1_mdr1_mem_in),
    .MDR2_MEM_IN(ins_rom_2_1_mdr2_mem_in), .MDR0_REG_IN(ins_rom_2_1_mdr0_reg_in),
    .MDR1_REG_IN(ins_rom_2_1_mdr1_reg_in), .MDR2_REG_IN(ins_rom_2_1_mdr2_reg_in),
    .MAR_REG_ID(ins_rom_2_1_mar_reg_id), .MDR0_REG_ID(ins_rom_2_1_mdr0_reg_id),
    .MDR1_REG_ID(ins_rom_2_1_mdr1_reg_id), .MDR2_REG_ID(ins_rom_2_1_mdr2_reg_id),
    .REG_OUT_MAR(ins_rom_2_1_reg_out_mar), .REG_OUT_MDR0(ins_rom_2_1_reg_out_mdr0),
    .REG_OUT_MDR1(ins_rom_2_1_reg_out_mdr1), .REG_OUT_MDR2(ins_rom_2_1_reg_out_mdr2),
    .REG_read(ins_rom_2_1_reg_read), .REG_write(ins_rom_2_1_reg_write), .MAR_MDR0(ins_rom_2_1_mar_mdr0),
    .MAR_MDR1(ins_rom_2_1_mar_mdr1), .MAR_MDR2(ins_rom_2_1_mar_mdr2), .MDR0_MAR(ins_rom_2_1_mdr0_mar),
    .MDR0_MDR1(ins_rom_2_1_mdr0_mdr1), .MDR0_MDR2(ins_rom_2_1_mdr0_mdr2), .MDR1_MAR(ins_rom_2_1_mdr1_mar),
    .MDR1_MDR0(ins_rom_2_1_mdr1_mdr0), .MDR1_MDR2(ins_rom_2_1_mdr1_mdr2), .MDR2_MAR(ins_rom_2_1_mdr2_mar),
    .MDR2_MDR0(ins_rom_2_1_mdr2_mdr0), .MDR2_MDR1(ins_rom_2_1_mdr2_mdr1),
    .MAR_ALU_IN0(ins_rom_2_1_mar_alu_in0), .MDR0_ALU_IN0(ins_rom_2_1_mdr0_alu_in0),
    .MDR1_ALU_IN0(ins_rom_2_1_mdr1_alu_in0), .MDR2_ALU_IN0(ins_rom_2_1_mdr2_alu_in0),
    .MAR_ALU_IN1(ins_rom_2_1_mar_alu_in1), .MDR0_ALU_IN1(ins_rom_2_1_mdr0_alu_in1),
    .MDR1_ALU_IN1(ins_rom_2_1_mdr1_alu_in1), .MDR2_ALU_IN1(ins_rom_2_1_mdr2_alu_in1),
    .ALU_SELECT(ins_rom_2_1_alu_select), .ALU_read(ins_rom_2_1_alu_read), .ALU_write(ins_rom_2_1_alu_write),
    .ALU_readFlags(ins_rom_2_1_alu_readflags), .ALU_OUT_MAR(ins_rom_2_1_alu_out_mar),
    .ALU_OUT_MDR0(ins_rom_2_1_alu_out_mdr0), .ALU_OUT_MDR1(ins_rom_2_1_alu_out_mdr1),
    .ALU_OUT_MDR2(ins_rom_2_1_alu_out_mdr2), .ALU_REMAINDER_MAR(ins_rom_2_1_alu_remainder_mar),
    .ALU_REMAINDER_MDR0(ins_rom_2_1_alu_remainder_mdr0), .ALU_REMAINDER_MDR1(ins_rom_2_1_alu_remainder_mdr1),
    .ALU_REMAINDER_MDR2(ins_rom_2_1_alu_remainder_mdr2), .CU_endInstruction(ins_rom_2_1_cu_endinstruction));
  INS_ROM_WEAVER ins_rom_weaver_2 (
    .in_1(ins_rom_weaver_1_ip_inc), .in_2(ins_rom_weaver_1_ip_read), .in_3(ins_rom_weaver_1_ip_write),
    .in_4(ins_rom_weaver_1_sp_inc), .in_5(ins_rom_weaver_1_sp_dec), .in_6(ins_rom_weaver_1_sp_read),
    .in_7(ins_rom_weaver_1_sp_write), .in_8(ins_rom_weaver_1_mar_read), .in_9(ins_rom_weaver_1_mar_write),
    .in_10(ins_rom_weaver_1_mdr0_read), .in_11(ins_rom_weaver_1_mdr0_write),
    .in_12(ins_rom_weaver_1_mdr0_zero), .in_13(ins_rom_weaver_1_mdr1_read),
    .in_14(ins_rom_weaver_1_mdr1_write), .in_15(ins_rom_weaver_1_mdr1_zero),
    .in_16(ins_rom_weaver_1_mdr2_read), .in_17(ins_rom_weaver_1_mdr2_write),
    .in_18(ins_rom_weaver_1_mdr2_zero), .in_19(ins_rom_weaver_1_mem_read),
    .in_20(ins_rom_weaver_1_mem_read2), .in_21(ins_rom_weaver_1_mem_write),
    .in_22(ins_rom_weaver_1_mdr0_mem_in), .in_23(ins_rom_weaver_1_mdr1_mem_in),
    .in_24(ins_rom_weaver_1_mdr2_mem_in), .in_25(ins_rom_weaver_1_mdr0_reg_in),
    .in_26(ins_rom_weaver_1_mdr1_reg_in), .in_27(ins_rom_weaver_1_mdr2_reg_in),
    .in_28(ins_rom_weaver_1_mar_reg_id), .in_29(ins_rom_weaver_1_mdr0_reg_id),
    .in_30(ins_rom_weaver_1_mdr1_reg_id), .in_31(ins_rom_weaver_1_mdr2_reg_id),
    .in_32(ins_rom_weaver_1_reg_out_mar), .in_33(ins_rom_weaver_1_reg_out_mdr0),
    .in_34(ins_rom_weaver_1_reg_out_mdr1), .in_35(ins_rom_weaver_1_reg_out_mdr2),
    .in_36(ins_rom_weaver_1_reg_read), .in_37(ins_rom_weaver_1_reg_write), .in_38(ins_rom_weaver_1_mar_mdr0),
    .in_39(ins_rom_weaver_1_mar_mdr1), .in_40(ins_rom_weaver_1_mar_mdr2), .in_41(ins_rom_weaver_1_mdr0_mar),
    .in_42(ins_rom_weaver_1_mdr0_mdr1), .in_43(ins_rom_weaver_1_mdr0_mdr2),
    .in_44(ins_rom_weaver_1_mdr1_mar), .in_45(ins_rom_weaver_1_mdr1_mdr0),
    .in_46(ins_rom_weaver_1_mdr1_mdr2), .in_47(ins_rom_weaver_1_mdr2_mar),
    .in_48(ins_rom_weaver_1_mdr2_mdr0), .in_49(ins_rom_weaver_1_mdr2_mdr1),
    .in_50(ins_rom_weaver_1_mar_alu_in0), .in_51(ins_rom_weaver_1_mdr0_alu_in0),
    .in_52(ins_rom_weaver_1_mdr1_alu_in0), .in_53(ins_rom_weaver_1_mdr2_alu_in0),
    .in_54(ins_rom_weaver_1_mar_alu_in1), .in_55(ins_rom_weaver_1_mdr0_alu_in1),
    .in_56(ins_rom_weaver_1_mdr1_alu_in1), .in_57(ins_rom_weaver_1_mdr2_alu_in1),
    .in_58(ins_rom_weaver_1_alu_select), .in_59(ins_rom_weaver_1_alu_read),
    .in_60(ins_rom_weaver_1_alu_write), .in_61(ins_rom_weaver_1_alu_readflags),
    .in_62(ins_rom_weaver_1_alu_out_mar), .in_63(ins_rom_weaver_1_alu_out_mdr0),
    .in_64(ins_rom_weaver_1_alu_out_mdr1), .in_65(ins_rom_weaver_1_alu_out_mdr2),
    .in_66(ins_rom_weaver_1_alu_remainder_mar), .in_67(ins_rom_weaver_1_alu_remainder_mdr0),
    .in_68(ins_rom_weaver_1_alu_remainder_mdr1), .in_69(ins_rom_weaver_1_alu_remainder_mdr2),
    .in_70(ins_rom_weaver_1_cu_endinstruction), .in_71(ins_rom_2_1_ip_inc), .in_72(ins_rom_2_1_ip_read),
    .in_73(ins_rom_2_1_ip_write), .in_74(ins_rom_2_1_sp_inc), .in_75(ins_rom_2_1_sp_dec),
    .in_76(ins_rom_2_1_sp_read), .in_77(ins_rom_2_1_sp_write), .in_78(ins_rom_2_1_mar_read),
    .in_79(ins_rom_2_1_mar_write), .in_80(ins_rom_2_1_mdr0_read), .in_81(ins_rom_2_1_mdr0_write),
    .in_82(ins_rom_2_1_mdr0_zero), .in_83(ins_rom_2_1_mdr1_read), .in_84(ins_rom_2_1_mdr1_write),
    .in_85(ins_rom_2_1_mdr1_zero), .in_86(ins_rom_2_1_mdr2_read), .in_87(ins_rom_2_1_mdr2_write),
    .in_88(ins_rom_2_1_mdr2_zero), .in_89(ins_rom_2_1_mem_read), .in_90(ins_rom_2_1_mem_read2),
    .in_91(ins_rom_2_1_mem_write), .in_92(ins_rom_2_1_mdr0_mem_in), .in_93(ins_rom_2_1_mdr1_mem_in),
    .in_94(ins_rom_2_1_mdr2_mem_in), .in_95(ins_rom_2_1_mdr0_reg_in), .in_96(ins_rom_2_1_mdr1_reg_in),
    .in_97(ins_rom_2_1_mdr2_reg_in), .in_98(ins_rom_2_1_mar_reg_id), .in_99(ins_rom_2_1_mdr0_reg_id),
    .in_100(ins_rom_2_1_mdr1_reg_id), .in_101(ins_rom_2_1_mdr2_reg_id), .in_102(ins_rom_2_1_reg_out_mar),
    .in_103(ins_rom_2_1_reg_out_mdr0), .in_104(ins_rom_2_1_reg_out_mdr1), .in_105(ins_rom_2_1_reg_out_mdr2),
    .in_106(ins_rom_2_1_reg_read), .in_107(ins_rom_2_1_reg_write), .in_108(ins_rom_2_1_mar_mdr0),
    .in_109(ins_rom_2_1_mar_mdr1), .in_110(ins_rom_2_1_mar_mdr2), .in_111(ins_rom_2_1_mdr0_mar),
    .in_112(ins_rom_2_1_mdr0_mdr1), .in_113(ins_rom_2_1_mdr0_mdr2), .in_114(ins_rom_2_1_mdr1_mar),
    .in_115(ins_rom_2_1_mdr1_mdr0), .in_116(ins_rom_2_1_mdr1_mdr2), .in_117(ins_rom_2_1_mdr2_mar),
    .in_118(ins_rom_2_1_mdr2_mdr0), .in_119(ins_rom_2_1_mdr2_mdr1), .in_120(ins_rom_2_1_mar_alu_in0),
    .in_121(ins_rom_2_1_mdr0_alu_in0), .in_122(ins_rom_2_1_mdr1_alu_in0), .in_123(ins_rom_2_1_mdr2_alu_in0),
    .in_124(ins_rom_2_1_mar_alu_in1), .in_125(ins_rom_2_1_mdr0_alu_in1), .in_126(ins_rom_2_1_mdr1_alu_in1),
    .in_127(ins_rom_2_1_mdr2_alu_in1), .in_128(ins_rom_2_1_alu_select), .in_129(ins_rom_2_1_alu_read),
    .in_130(ins_rom_2_1_alu_write), .in_131(ins_rom_2_1_alu_readflags), .in_132(ins_rom_2_1_alu_out_mar),
    .in_133(ins_rom_2_1_alu_out_mdr0), .in_134(ins_rom_2_1_alu_out_mdr1), .in_135(ins_rom_2_1_alu_out_mdr2),
    .in_136(ins_rom_2_1_alu_remainder_mar), .in_137(ins_rom_2_1_alu_remainder_mdr0),
    .in_138(ins_rom_2_1_alu_remainder_mdr1), .in_139(ins_rom_2_1_alu_remainder_mdr2),
    .in_140(ins_rom_2_1_cu_endinstruction), .IP_inc(ins_rom_weaver_2_ip_inc),
    .IP_read(ins_rom_weaver_2_ip_read), .IP_write(ins_rom_weaver_2_ip_write),
    .SP_inc(ins_rom_weaver_2_sp_inc), .SP_dec(ins_rom_weaver_2_sp_dec), .SP_read(ins_rom_weaver_2_sp_read),
    .SP_write(ins_rom_weaver_2_sp_write), .MAR_read(ins_rom_weaver_2_mar_read),
    .MAR_write(ins_rom_weaver_2_mar_write), .MDR0_read(ins_rom_weaver_2_mdr0_read),
    .MDR0_write(ins_rom_weaver_2_mdr0_write), .MDR0_zero(ins_rom_weaver_2_mdr0_zero),
    .MDR1_read(ins_rom_weaver_2_mdr1_read), .MDR1_write(ins_rom_weaver_2_mdr1_write),
    .MDR1_zero(ins_rom_weaver_2_mdr1_zero), .MDR2_read(ins_rom_weaver_2_mdr2_read),
    .MDR2_write(ins_rom_weaver_2_mdr2_write), .MDR2_zero(ins_rom_weaver_2_mdr2_zero),
    .MEM_read(ins_rom_weaver_2_mem_read), .MEM_read2(ins_rom_weaver_2_mem_read2),
    .MEM_write(ins_rom_weaver_2_mem_write), .MDR0_MEM_IN(ins_rom_weaver_2_mdr0_mem_in),
    .MDR1_MEM_IN(ins_rom_weaver_2_mdr1_mem_in), .MDR2_MEM_IN(ins_rom_weaver_2_mdr2_mem_in),
    .MDR0_REG_IN(ins_rom_weaver_2_mdr0_reg_in), .MDR1_REG_IN(ins_rom_weaver_2_mdr1_reg_in),
    .MDR2_REG_IN(ins_rom_weaver_2_mdr2_reg_in), .MAR_REG_ID(ins_rom_weaver_2_mar_reg_id),
    .MDR0_REG_ID(ins_rom_weaver_2_mdr0_reg_id), .MDR1_REG_ID(ins_rom_weaver_2_mdr1_reg_id),
    .MDR2_REG_ID(ins_rom_weaver_2_mdr2_reg_id), .REG_OUT_MAR(ins_rom_weaver_2_reg_out_mar),
    .REG_OUT_MDR0(ins_rom_weaver_2_reg_out_mdr0), .REG_OUT_MDR1(ins_rom_weaver_2_reg_out_mdr1),
    .REG_OUT_MDR2(ins_rom_weaver_2_reg_out_mdr2), .REG_read(ins_rom_weaver_2_reg_read),
    .REG_write(ins_rom_weaver_2_reg_write), .MAR_MDR0(ins_rom_weaver_2_mar_mdr0),
    .MAR_MDR1(ins_rom_weaver_2_mar_mdr1), .MAR_MDR2(ins_rom_weaver_2_mar_mdr2),
    .MDR0_MAR(ins_rom_weaver_2_mdr0_mar), .MDR0_MDR1(ins_rom_weaver_2_mdr0_mdr1),
    .MDR0_MDR2(ins_rom_weaver_2_mdr0_mdr2), .MDR1_MAR(ins_rom_weaver_2_mdr1_mar),
    .MDR1_MDR0(ins_rom_weaver_2_mdr1_mdr0), .MDR1_MDR2(ins_rom_weaver_2_mdr1_mdr2),
    .MDR2_MAR(ins_rom_weaver_2_mdr2_mar), .MDR2_MDR0(ins_rom_weaver_2_mdr2_mdr0),
    .MDR2_MDR1(ins_rom_weaver_2_mdr2_mdr1), .MAR_ALU_IN0(ins_rom_weaver_2_mar_alu_in0),
    .MDR0_ALU_IN0(ins_rom_weaver_2_mdr0_alu_in0), .MDR1_ALU_IN0(ins_rom_weaver_2_mdr1_alu_in0),
    .MDR2_ALU_IN0(ins_rom_weaver_2_mdr2_alu_in0), .MAR_ALU_IN1(ins_rom_weaver_2_mar_alu_in1),
    .MDR0_ALU_IN1(ins_rom_weaver_2_mdr0_alu_in1), .MDR1_ALU_IN1(ins_rom_weaver_2_mdr1_alu_in1),
    .MDR2_ALU_IN1(ins_rom_weaver_2_mdr2_alu_in1), .ALU_SELECT(ins_rom_weaver_2_alu_select),
    .ALU_read(ins_rom_weaver_2_alu_read), .ALU_write(ins_rom_weaver_2_alu_write),
    .ALU_readFlags(ins_rom_weaver_2_alu_readflags), .ALU_OUT_MAR(ins_rom_weaver_2_alu_out_mar),
    .ALU_OUT_MDR0(ins_rom_weaver_2_alu_out_mdr0), .ALU_OUT_MDR1(ins_rom_weaver_2_alu_out_mdr1),
    .ALU_OUT_MDR2(ins_rom_weaver_2_alu_out_mdr2), .ALU_REMAINDER_MAR(ins_rom_weaver_2_alu_remainder_mar),
    .ALU_REMAINDER_MDR0(ins_rom_weaver_2_alu_remainder_mdr0),
    .ALU_REMAINDER_MDR1(ins_rom_weaver_2_alu_remainder_mdr1),
    .ALU_REMAINDER_MDR2(ins_rom_weaver_2_alu_remainder_mdr2),
    .CU_endInstruction(ins_rom_weaver_2_cu_endinstruction));
  INS_ROM_3 ins_rom_3_1 (
    .in_1(Instruction), .CLK(demultiplexer_1_out3), .IP_inc(ins_rom_3_1_ip_inc),
    .IP_read(ins_rom_3_1_ip_read), .IP_write(ins_rom_3_1_ip_write), .SP_inc(ins_rom_3_1_sp_inc),
    .SP_dec(ins_rom_3_1_sp_dec), .SP_read(ins_rom_3_1_sp_read), .SP_write(ins_rom_3_1_sp_write),
    .MAR_read(ins_rom_3_1_mar_read), .MAR_write(ins_rom_3_1_mar_write), .MDR0_read(ins_rom_3_1_mdr0_read),
    .MDR0_write(ins_rom_3_1_mdr0_write), .MDR0_zero(ins_rom_3_1_mdr0_zero),
    .MDR1_read(ins_rom_3_1_mdr1_read), .MDR1_write(ins_rom_3_1_mdr1_write),
    .MDR1_zero(ins_rom_3_1_mdr1_zero), .MDR2_read(ins_rom_3_1_mdr2_read),
    .MDR2_write(ins_rom_3_1_mdr2_write), .MDR2_zero(ins_rom_3_1_mdr2_zero), .MEM_read(ins_rom_3_1_mem_read),
    .MEM_read2(ins_rom_3_1_mem_read2), .MEM_write(ins_rom_3_1_mem_write),
    .MDR0_MEM_IN(ins_rom_3_1_mdr0_mem_in), .MDR1_MEM_IN(ins_rom_3_1_mdr1_mem_in),
    .MDR2_MEM_IN(ins_rom_3_1_mdr2_mem_in), .MDR0_REG_IN(ins_rom_3_1_mdr0_reg_in),
    .MDR1_REG_IN(ins_rom_3_1_mdr1_reg_in), .MDR2_REG_IN(ins_rom_3_1_mdr2_reg_in),
    .MAR_REG_ID(ins_rom_3_1_mar_reg_id), .MDR0_REG_ID(ins_rom_3_1_mdr0_reg_id),
    .MDR1_REG_ID(ins_rom_3_1_mdr1_reg_id), .MDR2_REG_ID(ins_rom_3_1_mdr2_reg_id),
    .REG_OUT_MAR(ins_rom_3_1_reg_out_mar), .REG_OUT_MDR0(ins_rom_3_1_reg_out_mdr0),
    .REG_OUT_MDR1(ins_rom_3_1_reg_out_mdr1), .REG_OUT_MDR2(ins_rom_3_1_reg_out_mdr2),
    .REG_read(ins_rom_3_1_reg_read), .REG_write(ins_rom_3_1_reg_write), .MAR_MDR0(ins_rom_3_1_mar_mdr0),
    .MAR_MDR1(ins_rom_3_1_mar_mdr1), .MAR_MDR2(ins_rom_3_1_mar_mdr2), .MDR0_MAR(ins_rom_3_1_mdr0_mar),
    .MDR0_MDR1(ins_rom_3_1_mdr0_mdr1), .MDR0_MDR2(ins_rom_3_1_mdr0_mdr2), .MDR1_MAR(ins_rom_3_1_mdr1_mar),
    .MDR1_MDR0(ins_rom_3_1_mdr1_mdr0), .MDR1_MDR2(ins_rom_3_1_mdr1_mdr2), .MDR2_MAR(ins_rom_3_1_mdr2_mar),
    .MDR2_MDR0(ins_rom_3_1_mdr2_mdr0), .MDR2_MDR1(ins_rom_3_1_mdr2_mdr1),
    .MAR_ALU_IN0(ins_rom_3_1_mar_alu_in0), .MDR0_ALU_IN0(ins_rom_3_1_mdr0_alu_in0),
    .MDR1_ALU_IN0(ins_rom_3_1_mdr1_alu_in0), .MDR2_ALU_IN0(ins_rom_3_1_mdr2_alu_in0),
    .MAR_ALU_IN1(ins_rom_3_1_mar_alu_in1), .MDR0_ALU_IN1(ins_rom_3_1_mdr0_alu_in1),
    .MDR1_ALU_IN1(ins_rom_3_1_mdr1_alu_in1), .MDR2_ALU_IN1(ins_rom_3_1_mdr2_alu_in1),
    .ALU_SELECT(ins_rom_3_1_alu_select), .ALU_read(ins_rom_3_1_alu_read), .ALU_write(ins_rom_3_1_alu_write),
    .ALU_readFlags(ins_rom_3_1_alu_readflags), .ALU_OUT_MAR(ins_rom_3_1_alu_out_mar),
    .ALU_OUT_MDR0(ins_rom_3_1_alu_out_mdr0), .ALU_OUT_MDR1(ins_rom_3_1_alu_out_mdr1),
    .ALU_OUT_MDR2(ins_rom_3_1_alu_out_mdr2), .ALU_REMAINDER_MAR(ins_rom_3_1_alu_remainder_mar),
    .ALU_REMAINDER_MDR0(ins_rom_3_1_alu_remainder_mdr0), .ALU_REMAINDER_MDR1(ins_rom_3_1_alu_remainder_mdr1),
    .ALU_REMAINDER_MDR2(ins_rom_3_1_alu_remainder_mdr2), .CU_endInstruction(ins_rom_3_1_cu_endinstruction));
  INS_ROM_WEAVER ins_rom_weaver_3 (
    .in_1(ins_rom_weaver_2_ip_inc), .in_2(ins_rom_weaver_2_ip_read), .in_3(ins_rom_weaver_2_ip_write),
    .in_4(ins_rom_weaver_2_sp_inc), .in_5(ins_rom_weaver_2_sp_dec), .in_6(ins_rom_weaver_2_sp_read),
    .in_7(ins_rom_weaver_2_sp_write), .in_8(ins_rom_weaver_2_mar_read), .in_9(ins_rom_weaver_2_mar_write),
    .in_10(ins_rom_weaver_2_mdr0_read), .in_11(ins_rom_weaver_2_mdr0_write),
    .in_12(ins_rom_weaver_2_mdr0_zero), .in_13(ins_rom_weaver_2_mdr1_read),
    .in_14(ins_rom_weaver_2_mdr1_write), .in_15(ins_rom_weaver_2_mdr1_zero),
    .in_16(ins_rom_weaver_2_mdr2_read), .in_17(ins_rom_weaver_2_mdr2_write),
    .in_18(ins_rom_weaver_2_mdr2_zero), .in_19(ins_rom_weaver_2_mem_read),
    .in_20(ins_rom_weaver_2_mem_read2), .in_21(ins_rom_weaver_2_mem_write),
    .in_22(ins_rom_weaver_2_mdr0_mem_in), .in_23(ins_rom_weaver_2_mdr1_mem_in),
    .in_24(ins_rom_weaver_2_mdr2_mem_in), .in_25(ins_rom_weaver_2_mdr0_reg_in),
    .in_26(ins_rom_weaver_2_mdr1_reg_in), .in_27(ins_rom_weaver_2_mdr2_reg_in),
    .in_28(ins_rom_weaver_2_mar_reg_id), .in_29(ins_rom_weaver_2_mdr0_reg_id),
    .in_30(ins_rom_weaver_2_mdr1_reg_id), .in_31(ins_rom_weaver_2_mdr2_reg_id),
    .in_32(ins_rom_weaver_2_reg_out_mar), .in_33(ins_rom_weaver_2_reg_out_mdr0),
    .in_34(ins_rom_weaver_2_reg_out_mdr1), .in_35(ins_rom_weaver_2_reg_out_mdr2),
    .in_36(ins_rom_weaver_2_reg_read), .in_37(ins_rom_weaver_2_reg_write), .in_38(ins_rom_weaver_2_mar_mdr0),
    .in_39(ins_rom_weaver_2_mar_mdr1), .in_40(ins_rom_weaver_2_mar_mdr2), .in_41(ins_rom_weaver_2_mdr0_mar),
    .in_42(ins_rom_weaver_2_mdr0_mdr1), .in_43(ins_rom_weaver_2_mdr0_mdr2),
    .in_44(ins_rom_weaver_2_mdr1_mar), .in_45(ins_rom_weaver_2_mdr1_mdr0),
    .in_46(ins_rom_weaver_2_mdr1_mdr2), .in_47(ins_rom_weaver_2_mdr2_mar),
    .in_48(ins_rom_weaver_2_mdr2_mdr0), .in_49(ins_rom_weaver_2_mdr2_mdr1),
    .in_50(ins_rom_weaver_2_mar_alu_in0), .in_51(ins_rom_weaver_2_mdr0_alu_in0),
    .in_52(ins_rom_weaver_2_mdr1_alu_in0), .in_53(ins_rom_weaver_2_mdr2_alu_in0),
    .in_54(ins_rom_weaver_2_mar_alu_in1), .in_55(ins_rom_weaver_2_mdr0_alu_in1),
    .in_56(ins_rom_weaver_2_mdr1_alu_in1), .in_57(ins_rom_weaver_2_mdr2_alu_in1),
    .in_58(ins_rom_weaver_2_alu_select), .in_59(ins_rom_weaver_2_alu_read),
    .in_60(ins_rom_weaver_2_alu_write), .in_61(ins_rom_weaver_2_alu_readflags),
    .in_62(ins_rom_weaver_2_alu_out_mar), .in_63(ins_rom_weaver_2_alu_out_mdr0),
    .in_64(ins_rom_weaver_2_alu_out_mdr1), .in_65(ins_rom_weaver_2_alu_out_mdr2),
    .in_66(ins_rom_weaver_2_alu_remainder_mar), .in_67(ins_rom_weaver_2_alu_remainder_mdr0),
    .in_68(ins_rom_weaver_2_alu_remainder_mdr1), .in_69(ins_rom_weaver_2_alu_remainder_mdr2),
    .in_70(ins_rom_weaver_2_cu_endinstruction), .in_71(ins_rom_3_1_ip_inc), .in_72(ins_rom_3_1_ip_read),
    .in_73(ins_rom_3_1_ip_write), .in_74(ins_rom_3_1_sp_inc), .in_75(ins_rom_3_1_sp_dec),
    .in_76(ins_rom_3_1_sp_read), .in_77(ins_rom_3_1_sp_write), .in_78(ins_rom_3_1_mar_read),
    .in_79(ins_rom_3_1_mar_write), .in_80(ins_rom_3_1_mdr0_read), .in_81(ins_rom_3_1_mdr0_write),
    .in_82(ins_rom_3_1_mdr0_zero), .in_83(ins_rom_3_1_mdr1_read), .in_84(ins_rom_3_1_mdr1_write),
    .in_85(ins_rom_3_1_mdr1_zero), .in_86(ins_rom_3_1_mdr2_read), .in_87(ins_rom_3_1_mdr2_write),
    .in_88(ins_rom_3_1_mdr2_zero), .in_89(ins_rom_3_1_mem_read), .in_90(ins_rom_3_1_mem_read2),
    .in_91(ins_rom_3_1_mem_write), .in_92(ins_rom_3_1_mdr0_mem_in), .in_93(ins_rom_3_1_mdr1_mem_in),
    .in_94(ins_rom_3_1_mdr2_mem_in), .in_95(ins_rom_3_1_mdr0_reg_in), .in_96(ins_rom_3_1_mdr1_reg_in),
    .in_97(ins_rom_3_1_mdr2_reg_in), .in_98(ins_rom_3_1_mar_reg_id), .in_99(ins_rom_3_1_mdr0_reg_id),
    .in_100(ins_rom_3_1_mdr1_reg_id), .in_101(ins_rom_3_1_mdr2_reg_id), .in_102(ins_rom_3_1_reg_out_mar),
    .in_103(ins_rom_3_1_reg_out_mdr0), .in_104(ins_rom_3_1_reg_out_mdr1), .in_105(ins_rom_3_1_reg_out_mdr2),
    .in_106(ins_rom_3_1_reg_read), .in_107(ins_rom_3_1_reg_write), .in_108(ins_rom_3_1_mar_mdr0),
    .in_109(ins_rom_3_1_mar_mdr1), .in_110(ins_rom_3_1_mar_mdr2), .in_111(ins_rom_3_1_mdr0_mar),
    .in_112(ins_rom_3_1_mdr0_mdr1), .in_113(ins_rom_3_1_mdr0_mdr2), .in_114(ins_rom_3_1_mdr1_mar),
    .in_115(ins_rom_3_1_mdr1_mdr0), .in_116(ins_rom_3_1_mdr1_mdr2), .in_117(ins_rom_3_1_mdr2_mar),
    .in_118(ins_rom_3_1_mdr2_mdr0), .in_119(ins_rom_3_1_mdr2_mdr1), .in_120(ins_rom_3_1_mar_alu_in0),
    .in_121(ins_rom_3_1_mdr0_alu_in0), .in_122(ins_rom_3_1_mdr1_alu_in0), .in_123(ins_rom_3_1_mdr2_alu_in0),
    .in_124(ins_rom_3_1_mar_alu_in1), .in_125(ins_rom_3_1_mdr0_alu_in1), .in_126(ins_rom_3_1_mdr1_alu_in1),
    .in_127(ins_rom_3_1_mdr2_alu_in1), .in_128(ins_rom_3_1_alu_select), .in_129(ins_rom_3_1_alu_read),
    .in_130(ins_rom_3_1_alu_write), .in_131(ins_rom_3_1_alu_readflags), .in_132(ins_rom_3_1_alu_out_mar),
    .in_133(ins_rom_3_1_alu_out_mdr0), .in_134(ins_rom_3_1_alu_out_mdr1), .in_135(ins_rom_3_1_alu_out_mdr2),
    .in_136(ins_rom_3_1_alu_remainder_mar), .in_137(ins_rom_3_1_alu_remainder_mdr0),
    .in_138(ins_rom_3_1_alu_remainder_mdr1), .in_139(ins_rom_3_1_alu_remainder_mdr2),
    .in_140(ins_rom_3_1_cu_endinstruction), .IP_inc(ins_rom_weaver_3_ip_inc),
    .IP_read(ins_rom_weaver_3_ip_read), .IP_write(ins_rom_weaver_3_ip_write),
    .SP_inc(ins_rom_weaver_3_sp_inc), .SP_dec(ins_rom_weaver_3_sp_dec), .SP_read(ins_rom_weaver_3_sp_read),
    .SP_write(ins_rom_weaver_3_sp_write), .MAR_read(ins_rom_weaver_3_mar_read),
    .MAR_write(ins_rom_weaver_3_mar_write), .MDR0_read(ins_rom_weaver_3_mdr0_read),
    .MDR0_write(ins_rom_weaver_3_mdr0_write), .MDR0_zero(ins_rom_weaver_3_mdr0_zero),
    .MDR1_read(ins_rom_weaver_3_mdr1_read), .MDR1_write(ins_rom_weaver_3_mdr1_write),
    .MDR1_zero(ins_rom_weaver_3_mdr1_zero), .MDR2_read(ins_rom_weaver_3_mdr2_read),
    .MDR2_write(ins_rom_weaver_3_mdr2_write), .MDR2_zero(ins_rom_weaver_3_mdr2_zero),
    .MEM_read(ins_rom_weaver_3_mem_read), .MEM_read2(ins_rom_weaver_3_mem_read2),
    .MEM_write(ins_rom_weaver_3_mem_write), .MDR0_MEM_IN(ins_rom_weaver_3_mdr0_mem_in),
    .MDR1_MEM_IN(ins_rom_weaver_3_mdr1_mem_in), .MDR2_MEM_IN(ins_rom_weaver_3_mdr2_mem_in),
    .MDR0_REG_IN(ins_rom_weaver_3_mdr0_reg_in), .MDR1_REG_IN(ins_rom_weaver_3_mdr1_reg_in),
    .MDR2_REG_IN(ins_rom_weaver_3_mdr2_reg_in), .MAR_REG_ID(ins_rom_weaver_3_mar_reg_id),
    .MDR0_REG_ID(ins_rom_weaver_3_mdr0_reg_id), .MDR1_REG_ID(ins_rom_weaver_3_mdr1_reg_id),
    .MDR2_REG_ID(ins_rom_weaver_3_mdr2_reg_id), .REG_OUT_MAR(ins_rom_weaver_3_reg_out_mar),
    .REG_OUT_MDR0(ins_rom_weaver_3_reg_out_mdr0), .REG_OUT_MDR1(ins_rom_weaver_3_reg_out_mdr1),
    .REG_OUT_MDR2(ins_rom_weaver_3_reg_out_mdr2), .REG_read(ins_rom_weaver_3_reg_read),
    .REG_write(ins_rom_weaver_3_reg_write), .MAR_MDR0(ins_rom_weaver_3_mar_mdr0),
    .MAR_MDR1(ins_rom_weaver_3_mar_mdr1), .MAR_MDR2(ins_rom_weaver_3_mar_mdr2),
    .MDR0_MAR(ins_rom_weaver_3_mdr0_mar), .MDR0_MDR1(ins_rom_weaver_3_mdr0_mdr1),
    .MDR0_MDR2(ins_rom_weaver_3_mdr0_mdr2), .MDR1_MAR(ins_rom_weaver_3_mdr1_mar),
    .MDR1_MDR0(ins_rom_weaver_3_mdr1_mdr0), .MDR1_MDR2(ins_rom_weaver_3_mdr1_mdr2),
    .MDR2_MAR(ins_rom_weaver_3_mdr2_mar), .MDR2_MDR0(ins_rom_weaver_3_mdr2_mdr0),
    .MDR2_MDR1(ins_rom_weaver_3_mdr2_mdr1), .MAR_ALU_IN0(ins_rom_weaver_3_mar_alu_in0),
    .MDR0_ALU_IN0(ins_rom_weaver_3_mdr0_alu_in0), .MDR1_ALU_IN0(ins_rom_weaver_3_mdr1_alu_in0),
    .MDR2_ALU_IN0(ins_rom_weaver_3_mdr2_alu_in0), .MAR_ALU_IN1(ins_rom_weaver_3_mar_alu_in1),
    .MDR0_ALU_IN1(ins_rom_weaver_3_mdr0_alu_in1), .MDR1_ALU_IN1(ins_rom_weaver_3_mdr1_alu_in1),
    .MDR2_ALU_IN1(ins_rom_weaver_3_mdr2_alu_in1), .ALU_SELECT(ins_rom_weaver_3_alu_select),
    .ALU_read(ins_rom_weaver_3_alu_read), .ALU_write(ins_rom_weaver_3_alu_write),
    .ALU_readFlags(ins_rom_weaver_3_alu_readflags), .ALU_OUT_MAR(ins_rom_weaver_3_alu_out_mar),
    .ALU_OUT_MDR0(ins_rom_weaver_3_alu_out_mdr0), .ALU_OUT_MDR1(ins_rom_weaver_3_alu_out_mdr1),
    .ALU_OUT_MDR2(ins_rom_weaver_3_alu_out_mdr2), .ALU_REMAINDER_MAR(ins_rom_weaver_3_alu_remainder_mar),
    .ALU_REMAINDER_MDR0(ins_rom_weaver_3_alu_remainder_mdr0),
    .ALU_REMAINDER_MDR1(ins_rom_weaver_3_alu_remainder_mdr1),
    .ALU_REMAINDER_MDR2(ins_rom_weaver_3_alu_remainder_mdr2),
    .CU_endInstruction(ins_rom_weaver_3_cu_endinstruction));
  INS_ROM_4 ins_rom_4_1 (
    .in_1(Instruction), .CLK(demultiplexer_1_out4), .IP_inc(ins_rom_4_1_ip_inc),
    .IP_read(ins_rom_4_1_ip_read), .IP_write(ins_rom_4_1_ip_write), .SP_inc(ins_rom_4_1_sp_inc),
    .SP_dec(ins_rom_4_1_sp_dec), .SP_read(ins_rom_4_1_sp_read), .SP_write(ins_rom_4_1_sp_write),
    .MAR_read(ins_rom_4_1_mar_read), .MAR_write(ins_rom_4_1_mar_write), .MDR0_read(ins_rom_4_1_mdr0_read),
    .MDR0_write(ins_rom_4_1_mdr0_write), .MDR0_zero(ins_rom_4_1_mdr0_zero),
    .MDR1_read(ins_rom_4_1_mdr1_read), .MDR1_write(ins_rom_4_1_mdr1_write),
    .MDR1_zero(ins_rom_4_1_mdr1_zero), .MDR2_read(ins_rom_4_1_mdr2_read),
    .MDR2_write(ins_rom_4_1_mdr2_write), .MDR2_zero(ins_rom_4_1_mdr2_zero), .MEM_read(ins_rom_4_1_mem_read),
    .MEM_read2(ins_rom_4_1_mem_read2), .MEM_write(ins_rom_4_1_mem_write),
    .MDR0_MEM_IN(ins_rom_4_1_mdr0_mem_in), .MDR1_MEM_IN(ins_rom_4_1_mdr1_mem_in),
    .MDR2_MEM_IN(ins_rom_4_1_mdr2_mem_in), .MDR0_REG_IN(ins_rom_4_1_mdr0_reg_in),
    .MDR1_REG_IN(ins_rom_4_1_mdr1_reg_in), .MDR2_REG_IN(ins_rom_4_1_mdr2_reg_in),
    .MAR_REG_ID(ins_rom_4_1_mar_reg_id), .MDR0_REG_ID(ins_rom_4_1_mdr0_reg_id),
    .MDR1_REG_ID(ins_rom_4_1_mdr1_reg_id), .MDR2_REG_ID(ins_rom_4_1_mdr2_reg_id),
    .REG_OUT_MAR(ins_rom_4_1_reg_out_mar), .REG_OUT_MDR0(ins_rom_4_1_reg_out_mdr0),
    .REG_OUT_MDR1(ins_rom_4_1_reg_out_mdr1), .REG_OUT_MDR2(ins_rom_4_1_reg_out_mdr2),
    .REG_read(ins_rom_4_1_reg_read), .REG_write(ins_rom_4_1_reg_write), .MAR_MDR0(ins_rom_4_1_mar_mdr0),
    .MAR_MDR1(ins_rom_4_1_mar_mdr1), .MAR_MDR2(ins_rom_4_1_mar_mdr2), .MDR0_MAR(ins_rom_4_1_mdr0_mar),
    .MDR0_MDR1(ins_rom_4_1_mdr0_mdr1), .MDR0_MDR2(ins_rom_4_1_mdr0_mdr2), .MDR1_MAR(ins_rom_4_1_mdr1_mar),
    .MDR1_MDR0(ins_rom_4_1_mdr1_mdr0), .MDR1_MDR2(ins_rom_4_1_mdr1_mdr2), .MDR2_MAR(ins_rom_4_1_mdr2_mar),
    .MDR2_MDR0(ins_rom_4_1_mdr2_mdr0), .MDR2_MDR1(ins_rom_4_1_mdr2_mdr1),
    .MAR_ALU_IN0(ins_rom_4_1_mar_alu_in0), .MDR0_ALU_IN0(ins_rom_4_1_mdr0_alu_in0),
    .MDR1_ALU_IN0(ins_rom_4_1_mdr1_alu_in0), .MDR2_ALU_IN0(ins_rom_4_1_mdr2_alu_in0),
    .MAR_ALU_IN1(ins_rom_4_1_mar_alu_in1), .MDR0_ALU_IN1(ins_rom_4_1_mdr0_alu_in1),
    .MDR1_ALU_IN1(ins_rom_4_1_mdr1_alu_in1), .MDR2_ALU_IN1(ins_rom_4_1_mdr2_alu_in1),
    .ALU_SELECT(ins_rom_4_1_alu_select), .ALU_read(ins_rom_4_1_alu_read), .ALU_write(ins_rom_4_1_alu_write),
    .ALU_readFlags(ins_rom_4_1_alu_readflags), .ALU_OUT_MAR(ins_rom_4_1_alu_out_mar),
    .ALU_OUT_MDR0(ins_rom_4_1_alu_out_mdr0), .ALU_OUT_MDR1(ins_rom_4_1_alu_out_mdr1),
    .ALU_OUT_MDR2(ins_rom_4_1_alu_out_mdr2), .ALU_REMAINDER_MAR(ins_rom_4_1_alu_remainder_mar),
    .ALU_REMAINDER_MDR0(ins_rom_4_1_alu_remainder_mdr0), .ALU_REMAINDER_MDR1(ins_rom_4_1_alu_remainder_mdr1),
    .ALU_REMAINDER_MDR2(ins_rom_4_1_alu_remainder_mdr2), .CU_endInstruction(ins_rom_4_1_cu_endinstruction));
  INS_ROM_WEAVER ins_rom_weaver_4 (
    .in_1(ins_rom_weaver_3_ip_inc), .in_2(ins_rom_weaver_3_ip_read), .in_3(ins_rom_weaver_3_ip_write),
    .in_4(ins_rom_weaver_3_sp_inc), .in_5(ins_rom_weaver_3_sp_dec), .in_6(ins_rom_weaver_3_sp_read),
    .in_7(ins_rom_weaver_3_sp_write), .in_8(ins_rom_weaver_3_mar_read), .in_9(ins_rom_weaver_3_mar_write),
    .in_10(ins_rom_weaver_3_mdr0_read), .in_11(ins_rom_weaver_3_mdr0_write),
    .in_12(ins_rom_weaver_3_mdr0_zero), .in_13(ins_rom_weaver_3_mdr1_read),
    .in_14(ins_rom_weaver_3_mdr1_write), .in_15(ins_rom_weaver_3_mdr1_zero),
    .in_16(ins_rom_weaver_3_mdr2_read), .in_17(ins_rom_weaver_3_mdr2_write),
    .in_18(ins_rom_weaver_3_mdr2_zero), .in_19(ins_rom_weaver_3_mem_read),
    .in_20(ins_rom_weaver_3_mem_read2), .in_21(ins_rom_weaver_3_mem_write),
    .in_22(ins_rom_weaver_3_mdr0_mem_in), .in_23(ins_rom_weaver_3_mdr1_mem_in),
    .in_24(ins_rom_weaver_3_mdr2_mem_in), .in_25(ins_rom_weaver_3_mdr0_reg_in),
    .in_26(ins_rom_weaver_3_mdr1_reg_in), .in_27(ins_rom_weaver_3_mdr2_reg_in),
    .in_28(ins_rom_weaver_3_mar_reg_id), .in_29(ins_rom_weaver_3_mdr0_reg_id),
    .in_30(ins_rom_weaver_3_mdr1_reg_id), .in_31(ins_rom_weaver_3_mdr2_reg_id),
    .in_32(ins_rom_weaver_3_reg_out_mar), .in_33(ins_rom_weaver_3_reg_out_mdr0),
    .in_34(ins_rom_weaver_3_reg_out_mdr1), .in_35(ins_rom_weaver_3_reg_out_mdr2),
    .in_36(ins_rom_weaver_3_reg_read), .in_37(ins_rom_weaver_3_reg_write), .in_38(ins_rom_weaver_3_mar_mdr0),
    .in_39(ins_rom_weaver_3_mar_mdr1), .in_40(ins_rom_weaver_3_mar_mdr2), .in_41(ins_rom_weaver_3_mdr0_mar),
    .in_42(ins_rom_weaver_3_mdr0_mdr1), .in_43(ins_rom_weaver_3_mdr0_mdr2),
    .in_44(ins_rom_weaver_3_mdr1_mar), .in_45(ins_rom_weaver_3_mdr1_mdr0),
    .in_46(ins_rom_weaver_3_mdr1_mdr2), .in_47(ins_rom_weaver_3_mdr2_mar),
    .in_48(ins_rom_weaver_3_mdr2_mdr0), .in_49(ins_rom_weaver_3_mdr2_mdr1),
    .in_50(ins_rom_weaver_3_mar_alu_in0), .in_51(ins_rom_weaver_3_mdr0_alu_in0),
    .in_52(ins_rom_weaver_3_mdr1_alu_in0), .in_53(ins_rom_weaver_3_mdr2_alu_in0),
    .in_54(ins_rom_weaver_3_mar_alu_in1), .in_55(ins_rom_weaver_3_mdr0_alu_in1),
    .in_56(ins_rom_weaver_3_mdr1_alu_in1), .in_57(ins_rom_weaver_3_mdr2_alu_in1),
    .in_58(ins_rom_weaver_3_alu_select), .in_59(ins_rom_weaver_3_alu_read),
    .in_60(ins_rom_weaver_3_alu_write), .in_61(ins_rom_weaver_3_alu_readflags),
    .in_62(ins_rom_weaver_3_alu_out_mar), .in_63(ins_rom_weaver_3_alu_out_mdr0),
    .in_64(ins_rom_weaver_3_alu_out_mdr1), .in_65(ins_rom_weaver_3_alu_out_mdr2),
    .in_66(ins_rom_weaver_3_alu_remainder_mar), .in_67(ins_rom_weaver_3_alu_remainder_mdr0),
    .in_68(ins_rom_weaver_3_alu_remainder_mdr1), .in_69(ins_rom_weaver_3_alu_remainder_mdr2),
    .in_70(ins_rom_weaver_3_cu_endinstruction), .in_71(ins_rom_4_1_ip_inc), .in_72(ins_rom_4_1_ip_read),
    .in_73(ins_rom_4_1_ip_write), .in_74(ins_rom_4_1_sp_inc), .in_75(ins_rom_4_1_sp_dec),
    .in_76(ins_rom_4_1_sp_read), .in_77(ins_rom_4_1_sp_write), .in_78(ins_rom_4_1_mar_read),
    .in_79(ins_rom_4_1_mar_write), .in_80(ins_rom_4_1_mdr0_read), .in_81(ins_rom_4_1_mdr0_write),
    .in_82(ins_rom_4_1_mdr0_zero), .in_83(ins_rom_4_1_mdr1_read), .in_84(ins_rom_4_1_mdr1_write),
    .in_85(ins_rom_4_1_mdr1_zero), .in_86(ins_rom_4_1_mdr2_read), .in_87(ins_rom_4_1_mdr2_write),
    .in_88(ins_rom_4_1_mdr2_zero), .in_89(ins_rom_4_1_mem_read), .in_90(ins_rom_4_1_mem_read2),
    .in_91(ins_rom_4_1_mem_write), .in_92(ins_rom_4_1_mdr0_mem_in), .in_93(ins_rom_4_1_mdr1_mem_in),
    .in_94(ins_rom_4_1_mdr2_mem_in), .in_95(ins_rom_4_1_mdr0_reg_in), .in_96(ins_rom_4_1_mdr1_reg_in),
    .in_97(ins_rom_4_1_mdr2_reg_in), .in_98(ins_rom_4_1_mar_reg_id), .in_99(ins_rom_4_1_mdr0_reg_id),
    .in_100(ins_rom_4_1_mdr1_reg_id), .in_101(ins_rom_4_1_mdr2_reg_id), .in_102(ins_rom_4_1_reg_out_mar),
    .in_103(ins_rom_4_1_reg_out_mdr0), .in_104(ins_rom_4_1_reg_out_mdr1), .in_105(ins_rom_4_1_reg_out_mdr2),
    .in_106(ins_rom_4_1_reg_read), .in_107(ins_rom_4_1_reg_write), .in_108(ins_rom_4_1_mar_mdr0),
    .in_109(ins_rom_4_1_mar_mdr1), .in_110(ins_rom_4_1_mar_mdr2), .in_111(ins_rom_4_1_mdr0_mar),
    .in_112(ins_rom_4_1_mdr0_mdr1), .in_113(ins_rom_4_1_mdr0_mdr2), .in_114(ins_rom_4_1_mdr1_mar),
    .in_115(ins_rom_4_1_mdr1_mdr0), .in_116(ins_rom_4_1_mdr1_mdr2), .in_117(ins_rom_4_1_mdr2_mar),
    .in_118(ins_rom_4_1_mdr2_mdr0), .in_119(ins_rom_4_1_mdr2_mdr1), .in_120(ins_rom_4_1_mar_alu_in0),
    .in_121(ins_rom_4_1_mdr0_alu_in0), .in_122(ins_rom_4_1_mdr1_alu_in0), .in_123(ins_rom_4_1_mdr2_alu_in0),
    .in_124(ins_rom_4_1_mar_alu_in1), .in_125(ins_rom_4_1_mdr0_alu_in1), .in_126(ins_rom_4_1_mdr1_alu_in1),
    .in_127(ins_rom_4_1_mdr2_alu_in1), .in_128(ins_rom_4_1_alu_select), .in_129(ins_rom_4_1_alu_read),
    .in_130(ins_rom_4_1_alu_write), .in_131(ins_rom_4_1_alu_readflags), .in_132(ins_rom_4_1_alu_out_mar),
    .in_133(ins_rom_4_1_alu_out_mdr0), .in_134(ins_rom_4_1_alu_out_mdr1), .in_135(ins_rom_4_1_alu_out_mdr2),
    .in_136(ins_rom_4_1_alu_remainder_mar), .in_137(ins_rom_4_1_alu_remainder_mdr0),
    .in_138(ins_rom_4_1_alu_remainder_mdr1), .in_139(ins_rom_4_1_alu_remainder_mdr2),
    .in_140(ins_rom_4_1_cu_endinstruction), .IP_inc(ins_rom_weaver_4_ip_inc),
    .IP_read(ins_rom_weaver_4_ip_read), .IP_write(ins_rom_weaver_4_ip_write),
    .SP_inc(ins_rom_weaver_4_sp_inc), .SP_dec(ins_rom_weaver_4_sp_dec), .SP_read(ins_rom_weaver_4_sp_read),
    .SP_write(ins_rom_weaver_4_sp_write), .MAR_read(ins_rom_weaver_4_mar_read),
    .MAR_write(ins_rom_weaver_4_mar_write), .MDR0_read(ins_rom_weaver_4_mdr0_read),
    .MDR0_write(ins_rom_weaver_4_mdr0_write), .MDR0_zero(ins_rom_weaver_4_mdr0_zero),
    .MDR1_read(ins_rom_weaver_4_mdr1_read), .MDR1_write(ins_rom_weaver_4_mdr1_write),
    .MDR1_zero(ins_rom_weaver_4_mdr1_zero), .MDR2_read(ins_rom_weaver_4_mdr2_read),
    .MDR2_write(ins_rom_weaver_4_mdr2_write), .MDR2_zero(ins_rom_weaver_4_mdr2_zero),
    .MEM_read(ins_rom_weaver_4_mem_read), .MEM_read2(ins_rom_weaver_4_mem_read2),
    .MEM_write(ins_rom_weaver_4_mem_write), .MDR0_MEM_IN(ins_rom_weaver_4_mdr0_mem_in),
    .MDR1_MEM_IN(ins_rom_weaver_4_mdr1_mem_in), .MDR2_MEM_IN(ins_rom_weaver_4_mdr2_mem_in),
    .MDR0_REG_IN(ins_rom_weaver_4_mdr0_reg_in), .MDR1_REG_IN(ins_rom_weaver_4_mdr1_reg_in),
    .MDR2_REG_IN(ins_rom_weaver_4_mdr2_reg_in), .MAR_REG_ID(ins_rom_weaver_4_mar_reg_id),
    .MDR0_REG_ID(ins_rom_weaver_4_mdr0_reg_id), .MDR1_REG_ID(ins_rom_weaver_4_mdr1_reg_id),
    .MDR2_REG_ID(ins_rom_weaver_4_mdr2_reg_id), .REG_OUT_MAR(ins_rom_weaver_4_reg_out_mar),
    .REG_OUT_MDR0(ins_rom_weaver_4_reg_out_mdr0), .REG_OUT_MDR1(ins_rom_weaver_4_reg_out_mdr1),
    .REG_OUT_MDR2(ins_rom_weaver_4_reg_out_mdr2), .REG_read(ins_rom_weaver_4_reg_read),
    .REG_write(ins_rom_weaver_4_reg_write), .MAR_MDR0(ins_rom_weaver_4_mar_mdr0),
    .MAR_MDR1(ins_rom_weaver_4_mar_mdr1), .MAR_MDR2(ins_rom_weaver_4_mar_mdr2),
    .MDR0_MAR(ins_rom_weaver_4_mdr0_mar), .MDR0_MDR1(ins_rom_weaver_4_mdr0_mdr1),
    .MDR0_MDR2(ins_rom_weaver_4_mdr0_mdr2), .MDR1_MAR(ins_rom_weaver_4_mdr1_mar),
    .MDR1_MDR0(ins_rom_weaver_4_mdr1_mdr0), .MDR1_MDR2(ins_rom_weaver_4_mdr1_mdr2),
    .MDR2_MAR(ins_rom_weaver_4_mdr2_mar), .MDR2_MDR0(ins_rom_weaver_4_mdr2_mdr0),
    .MDR2_MDR1(ins_rom_weaver_4_mdr2_mdr1), .MAR_ALU_IN0(ins_rom_weaver_4_mar_alu_in0),
    .MDR0_ALU_IN0(ins_rom_weaver_4_mdr0_alu_in0), .MDR1_ALU_IN0(ins_rom_weaver_4_mdr1_alu_in0),
    .MDR2_ALU_IN0(ins_rom_weaver_4_mdr2_alu_in0), .MAR_ALU_IN1(ins_rom_weaver_4_mar_alu_in1),
    .MDR0_ALU_IN1(ins_rom_weaver_4_mdr0_alu_in1), .MDR1_ALU_IN1(ins_rom_weaver_4_mdr1_alu_in1),
    .MDR2_ALU_IN1(ins_rom_weaver_4_mdr2_alu_in1), .ALU_SELECT(ins_rom_weaver_4_alu_select),
    .ALU_read(ins_rom_weaver_4_alu_read), .ALU_write(ins_rom_weaver_4_alu_write),
    .ALU_readFlags(ins_rom_weaver_4_alu_readflags), .ALU_OUT_MAR(ins_rom_weaver_4_alu_out_mar),
    .ALU_OUT_MDR0(ins_rom_weaver_4_alu_out_mdr0), .ALU_OUT_MDR1(ins_rom_weaver_4_alu_out_mdr1),
    .ALU_OUT_MDR2(ins_rom_weaver_4_alu_out_mdr2), .ALU_REMAINDER_MAR(ins_rom_weaver_4_alu_remainder_mar),
    .ALU_REMAINDER_MDR0(ins_rom_weaver_4_alu_remainder_mdr0),
    .ALU_REMAINDER_MDR1(ins_rom_weaver_4_alu_remainder_mdr1),
    .ALU_REMAINDER_MDR2(ins_rom_weaver_4_alu_remainder_mdr2),
    .CU_endInstruction(ins_rom_weaver_4_cu_endinstruction));
  INS_ROM_5 ins_rom_5_1 (
    .in_1(Instruction), .CLK(demultiplexer_1_out5), .IP_inc(ins_rom_5_1_ip_inc),
    .IP_read(ins_rom_5_1_ip_read), .IP_write(ins_rom_5_1_ip_write), .SP_inc(ins_rom_5_1_sp_inc),
    .SP_dec(ins_rom_5_1_sp_dec), .SP_read(ins_rom_5_1_sp_read), .SP_write(ins_rom_5_1_sp_write),
    .MAR_read(ins_rom_5_1_mar_read), .MAR_write(ins_rom_5_1_mar_write), .MDR0_read(ins_rom_5_1_mdr0_read),
    .MDR0_write(ins_rom_5_1_mdr0_write), .MDR0_zero(ins_rom_5_1_mdr0_zero),
    .MDR1_read(ins_rom_5_1_mdr1_read), .MDR1_write(ins_rom_5_1_mdr1_write),
    .MDR1_zero(ins_rom_5_1_mdr1_zero), .MDR2_read(ins_rom_5_1_mdr2_read),
    .MDR2_write(ins_rom_5_1_mdr2_write), .MDR2_zero(ins_rom_5_1_mdr2_zero), .MEM_read(ins_rom_5_1_mem_read),
    .MEM_read2(ins_rom_5_1_mem_read2), .MEM_write(ins_rom_5_1_mem_write),
    .MDR0_MEM_IN(ins_rom_5_1_mdr0_mem_in), .MDR1_MEM_IN(ins_rom_5_1_mdr1_mem_in),
    .MDR2_MEM_IN(ins_rom_5_1_mdr2_mem_in), .MDR0_REG_IN(ins_rom_5_1_mdr0_reg_in),
    .MDR1_REG_IN(ins_rom_5_1_mdr1_reg_in), .MDR2_REG_IN(ins_rom_5_1_mdr2_reg_in),
    .MAR_REG_ID(ins_rom_5_1_mar_reg_id), .MDR0_REG_ID(ins_rom_5_1_mdr0_reg_id),
    .MDR1_REG_ID(ins_rom_5_1_mdr1_reg_id), .MDR2_REG_ID(ins_rom_5_1_mdr2_reg_id),
    .REG_OUT_MAR(ins_rom_5_1_reg_out_mar), .REG_OUT_MDR0(ins_rom_5_1_reg_out_mdr0),
    .REG_OUT_MDR1(ins_rom_5_1_reg_out_mdr1), .REG_OUT_MDR2(ins_rom_5_1_reg_out_mdr2),
    .REG_read(ins_rom_5_1_reg_read), .REG_write(ins_rom_5_1_reg_write), .MAR_MDR0(ins_rom_5_1_mar_mdr0),
    .MAR_MDR1(ins_rom_5_1_mar_mdr1), .MAR_MDR2(ins_rom_5_1_mar_mdr2), .MDR0_MAR(ins_rom_5_1_mdr0_mar),
    .MDR0_MDR1(ins_rom_5_1_mdr0_mdr1), .MDR0_MDR2(ins_rom_5_1_mdr0_mdr2), .MDR1_MAR(ins_rom_5_1_mdr1_mar),
    .MDR1_MDR0(ins_rom_5_1_mdr1_mdr0), .MDR1_MDR2(ins_rom_5_1_mdr1_mdr2), .MDR2_MAR(ins_rom_5_1_mdr2_mar),
    .MDR2_MDR0(ins_rom_5_1_mdr2_mdr0), .MDR2_MDR1(ins_rom_5_1_mdr2_mdr1),
    .MAR_ALU_IN0(ins_rom_5_1_mar_alu_in0), .MDR0_ALU_IN0(ins_rom_5_1_mdr0_alu_in0),
    .MDR1_ALU_IN0(ins_rom_5_1_mdr1_alu_in0), .MDR2_ALU_IN0(ins_rom_5_1_mdr2_alu_in0),
    .MAR_ALU_IN1(ins_rom_5_1_mar_alu_in1), .MDR0_ALU_IN1(ins_rom_5_1_mdr0_alu_in1),
    .MDR1_ALU_IN1(ins_rom_5_1_mdr1_alu_in1), .MDR2_ALU_IN1(ins_rom_5_1_mdr2_alu_in1),
    .ALU_SELECT(ins_rom_5_1_alu_select), .ALU_read(ins_rom_5_1_alu_read), .ALU_write(ins_rom_5_1_alu_write),
    .ALU_readFlags(ins_rom_5_1_alu_readflags), .ALU_OUT_MAR(ins_rom_5_1_alu_out_mar),
    .ALU_OUT_MDR0(ins_rom_5_1_alu_out_mdr0), .ALU_OUT_MDR1(ins_rom_5_1_alu_out_mdr1),
    .ALU_OUT_MDR2(ins_rom_5_1_alu_out_mdr2), .ALU_REMAINDER_MAR(ins_rom_5_1_alu_remainder_mar),
    .ALU_REMAINDER_MDR0(ins_rom_5_1_alu_remainder_mdr0), .ALU_REMAINDER_MDR1(ins_rom_5_1_alu_remainder_mdr1),
    .ALU_REMAINDER_MDR2(ins_rom_5_1_alu_remainder_mdr2), .CU_endInstruction(ins_rom_5_1_cu_endinstruction));
  INS_ROM_WEAVER ins_rom_weaver_5 (
    .in_1(ins_rom_weaver_4_ip_inc), .in_2(ins_rom_weaver_4_ip_read), .in_3(ins_rom_weaver_4_ip_write),
    .in_4(ins_rom_weaver_4_sp_inc), .in_5(ins_rom_weaver_4_sp_dec), .in_6(ins_rom_weaver_4_sp_read),
    .in_7(ins_rom_weaver_4_sp_write), .in_8(ins_rom_weaver_4_mar_read), .in_9(ins_rom_weaver_4_mar_write),
    .in_10(ins_rom_weaver_4_mdr0_read), .in_11(ins_rom_weaver_4_mdr0_write),
    .in_12(ins_rom_weaver_4_mdr0_zero), .in_13(ins_rom_weaver_4_mdr1_read),
    .in_14(ins_rom_weaver_4_mdr1_write), .in_15(ins_rom_weaver_4_mdr1_zero),
    .in_16(ins_rom_weaver_4_mdr2_read), .in_17(ins_rom_weaver_4_mdr2_write),
    .in_18(ins_rom_weaver_4_mdr2_zero), .in_19(ins_rom_weaver_4_mem_read),
    .in_20(ins_rom_weaver_4_mem_read2), .in_21(ins_rom_weaver_4_mem_write),
    .in_22(ins_rom_weaver_4_mdr0_mem_in), .in_23(ins_rom_weaver_4_mdr1_mem_in),
    .in_24(ins_rom_weaver_4_mdr2_mem_in), .in_25(ins_rom_weaver_4_mdr0_reg_in),
    .in_26(ins_rom_weaver_4_mdr1_reg_in), .in_27(ins_rom_weaver_4_mdr2_reg_in),
    .in_28(ins_rom_weaver_4_mar_reg_id), .in_29(ins_rom_weaver_4_mdr0_reg_id),
    .in_30(ins_rom_weaver_4_mdr1_reg_id), .in_31(ins_rom_weaver_4_mdr2_reg_id),
    .in_32(ins_rom_weaver_4_reg_out_mar), .in_33(ins_rom_weaver_4_reg_out_mdr0),
    .in_34(ins_rom_weaver_4_reg_out_mdr1), .in_35(ins_rom_weaver_4_reg_out_mdr2),
    .in_36(ins_rom_weaver_4_reg_read), .in_37(ins_rom_weaver_4_reg_write), .in_38(ins_rom_weaver_4_mar_mdr0),
    .in_39(ins_rom_weaver_4_mar_mdr1), .in_40(ins_rom_weaver_4_mar_mdr2), .in_41(ins_rom_weaver_4_mdr0_mar),
    .in_42(ins_rom_weaver_4_mdr0_mdr1), .in_43(ins_rom_weaver_4_mdr0_mdr2),
    .in_44(ins_rom_weaver_4_mdr1_mar), .in_45(ins_rom_weaver_4_mdr1_mdr0),
    .in_46(ins_rom_weaver_4_mdr1_mdr2), .in_47(ins_rom_weaver_4_mdr2_mar),
    .in_48(ins_rom_weaver_4_mdr2_mdr0), .in_49(ins_rom_weaver_4_mdr2_mdr1),
    .in_50(ins_rom_weaver_4_mar_alu_in0), .in_51(ins_rom_weaver_4_mdr0_alu_in0),
    .in_52(ins_rom_weaver_4_mdr1_alu_in0), .in_53(ins_rom_weaver_4_mdr2_alu_in0),
    .in_54(ins_rom_weaver_4_mar_alu_in1), .in_55(ins_rom_weaver_4_mdr0_alu_in1),
    .in_56(ins_rom_weaver_4_mdr1_alu_in1), .in_57(ins_rom_weaver_4_mdr2_alu_in1),
    .in_58(ins_rom_weaver_4_alu_select), .in_59(ins_rom_weaver_4_alu_read),
    .in_60(ins_rom_weaver_4_alu_write), .in_61(ins_rom_weaver_4_alu_readflags),
    .in_62(ins_rom_weaver_4_alu_out_mar), .in_63(ins_rom_weaver_4_alu_out_mdr0),
    .in_64(ins_rom_weaver_4_alu_out_mdr1), .in_65(ins_rom_weaver_4_alu_out_mdr2),
    .in_66(ins_rom_weaver_4_alu_remainder_mar), .in_67(ins_rom_weaver_4_alu_remainder_mdr0),
    .in_68(ins_rom_weaver_4_alu_remainder_mdr1), .in_69(ins_rom_weaver_4_alu_remainder_mdr2),
    .in_70(ins_rom_weaver_4_cu_endinstruction), .in_71(ins_rom_5_1_ip_inc), .in_72(ins_rom_5_1_ip_read),
    .in_73(ins_rom_5_1_ip_write), .in_74(ins_rom_5_1_sp_inc), .in_75(ins_rom_5_1_sp_dec),
    .in_76(ins_rom_5_1_sp_read), .in_77(ins_rom_5_1_sp_write), .in_78(ins_rom_5_1_mar_read),
    .in_79(ins_rom_5_1_mar_write), .in_80(ins_rom_5_1_mdr0_read), .in_81(ins_rom_5_1_mdr0_write),
    .in_82(ins_rom_5_1_mdr0_zero), .in_83(ins_rom_5_1_mdr1_read), .in_84(ins_rom_5_1_mdr1_write),
    .in_85(ins_rom_5_1_mdr1_zero), .in_86(ins_rom_5_1_mdr2_read), .in_87(ins_rom_5_1_mdr2_write),
    .in_88(ins_rom_5_1_mdr2_zero), .in_89(ins_rom_5_1_mem_read), .in_90(ins_rom_5_1_mem_read2),
    .in_91(ins_rom_5_1_mem_write), .in_92(ins_rom_5_1_mdr0_mem_in), .in_93(ins_rom_5_1_mdr1_mem_in),
    .in_94(ins_rom_5_1_mdr2_mem_in), .in_95(ins_rom_5_1_mdr0_reg_in), .in_96(ins_rom_5_1_mdr1_reg_in),
    .in_97(ins_rom_5_1_mdr2_reg_in), .in_98(ins_rom_5_1_mar_reg_id), .in_99(ins_rom_5_1_mdr0_reg_id),
    .in_100(ins_rom_5_1_mdr1_reg_id), .in_101(ins_rom_5_1_mdr2_reg_id), .in_102(ins_rom_5_1_reg_out_mar),
    .in_103(ins_rom_5_1_reg_out_mdr0), .in_104(ins_rom_5_1_reg_out_mdr1), .in_105(ins_rom_5_1_reg_out_mdr2),
    .in_106(ins_rom_5_1_reg_read), .in_107(ins_rom_5_1_reg_write), .in_108(ins_rom_5_1_mar_mdr0),
    .in_109(ins_rom_5_1_mar_mdr1), .in_110(ins_rom_5_1_mar_mdr2), .in_111(ins_rom_5_1_mdr0_mar),
    .in_112(ins_rom_5_1_mdr0_mdr1), .in_113(ins_rom_5_1_mdr0_mdr2), .in_114(ins_rom_5_1_mdr1_mar),
    .in_115(ins_rom_5_1_mdr1_mdr0), .in_116(ins_rom_5_1_mdr1_mdr2), .in_117(ins_rom_5_1_mdr2_mar),
    .in_118(ins_rom_5_1_mdr2_mdr0), .in_119(ins_rom_5_1_mdr2_mdr1), .in_120(ins_rom_5_1_mar_alu_in0),
    .in_121(ins_rom_5_1_mdr0_alu_in0), .in_122(ins_rom_5_1_mdr1_alu_in0), .in_123(ins_rom_5_1_mdr2_alu_in0),
    .in_124(ins_rom_5_1_mar_alu_in1), .in_125(ins_rom_5_1_mdr0_alu_in1), .in_126(ins_rom_5_1_mdr1_alu_in1),
    .in_127(ins_rom_5_1_mdr2_alu_in1), .in_128(ins_rom_5_1_alu_select), .in_129(ins_rom_5_1_alu_read),
    .in_130(ins_rom_5_1_alu_write), .in_131(ins_rom_5_1_alu_readflags), .in_132(ins_rom_5_1_alu_out_mar),
    .in_133(ins_rom_5_1_alu_out_mdr0), .in_134(ins_rom_5_1_alu_out_mdr1), .in_135(ins_rom_5_1_alu_out_mdr2),
    .in_136(ins_rom_5_1_alu_remainder_mar), .in_137(ins_rom_5_1_alu_remainder_mdr0),
    .in_138(ins_rom_5_1_alu_remainder_mdr1), .in_139(ins_rom_5_1_alu_remainder_mdr2),
    .in_140(ins_rom_5_1_cu_endinstruction), .IP_inc(ins_rom_weaver_5_ip_inc),
    .IP_read(ins_rom_weaver_5_ip_read), .IP_write(ins_rom_weaver_5_ip_write),
    .SP_inc(ins_rom_weaver_5_sp_inc), .SP_dec(ins_rom_weaver_5_sp_dec), .SP_read(ins_rom_weaver_5_sp_read),
    .SP_write(ins_rom_weaver_5_sp_write), .MAR_read(ins_rom_weaver_5_mar_read),
    .MAR_write(ins_rom_weaver_5_mar_write), .MDR0_read(ins_rom_weaver_5_mdr0_read),
    .MDR0_write(ins_rom_weaver_5_mdr0_write), .MDR0_zero(ins_rom_weaver_5_mdr0_zero),
    .MDR1_read(ins_rom_weaver_5_mdr1_read), .MDR1_write(ins_rom_weaver_5_mdr1_write),
    .MDR1_zero(ins_rom_weaver_5_mdr1_zero), .MDR2_read(ins_rom_weaver_5_mdr2_read),
    .MDR2_write(ins_rom_weaver_5_mdr2_write), .MDR2_zero(ins_rom_weaver_5_mdr2_zero),
    .MEM_read(ins_rom_weaver_5_mem_read), .MEM_read2(ins_rom_weaver_5_mem_read2),
    .MEM_write(ins_rom_weaver_5_mem_write), .MDR0_MEM_IN(ins_rom_weaver_5_mdr0_mem_in),
    .MDR1_MEM_IN(ins_rom_weaver_5_mdr1_mem_in), .MDR2_MEM_IN(ins_rom_weaver_5_mdr2_mem_in),
    .MDR0_REG_IN(ins_rom_weaver_5_mdr0_reg_in), .MDR1_REG_IN(ins_rom_weaver_5_mdr1_reg_in),
    .MDR2_REG_IN(ins_rom_weaver_5_mdr2_reg_in), .MAR_REG_ID(ins_rom_weaver_5_mar_reg_id),
    .MDR0_REG_ID(ins_rom_weaver_5_mdr0_reg_id), .MDR1_REG_ID(ins_rom_weaver_5_mdr1_reg_id),
    .MDR2_REG_ID(ins_rom_weaver_5_mdr2_reg_id), .REG_OUT_MAR(ins_rom_weaver_5_reg_out_mar),
    .REG_OUT_MDR0(ins_rom_weaver_5_reg_out_mdr0), .REG_OUT_MDR1(ins_rom_weaver_5_reg_out_mdr1),
    .REG_OUT_MDR2(ins_rom_weaver_5_reg_out_mdr2), .REG_read(ins_rom_weaver_5_reg_read),
    .REG_write(ins_rom_weaver_5_reg_write), .MAR_MDR0(ins_rom_weaver_5_mar_mdr0),
    .MAR_MDR1(ins_rom_weaver_5_mar_mdr1), .MAR_MDR2(ins_rom_weaver_5_mar_mdr2),
    .MDR0_MAR(ins_rom_weaver_5_mdr0_mar), .MDR0_MDR1(ins_rom_weaver_5_mdr0_mdr1),
    .MDR0_MDR2(ins_rom_weaver_5_mdr0_mdr2), .MDR1_MAR(ins_rom_weaver_5_mdr1_mar),
    .MDR1_MDR0(ins_rom_weaver_5_mdr1_mdr0), .MDR1_MDR2(ins_rom_weaver_5_mdr1_mdr2),
    .MDR2_MAR(ins_rom_weaver_5_mdr2_mar), .MDR2_MDR0(ins_rom_weaver_5_mdr2_mdr0),
    .MDR2_MDR1(ins_rom_weaver_5_mdr2_mdr1), .MAR_ALU_IN0(ins_rom_weaver_5_mar_alu_in0),
    .MDR0_ALU_IN0(ins_rom_weaver_5_mdr0_alu_in0), .MDR1_ALU_IN0(ins_rom_weaver_5_mdr1_alu_in0),
    .MDR2_ALU_IN0(ins_rom_weaver_5_mdr2_alu_in0), .MAR_ALU_IN1(ins_rom_weaver_5_mar_alu_in1),
    .MDR0_ALU_IN1(ins_rom_weaver_5_mdr0_alu_in1), .MDR1_ALU_IN1(ins_rom_weaver_5_mdr1_alu_in1),
    .MDR2_ALU_IN1(ins_rom_weaver_5_mdr2_alu_in1), .ALU_SELECT(ins_rom_weaver_5_alu_select),
    .ALU_read(ins_rom_weaver_5_alu_read), .ALU_write(ins_rom_weaver_5_alu_write),
    .ALU_readFlags(ins_rom_weaver_5_alu_readflags), .ALU_OUT_MAR(ins_rom_weaver_5_alu_out_mar),
    .ALU_OUT_MDR0(ins_rom_weaver_5_alu_out_mdr0), .ALU_OUT_MDR1(ins_rom_weaver_5_alu_out_mdr1),
    .ALU_OUT_MDR2(ins_rom_weaver_5_alu_out_mdr2), .ALU_REMAINDER_MAR(ins_rom_weaver_5_alu_remainder_mar),
    .ALU_REMAINDER_MDR0(ins_rom_weaver_5_alu_remainder_mdr0),
    .ALU_REMAINDER_MDR1(ins_rom_weaver_5_alu_remainder_mdr1),
    .ALU_REMAINDER_MDR2(ins_rom_weaver_5_alu_remainder_mdr2),
    .CU_endInstruction(ins_rom_weaver_5_cu_endinstruction));
  INS_ROM_6 ins_rom_6_1 (
    .in_1(Instruction), .CLK(demultiplexer_1_out6), .IP_inc(ins_rom_6_1_ip_inc),
    .IP_read(ins_rom_6_1_ip_read), .IP_write(ins_rom_6_1_ip_write), .SP_inc(ins_rom_6_1_sp_inc),
    .SP_dec(ins_rom_6_1_sp_dec), .SP_read(ins_rom_6_1_sp_read), .SP_write(ins_rom_6_1_sp_write),
    .MAR_read(ins_rom_6_1_mar_read), .MAR_write(ins_rom_6_1_mar_write), .MDR0_read(ins_rom_6_1_mdr0_read),
    .MDR0_write(ins_rom_6_1_mdr0_write), .MDR0_zero(ins_rom_6_1_mdr0_zero),
    .MDR1_read(ins_rom_6_1_mdr1_read), .MDR1_write(ins_rom_6_1_mdr1_write),
    .MDR1_zero(ins_rom_6_1_mdr1_zero), .MDR2_read(ins_rom_6_1_mdr2_read),
    .MDR2_write(ins_rom_6_1_mdr2_write), .MDR2_zero(ins_rom_6_1_mdr2_zero), .MEM_read(ins_rom_6_1_mem_read),
    .MEM_read2(ins_rom_6_1_mem_read2), .MEM_write(ins_rom_6_1_mem_write),
    .MDR0_MEM_IN(ins_rom_6_1_mdr0_mem_in), .MDR1_MEM_IN(ins_rom_6_1_mdr1_mem_in),
    .MDR2_MEM_IN(ins_rom_6_1_mdr2_mem_in), .MDR0_REG_IN(ins_rom_6_1_mdr0_reg_in),
    .MDR1_REG_IN(ins_rom_6_1_mdr1_reg_in), .MDR2_REG_IN(ins_rom_6_1_mdr2_reg_in),
    .MAR_REG_ID(ins_rom_6_1_mar_reg_id), .MDR0_REG_ID(ins_rom_6_1_mdr0_reg_id),
    .MDR1_REG_ID(ins_rom_6_1_mdr1_reg_id), .MDR2_REG_ID(ins_rom_6_1_mdr2_reg_id),
    .REG_OUT_MAR(ins_rom_6_1_reg_out_mar), .REG_OUT_MDR0(ins_rom_6_1_reg_out_mdr0),
    .REG_OUT_MDR1(ins_rom_6_1_reg_out_mdr1), .REG_OUT_MDR2(ins_rom_6_1_reg_out_mdr2),
    .REG_read(ins_rom_6_1_reg_read), .REG_write(ins_rom_6_1_reg_write), .MAR_MDR0(ins_rom_6_1_mar_mdr0),
    .MAR_MDR1(ins_rom_6_1_mar_mdr1), .MAR_MDR2(ins_rom_6_1_mar_mdr2), .MDR0_MAR(ins_rom_6_1_mdr0_mar),
    .MDR0_MDR1(ins_rom_6_1_mdr0_mdr1), .MDR0_MDR2(ins_rom_6_1_mdr0_mdr2), .MDR1_MAR(ins_rom_6_1_mdr1_mar),
    .MDR1_MDR0(ins_rom_6_1_mdr1_mdr0), .MDR1_MDR2(ins_rom_6_1_mdr1_mdr2), .MDR2_MAR(ins_rom_6_1_mdr2_mar),
    .MDR2_MDR0(ins_rom_6_1_mdr2_mdr0), .MDR2_MDR1(ins_rom_6_1_mdr2_mdr1),
    .MAR_ALU_IN0(ins_rom_6_1_mar_alu_in0), .MDR0_ALU_IN0(ins_rom_6_1_mdr0_alu_in0),
    .MDR1_ALU_IN0(ins_rom_6_1_mdr1_alu_in0), .MDR2_ALU_IN0(ins_rom_6_1_mdr2_alu_in0),
    .MAR_ALU_IN1(ins_rom_6_1_mar_alu_in1), .MDR0_ALU_IN1(ins_rom_6_1_mdr0_alu_in1),
    .MDR1_ALU_IN1(ins_rom_6_1_mdr1_alu_in1), .MDR2_ALU_IN1(ins_rom_6_1_mdr2_alu_in1),
    .ALU_SELECT(ins_rom_6_1_alu_select), .ALU_read(ins_rom_6_1_alu_read), .ALU_write(ins_rom_6_1_alu_write),
    .ALU_readFlags(ins_rom_6_1_alu_readflags), .ALU_OUT_MAR(ins_rom_6_1_alu_out_mar),
    .ALU_OUT_MDR0(ins_rom_6_1_alu_out_mdr0), .ALU_OUT_MDR1(ins_rom_6_1_alu_out_mdr1),
    .ALU_OUT_MDR2(ins_rom_6_1_alu_out_mdr2), .ALU_REMAINDER_MAR(ins_rom_6_1_alu_remainder_mar),
    .ALU_REMAINDER_MDR0(ins_rom_6_1_alu_remainder_mdr0), .ALU_REMAINDER_MDR1(ins_rom_6_1_alu_remainder_mdr1),
    .ALU_REMAINDER_MDR2(ins_rom_6_1_alu_remainder_mdr2), .CU_endInstruction(ins_rom_6_1_cu_endinstruction));
  INS_ROM_WEAVER ins_rom_weaver_6 (
    .in_1(ins_rom_weaver_5_ip_inc), .in_2(ins_rom_weaver_5_ip_read), .in_3(ins_rom_weaver_5_ip_write),
    .in_4(ins_rom_weaver_5_sp_inc), .in_5(ins_rom_weaver_5_sp_dec), .in_6(ins_rom_weaver_5_sp_read),
    .in_7(ins_rom_weaver_5_sp_write), .in_8(ins_rom_weaver_5_mar_read), .in_9(ins_rom_weaver_5_mar_write),
    .in_10(ins_rom_weaver_5_mdr0_read), .in_11(ins_rom_weaver_5_mdr0_write),
    .in_12(ins_rom_weaver_5_mdr0_zero), .in_13(ins_rom_weaver_5_mdr1_read),
    .in_14(ins_rom_weaver_5_mdr1_write), .in_15(ins_rom_weaver_5_mdr1_zero),
    .in_16(ins_rom_weaver_5_mdr2_read), .in_17(ins_rom_weaver_5_mdr2_write),
    .in_18(ins_rom_weaver_5_mdr2_zero), .in_19(ins_rom_weaver_5_mem_read),
    .in_20(ins_rom_weaver_5_mem_read2), .in_21(ins_rom_weaver_5_mem_write),
    .in_22(ins_rom_weaver_5_mdr0_mem_in), .in_23(ins_rom_weaver_5_mdr1_mem_in),
    .in_24(ins_rom_weaver_5_mdr2_mem_in), .in_25(ins_rom_weaver_5_mdr0_reg_in),
    .in_26(ins_rom_weaver_5_mdr1_reg_in), .in_27(ins_rom_weaver_5_mdr2_reg_in),
    .in_28(ins_rom_weaver_5_mar_reg_id), .in_29(ins_rom_weaver_5_mdr0_reg_id),
    .in_30(ins_rom_weaver_5_mdr1_reg_id), .in_31(ins_rom_weaver_5_mdr2_reg_id),
    .in_32(ins_rom_weaver_5_reg_out_mar), .in_33(ins_rom_weaver_5_reg_out_mdr0),
    .in_34(ins_rom_weaver_5_reg_out_mdr1), .in_35(ins_rom_weaver_5_reg_out_mdr2),
    .in_36(ins_rom_weaver_5_reg_read), .in_37(ins_rom_weaver_5_reg_write), .in_38(ins_rom_weaver_5_mar_mdr0),
    .in_39(ins_rom_weaver_5_mar_mdr1), .in_40(ins_rom_weaver_5_mar_mdr2), .in_41(ins_rom_weaver_5_mdr0_mar),
    .in_42(ins_rom_weaver_5_mdr0_mdr1), .in_43(ins_rom_weaver_5_mdr0_mdr2),
    .in_44(ins_rom_weaver_5_mdr1_mar), .in_45(ins_rom_weaver_5_mdr1_mdr0),
    .in_46(ins_rom_weaver_5_mdr1_mdr2), .in_47(ins_rom_weaver_5_mdr2_mar),
    .in_48(ins_rom_weaver_5_mdr2_mdr0), .in_49(ins_rom_weaver_5_mdr2_mdr1),
    .in_50(ins_rom_weaver_5_mar_alu_in0), .in_51(ins_rom_weaver_5_mdr0_alu_in0),
    .in_52(ins_rom_weaver_5_mdr1_alu_in0), .in_53(ins_rom_weaver_5_mdr2_alu_in0),
    .in_54(ins_rom_weaver_5_mar_alu_in1), .in_55(ins_rom_weaver_5_mdr0_alu_in1),
    .in_56(ins_rom_weaver_5_mdr1_alu_in1), .in_57(ins_rom_weaver_5_mdr2_alu_in1),
    .in_58(ins_rom_weaver_5_alu_select), .in_59(ins_rom_weaver_5_alu_read),
    .in_60(ins_rom_weaver_5_alu_write), .in_61(ins_rom_weaver_5_alu_readflags),
    .in_62(ins_rom_weaver_5_alu_out_mar), .in_63(ins_rom_weaver_5_alu_out_mdr0),
    .in_64(ins_rom_weaver_5_alu_out_mdr1), .in_65(ins_rom_weaver_5_alu_out_mdr2),
    .in_66(ins_rom_weaver_5_alu_remainder_mar), .in_67(ins_rom_weaver_5_alu_remainder_mdr0),
    .in_68(ins_rom_weaver_5_alu_remainder_mdr1), .in_69(ins_rom_weaver_5_alu_remainder_mdr2),
    .in_70(ins_rom_weaver_5_cu_endinstruction), .in_71(ins_rom_6_1_ip_inc), .in_72(ins_rom_6_1_ip_read),
    .in_73(ins_rom_6_1_ip_write), .in_74(ins_rom_6_1_sp_inc), .in_75(ins_rom_6_1_sp_dec),
    .in_76(ins_rom_6_1_sp_read), .in_77(ins_rom_6_1_sp_write), .in_78(ins_rom_6_1_mar_read),
    .in_79(ins_rom_6_1_mar_write), .in_80(ins_rom_6_1_mdr0_read), .in_81(ins_rom_6_1_mdr0_write),
    .in_82(ins_rom_6_1_mdr0_zero), .in_83(ins_rom_6_1_mdr1_read), .in_84(ins_rom_6_1_mdr1_write),
    .in_85(ins_rom_6_1_mdr1_zero), .in_86(ins_rom_6_1_mdr2_read), .in_87(ins_rom_6_1_mdr2_write),
    .in_88(ins_rom_6_1_mdr2_zero), .in_89(ins_rom_6_1_mem_read), .in_90(ins_rom_6_1_mem_read2),
    .in_91(ins_rom_6_1_mem_write), .in_92(ins_rom_6_1_mdr0_mem_in), .in_93(ins_rom_6_1_mdr1_mem_in),
    .in_94(ins_rom_6_1_mdr2_mem_in), .in_95(ins_rom_6_1_mdr0_reg_in), .in_96(ins_rom_6_1_mdr1_reg_in),
    .in_97(ins_rom_6_1_mdr2_reg_in), .in_98(ins_rom_6_1_mar_reg_id), .in_99(ins_rom_6_1_mdr0_reg_id),
    .in_100(ins_rom_6_1_mdr1_reg_id), .in_101(ins_rom_6_1_mdr2_reg_id), .in_102(ins_rom_6_1_reg_out_mar),
    .in_103(ins_rom_6_1_reg_out_mdr0), .in_104(ins_rom_6_1_reg_out_mdr1), .in_105(ins_rom_6_1_reg_out_mdr2),
    .in_106(ins_rom_6_1_reg_read), .in_107(ins_rom_6_1_reg_write), .in_108(ins_rom_6_1_mar_mdr0),
    .in_109(ins_rom_6_1_mar_mdr1), .in_110(ins_rom_6_1_mar_mdr2), .in_111(ins_rom_6_1_mdr0_mar),
    .in_112(ins_rom_6_1_mdr0_mdr1), .in_113(ins_rom_6_1_mdr0_mdr2), .in_114(ins_rom_6_1_mdr1_mar),
    .in_115(ins_rom_6_1_mdr1_mdr0), .in_116(ins_rom_6_1_mdr1_mdr2), .in_117(ins_rom_6_1_mdr2_mar),
    .in_118(ins_rom_6_1_mdr2_mdr0), .in_119(ins_rom_6_1_mdr2_mdr1), .in_120(ins_rom_6_1_mar_alu_in0),
    .in_121(ins_rom_6_1_mdr0_alu_in0), .in_122(ins_rom_6_1_mdr1_alu_in0), .in_123(ins_rom_6_1_mdr2_alu_in0),
    .in_124(ins_rom_6_1_mar_alu_in1), .in_125(ins_rom_6_1_mdr0_alu_in1), .in_126(ins_rom_6_1_mdr1_alu_in1),
    .in_127(ins_rom_6_1_mdr2_alu_in1), .in_128(ins_rom_6_1_alu_select), .in_129(ins_rom_6_1_alu_read),
    .in_130(ins_rom_6_1_alu_write), .in_131(ins_rom_6_1_alu_readflags), .in_132(ins_rom_6_1_alu_out_mar),
    .in_133(ins_rom_6_1_alu_out_mdr0), .in_134(ins_rom_6_1_alu_out_mdr1), .in_135(ins_rom_6_1_alu_out_mdr2),
    .in_136(ins_rom_6_1_alu_remainder_mar), .in_137(ins_rom_6_1_alu_remainder_mdr0),
    .in_138(ins_rom_6_1_alu_remainder_mdr1), .in_139(ins_rom_6_1_alu_remainder_mdr2),
    .in_140(ins_rom_6_1_cu_endinstruction), .IP_inc(ins_rom_weaver_6_ip_inc),
    .IP_read(ins_rom_weaver_6_ip_read), .IP_write(ins_rom_weaver_6_ip_write),
    .SP_inc(ins_rom_weaver_6_sp_inc), .SP_dec(ins_rom_weaver_6_sp_dec), .SP_read(ins_rom_weaver_6_sp_read),
    .SP_write(ins_rom_weaver_6_sp_write), .MAR_read(ins_rom_weaver_6_mar_read),
    .MAR_write(ins_rom_weaver_6_mar_write), .MDR0_read(ins_rom_weaver_6_mdr0_read),
    .MDR0_write(ins_rom_weaver_6_mdr0_write), .MDR0_zero(ins_rom_weaver_6_mdr0_zero),
    .MDR1_read(ins_rom_weaver_6_mdr1_read), .MDR1_write(ins_rom_weaver_6_mdr1_write),
    .MDR1_zero(ins_rom_weaver_6_mdr1_zero), .MDR2_read(ins_rom_weaver_6_mdr2_read),
    .MDR2_write(ins_rom_weaver_6_mdr2_write), .MDR2_zero(ins_rom_weaver_6_mdr2_zero),
    .MEM_read(ins_rom_weaver_6_mem_read), .MEM_read2(ins_rom_weaver_6_mem_read2),
    .MEM_write(ins_rom_weaver_6_mem_write), .MDR0_MEM_IN(ins_rom_weaver_6_mdr0_mem_in),
    .MDR1_MEM_IN(ins_rom_weaver_6_mdr1_mem_in), .MDR2_MEM_IN(ins_rom_weaver_6_mdr2_mem_in),
    .MDR0_REG_IN(ins_rom_weaver_6_mdr0_reg_in), .MDR1_REG_IN(ins_rom_weaver_6_mdr1_reg_in),
    .MDR2_REG_IN(ins_rom_weaver_6_mdr2_reg_in), .MAR_REG_ID(ins_rom_weaver_6_mar_reg_id),
    .MDR0_REG_ID(ins_rom_weaver_6_mdr0_reg_id), .MDR1_REG_ID(ins_rom_weaver_6_mdr1_reg_id),
    .MDR2_REG_ID(ins_rom_weaver_6_mdr2_reg_id), .REG_OUT_MAR(ins_rom_weaver_6_reg_out_mar),
    .REG_OUT_MDR0(ins_rom_weaver_6_reg_out_mdr0), .REG_OUT_MDR1(ins_rom_weaver_6_reg_out_mdr1),
    .REG_OUT_MDR2(ins_rom_weaver_6_reg_out_mdr2), .REG_read(ins_rom_weaver_6_reg_read),
    .REG_write(ins_rom_weaver_6_reg_write), .MAR_MDR0(ins_rom_weaver_6_mar_mdr0),
    .MAR_MDR1(ins_rom_weaver_6_mar_mdr1), .MAR_MDR2(ins_rom_weaver_6_mar_mdr2),
    .MDR0_MAR(ins_rom_weaver_6_mdr0_mar), .MDR0_MDR1(ins_rom_weaver_6_mdr0_mdr1),
    .MDR0_MDR2(ins_rom_weaver_6_mdr0_mdr2), .MDR1_MAR(ins_rom_weaver_6_mdr1_mar),
    .MDR1_MDR0(ins_rom_weaver_6_mdr1_mdr0), .MDR1_MDR2(ins_rom_weaver_6_mdr1_mdr2),
    .MDR2_MAR(ins_rom_weaver_6_mdr2_mar), .MDR2_MDR0(ins_rom_weaver_6_mdr2_mdr0),
    .MDR2_MDR1(ins_rom_weaver_6_mdr2_mdr1), .MAR_ALU_IN0(ins_rom_weaver_6_mar_alu_in0),
    .MDR0_ALU_IN0(ins_rom_weaver_6_mdr0_alu_in0), .MDR1_ALU_IN0(ins_rom_weaver_6_mdr1_alu_in0),
    .MDR2_ALU_IN0(ins_rom_weaver_6_mdr2_alu_in0), .MAR_ALU_IN1(ins_rom_weaver_6_mar_alu_in1),
    .MDR0_ALU_IN1(ins_rom_weaver_6_mdr0_alu_in1), .MDR1_ALU_IN1(ins_rom_weaver_6_mdr1_alu_in1),
    .MDR2_ALU_IN1(ins_rom_weaver_6_mdr2_alu_in1), .ALU_SELECT(ins_rom_weaver_6_alu_select),
    .ALU_read(ins_rom_weaver_6_alu_read), .ALU_write(ins_rom_weaver_6_alu_write),
    .ALU_readFlags(ins_rom_weaver_6_alu_readflags), .ALU_OUT_MAR(ins_rom_weaver_6_alu_out_mar),
    .ALU_OUT_MDR0(ins_rom_weaver_6_alu_out_mdr0), .ALU_OUT_MDR1(ins_rom_weaver_6_alu_out_mdr1),
    .ALU_OUT_MDR2(ins_rom_weaver_6_alu_out_mdr2), .ALU_REMAINDER_MAR(ins_rom_weaver_6_alu_remainder_mar),
    .ALU_REMAINDER_MDR0(ins_rom_weaver_6_alu_remainder_mdr0),
    .ALU_REMAINDER_MDR1(ins_rom_weaver_6_alu_remainder_mdr1),
    .ALU_REMAINDER_MDR2(ins_rom_weaver_6_alu_remainder_mdr2),
    .CU_endInstruction(ins_rom_weaver_6_cu_endinstruction));
  INS_ROM_7 ins_rom_7_1 (
    .in_1(Instruction), .CLK(demultiplexer_1_out7), .IP_inc(ins_rom_7_1_ip_inc),
    .IP_read(ins_rom_7_1_ip_read), .IP_write(ins_rom_7_1_ip_write), .SP_inc(ins_rom_7_1_sp_inc),
    .SP_dec(ins_rom_7_1_sp_dec), .SP_read(ins_rom_7_1_sp_read), .SP_write(ins_rom_7_1_sp_write),
    .MAR_read(ins_rom_7_1_mar_read), .MAR_write(ins_rom_7_1_mar_write), .MDR0_read(ins_rom_7_1_mdr0_read),
    .MDR0_write(ins_rom_7_1_mdr0_write), .MDR0_zero(ins_rom_7_1_mdr0_zero),
    .MDR1_read(ins_rom_7_1_mdr1_read), .MDR1_write(ins_rom_7_1_mdr1_write),
    .MDR1_zero(ins_rom_7_1_mdr1_zero), .MDR2_read(ins_rom_7_1_mdr2_read),
    .MDR2_write(ins_rom_7_1_mdr2_write), .MDR2_zero(ins_rom_7_1_mdr2_zero), .MEM_read(ins_rom_7_1_mem_read),
    .MEM_read2(ins_rom_7_1_mem_read2), .MEM_write(ins_rom_7_1_mem_write),
    .MDR0_MEM_IN(ins_rom_7_1_mdr0_mem_in), .MDR1_MEM_IN(ins_rom_7_1_mdr1_mem_in),
    .MDR2_MEM_IN(ins_rom_7_1_mdr2_mem_in), .MDR0_REG_IN(ins_rom_7_1_mdr0_reg_in),
    .MDR1_REG_IN(ins_rom_7_1_mdr1_reg_in), .MDR2_REG_IN(ins_rom_7_1_mdr2_reg_in),
    .MAR_REG_ID(ins_rom_7_1_mar_reg_id), .MDR0_REG_ID(ins_rom_7_1_mdr0_reg_id),
    .MDR1_REG_ID(ins_rom_7_1_mdr1_reg_id), .MDR2_REG_ID(ins_rom_7_1_mdr2_reg_id),
    .REG_OUT_MAR(ins_rom_7_1_reg_out_mar), .REG_OUT_MDR0(ins_rom_7_1_reg_out_mdr0),
    .REG_OUT_MDR1(ins_rom_7_1_reg_out_mdr1), .REG_OUT_MDR2(ins_rom_7_1_reg_out_mdr2),
    .REG_read(ins_rom_7_1_reg_read), .REG_write(ins_rom_7_1_reg_write), .MAR_MDR0(ins_rom_7_1_mar_mdr0),
    .MAR_MDR1(ins_rom_7_1_mar_mdr1), .MAR_MDR2(ins_rom_7_1_mar_mdr2), .MDR0_MAR(ins_rom_7_1_mdr0_mar),
    .MDR0_MDR1(ins_rom_7_1_mdr0_mdr1), .MDR0_MDR2(ins_rom_7_1_mdr0_mdr2), .MDR1_MAR(ins_rom_7_1_mdr1_mar),
    .MDR1_MDR0(ins_rom_7_1_mdr1_mdr0), .MDR1_MDR2(ins_rom_7_1_mdr1_mdr2), .MDR2_MAR(ins_rom_7_1_mdr2_mar),
    .MDR2_MDR0(ins_rom_7_1_mdr2_mdr0), .MDR2_MDR1(ins_rom_7_1_mdr2_mdr1),
    .MAR_ALU_IN0(ins_rom_7_1_mar_alu_in0), .MDR0_ALU_IN0(ins_rom_7_1_mdr0_alu_in0),
    .MDR1_ALU_IN0(ins_rom_7_1_mdr1_alu_in0), .MDR2_ALU_IN0(ins_rom_7_1_mdr2_alu_in0),
    .MAR_ALU_IN1(ins_rom_7_1_mar_alu_in1), .MDR0_ALU_IN1(ins_rom_7_1_mdr0_alu_in1),
    .MDR1_ALU_IN1(ins_rom_7_1_mdr1_alu_in1), .MDR2_ALU_IN1(ins_rom_7_1_mdr2_alu_in1),
    .ALU_SELECT(ins_rom_7_1_alu_select), .ALU_read(ins_rom_7_1_alu_read), .ALU_write(ins_rom_7_1_alu_write),
    .ALU_readFlags(ins_rom_7_1_alu_readflags), .ALU_OUT_MAR(ins_rom_7_1_alu_out_mar),
    .ALU_OUT_MDR0(ins_rom_7_1_alu_out_mdr0), .ALU_OUT_MDR1(ins_rom_7_1_alu_out_mdr1),
    .ALU_OUT_MDR2(ins_rom_7_1_alu_out_mdr2), .ALU_REMAINDER_MAR(ins_rom_7_1_alu_remainder_mar),
    .ALU_REMAINDER_MDR0(ins_rom_7_1_alu_remainder_mdr0), .ALU_REMAINDER_MDR1(ins_rom_7_1_alu_remainder_mdr1),
    .ALU_REMAINDER_MDR2(ins_rom_7_1_alu_remainder_mdr2), .CU_endInstruction(ins_rom_7_1_cu_endinstruction));
  INS_ROM_WEAVER ins_rom_weaver_7 (
    .in_1(ins_rom_weaver_6_ip_inc), .in_2(ins_rom_weaver_6_ip_read), .in_3(ins_rom_weaver_6_ip_write),
    .in_4(ins_rom_weaver_6_sp_inc), .in_5(ins_rom_weaver_6_sp_dec), .in_6(ins_rom_weaver_6_sp_read),
    .in_7(ins_rom_weaver_6_sp_write), .in_8(ins_rom_weaver_6_mar_read), .in_9(ins_rom_weaver_6_mar_write),
    .in_10(ins_rom_weaver_6_mdr0_read), .in_11(ins_rom_weaver_6_mdr0_write),
    .in_12(ins_rom_weaver_6_mdr0_zero), .in_13(ins_rom_weaver_6_mdr1_read),
    .in_14(ins_rom_weaver_6_mdr1_write), .in_15(ins_rom_weaver_6_mdr1_zero),
    .in_16(ins_rom_weaver_6_mdr2_read), .in_17(ins_rom_weaver_6_mdr2_write),
    .in_18(ins_rom_weaver_6_mdr2_zero), .in_19(ins_rom_weaver_6_mem_read),
    .in_20(ins_rom_weaver_6_mem_read2), .in_21(ins_rom_weaver_6_mem_write),
    .in_22(ins_rom_weaver_6_mdr0_mem_in), .in_23(ins_rom_weaver_6_mdr1_mem_in),
    .in_24(ins_rom_weaver_6_mdr2_mem_in), .in_25(ins_rom_weaver_6_mdr0_reg_in),
    .in_26(ins_rom_weaver_6_mdr1_reg_in), .in_27(ins_rom_weaver_6_mdr2_reg_in),
    .in_28(ins_rom_weaver_6_mar_reg_id), .in_29(ins_rom_weaver_6_mdr0_reg_id),
    .in_30(ins_rom_weaver_6_mdr1_reg_id), .in_31(ins_rom_weaver_6_mdr2_reg_id),
    .in_32(ins_rom_weaver_6_reg_out_mar), .in_33(ins_rom_weaver_6_reg_out_mdr0),
    .in_34(ins_rom_weaver_6_reg_out_mdr1), .in_35(ins_rom_weaver_6_reg_out_mdr2),
    .in_36(ins_rom_weaver_6_reg_read), .in_37(ins_rom_weaver_6_reg_write), .in_38(ins_rom_weaver_6_mar_mdr0),
    .in_39(ins_rom_weaver_6_mar_mdr1), .in_40(ins_rom_weaver_6_mar_mdr2), .in_41(ins_rom_weaver_6_mdr0_mar),
    .in_42(ins_rom_weaver_6_mdr0_mdr1), .in_43(ins_rom_weaver_6_mdr0_mdr2),
    .in_44(ins_rom_weaver_6_mdr1_mar), .in_45(ins_rom_weaver_6_mdr1_mdr0),
    .in_46(ins_rom_weaver_6_mdr1_mdr2), .in_47(ins_rom_weaver_6_mdr2_mar),
    .in_48(ins_rom_weaver_6_mdr2_mdr0), .in_49(ins_rom_weaver_6_mdr2_mdr1),
    .in_50(ins_rom_weaver_6_mar_alu_in0), .in_51(ins_rom_weaver_6_mdr0_alu_in0),
    .in_52(ins_rom_weaver_6_mdr1_alu_in0), .in_53(ins_rom_weaver_6_mdr2_alu_in0),
    .in_54(ins_rom_weaver_6_mar_alu_in1), .in_55(ins_rom_weaver_6_mdr0_alu_in1),
    .in_56(ins_rom_weaver_6_mdr1_alu_in1), .in_57(ins_rom_weaver_6_mdr2_alu_in1),
    .in_58(ins_rom_weaver_6_alu_select), .in_59(ins_rom_weaver_6_alu_read),
    .in_60(ins_rom_weaver_6_alu_write), .in_61(ins_rom_weaver_6_alu_readflags),
    .in_62(ins_rom_weaver_6_alu_out_mar), .in_63(ins_rom_weaver_6_alu_out_mdr0),
    .in_64(ins_rom_weaver_6_alu_out_mdr1), .in_65(ins_rom_weaver_6_alu_out_mdr2),
    .in_66(ins_rom_weaver_6_alu_remainder_mar), .in_67(ins_rom_weaver_6_alu_remainder_mdr0),
    .in_68(ins_rom_weaver_6_alu_remainder_mdr1), .in_69(ins_rom_weaver_6_alu_remainder_mdr2),
    .in_70(ins_rom_weaver_6_cu_endinstruction), .in_71(ins_rom_7_1_ip_inc), .in_72(ins_rom_7_1_ip_read),
    .in_73(ins_rom_7_1_ip_write), .in_74(ins_rom_7_1_sp_inc), .in_75(ins_rom_7_1_sp_dec),
    .in_76(ins_rom_7_1_sp_read), .in_77(ins_rom_7_1_sp_write), .in_78(ins_rom_7_1_mar_read),
    .in_79(ins_rom_7_1_mar_write), .in_80(ins_rom_7_1_mdr0_read), .in_81(ins_rom_7_1_mdr0_write),
    .in_82(ins_rom_7_1_mdr0_zero), .in_83(ins_rom_7_1_mdr1_read), .in_84(ins_rom_7_1_mdr1_write),
    .in_85(ins_rom_7_1_mdr1_zero), .in_86(ins_rom_7_1_mdr2_read), .in_87(ins_rom_7_1_mdr2_write),
    .in_88(ins_rom_7_1_mdr2_zero), .in_89(ins_rom_7_1_mem_read), .in_90(ins_rom_7_1_mem_read2),
    .in_91(ins_rom_7_1_mem_write), .in_92(ins_rom_7_1_mdr0_mem_in), .in_93(ins_rom_7_1_mdr1_mem_in),
    .in_94(ins_rom_7_1_mdr2_mem_in), .in_95(ins_rom_7_1_mdr0_reg_in), .in_96(ins_rom_7_1_mdr1_reg_in),
    .in_97(ins_rom_7_1_mdr2_reg_in), .in_98(ins_rom_7_1_mar_reg_id), .in_99(ins_rom_7_1_mdr0_reg_id),
    .in_100(ins_rom_7_1_mdr1_reg_id), .in_101(ins_rom_7_1_mdr2_reg_id), .in_102(ins_rom_7_1_reg_out_mar),
    .in_103(ins_rom_7_1_reg_out_mdr0), .in_104(ins_rom_7_1_reg_out_mdr1), .in_105(ins_rom_7_1_reg_out_mdr2),
    .in_106(ins_rom_7_1_reg_read), .in_107(ins_rom_7_1_reg_write), .in_108(ins_rom_7_1_mar_mdr0),
    .in_109(ins_rom_7_1_mar_mdr1), .in_110(ins_rom_7_1_mar_mdr2), .in_111(ins_rom_7_1_mdr0_mar),
    .in_112(ins_rom_7_1_mdr0_mdr1), .in_113(ins_rom_7_1_mdr0_mdr2), .in_114(ins_rom_7_1_mdr1_mar),
    .in_115(ins_rom_7_1_mdr1_mdr0), .in_116(ins_rom_7_1_mdr1_mdr2), .in_117(ins_rom_7_1_mdr2_mar),
    .in_118(ins_rom_7_1_mdr2_mdr0), .in_119(ins_rom_7_1_mdr2_mdr1), .in_120(ins_rom_7_1_mar_alu_in0),
    .in_121(ins_rom_7_1_mdr0_alu_in0), .in_122(ins_rom_7_1_mdr1_alu_in0), .in_123(ins_rom_7_1_mdr2_alu_in0),
    .in_124(ins_rom_7_1_mar_alu_in1), .in_125(ins_rom_7_1_mdr0_alu_in1), .in_126(ins_rom_7_1_mdr1_alu_in1),
    .in_127(ins_rom_7_1_mdr2_alu_in1), .in_128(ins_rom_7_1_alu_select), .in_129(ins_rom_7_1_alu_read),
    .in_130(ins_rom_7_1_alu_write), .in_131(ins_rom_7_1_alu_readflags), .in_132(ins_rom_7_1_alu_out_mar),
    .in_133(ins_rom_7_1_alu_out_mdr0), .in_134(ins_rom_7_1_alu_out_mdr1), .in_135(ins_rom_7_1_alu_out_mdr2),
    .in_136(ins_rom_7_1_alu_remainder_mar), .in_137(ins_rom_7_1_alu_remainder_mdr0),
    .in_138(ins_rom_7_1_alu_remainder_mdr1), .in_139(ins_rom_7_1_alu_remainder_mdr2),
    .in_140(ins_rom_7_1_cu_endinstruction), .IP_inc(ins_rom_weaver_7_ip_inc),
    .IP_read(ins_rom_weaver_7_ip_read), .IP_write(ins_rom_weaver_7_ip_write),
    .SP_inc(ins_rom_weaver_7_sp_inc), .SP_dec(ins_rom_weaver_7_sp_dec), .SP_read(ins_rom_weaver_7_sp_read),
    .SP_write(ins_rom_weaver_7_sp_write), .MAR_read(ins_rom_weaver_7_mar_read),
    .MAR_write(ins_rom_weaver_7_mar_write), .MDR0_read(ins_rom_weaver_7_mdr0_read),
    .MDR0_write(ins_rom_weaver_7_mdr0_write), .MDR0_zero(ins_rom_weaver_7_mdr0_zero),
    .MDR1_read(ins_rom_weaver_7_mdr1_read), .MDR1_write(ins_rom_weaver_7_mdr1_write),
    .MDR1_zero(ins_rom_weaver_7_mdr1_zero), .MDR2_read(ins_rom_weaver_7_mdr2_read),
    .MDR2_write(ins_rom_weaver_7_mdr2_write), .MDR2_zero(ins_rom_weaver_7_mdr2_zero),
    .MEM_read(ins_rom_weaver_7_mem_read), .MEM_read2(ins_rom_weaver_7_mem_read2),
    .MEM_write(ins_rom_weaver_7_mem_write), .MDR0_MEM_IN(ins_rom_weaver_7_mdr0_mem_in),
    .MDR1_MEM_IN(ins_rom_weaver_7_mdr1_mem_in), .MDR2_MEM_IN(ins_rom_weaver_7_mdr2_mem_in),
    .MDR0_REG_IN(ins_rom_weaver_7_mdr0_reg_in), .MDR1_REG_IN(ins_rom_weaver_7_mdr1_reg_in),
    .MDR2_REG_IN(ins_rom_weaver_7_mdr2_reg_in), .MAR_REG_ID(ins_rom_weaver_7_mar_reg_id),
    .MDR0_REG_ID(ins_rom_weaver_7_mdr0_reg_id), .MDR1_REG_ID(ins_rom_weaver_7_mdr1_reg_id),
    .MDR2_REG_ID(ins_rom_weaver_7_mdr2_reg_id), .REG_OUT_MAR(ins_rom_weaver_7_reg_out_mar),
    .REG_OUT_MDR0(ins_rom_weaver_7_reg_out_mdr0), .REG_OUT_MDR1(ins_rom_weaver_7_reg_out_mdr1),
    .REG_OUT_MDR2(ins_rom_weaver_7_reg_out_mdr2), .REG_read(ins_rom_weaver_7_reg_read),
    .REG_write(ins_rom_weaver_7_reg_write), .MAR_MDR0(ins_rom_weaver_7_mar_mdr0),
    .MAR_MDR1(ins_rom_weaver_7_mar_mdr1), .MAR_MDR2(ins_rom_weaver_7_mar_mdr2),
    .MDR0_MAR(ins_rom_weaver_7_mdr0_mar), .MDR0_MDR1(ins_rom_weaver_7_mdr0_mdr1),
    .MDR0_MDR2(ins_rom_weaver_7_mdr0_mdr2), .MDR1_MAR(ins_rom_weaver_7_mdr1_mar),
    .MDR1_MDR0(ins_rom_weaver_7_mdr1_mdr0), .MDR1_MDR2(ins_rom_weaver_7_mdr1_mdr2),
    .MDR2_MAR(ins_rom_weaver_7_mdr2_mar), .MDR2_MDR0(ins_rom_weaver_7_mdr2_mdr0),
    .MDR2_MDR1(ins_rom_weaver_7_mdr2_mdr1), .MAR_ALU_IN0(ins_rom_weaver_7_mar_alu_in0),
    .MDR0_ALU_IN0(ins_rom_weaver_7_mdr0_alu_in0), .MDR1_ALU_IN0(ins_rom_weaver_7_mdr1_alu_in0),
    .MDR2_ALU_IN0(ins_rom_weaver_7_mdr2_alu_in0), .MAR_ALU_IN1(ins_rom_weaver_7_mar_alu_in1),
    .MDR0_ALU_IN1(ins_rom_weaver_7_mdr0_alu_in1), .MDR1_ALU_IN1(ins_rom_weaver_7_mdr1_alu_in1),
    .MDR2_ALU_IN1(ins_rom_weaver_7_mdr2_alu_in1), .ALU_SELECT(ins_rom_weaver_7_alu_select),
    .ALU_read(ins_rom_weaver_7_alu_read), .ALU_write(ins_rom_weaver_7_alu_write),
    .ALU_readFlags(ins_rom_weaver_7_alu_readflags), .ALU_OUT_MAR(ins_rom_weaver_7_alu_out_mar),
    .ALU_OUT_MDR0(ins_rom_weaver_7_alu_out_mdr0), .ALU_OUT_MDR1(ins_rom_weaver_7_alu_out_mdr1),
    .ALU_OUT_MDR2(ins_rom_weaver_7_alu_out_mdr2), .ALU_REMAINDER_MAR(ins_rom_weaver_7_alu_remainder_mar),
    .ALU_REMAINDER_MDR0(ins_rom_weaver_7_alu_remainder_mdr0),
    .ALU_REMAINDER_MDR1(ins_rom_weaver_7_alu_remainder_mdr1),
    .ALU_REMAINDER_MDR2(ins_rom_weaver_7_alu_remainder_mdr2),
    .CU_endInstruction(ins_rom_weaver_7_cu_endinstruction));
  INS_ROM_8 ins_rom_8_1 (
    .in_1(Instruction), .CLK(demultiplexer_1_out8), .IP_inc(ins_rom_8_1_ip_inc),
    .IP_read(ins_rom_8_1_ip_read), .IP_write(ins_rom_8_1_ip_write), .SP_inc(ins_rom_8_1_sp_inc),
    .SP_dec(ins_rom_8_1_sp_dec), .SP_read(ins_rom_8_1_sp_read), .SP_write(ins_rom_8_1_sp_write),
    .MAR_read(ins_rom_8_1_mar_read), .MAR_write(ins_rom_8_1_mar_write), .MDR0_read(ins_rom_8_1_mdr0_read),
    .MDR0_write(ins_rom_8_1_mdr0_write), .MDR0_zero(ins_rom_8_1_mdr0_zero),
    .MDR1_read(ins_rom_8_1_mdr1_read), .MDR1_write(ins_rom_8_1_mdr1_write),
    .MDR1_zero(ins_rom_8_1_mdr1_zero), .MDR2_read(ins_rom_8_1_mdr2_read),
    .MDR2_write(ins_rom_8_1_mdr2_write), .MDR2_zero(ins_rom_8_1_mdr2_zero), .MEM_read(ins_rom_8_1_mem_read),
    .MEM_read2(ins_rom_8_1_mem_read2), .MEM_write(ins_rom_8_1_mem_write),
    .MDR0_MEM_IN(ins_rom_8_1_mdr0_mem_in), .MDR1_MEM_IN(ins_rom_8_1_mdr1_mem_in),
    .MDR2_MEM_IN(ins_rom_8_1_mdr2_mem_in), .MDR0_REG_IN(ins_rom_8_1_mdr0_reg_in),
    .MDR1_REG_IN(ins_rom_8_1_mdr1_reg_in), .MDR2_REG_IN(ins_rom_8_1_mdr2_reg_in),
    .MAR_REG_ID(ins_rom_8_1_mar_reg_id), .MDR0_REG_ID(ins_rom_8_1_mdr0_reg_id),
    .MDR1_REG_ID(ins_rom_8_1_mdr1_reg_id), .MDR2_REG_ID(ins_rom_8_1_mdr2_reg_id),
    .REG_OUT_MAR(ins_rom_8_1_reg_out_mar), .REG_OUT_MDR0(ins_rom_8_1_reg_out_mdr0),
    .REG_OUT_MDR1(ins_rom_8_1_reg_out_mdr1), .REG_OUT_MDR2(ins_rom_8_1_reg_out_mdr2),
    .REG_read(ins_rom_8_1_reg_read), .REG_write(ins_rom_8_1_reg_write), .MAR_MDR0(ins_rom_8_1_mar_mdr0),
    .MAR_MDR1(ins_rom_8_1_mar_mdr1), .MAR_MDR2(ins_rom_8_1_mar_mdr2), .MDR0_MAR(ins_rom_8_1_mdr0_mar),
    .MDR0_MDR1(ins_rom_8_1_mdr0_mdr1), .MDR0_MDR2(ins_rom_8_1_mdr0_mdr2), .MDR1_MAR(ins_rom_8_1_mdr1_mar),
    .MDR1_MDR0(ins_rom_8_1_mdr1_mdr0), .MDR1_MDR2(ins_rom_8_1_mdr1_mdr2), .MDR2_MAR(ins_rom_8_1_mdr2_mar),
    .MDR2_MDR0(ins_rom_8_1_mdr2_mdr0), .MDR2_MDR1(ins_rom_8_1_mdr2_mdr1),
    .MAR_ALU_IN0(ins_rom_8_1_mar_alu_in0), .MDR0_ALU_IN0(ins_rom_8_1_mdr0_alu_in0),
    .MDR1_ALU_IN0(ins_rom_8_1_mdr1_alu_in0), .MDR2_ALU_IN0(ins_rom_8_1_mdr2_alu_in0),
    .MAR_ALU_IN1(ins_rom_8_1_mar_alu_in1), .MDR0_ALU_IN1(ins_rom_8_1_mdr0_alu_in1),
    .MDR1_ALU_IN1(ins_rom_8_1_mdr1_alu_in1), .MDR2_ALU_IN1(ins_rom_8_1_mdr2_alu_in1),
    .ALU_SELECT(ins_rom_8_1_alu_select), .ALU_read(ins_rom_8_1_alu_read), .ALU_write(ins_rom_8_1_alu_write),
    .ALU_readFlags(ins_rom_8_1_alu_readflags), .ALU_OUT_MAR(ins_rom_8_1_alu_out_mar),
    .ALU_OUT_MDR0(ins_rom_8_1_alu_out_mdr0), .ALU_OUT_MDR1(ins_rom_8_1_alu_out_mdr1),
    .ALU_OUT_MDR2(ins_rom_8_1_alu_out_mdr2), .ALU_REMAINDER_MAR(ins_rom_8_1_alu_remainder_mar),
    .ALU_REMAINDER_MDR0(ins_rom_8_1_alu_remainder_mdr0), .ALU_REMAINDER_MDR1(ins_rom_8_1_alu_remainder_mdr1),
    .ALU_REMAINDER_MDR2(ins_rom_8_1_alu_remainder_mdr2), .CU_endInstruction(ins_rom_8_1_cu_endinstruction));
  INS_ROM_WEAVER ins_rom_weaver_8 (
    .in_1(ins_rom_weaver_7_ip_inc), .in_2(ins_rom_weaver_7_ip_read), .in_3(ins_rom_weaver_7_ip_write),
    .in_4(ins_rom_weaver_7_sp_inc), .in_5(ins_rom_weaver_7_sp_dec), .in_6(ins_rom_weaver_7_sp_read),
    .in_7(ins_rom_weaver_7_sp_write), .in_8(ins_rom_weaver_7_mar_read), .in_9(ins_rom_weaver_7_mar_write),
    .in_10(ins_rom_weaver_7_mdr0_read), .in_11(ins_rom_weaver_7_mdr0_write),
    .in_12(ins_rom_weaver_7_mdr0_zero), .in_13(ins_rom_weaver_7_mdr1_read),
    .in_14(ins_rom_weaver_7_mdr1_write), .in_15(ins_rom_weaver_7_mdr1_zero),
    .in_16(ins_rom_weaver_7_mdr2_read), .in_17(ins_rom_weaver_7_mdr2_write),
    .in_18(ins_rom_weaver_7_mdr2_zero), .in_19(ins_rom_weaver_7_mem_read),
    .in_20(ins_rom_weaver_7_mem_read2), .in_21(ins_rom_weaver_7_mem_write),
    .in_22(ins_rom_weaver_7_mdr0_mem_in), .in_23(ins_rom_weaver_7_mdr1_mem_in),
    .in_24(ins_rom_weaver_7_mdr2_mem_in), .in_25(ins_rom_weaver_7_mdr0_reg_in),
    .in_26(ins_rom_weaver_7_mdr1_reg_in), .in_27(ins_rom_weaver_7_mdr2_reg_in),
    .in_28(ins_rom_weaver_7_mar_reg_id), .in_29(ins_rom_weaver_7_mdr0_reg_id),
    .in_30(ins_rom_weaver_7_mdr1_reg_id), .in_31(ins_rom_weaver_7_mdr2_reg_id),
    .in_32(ins_rom_weaver_7_reg_out_mar), .in_33(ins_rom_weaver_7_reg_out_mdr0),
    .in_34(ins_rom_weaver_7_reg_out_mdr1), .in_35(ins_rom_weaver_7_reg_out_mdr2),
    .in_36(ins_rom_weaver_7_reg_read), .in_37(ins_rom_weaver_7_reg_write), .in_38(ins_rom_weaver_7_mar_mdr0),
    .in_39(ins_rom_weaver_7_mar_mdr1), .in_40(ins_rom_weaver_7_mar_mdr2), .in_41(ins_rom_weaver_7_mdr0_mar),
    .in_42(ins_rom_weaver_7_mdr0_mdr1), .in_43(ins_rom_weaver_7_mdr0_mdr2),
    .in_44(ins_rom_weaver_7_mdr1_mar), .in_45(ins_rom_weaver_7_mdr1_mdr0),
    .in_46(ins_rom_weaver_7_mdr1_mdr2), .in_47(ins_rom_weaver_7_mdr2_mar),
    .in_48(ins_rom_weaver_7_mdr2_mdr0), .in_49(ins_rom_weaver_7_mdr2_mdr1),
    .in_50(ins_rom_weaver_7_mar_alu_in0), .in_51(ins_rom_weaver_7_mdr0_alu_in0),
    .in_52(ins_rom_weaver_7_mdr1_alu_in0), .in_53(ins_rom_weaver_7_mdr2_alu_in0),
    .in_54(ins_rom_weaver_7_mar_alu_in1), .in_55(ins_rom_weaver_7_mdr0_alu_in1),
    .in_56(ins_rom_weaver_7_mdr1_alu_in1), .in_57(ins_rom_weaver_7_mdr2_alu_in1),
    .in_58(ins_rom_weaver_7_alu_select), .in_59(ins_rom_weaver_7_alu_read),
    .in_60(ins_rom_weaver_7_alu_write), .in_61(ins_rom_weaver_7_alu_readflags),
    .in_62(ins_rom_weaver_7_alu_out_mar), .in_63(ins_rom_weaver_7_alu_out_mdr0),
    .in_64(ins_rom_weaver_7_alu_out_mdr1), .in_65(ins_rom_weaver_7_alu_out_mdr2),
    .in_66(ins_rom_weaver_7_alu_remainder_mar), .in_67(ins_rom_weaver_7_alu_remainder_mdr0),
    .in_68(ins_rom_weaver_7_alu_remainder_mdr1), .in_69(ins_rom_weaver_7_alu_remainder_mdr2),
    .in_70(ins_rom_weaver_7_cu_endinstruction), .in_71(ins_rom_8_1_ip_inc), .in_72(ins_rom_8_1_ip_read),
    .in_73(ins_rom_8_1_ip_write), .in_74(ins_rom_8_1_sp_inc), .in_75(ins_rom_8_1_sp_dec),
    .in_76(ins_rom_8_1_sp_read), .in_77(ins_rom_8_1_sp_write), .in_78(ins_rom_8_1_mar_read),
    .in_79(ins_rom_8_1_mar_write), .in_80(ins_rom_8_1_mdr0_read), .in_81(ins_rom_8_1_mdr0_write),
    .in_82(ins_rom_8_1_mdr0_zero), .in_83(ins_rom_8_1_mdr1_read), .in_84(ins_rom_8_1_mdr1_write),
    .in_85(ins_rom_8_1_mdr1_zero), .in_86(ins_rom_8_1_mdr2_read), .in_87(ins_rom_8_1_mdr2_write),
    .in_88(ins_rom_8_1_mdr2_zero), .in_89(ins_rom_8_1_mem_read), .in_90(ins_rom_8_1_mem_read2),
    .in_91(ins_rom_8_1_mem_write), .in_92(ins_rom_8_1_mdr0_mem_in), .in_93(ins_rom_8_1_mdr1_mem_in),
    .in_94(ins_rom_8_1_mdr2_mem_in), .in_95(ins_rom_8_1_mdr0_reg_in), .in_96(ins_rom_8_1_mdr1_reg_in),
    .in_97(ins_rom_8_1_mdr2_reg_in), .in_98(ins_rom_8_1_mar_reg_id), .in_99(ins_rom_8_1_mdr0_reg_id),
    .in_100(ins_rom_8_1_mdr1_reg_id), .in_101(ins_rom_8_1_mdr2_reg_id), .in_102(ins_rom_8_1_reg_out_mar),
    .in_103(ins_rom_8_1_reg_out_mdr0), .in_104(ins_rom_8_1_reg_out_mdr1), .in_105(ins_rom_8_1_reg_out_mdr2),
    .in_106(ins_rom_8_1_reg_read), .in_107(ins_rom_8_1_reg_write), .in_108(ins_rom_8_1_mar_mdr0),
    .in_109(ins_rom_8_1_mar_mdr1), .in_110(ins_rom_8_1_mar_mdr2), .in_111(ins_rom_8_1_mdr0_mar),
    .in_112(ins_rom_8_1_mdr0_mdr1), .in_113(ins_rom_8_1_mdr0_mdr2), .in_114(ins_rom_8_1_mdr1_mar),
    .in_115(ins_rom_8_1_mdr1_mdr0), .in_116(ins_rom_8_1_mdr1_mdr2), .in_117(ins_rom_8_1_mdr2_mar),
    .in_118(ins_rom_8_1_mdr2_mdr0), .in_119(ins_rom_8_1_mdr2_mdr1), .in_120(ins_rom_8_1_mar_alu_in0),
    .in_121(ins_rom_8_1_mdr0_alu_in0), .in_122(ins_rom_8_1_mdr1_alu_in0), .in_123(ins_rom_8_1_mdr2_alu_in0),
    .in_124(ins_rom_8_1_mar_alu_in1), .in_125(ins_rom_8_1_mdr0_alu_in1), .in_126(ins_rom_8_1_mdr1_alu_in1),
    .in_127(ins_rom_8_1_mdr2_alu_in1), .in_128(ins_rom_8_1_alu_select), .in_129(ins_rom_8_1_alu_read),
    .in_130(ins_rom_8_1_alu_write), .in_131(ins_rom_8_1_alu_readflags), .in_132(ins_rom_8_1_alu_out_mar),
    .in_133(ins_rom_8_1_alu_out_mdr0), .in_134(ins_rom_8_1_alu_out_mdr1), .in_135(ins_rom_8_1_alu_out_mdr2),
    .in_136(ins_rom_8_1_alu_remainder_mar), .in_137(ins_rom_8_1_alu_remainder_mdr0),
    .in_138(ins_rom_8_1_alu_remainder_mdr1), .in_139(ins_rom_8_1_alu_remainder_mdr2),
    .in_140(ins_rom_8_1_cu_endinstruction), .IP_inc(ins_rom_weaver_8_ip_inc),
    .IP_read(ins_rom_weaver_8_ip_read), .IP_write(ins_rom_weaver_8_ip_write),
    .SP_inc(ins_rom_weaver_8_sp_inc), .SP_dec(ins_rom_weaver_8_sp_dec), .SP_read(ins_rom_weaver_8_sp_read),
    .SP_write(ins_rom_weaver_8_sp_write), .MAR_read(ins_rom_weaver_8_mar_read),
    .MAR_write(ins_rom_weaver_8_mar_write), .MDR0_read(ins_rom_weaver_8_mdr0_read),
    .MDR0_write(ins_rom_weaver_8_mdr0_write), .MDR0_zero(ins_rom_weaver_8_mdr0_zero),
    .MDR1_read(ins_rom_weaver_8_mdr1_read), .MDR1_write(ins_rom_weaver_8_mdr1_write),
    .MDR1_zero(ins_rom_weaver_8_mdr1_zero), .MDR2_read(ins_rom_weaver_8_mdr2_read),
    .MDR2_write(ins_rom_weaver_8_mdr2_write), .MDR2_zero(ins_rom_weaver_8_mdr2_zero),
    .MEM_read(ins_rom_weaver_8_mem_read), .MEM_read2(ins_rom_weaver_8_mem_read2),
    .MEM_write(ins_rom_weaver_8_mem_write), .MDR0_MEM_IN(ins_rom_weaver_8_mdr0_mem_in),
    .MDR1_MEM_IN(ins_rom_weaver_8_mdr1_mem_in), .MDR2_MEM_IN(ins_rom_weaver_8_mdr2_mem_in),
    .MDR0_REG_IN(ins_rom_weaver_8_mdr0_reg_in), .MDR1_REG_IN(ins_rom_weaver_8_mdr1_reg_in),
    .MDR2_REG_IN(ins_rom_weaver_8_mdr2_reg_in), .MAR_REG_ID(ins_rom_weaver_8_mar_reg_id),
    .MDR0_REG_ID(ins_rom_weaver_8_mdr0_reg_id), .MDR1_REG_ID(ins_rom_weaver_8_mdr1_reg_id),
    .MDR2_REG_ID(ins_rom_weaver_8_mdr2_reg_id), .REG_OUT_MAR(ins_rom_weaver_8_reg_out_mar),
    .REG_OUT_MDR0(ins_rom_weaver_8_reg_out_mdr0), .REG_OUT_MDR1(ins_rom_weaver_8_reg_out_mdr1),
    .REG_OUT_MDR2(ins_rom_weaver_8_reg_out_mdr2), .REG_read(ins_rom_weaver_8_reg_read),
    .REG_write(ins_rom_weaver_8_reg_write), .MAR_MDR0(ins_rom_weaver_8_mar_mdr0),
    .MAR_MDR1(ins_rom_weaver_8_mar_mdr1), .MAR_MDR2(ins_rom_weaver_8_mar_mdr2),
    .MDR0_MAR(ins_rom_weaver_8_mdr0_mar), .MDR0_MDR1(ins_rom_weaver_8_mdr0_mdr1),
    .MDR0_MDR2(ins_rom_weaver_8_mdr0_mdr2), .MDR1_MAR(ins_rom_weaver_8_mdr1_mar),
    .MDR1_MDR0(ins_rom_weaver_8_mdr1_mdr0), .MDR1_MDR2(ins_rom_weaver_8_mdr1_mdr2),
    .MDR2_MAR(ins_rom_weaver_8_mdr2_mar), .MDR2_MDR0(ins_rom_weaver_8_mdr2_mdr0),
    .MDR2_MDR1(ins_rom_weaver_8_mdr2_mdr1), .MAR_ALU_IN0(ins_rom_weaver_8_mar_alu_in0),
    .MDR0_ALU_IN0(ins_rom_weaver_8_mdr0_alu_in0), .MDR1_ALU_IN0(ins_rom_weaver_8_mdr1_alu_in0),
    .MDR2_ALU_IN0(ins_rom_weaver_8_mdr2_alu_in0), .MAR_ALU_IN1(ins_rom_weaver_8_mar_alu_in1),
    .MDR0_ALU_IN1(ins_rom_weaver_8_mdr0_alu_in1), .MDR1_ALU_IN1(ins_rom_weaver_8_mdr1_alu_in1),
    .MDR2_ALU_IN1(ins_rom_weaver_8_mdr2_alu_in1), .ALU_SELECT(ins_rom_weaver_8_alu_select),
    .ALU_read(ins_rom_weaver_8_alu_read), .ALU_write(ins_rom_weaver_8_alu_write),
    .ALU_readFlags(ins_rom_weaver_8_alu_readflags), .ALU_OUT_MAR(ins_rom_weaver_8_alu_out_mar),
    .ALU_OUT_MDR0(ins_rom_weaver_8_alu_out_mdr0), .ALU_OUT_MDR1(ins_rom_weaver_8_alu_out_mdr1),
    .ALU_OUT_MDR2(ins_rom_weaver_8_alu_out_mdr2), .ALU_REMAINDER_MAR(ins_rom_weaver_8_alu_remainder_mar),
    .ALU_REMAINDER_MDR0(ins_rom_weaver_8_alu_remainder_mdr0),
    .ALU_REMAINDER_MDR1(ins_rom_weaver_8_alu_remainder_mdr1),
    .ALU_REMAINDER_MDR2(ins_rom_weaver_8_alu_remainder_mdr2),
    .CU_endInstruction(ins_rom_weaver_8_cu_endinstruction));
  INS_ROM_9 ins_rom_9_1 (
    .in_1(Instruction), .CLK(demultiplexer_1_out9), .IP_inc(ins_rom_9_1_ip_inc),
    .IP_read(ins_rom_9_1_ip_read), .IP_write(ins_rom_9_1_ip_write), .SP_inc(ins_rom_9_1_sp_inc),
    .SP_dec(ins_rom_9_1_sp_dec), .SP_read(ins_rom_9_1_sp_read), .SP_write(ins_rom_9_1_sp_write),
    .MAR_read(ins_rom_9_1_mar_read), .MAR_write(ins_rom_9_1_mar_write), .MDR0_read(ins_rom_9_1_mdr0_read),
    .MDR0_write(ins_rom_9_1_mdr0_write), .MDR0_zero(ins_rom_9_1_mdr0_zero),
    .MDR1_read(ins_rom_9_1_mdr1_read), .MDR1_write(ins_rom_9_1_mdr1_write),
    .MDR1_zero(ins_rom_9_1_mdr1_zero), .MDR2_read(ins_rom_9_1_mdr2_read),
    .MDR2_write(ins_rom_9_1_mdr2_write), .MDR2_zero(ins_rom_9_1_mdr2_zero), .MEM_read(ins_rom_9_1_mem_read),
    .MEM_read2(ins_rom_9_1_mem_read2), .MEM_write(ins_rom_9_1_mem_write),
    .MDR0_MEM_IN(ins_rom_9_1_mdr0_mem_in), .MDR1_MEM_IN(ins_rom_9_1_mdr1_mem_in),
    .MDR2_MEM_IN(ins_rom_9_1_mdr2_mem_in), .MDR0_REG_IN(ins_rom_9_1_mdr0_reg_in),
    .MDR1_REG_IN(ins_rom_9_1_mdr1_reg_in), .MDR2_REG_IN(ins_rom_9_1_mdr2_reg_in),
    .MAR_REG_ID(ins_rom_9_1_mar_reg_id), .MDR0_REG_ID(ins_rom_9_1_mdr0_reg_id),
    .MDR1_REG_ID(ins_rom_9_1_mdr1_reg_id), .MDR2_REG_ID(ins_rom_9_1_mdr2_reg_id),
    .REG_OUT_MAR(ins_rom_9_1_reg_out_mar), .REG_OUT_MDR0(ins_rom_9_1_reg_out_mdr0),
    .REG_OUT_MDR1(ins_rom_9_1_reg_out_mdr1), .REG_OUT_MDR2(ins_rom_9_1_reg_out_mdr2),
    .REG_read(ins_rom_9_1_reg_read), .REG_write(ins_rom_9_1_reg_write), .MAR_MDR0(ins_rom_9_1_mar_mdr0),
    .MAR_MDR1(ins_rom_9_1_mar_mdr1), .MAR_MDR2(ins_rom_9_1_mar_mdr2), .MDR0_MAR(ins_rom_9_1_mdr0_mar),
    .MDR0_MDR1(ins_rom_9_1_mdr0_mdr1), .MDR0_MDR2(ins_rom_9_1_mdr0_mdr2), .MDR1_MAR(ins_rom_9_1_mdr1_mar),
    .MDR1_MDR0(ins_rom_9_1_mdr1_mdr0), .MDR1_MDR2(ins_rom_9_1_mdr1_mdr2), .MDR2_MAR(ins_rom_9_1_mdr2_mar),
    .MDR2_MDR0(ins_rom_9_1_mdr2_mdr0), .MDR2_MDR1(ins_rom_9_1_mdr2_mdr1),
    .MAR_ALU_IN0(ins_rom_9_1_mar_alu_in0), .MDR0_ALU_IN0(ins_rom_9_1_mdr0_alu_in0),
    .MDR1_ALU_IN0(ins_rom_9_1_mdr1_alu_in0), .MDR2_ALU_IN0(ins_rom_9_1_mdr2_alu_in0),
    .MAR_ALU_IN1(ins_rom_9_1_mar_alu_in1), .MDR0_ALU_IN1(ins_rom_9_1_mdr0_alu_in1),
    .MDR1_ALU_IN1(ins_rom_9_1_mdr1_alu_in1), .MDR2_ALU_IN1(ins_rom_9_1_mdr2_alu_in1),
    .ALU_SELECT(ins_rom_9_1_alu_select), .ALU_read(ins_rom_9_1_alu_read), .ALU_write(ins_rom_9_1_alu_write),
    .ALU_readFlags(ins_rom_9_1_alu_readflags), .ALU_OUT_MAR(ins_rom_9_1_alu_out_mar),
    .ALU_OUT_MDR0(ins_rom_9_1_alu_out_mdr0), .ALU_OUT_MDR1(ins_rom_9_1_alu_out_mdr1),
    .ALU_OUT_MDR2(ins_rom_9_1_alu_out_mdr2), .ALU_REMAINDER_MAR(ins_rom_9_1_alu_remainder_mar),
    .ALU_REMAINDER_MDR0(ins_rom_9_1_alu_remainder_mdr0), .ALU_REMAINDER_MDR1(ins_rom_9_1_alu_remainder_mdr1),
    .ALU_REMAINDER_MDR2(ins_rom_9_1_alu_remainder_mdr2), .CU_endInstruction(ins_rom_9_1_cu_endinstruction));
  INS_ROM_WEAVER ins_rom_weaver_9 (
    .in_1(ins_rom_weaver_8_ip_inc), .in_2(ins_rom_weaver_8_ip_read), .in_3(ins_rom_weaver_8_ip_write),
    .in_4(ins_rom_weaver_8_sp_inc), .in_5(ins_rom_weaver_8_sp_dec), .in_6(ins_rom_weaver_8_sp_read),
    .in_7(ins_rom_weaver_8_sp_write), .in_8(ins_rom_weaver_8_mar_read), .in_9(ins_rom_weaver_8_mar_write),
    .in_10(ins_rom_weaver_8_mdr0_read), .in_11(ins_rom_weaver_8_mdr0_write),
    .in_12(ins_rom_weaver_8_mdr0_zero), .in_13(ins_rom_weaver_8_mdr1_read),
    .in_14(ins_rom_weaver_8_mdr1_write), .in_15(ins_rom_weaver_8_mdr1_zero),
    .in_16(ins_rom_weaver_8_mdr2_read), .in_17(ins_rom_weaver_8_mdr2_write),
    .in_18(ins_rom_weaver_8_mdr2_zero), .in_19(ins_rom_weaver_8_mem_read),
    .in_20(ins_rom_weaver_8_mem_read2), .in_21(ins_rom_weaver_8_mem_write),
    .in_22(ins_rom_weaver_8_mdr0_mem_in), .in_23(ins_rom_weaver_8_mdr1_mem_in),
    .in_24(ins_rom_weaver_8_mdr2_mem_in), .in_25(ins_rom_weaver_8_mdr0_reg_in),
    .in_26(ins_rom_weaver_8_mdr1_reg_in), .in_27(ins_rom_weaver_8_mdr2_reg_in),
    .in_28(ins_rom_weaver_8_mar_reg_id), .in_29(ins_rom_weaver_8_mdr0_reg_id),
    .in_30(ins_rom_weaver_8_mdr1_reg_id), .in_31(ins_rom_weaver_8_mdr2_reg_id),
    .in_32(ins_rom_weaver_8_reg_out_mar), .in_33(ins_rom_weaver_8_reg_out_mdr0),
    .in_34(ins_rom_weaver_8_reg_out_mdr1), .in_35(ins_rom_weaver_8_reg_out_mdr2),
    .in_36(ins_rom_weaver_8_reg_read), .in_37(ins_rom_weaver_8_reg_write), .in_38(ins_rom_weaver_8_mar_mdr0),
    .in_39(ins_rom_weaver_8_mar_mdr1), .in_40(ins_rom_weaver_8_mar_mdr2), .in_41(ins_rom_weaver_8_mdr0_mar),
    .in_42(ins_rom_weaver_8_mdr0_mdr1), .in_43(ins_rom_weaver_8_mdr0_mdr2),
    .in_44(ins_rom_weaver_8_mdr1_mar), .in_45(ins_rom_weaver_8_mdr1_mdr0),
    .in_46(ins_rom_weaver_8_mdr1_mdr2), .in_47(ins_rom_weaver_8_mdr2_mar),
    .in_48(ins_rom_weaver_8_mdr2_mdr0), .in_49(ins_rom_weaver_8_mdr2_mdr1),
    .in_50(ins_rom_weaver_8_mar_alu_in0), .in_51(ins_rom_weaver_8_mdr0_alu_in0),
    .in_52(ins_rom_weaver_8_mdr1_alu_in0), .in_53(ins_rom_weaver_8_mdr2_alu_in0),
    .in_54(ins_rom_weaver_8_mar_alu_in1), .in_55(ins_rom_weaver_8_mdr0_alu_in1),
    .in_56(ins_rom_weaver_8_mdr1_alu_in1), .in_57(ins_rom_weaver_8_mdr2_alu_in1),
    .in_58(ins_rom_weaver_8_alu_select), .in_59(ins_rom_weaver_8_alu_read),
    .in_60(ins_rom_weaver_8_alu_write), .in_61(ins_rom_weaver_8_alu_readflags),
    .in_62(ins_rom_weaver_8_alu_out_mar), .in_63(ins_rom_weaver_8_alu_out_mdr0),
    .in_64(ins_rom_weaver_8_alu_out_mdr1), .in_65(ins_rom_weaver_8_alu_out_mdr2),
    .in_66(ins_rom_weaver_8_alu_remainder_mar), .in_67(ins_rom_weaver_8_alu_remainder_mdr0),
    .in_68(ins_rom_weaver_8_alu_remainder_mdr1), .in_69(ins_rom_weaver_8_alu_remainder_mdr2),
    .in_70(ins_rom_weaver_8_cu_endinstruction), .in_71(ins_rom_9_1_ip_inc), .in_72(ins_rom_9_1_ip_read),
    .in_73(ins_rom_9_1_ip_write), .in_74(ins_rom_9_1_sp_inc), .in_75(ins_rom_9_1_sp_dec),
    .in_76(ins_rom_9_1_sp_read), .in_77(ins_rom_9_1_sp_write), .in_78(ins_rom_9_1_mar_read),
    .in_79(ins_rom_9_1_mar_write), .in_80(ins_rom_9_1_mdr0_read), .in_81(ins_rom_9_1_mdr0_write),
    .in_82(ins_rom_9_1_mdr0_zero), .in_83(ins_rom_9_1_mdr1_read), .in_84(ins_rom_9_1_mdr1_write),
    .in_85(ins_rom_9_1_mdr1_zero), .in_86(ins_rom_9_1_mdr2_read), .in_87(ins_rom_9_1_mdr2_write),
    .in_88(ins_rom_9_1_mdr2_zero), .in_89(ins_rom_9_1_mem_read), .in_90(ins_rom_9_1_mem_read2),
    .in_91(ins_rom_9_1_mem_write), .in_92(ins_rom_9_1_mdr0_mem_in), .in_93(ins_rom_9_1_mdr1_mem_in),
    .in_94(ins_rom_9_1_mdr2_mem_in), .in_95(ins_rom_9_1_mdr0_reg_in), .in_96(ins_rom_9_1_mdr1_reg_in),
    .in_97(ins_rom_9_1_mdr2_reg_in), .in_98(ins_rom_9_1_mar_reg_id), .in_99(ins_rom_9_1_mdr0_reg_id),
    .in_100(ins_rom_9_1_mdr1_reg_id), .in_101(ins_rom_9_1_mdr2_reg_id), .in_102(ins_rom_9_1_reg_out_mar),
    .in_103(ins_rom_9_1_reg_out_mdr0), .in_104(ins_rom_9_1_reg_out_mdr1), .in_105(ins_rom_9_1_reg_out_mdr2),
    .in_106(ins_rom_9_1_reg_read), .in_107(ins_rom_9_1_reg_write), .in_108(ins_rom_9_1_mar_mdr0),
    .in_109(ins_rom_9_1_mar_mdr1), .in_110(ins_rom_9_1_mar_mdr2), .in_111(ins_rom_9_1_mdr0_mar),
    .in_112(ins_rom_9_1_mdr0_mdr1), .in_113(ins_rom_9_1_mdr0_mdr2), .in_114(ins_rom_9_1_mdr1_mar),
    .in_115(ins_rom_9_1_mdr1_mdr0), .in_116(ins_rom_9_1_mdr1_mdr2), .in_117(ins_rom_9_1_mdr2_mar),
    .in_118(ins_rom_9_1_mdr2_mdr0), .in_119(ins_rom_9_1_mdr2_mdr1), .in_120(ins_rom_9_1_mar_alu_in0),
    .in_121(ins_rom_9_1_mdr0_alu_in0), .in_122(ins_rom_9_1_mdr1_alu_in0), .in_123(ins_rom_9_1_mdr2_alu_in0),
    .in_124(ins_rom_9_1_mar_alu_in1), .in_125(ins_rom_9_1_mdr0_alu_in1), .in_126(ins_rom_9_1_mdr1_alu_in1),
    .in_127(ins_rom_9_1_mdr2_alu_in1), .in_128(ins_rom_9_1_alu_select), .in_129(ins_rom_9_1_alu_read),
    .in_130(ins_rom_9_1_alu_write), .in_131(ins_rom_9_1_alu_readflags), .in_132(ins_rom_9_1_alu_out_mar),
    .in_133(ins_rom_9_1_alu_out_mdr0), .in_134(ins_rom_9_1_alu_out_mdr1), .in_135(ins_rom_9_1_alu_out_mdr2),
    .in_136(ins_rom_9_1_alu_remainder_mar), .in_137(ins_rom_9_1_alu_remainder_mdr0),
    .in_138(ins_rom_9_1_alu_remainder_mdr1), .in_139(ins_rom_9_1_alu_remainder_mdr2),
    .in_140(ins_rom_9_1_cu_endinstruction), .IP_inc(IP_inc), .IP_read(IP_read), .IP_write(IP_write),
    .SP_inc(SP_inc), .SP_dec(SP_dec), .SP_read(SP_read), .SP_write(SP_write), .MAR_read(MAR_read),
    .MAR_write(MAR_write), .MDR0_read(MDR0_read), .MDR0_write(MDR0_write), .MDR0_zero(MDR0_zero),
    .MDR1_read(MDR1_read), .MDR1_write(MDR1_write), .MDR1_zero(MDR1_zero), .MDR2_read(MDR2_read),
    .MDR2_write(MDR2_write), .MDR2_zero(MDR2_zero), .MEM_read(MEM_read), .MEM_read2(MEM_read2),
    .MEM_write(MEM_write), .MDR0_MEM_IN(MDR0_MEM_IN), .MDR1_MEM_IN(MDR1_MEM_IN), .MDR2_MEM_IN(MDR2_MEM_IN),
    .MDR0_REG_IN(MDR0_REG_IN), .MDR1_REG_IN(MDR1_REG_IN), .MDR2_REG_IN(MDR2_REG_IN), .MAR_REG_ID(MAR_REG_ID),
    .MDR0_REG_ID(MDR0_REG_ID), .MDR1_REG_ID(MDR1_REG_ID), .MDR2_REG_ID(MDR2_REG_ID),
    .REG_OUT_MAR(REG_OUT_MAR), .REG_OUT_MDR0(REG_OUT_MDR0), .REG_OUT_MDR1(REG_OUT_MDR1),
    .REG_OUT_MDR2(REG_OUT_MDR2), .REG_read(REG_read), .REG_write(REG_write), .MAR_MDR0(MAR_MDR0),
    .MAR_MDR1(MAR_MDR1), .MAR_MDR2(MAR_MDR2), .MDR0_MAR(MDR0_MAR), .MDR0_MDR1(MDR0_MDR1),
    .MDR0_MDR2(MDR0_MDR2), .MDR1_MAR(MDR1_MAR), .MDR1_MDR0(MDR1_MDR0), .MDR1_MDR2(MDR1_MDR2),
    .MDR2_MAR(MDR2_MAR), .MDR2_MDR0(MDR2_MDR0), .MDR2_MDR1(MDR2_MDR1), .MAR_ALU_IN0(MAR_ALU_IN0),
    .MDR0_ALU_IN0(MDR0_ALU_IN0), .MDR1_ALU_IN0(MDR1_ALU_IN0), .MDR2_ALU_IN0(MDR2_ALU_IN0),
    .MAR_ALU_IN1(MAR_ALU_IN1), .MDR0_ALU_IN1(MDR0_ALU_IN1), .MDR1_ALU_IN1(MDR1_ALU_IN1),
    .MDR2_ALU_IN1(MDR2_ALU_IN1), .ALU_SELECT(ALU_SELECT), .ALU_read(ALU_read), .ALU_write(ALU_write),
    .ALU_readFlags(ALU_readFlags), .ALU_OUT_MAR(ALU_OUT_MAR), .ALU_OUT_MDR0(ALU_OUT_MDR0),
    .ALU_OUT_MDR1(ALU_OUT_MDR1), .ALU_OUT_MDR2(ALU_OUT_MDR2), .ALU_REMAINDER_MAR(ALU_REMAINDER_MAR),
    .ALU_REMAINDER_MDR0(ALU_REMAINDER_MDR0), .ALU_REMAINDER_MDR1(ALU_REMAINDER_MDR1),
    .ALU_REMAINDER_MDR2(ALU_REMAINDER_MDR2), .CU_endInstruction(CU_endInstruction));
endmodule

module INS_ROM_WEAVER (
  input  in_1,
  input  in_2,
  input  in_3,
  input  in_4,
  input  in_5,
  input  in_6,
  input  in_7,
  input  in_8,
  input  in_9,
  input  in_10,
  input  in_11,
  input  in_12,
  input  in_13,
  input  in_14,
  input  in_15,
  input  in_16,
  input  in_17,
  input  in_18,
  input  in_19,
  input  in_20,
  input  in_21,
  input  in_22,
  input  in_23,
  input  in_24,
  input  in_25,
  input  in_26,
  input  in_27,
  input  in_28,
  input  in_29,
  input  in_30,
  input  in_31,
  input  in_32,
  input  in_33,
  input  in_34,
  input  in_35,
  input  in_36,
  input  in_37,
  input  in_38,
  input  in_39,
  input  in_40,
  input  in_41,
  input  in_42,
  input  in_43,
  input  in_44,
  input  in_45,
  input  in_46,
  input  in_47,
  input  in_48,
  input  in_49,
  input  in_50,
  input  in_51,
  input  in_52,
  input  in_53,
  input  in_54,
  input  in_55,
  input  in_56,
  input  in_57,
  input  [7:0] in_58,
  input  in_59,
  input  in_60,
  input  in_61,
  input  in_62,
  input  in_63,
  input  in_64,
  input  in_65,
  input  in_66,
  input  in_67,
  input  in_68,
  input  in_69,
  input  in_70,
  input  in_71,
  input  in_72,
  input  in_73,
  input  in_74,
  input  in_75,
  input  in_76,
  input  in_77,
  input  in_78,
  input  in_79,
  input  in_80,
  input  in_81,
  input  in_82,
  input  in_83,
  input  in_84,
  input  in_85,
  input  in_86,
  input  in_87,
  input  in_88,
  input  in_89,
  input  in_90,
  input  in_91,
  input  in_92,
  input  in_93,
  input  in_94,
  input  in_95,
  input  in_96,
  input  in_97,
  input  in_98,
  input  in_99,
  input  in_100,
  input  in_101,
  input  in_102,
  input  in_103,
  input  in_104,
  input  in_105,
  input  in_106,
  input  in_107,
  input  in_108,
  input  in_109,
  input  in_110,
  input  in_111,
  input  in_112,
  input  in_113,
  input  in_114,
  input  in_115,
  input  in_116,
  input  in_117,
  input  in_118,
  input  in_119,
  input  in_120,
  input  in_121,
  input  in_122,
  input  in_123,
  input  in_124,
  input  in_125,
  input  in_126,
  input  in_127,
  input  [7:0] in_128,
  input  in_129,
  input  in_130,
  input  in_131,
  input  in_132,
  input  in_133,
  input  in_134,
  input  in_135,
  input  in_136,
  input  in_137,
  input  in_138,
  input  in_139,
  input  in_140,
  output IP_inc,
  output IP_read,
  output IP_write,
  output SP_inc,
  output SP_dec,
  output SP_read,
  output SP_write,
  output MAR_read,
  output MAR_write,
  output MDR0_read,
  output MDR0_write,
  output MDR0_zero,
  output MDR1_read,
  output MDR1_write,
  output MDR1_zero,
  output MDR2_read,
  output MDR2_write,
  output MDR2_zero,
  output MEM_read,
  output MEM_read2,
  output MEM_write,
  output MDR0_MEM_IN,
  output MDR1_MEM_IN,
  output MDR2_MEM_IN,
  output MDR0_REG_IN,
  output MDR1_REG_IN,
  output MDR2_REG_IN,
  output MAR_REG_ID,
  output MDR0_REG_ID,
  output MDR1_REG_ID,
  output MDR2_REG_ID,
  output REG_OUT_MAR,
  output REG_OUT_MDR0,
  output REG_OUT_MDR1,
  output REG_OUT_MDR2,
  output REG_read,
  output REG_write,
  output MAR_MDR0,
  output MAR_MDR1,
  output MAR_MDR2,
  output MDR0_MAR,
  output MDR0_MDR1,
  output MDR0_MDR2,
  output MDR1_MAR,
  output MDR1_MDR0,
  output MDR1_MDR2,
  output MDR2_MAR,
  output MDR2_MDR0,
  output MDR2_MDR1,
  output MAR_ALU_IN0,
  output MDR0_ALU_IN0,
  output MDR1_ALU_IN0,
  output MDR2_ALU_IN0,
  output MAR_ALU_IN1,
  output MDR0_ALU_IN1,
  output MDR1_ALU_IN1,
  output MDR2_ALU_IN1,
  output [7:0] ALU_SELECT,
  output ALU_read,
  output ALU_write,
  output ALU_readFlags,
  output ALU_OUT_MAR,
  output ALU_OUT_MDR0,
  output ALU_OUT_MDR1,
  output ALU_OUT_MDR2,
  output ALU_REMAINDER_MAR,
  output ALU_REMAINDER_MDR0,
  output ALU_REMAINDER_MDR1,
  output ALU_REMAINDER_MDR2,
  output CU_endInstruction
);

  or or_1 (IP_inc, in_1, in_71);
  or or_2 (IP_read, in_2, in_72);
  or or_3 (IP_write, in_3, in_73);
  or or_4 (SP_inc, in_4, in_74);
  or or_5 (SP_dec, in_5, in_75);
  or or_6 (SP_read, in_6, in_76);
  or or_7 (SP_write, in_7, in_77);
  or or_8 (MAR_read, in_8, in_78);
  or or_9 (MAR_write, in_9, in_79);
  or or_10 (MDR0_read, in_10, in_80);
  or or_11 (MDR0_write, in_11, in_81);
  or or_12 (MDR0_zero, in_12, in_82);
  or or_13 (MDR1_read, in_13, in_83);
  or or_14 (MDR1_write, in_14, in_84);
  or or_15 (MDR1_zero, in_15, in_85);
  or or_16 (MDR2_read, in_16, in_86);
  or or_17 (MDR2_write, in_17, in_87);
  or or_18 (MDR2_zero, in_18, in_88);
  or or_19 (MEM_read, in_19, in_89);
  or or_20 (MEM_read2, in_20, in_90);
  or or_21 (MEM_write, in_21, in_91);
  or or_22 (MDR0_MEM_IN, in_22, in_92);
  or or_23 (MDR1_MEM_IN, in_23, in_93);
  or or_24 (MDR2_MEM_IN, in_24, in_94);
  or or_25 (MDR0_REG_IN, in_25, in_95);
  or or_26 (MDR1_REG_IN, in_26, in_96);
  or or_27 (MDR2_REG_IN, in_27, in_97);
  or or_28 (MAR_REG_ID, in_28, in_98);
  or or_29 (MDR0_REG_ID, in_29, in_99);
  or or_30 (MDR1_REG_ID, in_30, in_100);
  or or_31 (MDR2_REG_ID, in_31, in_101);
  or or_32 (REG_OUT_MAR, in_32, in_102);
  or or_33 (REG_OUT_MDR0, in_33, in_103);
  or or_34 (REG_OUT_MDR1, in_34, in_104);
  or or_35 (REG_OUT_MDR2, in_35, in_105);
  or or_36 (REG_read, in_36, in_106);
  or or_37 (REG_write, in_37, in_107);
  or or_38 (MAR_MDR0, in_38, in_108);
  or or_39 (MAR_MDR1, in_39, in_109);
  or or_40 (MAR_MDR2, in_40, in_110);
  or or_41 (MDR0_MAR, in_41, in_111);
  or or_42 (MDR0_MDR1, in_42, in_112);
  or or_43 (MDR0_MDR2, in_43, in_113);
  or or_44 (MDR1_MAR, in_44, in_114);
  or or_45 (MDR1_MDR0, in_45, in_115);
  or or_46 (MDR1_MDR2, in_46, in_116);
  or or_47 (MDR2_MAR, in_47, in_117);
  or or_48 (MDR2_MDR0, in_48, in_118);
  or or_49 (MDR2_MDR1, in_49, in_119);
  or or_50 (MAR_ALU_IN0, in_50, in_120);
  or or_51 (MDR0_ALU_IN0, in_51, in_121);
  or or_52 (MDR1_ALU_IN0, in_52, in_122);
  or or_53 (MDR2_ALU_IN0, in_53, in_123);
  or or_54 (MAR_ALU_IN1, in_54, in_124);
  or or_55 (MDR0_ALU_IN1, in_55, in_125);
  or or_56 (MDR1_ALU_IN1, in_56, in_126);
  or or_57 (MDR2_ALU_IN1, in_57, in_127);
  assign ALU_SELECT = in_58 | in_128;  // OR_Gate or_58, 8 bits wide
  or or_59 (ALU_read, in_59, in_129);
  or or_60 (ALU_write, in_60, in_130);
  or or_61 (ALU_readFlags, in_61, in_131);
  or or_62 (ALU_OUT_MAR, in_62, in_132);
  or or_63 (ALU_OUT_MDR0, in_63, in_133);
  or or_64 (ALU_OUT_MDR1, in_64, in_134);
  or or_65 (ALU_OUT_MDR2, in_65, in_135);
  or or_66 (ALU_REMAINDER_MAR, in_66, in_136);
  or or_67 (ALU_REMAINDER_MDR0, in_67, in_137);
  or or_68 (ALU_REMAINDER_MDR1, in_68, in_138);
  or or_69 (ALU_REMAINDER_MDR2, in_69, in_139);
  or or_70 (CU_endInstruction, in_70, in_140);
endmodule

module INS_ROM_AND (
  input  in_1,
  input  in_2,
  input  in_3,
  input  in_4,
  input  in_5,
  input  in_6,
  input  in_7,
  input  in_8,
  input  in_9,
  input  in_10,
  input  in_11,
  input  in_12,
  input  in_13,
  input  in_14,
  input  in_15,
  input  in_16,
  input  in_17,
  input  in_18,
  input  in_19,
  input  in_20,
  input  in_21,
  input  in_22,
  input  in_23,
  input  in_24,
  input  in_25,
  input  in_26,
  input  in_27,
  input  in_28,
  input  in_29,
  input  in_30,
  input  in_31,
  input  in_32,
  input  in_33,
  input  in_34,
  input  in_35,
  input  in_36,
  input  in_37,
  input  in_38,
  input  in_39,
  input  in_40,
  input  in_41,
  input  in_42,
  input  in_43,
  input  in_44,
  input  in_45,
  input  in_46,
  input  in_47,
  input  in_48,
  input  in_49,
  input  in_50,
  input  in_51,
  input  in_52,
  input  in_53,
  input  in_54,
  input  in_55,
  input  in_56,
  input  in_57,
  input  [7:0] in_58,
  input  in_59,
  input  in_60,
  input  in_61,
  input  in_62,
  input  in_63,
  input  in_64,
  input  in_65,
  input  in_66,
  input  in_67,
  input  in_68,
  input  in_69,
  input  in_70,
  input  CLK,
  output IP_inc,
  output IP_read,
  output IP_write,
  output SP_inc,
  output SP_dec,
  output SP_read,
  output SP_write,
  output MAR_read,
  output MAR_write,
  output MDR0_read,
  output MDR0_write,
  output MDR0_zero,
  output MDR1_read,
  output MDR1_write,
  output MDR1_zero,
  output MDR2_read,
  output MDR2_write,
  output MDR2_zero,
  output MEM_read,
  output MEM_read2,
  output MEM_write,
  output MDR0_MEM_IN,
  output MDR1_MEM_IN,
  output MDR2_MEM_IN,
  output MDR0_REG_IN,
  output MDR1_REG_IN,
  output MDR2_REG_IN,
  output MAR_REG_ID,
  output MDR0_REG_ID,
  output MDR1_REG_ID,
  output MDR2_REG_ID,
  output REG_OUT_MAR,
  output REG_OUT_MDR0,
  output REG_OUT_MDR1,
  output REG_OUT_MDR2,
  output REG_read,
  output REG_write,
  output MAR_MDR0,
  output MAR_MDR1,
  output MAR_MDR2,
  output MDR0_MAR,
  output MDR0_MDR1,
  output MDR0_MDR2,
  output MDR1_MAR,
  output MDR1_MDR0,
  output MDR1_MDR2,
  output MDR2_MAR,
  output MDR2_MDR0,
  output MDR2_MDR1,
  output MAR_ALU_IN0,
  output MDR0_ALU_IN0,
  output MDR1_ALU_IN0,
  output MDR2_ALU_IN0,
  output MAR_ALU_IN1,
  output MDR0_ALU_IN1,
  output MDR1_ALU_IN1,
  output MDR2_ALU_IN1,
  output [7:0] ALU_SELECT,
  output ALU_read,
  output ALU_write,
  output ALU_readFlags,
  output ALU_OUT_MAR,
  output ALU_OUT_MDR0,
  output ALU_OUT_MDR1,
  output ALU_OUT_MDR2,
  output ALU_REMAINDER_MAR,
  output ALU_REMAINDER_MDR0,
  output ALU_REMAINDER_MDR1,
  output ALU_REMAINDER_MDR2,
  output CU_endInstruction
);

  wire [7:0] bit_extender_1_out;

  assign bit_extender_1_out = {{7{CLK}}, CLK};  // Bit_Extender bit_extender_1
  and and_1 (IP_inc, in_1, CLK);
  and and_2 (IP_read, in_2, CLK);
  and and_3 (IP_write, in_3, CLK);
  and and_4 (SP_inc, in_4, CLK);
  and and_5 (SP_dec, in_5, CLK);
  and and_6 (SP_read, in_6, CLK);
  and and_7 (SP_write, in_7, CLK);
  and and_8 (MAR_read, in_8, CLK);
  and and_9 (MAR_write, in_9, CLK);
  and and_10 (MDR0_read, in_10, CLK);
  and and_11 (MDR0_write, in_11, CLK);
  and and_12 (MDR0_zero, in_12, CLK);
  and and_13 (MDR1_read, in_13, CLK);
  and and_14 (MDR1_write, in_14, CLK);
  and and_15 (MDR1_zero, in_15, CLK);
  and and_16 (MDR2_read, in_16, CLK);
  and and_17 (MDR2_write, in_17, CLK);
  and and_18 (MDR2_zero, in_18, CLK);
  and and_19 (MEM_read, in_19, CLK);
  and and_20 (MEM_read2, in_20, CLK);
  and and_21 (MEM_write, in_21, CLK);
  and and_22 (MDR0_MEM_IN, in_22, CLK);
  and and_23 (MDR1_MEM_IN, in_23, CLK);
  and and_24 (MDR2_MEM_IN, in_24, CLK);
  and and_25 (MDR0_REG_IN, in_25, CLK);
  and and_26 (MDR1_REG_IN, in_26, CLK);
  and and_27 (MDR2_REG_IN, in_27, CLK);
  and and_28 (MAR_REG_ID, in_28, CLK);
  and and_29 (MDR0_REG_ID, in_29, CLK);
  and and_30 (MDR1_REG_ID, in_30, CLK);
  and and_31 (MDR2_REG_ID, in_31, CLK);
  and and_32 (REG_OUT_MAR, in_32, CLK);
  and and_33 (REG_OUT_MDR0, in_33, CLK);
  and and_34 (REG_OUT_MDR1, in_34, CLK);
  and and_35 (REG_OUT_MDR2, in_35, CLK);
  and and_36 (REG_read, in_36, CLK);
  and and_37 (REG_write, in_37, CLK);
  and and_38 (MAR_MDR0, in_38, CLK);
  and and_39 (MAR_MDR1, in_39, CLK);
  and and_40 (MAR_MDR2, in_40, CLK);
  and and_41 (MDR0_MAR, in_41, CLK);
  and and_42 (MDR0_MDR1, in_42, CLK);
  and and_43 (MDR0_MDR2, in_43, CLK);
  and and_44 (MDR1_MAR, in_44, CLK);
  and and_45 (MDR1_MDR0, in_45, CLK);
  and and_46 (MDR1_MDR2, in_46, CLK);
  and and_47 (MDR2_MAR, in_47, CLK);
  and and_48 (MDR2_MDR0, in_48, CLK);
  and and_49 (MDR2_MDR1, in_49, CLK);
  and and_50 (MAR_ALU_IN0, in_50, CLK);
  and and_51 (MDR0_ALU_IN0, in_51, CLK);
  and and_52 (MDR1_ALU_IN0, in_52, CLK);
  and and_53 (MDR2_ALU_IN0, in_53, CLK);
  and and_54 (MAR_ALU_IN1, in_54, CLK);
  and and_55 (MDR0_ALU_IN1, in_55, CLK);
  and and_56 (MDR1_ALU_IN1, in_56, CLK);
  and and_57 (MDR2_ALU_IN1, in_57, CLK);
  assign ALU_SELECT = in_58 & bit_extender_1_out;  // AND_Gate and_58, 8 bits wide
  and and_59 (ALU_read, in_59, CLK);
  and and_60 (ALU_write, in_60, CLK);
  and and_61 (ALU_readFlags, in_61, CLK);
  and and_62 (ALU_OUT_MAR, in_62, CLK);
  and and_63 (ALU_OUT_MDR0, in_63, CLK);
  and and_64 (ALU_OUT_MDR1, in_64, CLK);
  and and_65 (ALU_OUT_MDR2, in_65, CLK);
  and and_66 (ALU_REMAINDER_MAR, in_66, CLK);
  and and_67 (ALU_REMAINDER_MDR0, in_67, CLK);
  and and_68 (ALU_REMAINDER_MDR1, in_68, CLK);
  and and_69 (ALU_REMAINDER_MDR2, in_69, CLK);
  and and_70 (CU_endInstruction, in_70, CLK);
endmodule

module INS_ROM_JUMPS (
  input  [7:0] in_1,
  input  [7:0] Flags,
  output out_3
);

  wire and_1_out, and_2_out, and_3_out, and_4_out, and_5_out, and_6_out, and_7_out, and_8_out, and_9_out,
       and_10_out, and_11_out, and_12_out, and_13_out, and_14_out, and_15_out, and_16_out, and_17_out,
       and_18_out, and_19_out, demultiplexer_1_out0, demultiplexer_1_out1, demultiplexer_1_out2,
       demultiplexer_1_out3, demultiplexer_1_out4, demultiplexer_1_out5, demultiplexer_1_out6,
       demultiplexer_1_out7, demultiplexer_4_out7, demultiplexer_4_out8, demultiplexer_4_out9,
       demultiplexer_4_out10, demultiplexer_4_out11, demultiplexer_4_out12, demultiplexer_4_out13,
       demultiplexer_4_out14, demultiplexer_4_out15, demultiplexer_4_out16, demultiplexer_4_out17,
       demultiplexer_4_out18, demultiplexer_4_out19, demultiplexer_4_out20, demultiplexer_4_out21,
       demultiplexer_4_out22, demultiplexer_4_out23, demultiplexer_4_out24, demultiplexer_4_out25,
       demultiplexer_4_out26, demultiplexer_4_out27, demultiplexer_4_out28, demultiplexer_4_out29,
       demultiplexer_4_out30, demultiplexer_4_out31, demultiplexer_5_out0, demultiplexer_5_out1,
       demultiplexer_5_out2, demultiplexer_5_out3, demultiplexer_5_out4, demultiplexer_5_out5,
       demultiplexer_5_out6, not_1_out, not_3_out, not_4_out, not_5_out, not_6_out, or_1_out, or_2_out,
       or_3_out, or_4_out, or_5_out, or_6_out, or_7_out, or_8_out, or_9_out, or_10_out, or_11_out, or_12_out,
       or_13_out, or_14_out, or_15_out, or_16_out, or_17_out, xor_1_out;

  Demultiplexer #(.select(3)) demultiplexer_1 (
    .out0(demultiplexer_1_out0), .out1(demultiplexer_1_out1), .out2(demultiplexer_1_out2),
    .out3(demultiplexer_1_out3), .out4(demultiplexer_1_out4), .out5(demultiplexer_1_out5),
    .out6(demultiplexer_1_out6), .out7(demultiplexer_1_out7), .in(1'b1), .sel(in_1[7:5]));
  Demultiplexer #(.select(5)) demultiplexer_2 (
    .in(demultiplexer_1_out0), .sel(in_1[4:0]));  // open: out0, out1, out2, out3, out4, out5, out6, out7, out8, out9, out10, out11, out12, out13, out14, out15, out16, out17, out18, out19, out20, out21, out22, out23, out24, out25, out26, out27, out28, out29, out30, out31
  Demultiplexer #(.select(5)) demultiplexer_3 (
    .in(demultiplexer_1_out1), .sel(in_1[4:0]));  // open: out0, out1, out2, out3, out4, out5, out6, out7, out8, out9, out10, out11, out12, out13, out14, out15, out16, out17, out18, out19, out20, out21, out22, out23, out24, out25, out26, out27, out28, out29, out30, out31
  Demultiplexer #(.select(5)) demultiplexer_4 (
    .out7(demultiplexer_4_out7), .out8(demultiplexer_4_out8), .out9(demultiplexer_4_out9),
    .out10(demultiplexer_4_out10), .out11(demultiplexer_4_out11), .out12(demultiplexer_4_out12),
    .out13(demultiplexer_4_out13), .out14(demultiplexer_4_out14), .out15(demultiplexer_4_out15),
    .out16(demultiplexer_4_out16), .out17(demultiplexer_4_out17), .out18(demultiplexer_4_out18),
    .out19(demultiplexer_4_out19), .out20(demultiplexer_4_out20), .out21(demultiplexer_4_out21),
    .out22(demultiplexer_4_out22), .out23(demultiplexer_4_out23), .out24(demultiplexer_4_out24),
    .out25(demultiplexer_4_out25), .out26(demultiplexer_4_out26), .out27(demultiplexer_4_out27),
    .out28(demultiplexer_4_out28), .out29(demultiplexer_4_out29), .out30(demultiplexer_4_out30),
    .out31(demultiplexer_4_out31), .in(demultiplexer_1_out2), .sel(in_1[4:0]));  // open: out0, out1, out2, out3, out4, out5, out6
  Demultiplexer #(.select(5)) demultiplexer_5 (
    .out0(demultiplexer_5_out0), .out1(demultiplexer_5_out1), .out2(demultiplexer_5_out2),
    .out3(demultiplexer_5_out3), .out4(demultiplexer_5_out4), .out5(demultiplexer_5_out5),
    .out6(demultiplexer_5_out6), .in(demultiplexer_1_out3), .sel(in_1[4:0]));  // open: out7, out8, out9, out10, out11, out12, out13, out14, out15, out16, out17, out18, out19, out20, out21, out22, out23, out24, out25, out26, out27, out28, out29, out30, out31
  Demultiplexer #(.select(5)) demultiplexer_6 (
    .in(demultiplexer_1_out4), .sel(in_1[4:0]));  // open: out0, out1, out2, out3, out4, out5, out6, out7, out8, out9, out10, out11, out12, out13, out14, out15, out16, out17, out18, out19, out20, out21, out22, out23, out24, out25, out26, out27, out28, out29, out30, out31
  Demultiplexer #(.select(5)) demultiplexer_7 (
    .in(demultiplexer_1_out5), .sel(in_1[4:0]));  // open: out0, out1, out2, out3, out4, out5, out6, out7, out8, out9, out10, out11, out12, out13, out14, out15, out16, out17, out18, out19, out20, out21, out22, out23, out24, out25, out26, out27, out28, out29, out30, out31
  Demultiplexer #(.select(5)) demultiplexer_8 (
    .in(demultiplexer_1_out6), .sel(in_1[4:0]));  // open: out0, out1, out2, out3, out4, out5, out6, out7, out8, out9, out10, out11, out12, out13, out14, out15, out16, out17, out18, out19, out20, out21, out22, out23, out24, out25, out26, out27, out28, out29, out30, out31
  Demultiplexer #(.select(5)) demultiplexer_9 (
    .in(demultiplexer_1_out7), .sel(in_1[4:0]));  // open: out0, out1, out2, out3, out4, out5, out6, out7, out8, out9, out10, out11, out12, out13, out14, out15, out16, out17, out18, out19, out20, out21, out22, out23, out24, out25, out26, out27, out28, out29, out30, out31
  or or_1 (or_1_out, demultiplexer_4_out7, demultiplexer_4_out8);
  or or_2 (or_2_out, demultiplexer_4_out9, demultiplexer_4_out10);
  or or_3 (or_3_out, demultiplexer_4_out11, demultiplexer_4_out12);
  or or_4 (or_4_out, demultiplexer_4_out13, demultiplexer_4_out14);
  or or_5 (or_5_out, demultiplexer_4_out15, demultiplexer_4_out16);
  or or_6 (or_6_out, demultiplexer_4_out17, demultiplexer_4_out18);
  or or_7 (or_7_out, demultiplexer_4_out19, demultiplexer_4_out20);
  or or_8 (or_8_out, demultiplexer_4_out21, demultiplexer_4_out22);
  or or_9 (or_9_out, demultiplexer_4_out23, demultiplexer_4_out24);
  or or_10 (or_10_out, demultiplexer_4_out25, demultiplexer_4_out26);
  or or_11 (or_11_out, demultiplexer_4_out27, demultiplexer_4_out28);
  or or_12 (or_12_out, demultiplexer_4_out29, demultiplexer_4_out30);
  or or_13 (or_13_out, demultiplexer_4_out31, demultiplexer_5_out0);
  or or_14 (or_14_out, demultiplexer_5_out1, demultiplexer_5_out2);
  or or_15 (or_15_out, demultiplexer_5_out3, demultiplexer_5_out4);
  or or_16 (or_16_out, demultiplexer_5_out5, demultiplexer_5_out6);
  not not_1 (not_1_out, Flags[0]);
  not not_2 (not_1_out, Flags[1]);
  and and_1 (and_1_out, not_1_out, not_1_out);
  not not_3 (not_3_out, Flags[2]);
  not not_4 (not_4_out, Flags[3]);
  not not_5 (not_5_out, Flags[4]);
  and and_2 (and_2_out, not_1_out, not_6_out);
  xor xor_1 (xor_1_out, Flags[2], Flags[3]);
  not not_6 (not_6_out, xor_1_out);
  or or_17 (or_17_out, Flags[0], Flags[1]);
  and and_3 (and_3_out, Flags[0], xor_1_out);
  and and_4 (and_4_out, or_1_out, Flags[0]);
  and and_5 (and_5_out, or_2_out, not_1_out);
  and and_6 (and_6_out, or_3_out, Flags[2]);
  and and_7 (and_7_out, or_4_out, not_3_out);
  and and_8 (and_8_out, or_5_out, and_2_out);
  and and_9 (and_9_out, or_6_out, not_6_out);
  and and_10 (and_10_out, or_7_out, xor_1_out);
  and and_11 (and_11_out, or_8_out, and_3_out);
  and and_12 (and_12_out, or_9_out, and_1_out);
  and and_13 (and_13_out, or_10_out, not_1_out);
  and and_14 (and_14_out, or_11_out, Flags[1]);
  and and_15 (and_15_out, or_12_out, or_17_out);
  and and_16 (and_16_out, or_13_out, Flags[4]);
  and and_17 (and_17_out, or_14_out, not_5_out);
  and and_18 (and_18_out, or_15_out, Flags[3]);
  and and_19 (and_19_out, or_16_out, not_4_out);
  or or_18 (out_3, and_4_out, and_5_out, and_6_out, and_7_out, and_8_out, and_9_out, and_10_out, and_11_out, and_12_out, and_13_out, and_14_out, and_15_out, and_16_out, and_17_out, and_18_out, and_19_out);

  // Notes on the sheet:
  //   ZF
  //   CF
  //   SF
  //   OF
  //   PF
endmodule

module INS_ROM_REG (
  input  Write,
  input  Read,
  input  Clk,
  input  in_4,
  input  in_5,
  input  in_6,
  input  in_7,
  input  in_8,
  input  in_9,
  input  in_10,
  input  in_11,
  input  in_12,
  input  in_13,
  input  in_14,
  input  in_15,
  input  in_16,
  input  in_17,
  input  in_18,
  input  in_19,
  input  in_20,
  input  in_21,
  input  in_22,
  input  in_23,
  input  in_24,
  input  in_25,
  input  in_26,
  input  in_27,
  input  in_28,
  input  in_29,
  input  in_30,
  input  in_31,
  input  in_32,
  input  in_33,
  input  in_34,
  input  in_35,
  input  in_36,
  input  in_37,
  input  in_38,
  input  in_39,
  input  in_40,
  input  in_41,
  input  in_42,
  input  in_43,
  input  in_44,
  input  in_45,
  input  in_46,
  input  in_47,
  input  in_48,
  input  in_49,
  input  in_50,
  input  in_51,
  input  in_52,
  input  in_53,
  input  in_54,
  input  in_55,
  input  in_56,
  input  in_57,
  input  in_58,
  input  in_59,
  input  in_60,
  input  [7:0] in_61,
  input  in_62,
  input  in_63,
  input  in_64,
  input  in_65,
  input  in_66,
  input  in_67,
  input  in_68,
  input  in_69,
  input  in_70,
  input  in_71,
  input  in_72,
  input  in_73,
  output IP_inc,
  output IP_read,
  output IP_write,
  output SP_inc,
  output SP_dec,
  output SP_read,
  output SP_write,
  output MAR_read,
  output MAR_write,
  output MDR0_read,
  output MDR0_write,
  output MDR0_zero,
  output MDR1_read,
  output MDR1_write,
  output MDR1_zero,
  output MDR2_read,
  output MDR2_write,
  output MDR2_zero,
  output MEM_read,
  output MEM_read2,
  output MEM_write,
  output MDR0_MEM_IN,
  output MDR1_MEM_IN,
  output MDR2_MEM_IN,
  output MDR0_REG_IN,
  output MDR1_REG_IN,
  output MDR2_REG_IN,
  output MAR_REG_ID,
  output MDR0_REG_ID,
  output MDR1_REG_ID,
  output MDR2_REG_ID,
  output REG_OUT_MAR,
  output REG_OUT_MDR0,
  output REG_OUT_MDR1,
  output REG_OUT_MDR2,
  output REG_read,
  output REG_write,
  output MAR_MDR0,
  output MAR_MDR1,
  output MAR_MDR2,
  output MDR0_MAR,
  output MDR0_MDR1,
  output MDR0_MDR2,
  output MDR1_MAR,
  output MDR1_MDR0,
  output MDR1_MDR2,
  output MDR2_MAR,
  output MDR2_MDR0,
  output MDR2_MDR1,
  output MAR_ALU_IN0,
  output MDR0_ALU_IN0,
  output MDR1_ALU_IN0,
  output MDR2_ALU_IN0,
  output MAR_ALU_IN1,
  output MDR0_ALU_IN1,
  output MDR1_ALU_IN1,
  output MDR2_ALU_IN1,
  output [7:0] ALU_SELECT,
  output ALU_read,
  output ALU_write,
  output ALU_readFlags,
  output ALU_OUT_MAR,
  output ALU_OUT_MDR0,
  output ALU_OUT_MDR1,
  output ALU_OUT_MDR2,
  output ALU_REMAINDER_MAR,
  output ALU_REMAINDER_MDR0,
  output ALU_REMAINDER_MDR1,
  output ALU_REMAINDER_MDR2,
  output CU_endInstruction
);

  wire [19:0] bit_extender_2_out, register_2_q;
  wire [56:0] bit_extender_1_out, register_1_q;

  Register #(.trigger("high"), .width(57)) register_1 (
    .D({in_60, in_59, in_58, in_57, in_56, in_55, in_54, in_53, in_52, in_51, in_50, in_49, in_48, in_47, in_46, in_45, in_44, in_43, in_42, in_41, in_40, in_39, in_38, in_37, in_36, in_35, in_34, in_33, in_32, in_31, in_30, in_29, in_28, in_27, in_26, in_25, in_24, in_23, in_22, in_21, in_20, in_19, in_18, in_17, in_16, in_15, in_14, in_13, in_12, in_11, in_10, in_9, in_8, in_7, in_6, in_5, in_4}),
    .en(Write), .clk(Clk), .Q(register_1_q));  // open: clr
  Register #(.trigger("high"), .width(20)) register_2 (
    .D({in_73, in_72, in_71, in_70, in_69, in_68, in_67, in_66, in_65, in_64, in_63, in_62, in_61}),
    .en(Write), .clk(Clk), .Q(register_2_q));  // open: clr
  assign bit_extender_1_out = {{56{Read}}, Read};  // Bit_Extender bit_extender_1
  assign bit_extender_2_out = {{19{Read}}, Read};  // Bit_Extender bit_extender_2
  assign {MDR2_ALU_IN1, MDR1_ALU_IN1, MDR0_ALU_IN1, MAR_ALU_IN1, MDR2_ALU_IN0, MDR1_ALU_IN0, MDR0_ALU_IN0, MAR_ALU_IN0, MDR2_MDR1, MDR2_MDR0, MDR2_MAR, MDR1_MDR2, MDR1_MDR0, MDR1_MAR, MDR0_MDR2, MDR0_MDR1, MDR0_MAR, MAR_MDR2, MAR_MDR1, MAR_MDR0, REG_write, REG_read, REG_OUT_MDR2, REG_OUT_MDR1, REG_OUT_MDR0, REG_OUT_MAR, MDR2_REG_ID, MDR1_REG_ID, MDR0_REG_ID, MAR_REG_ID, MDR2_REG_IN, MDR1_REG_IN, MDR0_REG_IN, MDR2_MEM_IN, MDR1_MEM_IN, MDR0_MEM_IN, MEM_write, MEM_read2, MEM_read, MDR2_zero, MDR2_write, MDR2_read, MDR1_zero, MDR1_write, MDR1_read, MDR0_zero, MDR0_write, MDR0_read, MAR_write, MAR_read, SP_write, SP_read, SP_dec, SP_inc, IP_write, IP_read, IP_inc} = register_1_q & bit_extender_1_out;  // AND_Gate and_1, 57 bits wide
  assign {CU_endInstruction, ALU_REMAINDER_MDR2, ALU_REMAINDER_MDR1, ALU_REMAINDER_MDR0, ALU_REMAINDER_MAR, ALU_OUT_MDR2, ALU_OUT_MDR1, ALU_OUT_MDR0, ALU_OUT_MAR, ALU_readFlags, ALU_write, ALU_read, ALU_SELECT} = register_2_q & bit_extender_2_out;  // AND_Gate and_2, 20 bits wide
endmodule
