// Logisim project main.circ as structural Verilog: 14 circuits, main circuit Computer
module Computer (
  input  Clear,
  input  Clk,
  input  [7:0] in_3,
  input  [7:0] in_4,
  input  [7:0] in_5,
  input  [7:0] in_6,
  output [7:0] out_7,
  output [7:0] out_8,
  output [7:0] out_9,
  output [7:0] out_10
);

  wire and_1_out, clock_1_out, cpu_1_mem_read, cpu_1_mem_read2, cpu_1_mem_write, not_1_out, or_1_out;
  wire [7:0] cpu_1_mem_addr_in, cpu_1_mem_in, cpu_1_page_out, ram_1_dout, ram_2_dout;
  wire [15:0] adder_1_out;

  or or_1 (or_1_out, Clk, clock_1_out);
  Clock clock_1 (.out(clock_1_out));
  CPU cpu_1 (
    .MEM_OUT(ram_1_dout), .MEM_OUT2(ram_2_dout), .Clear(Clear), .Clk(or_1_out), .I0(in_3), .I1(in_4),
    .I2(in_5), .I3(in_6), .MEM_read(cpu_1_mem_read), .MEM_read2(cpu_1_mem_read2),
    .MEM_write(cpu_1_mem_write), .MEM_ADDR_IN(cpu_1_mem_addr_in), .PAGE_out(cpu_1_page_out),
    .MEM_IN(cpu_1_mem_in), .p3(out_7), .p2(out_8), .p1(out_9), .p0(out_10));
  and and_1 (and_1_out, cpu_1_mem_read2, not_1_out);
  not not_1 (not_1_out, cpu_1_mem_write);
  Adder #(.width(16)) adder_1 (
    .a({cpu_1_page_out, cpu_1_mem_addr_in}), .b({16{1'b0}}), .out(adder_1_out), .cin(and_1_out));  // open: cout
  RAM #(.addrWidth(16), .asyncread("true"), .trigger("falling")) ram_1 (
    .addr({cpu_1_page_out, cpu_1_mem_addr_in}), .we(cpu_1_mem_write), .oe(cpu_1_mem_read), .clk(or_1_out),
    .din(cpu_1_mem_in), .dout(ram_1_dout));
  RAM #(.addrWidth(16), .asyncread("true"), .trigger("falling")) ram_2 (
    .addr(adder_1_out), .we(cpu_1_mem_write), .oe(cpu_1_mem_read2), .clk(or_1_out), .din(cpu_1_mem_in),
    .dout(ram_2_dout));
endmodule

module FullRAM (
  input  [7:0] MEM_ADDR_IN,
  input  [7:0] MEM_IN,
  input  MEM_read,
  input  MEM_read2,
  input  MEM_write,
  input  Clk,
  output [7:0] MEM_OUT,
  output [7:0] MEM_OUT2
);

  wire and_1_out, not_1_out;
  wire [7:0] adder_1_out;

  and and_1 (and_1_out, MEM_read2, not_1_out);
  not not_1 (not_1_out, MEM_write);
  RAM #(.asyncread("true"), .trigger("falling")) ram_1 (
    .addr(MEM_ADDR_IN), .we(MEM_write), .oe(MEM_read), .clk(Clk), .din(MEM_IN), .dout(MEM_OUT));
  RAM #(.asyncread("true"), .trigger("falling")) ram_2 (
    .addr(adder_1_out), .we(MEM_write), .oe(MEM_read2), .clk(Clk), .din(MEM_IN), .dout(MEM_OUT2));
  Adder adder_1 (.a(MEM_ADDR_IN), .b({8{1'b0}}), .out(adder_1_out), .cin(and_1_out));  // open: cout
endmodule

module CPU (
  input  [7:0] MEM_OUT,
  input  [7:0] MEM_OUT2,
  input  Clear,
  input  Clk,
  input  [7:0] I0,
  input  [7:0] I1,
  input  [7:0] I2,
  input  [7:0] I3,
  output MEM_read,
  output MEM_read2,
  output MEM_write,
  output [7:0] MEM_ADDR_IN,
  output [7:0] PAGE_out,
  output [7:0] MEM_IN,
  output [7:0] p3,
  output [7:0] p2,
  output [7:0] p1,
  output [7:0] p0
);

  wire and_1_out, cu_1_alu_out_mar, cu_1_alu_out_mdr0, cu_1_alu_out_mdr1, cu_1_alu_out_mdr2, cu_1_alu_read,
       cu_1_alu_readflags, cu_1_alu_remainder_mar, cu_1_alu_remainder_mdr0, cu_1_alu_remainder_mdr1,
       cu_1_alu_remainder_mdr2, cu_1_alu_write, cu_1_cu_endinstruction, cu_1_hlt, cu_1_ip_inc, cu_1_ip_read,
       cu_1_ip_write, cu_1_mar_alu_in0, cu_1_mar_alu_in1, cu_1_mar_mdr0, cu_1_mar_mdr1, cu_1_mar_mdr2,
       cu_1_mar_read, cu_1_mar_reg_id, cu_1_mar_write, cu_1_mdr0_alu_in0, cu_1_mdr0_alu_in1,
       cu_1_mdr0_in_reg_in, cu_1_mdr0_mar, cu_1_mdr0_mdr1, cu_1_mdr0_mdr2, cu_1_mdr0_mem_in, cu_1_mdr0_read,
       cu_1_mdr0_reg_id, cu_1_mdr0_reg_in, cu_1_mdr0_write, cu_1_mdr0_zero, cu_1_mdr1_alu_in0,
       cu_1_mdr1_alu_in1, cu_1_mdr1_in_reg_in, cu_1_mdr1_mar, cu_1_mdr1_mdr0, cu_1_mdr1_mdr2,
       cu_1_mdr1_mem_in, cu_1_mdr1_read, cu_1_mdr1_reg_id, cu_1_mdr1_reg_in, cu_1_mdr1_write, cu_1_mdr1_zero,
       cu_1_mdr2_alu_in0, cu_1_mdr2_alu_in1, cu_1_mdr2_in_reg_in, cu_1_mdr2_mar, cu_1_mdr2_mdr0,
       cu_1_mdr2_mdr1, cu_1_mdr2_mem_in, cu_1_mdr2_read, cu_1_mdr2_reg_id, cu_1_mdr2_reg_in, cu_1_mdr2_write,
       cu_1_mdr2_zero, cu_1_page_read, cu_1_page_write, cu_1_reg_out_mar, cu_1_reg_out_mdr0,
       cu_1_reg_out_mdr1, cu_1_reg_out_mdr2, cu_1_reg_read, cu_1_reg_write, cu_1_sp_dec, cu_1_sp_inc,
       cu_1_sp_read, cu_1_sp_write, demultiplexer_1_out0, demultiplexer_1_out1, demultiplexer_1_out2,
       demultiplexer_1_out3, demultiplexer_2_out0, demultiplexer_2_out1, demultiplexer_2_out2,
       demultiplexer_2_out3, demultiplexer_3_out0, demultiplexer_3_out1, demultiplexer_3_out2,
       demultiplexer_3_out3, not_1_out, or_2_out, or_7_out, or_8_out, or_9_out, or_10_out, or_11_out,
       or_17_out, s_r_ff_1_q;
  wire [7:0] alu_1_flags, alu_1_out_8, alu_1_remainder, and8_1_1_out_3, and8_1_2_out_3, and8_1_3_out_3,
       and8_1_4_out_3, and8_1_5_out_3, and8_1_6_out_3, and8_1_7_out_3, and8_1_8_out_3, and8_1_9_out_3,
       and8_1_10_out_3, and8_1_11_out_3, and8_1_12_out_3, and8_1_13_out_3, and8_1_14_out_3, and8_1_15_out_3,
       and8_1_16_out_3, and8_1_17_out_3, and8_1_18_out_3, and8_1_19_out_3, and8_1_20_out_3, and8_1_21_out_3,
       and8_1_22_out_3, and8_1_23_out_3, and8_1_24_out_3, and8_1_25_out_3, and8_1_26_out_3, and8_1_27_out_3,
       and8_1_28_out_3, and8_1_29_out_3, and8_1_30_out_3, and8_1_31_out_3, and8_1_32_out_3, and8_1_33_out_3,
       and8_1_34_out_3, and8_1_35_out_3, and8_1_36_out_3, and8_1_37_out_3, and8_1_38_out_3, and8_1_39_out_3,
       and8_1_40_out_3, and8_1_41_out_3, and8_1_42_out_3, and8_1_43_out_3, and8_1_44_out_3, and8_1_45_out_3,
       and8_1_46_out_3, and8_1_47_out_3, and8_1_48_out_3, and8_1_49_out_3, cu_1_alu_select, IP_out_8,
       MDR0_out_8, MDR1_out_8, MDR2_out_8, or_1_out, or_3_out, or_4_out, or_5_out, or_6_out, or_13_out,
       or_14_out, or_15_out, or_16_out, regfile_1_out_6, SP_out_8;

  S_R_Flip_Flop s_r_ff_1 (.S(Clear), .R(cu_1_hlt), .clk(Clk), .Q(s_r_ff_1_q));  // open: reset, Qn, preset
  and and_1 (and_1_out, s_r_ff_1_q, Clk);
  CU cu_1 (
    .Instruction(MEM_OUT), .Flags(alu_1_flags), .Reset(Clear), .Clk(and_1_out), .IP_inc(cu_1_ip_inc),
    .IP_read(cu_1_ip_read), .IP_write(cu_1_ip_write), .SP_inc(cu_1_sp_inc), .SP_dec(cu_1_sp_dec),
    .SP_read(cu_1_sp_read), .SP_write(cu_1_sp_write), .MAR_read(cu_1_mar_read), .MAR_write(cu_1_mar_write),
    .MDR0_read(cu_1_mdr0_read), .MDR0_write(cu_1_mdr0_write), .MDR0_zero(cu_1_mdr0_zero),
    .MDR1_read(cu_1_mdr1_read), .MDR1_write(cu_1_mdr1_write), .MDR1_zero(cu_1_mdr1_zero),
    .MDR2_read(cu_1_mdr2_read), .MDR2_write(cu_1_mdr2_write), .MDR2_zero(cu_1_mdr2_zero),
    .MEM_read(MEM_read), .MEM_read2(MEM_read2), .MEM_write(MEM_write), .MDR0_MEM_IN(cu_1_mdr0_mem_in),
    .MDR1_MEM_IN(cu_1_mdr1_mem_in), .MDR2_MEM_IN(cu_1_mdr2_mem_in), .MDR0_REG_IN(cu_1_mdr0_reg_in),
    .MDR1_REG_IN(cu_1_mdr1_reg_in), .MDR2_REG_IN(cu_1_mdr2_reg_in), .MDR0_IN_REG_IN(cu_1_mdr0_in_reg_in),
    .MDR1_IN_REG_IN(cu_1_mdr1_in_reg_in), .MDR2_IN_REG_IN(cu_1_mdr2_in_reg_in), .MAR_REG_ID(cu_1_mar_reg_id),
    .MDR0_REG_ID(cu_1_mdr0_reg_id), .MDR1_REG_ID(cu_1_mdr1_reg_id), .MDR2_REG_ID(cu_1_mdr2_reg_id),
    .REG_OUT_MAR(cu_1_reg_out_mar), .REG_OUT_MDR0(cu_1_reg_out_mdr0), .REG_OUT_MDR1(cu_1_reg_out_mdr1),
    .REG_OUT_MDR2(cu_1_reg_out_mdr2), .REG_read(cu_1_reg_read), .REG_write(cu_1_reg_write),
    .MAR_MDR0(cu_1_mar_mdr0), .MAR_MDR1(cu_1_mar_mdr1), .MAR_MDR2(cu_1_mar_mdr2), .MDR0_MAR(cu_1_mdr0_mar),
    .MDR0_MDR1(cu_1_mdr0_mdr1), .MDR0_MDR2(cu_1_mdr0_mdr2), .MDR1_MAR(cu_1_mdr1_mar),
    .MDR1_MDR0(cu_1_mdr1_mdr0), .MDR1_MDR2(cu_1_mdr1_mdr2), .MDR2_MAR(cu_1_mdr2_mar),
    .MDR2_MDR0(cu_1_mdr2_mdr0), .MDR2_MDR1(cu_1_mdr2_mdr1), .MAR_ALU_IN0(cu_1_mar_alu_in0),
    .MDR0_ALU_IN0(cu_1_mdr0_alu_in0), .MDR1_ALU_IN0(cu_1_mdr1_alu_in0), .MDR2_ALU_IN0(cu_1_mdr2_alu_in0),
    .MAR_ALU_IN1(cu_1_mar_alu_in1), .MDR0_ALU_IN1(cu_1_mdr0_alu_in1), .MDR1_ALU_IN1(cu_1_mdr1_alu_in1),
    .MDR2_ALU_IN1(cu_1_mdr2_alu_in1), .ALU_SELECT(cu_1_alu_select), .ALU_read(cu_1_alu_read),
    .ALU_write(cu_1_alu_write), .ALU_readFlags(cu_1_alu_readflags), .ALU_OUT_MAR(cu_1_alu_out_mar),
    .ALU_OUT_MDR0(cu_1_alu_out_mdr0), .ALU_OUT_MDR1(cu_1_alu_out_mdr1), .ALU_OUT_MDR2(cu_1_alu_out_mdr2),
    .ALU_REMAINDER_MAR(cu_1_alu_remainder_mar), .ALU_REMAINDER_MDR0(cu_1_alu_remainder_mdr0),
    .ALU_REMAINDER_MDR1(cu_1_alu_remainder_mdr1), .ALU_REMAINDER_MDR2(cu_1_alu_remainder_mdr2),
    .PAGE_read(cu_1_page_read), .PAGE_write(cu_1_page_write), .CU_endInstruction(cu_1_cu_endinstruction),
    .hlt(cu_1_hlt));
  assign or_1_out = MDR0_out_8 | MDR1_out_8 | MDR2_out_8;  // OR_Gate or_1, 8 bits wide
  or or_2 (or_2_out, and_1_out, Clear);
  Reg8Ext IP (
    .in_1(or_1_out), .Inc(cu_1_ip_inc), .Zero(Clear), .Write(cu_1_ip_write), .Read(cu_1_ip_read),
    .Clk(or_2_out), .out_8(IP_out_8));  // open: Dec
  Reg8Ext SP (
    .Inc(cu_1_sp_inc), .Dec(cu_1_sp_dec), .Zero(Clear), .Write(cu_1_sp_write), .Read(cu_1_sp_read),
    .Clk(and_1_out), .out_8(SP_out_8));  // open: in_1
  AND8_1 and8_1_1 (.in_1(MEM_OUT), .in_2(MEM_read), .out_3(and8_1_1_out_3));
  AND8_1 and8_1_2 (.in_1(MEM_ADDR_IN), .in_2(cu_1_mar_mdr0), .out_3(and8_1_2_out_3));
  AND8_1 and8_1_3 (.in_1(MDR1_out_8), .in_2(cu_1_mdr1_mdr0), .out_3(and8_1_3_out_3));
  AND8_1 and8_1_4 (.in_1(MDR2_out_8), .in_2(cu_1_mdr2_mdr0), .out_3(and8_1_4_out_3));
  AND8_1 and8_1_5 (.in_1(regfile_1_out_6), .in_2(cu_1_reg_out_mdr0), .out_3(and8_1_5_out_3));
  AND8_1 and8_1_6 (.in_1(alu_1_out_8), .in_2(cu_1_alu_out_mdr0), .out_3(and8_1_6_out_3));
  AND8_1 and8_1_7 (.in_1(alu_1_remainder), .in_2(cu_1_alu_remainder_mdr0), .out_3(and8_1_7_out_3));
  AND8_1 and8_1_8 (.in_1(MEM_OUT2), .in_2(MEM_read2), .out_3(and8_1_8_out_3));
  AND8_1 and8_1_9 (.in_1(MEM_ADDR_IN), .in_2(cu_1_mar_mdr1), .out_3(and8_1_9_out_3));
  AND8_1 and8_1_10 (.in_1(MDR0_out_8), .in_2(cu_1_mdr0_mdr1), .out_3(and8_1_10_out_3));
  AND8_1 and8_1_11 (.in_1(MDR2_out_8), .in_2(cu_1_mdr2_mdr1), .out_3(and8_1_11_out_3));
  AND8_1 and8_1_12 (.in_1(regfile_1_out_6), .in_2(cu_1_reg_out_mdr1), .out_3(and8_1_12_out_3));
  AND8_1 and8_1_13 (.in_1(alu_1_out_8), .in_2(cu_1_alu_out_mdr1), .out_3(and8_1_13_out_3));
  AND8_1 and8_1_14 (.in_1(alu_1_remainder), .in_2(cu_1_alu_remainder_mdr1), .out_3(and8_1_14_out_3));
  AND8_1 and8_1_15 (.in_1(MEM_ADDR_IN), .in_2(cu_1_mar_mdr2), .out_3(and8_1_15_out_3));
  AND8_1 and8_1_16 (.in_1(MDR0_out_8), .in_2(cu_1_mdr0_mdr2), .out_3(and8_1_16_out_3));
  AND8_1 and8_1_17 (.in_1(MDR1_out_8), .in_2(cu_1_mdr1_mdr2), .out_3(and8_1_17_out_3));
  AND8_1 and8_1_18 (.in_1(regfile_1_out_6), .in_2(cu_1_reg_out_mdr2), .out_3(and8_1_18_out_3));
  AND8_1 and8_1_19 (.in_1(alu_1_out_8), .in_2(cu_1_alu_out_mdr2), .out_3(and8_1_19_out_3));
  AND8_1 and8_1_20 (.in_1(alu_1_remainder), .in_2(cu_1_alu_remainder_mdr2), .out_3(and8_1_20_out_3));
  AND8_1 and8_1_21 (.in_1(MDR0_out_8), .in_2(cu_1_mdr0_mar), .out_3(and8_1_21_out_3));
  AND8_1 and8_1_22 (.in_1(MDR1_out_8), .in_2(cu_1_mdr1_mar), .out_3(and8_1_22_out_3));
  AND8_1 and8_1_23 (.in_1(MDR2_out_8), .in_2(cu_1_mdr2_mar), .out_3(and8_1_23_out_3));
  AND8_1 and8_1_24 (.in_1(regfile_1_out_6), .in_2(cu_1_reg_out_mar), .out_3(and8_1_24_out_3));
  AND8_1 and8_1_25 (.in_1(alu_1_out_8), .in_2(cu_1_alu_out_mar), .out_3(and8_1_25_out_3));
  AND8_1 and8_1_26 (.in_1(alu_1_remainder), .in_2(cu_1_alu_remainder_mar), .out_3(and8_1_26_out_3));
  assign or_3_out = and8_1_1_out_3 | and8_1_2_out_3 | and8_1_3_out_3 | and8_1_4_out_3 | and8_1_5_out_3 | and8_1_6_out_3 | and8_1_7_out_3;  // OR_Gate or_3, 8 bits wide
  assign or_4_out = and8_1_8_out_3 | and8_1_9_out_3 | and8_1_10_out_3 | and8_1_11_out_3 | and8_1_12_out_3 | and8_1_13_out_3 | and8_1_14_out_3;  // OR_Gate or_4, 8 bits wide
  assign or_5_out = and8_1_15_out_3 | and8_1_16_out_3 | and8_1_17_out_3 | and8_1_18_out_3 | and8_1_19_out_3 | and8_1_20_out_3;  // OR_Gate or_5, 8 bits wide
  assign or_6_out = IP_out_8 | SP_out_8 | and8_1_21_out_3 | and8_1_22_out_3 | and8_1_23_out_3 | and8_1_24_out_3 | and8_1_25_out_3 | and8_1_26_out_3;  // OR_Gate or_6, 8 bits wide
  AND8_1 and8_1_27 (.in_1(MDR0_out_8), .in_2(cu_1_page_write), .out_3(and8_1_27_out_3));
  or or_7 (or_7_out, cu_1_cu_endinstruction, and_1_out);
  Reg8Ext MDR0 (
    .in_1(or_3_out), .Zero(cu_1_mdr0_zero), .Write(cu_1_mdr0_write), .Read(cu_1_mdr0_read), .Clk(and_1_out),
    .out_8(MDR0_out_8));  // open: Inc, Dec
  Reg8Ext MDR1 (
    .in_1(or_4_out), .Zero(cu_1_mdr1_zero), .Write(cu_1_mdr1_write), .Read(cu_1_mdr1_read), .Clk(and_1_out),
    .out_8(MDR1_out_8));  // open: Inc, Dec
  Reg8Ext MDR2 (
    .in_1(or_5_out), .Zero(cu_1_mdr2_zero), .Write(cu_1_mdr2_write), .Read(cu_1_mdr2_read), .Clk(and_1_out),
    .out_8(MDR2_out_8));  // open: Inc, Dec
  Reg8Ext PAGE (
    .in_1(and8_1_27_out_3), .Write(cu_1_page_write), .Read(cu_1_page_read), .Clk(and_1_out), .out_8(PAGE_out));  // open: Inc, Dec, Zero
  Reg8Ext MAR (
    .in_1(or_6_out), .Zero(Clear), .Write(cu_1_mar_write), .Read(cu_1_mar_read), .Clk(or_7_out),
    .out_8(MEM_ADDR_IN));  // open: Inc, Dec
  Demultiplexer #(.select(2)) demultiplexer_1 (
    .out0(demultiplexer_1_out0), .out1(demultiplexer_1_out1), .out2(demultiplexer_1_out2),
    .out3(demultiplexer_1_out3), .in(cu_1_mdr0_in_reg_in), .sel(MDR0_out_8[1:0]));
  Demultiplexer #(.select(2)) demultiplexer_2 (
    .out0(demultiplexer_2_out0), .out1(demultiplexer_2_out1), .out2(demultiplexer_2_out2),
    .out3(demultiplexer_2_out3), .in(cu_1_mdr1_in_reg_in), .sel(MDR1_out_8[1:0]));
  Demultiplexer #(.select(2)) demultiplexer_3 (
    .out0(demultiplexer_3_out0), .out1(demultiplexer_3_out1), .out2(demultiplexer_3_out2),
    .out3(demultiplexer_3_out3), .in(cu_1_mdr2_in_reg_in), .sel(MDR2_out_8[1:0]));
  or or_8 (or_8_out, demultiplexer_1_out0, demultiplexer_2_out0, demultiplexer_3_out0);
  or or_9 (or_9_out, demultiplexer_1_out1, demultiplexer_2_out1, demultiplexer_3_out1);
  or or_10 (or_10_out, demultiplexer_1_out2, demultiplexer_2_out2, demultiplexer_3_out2);
  or or_11 (or_11_out, demultiplexer_1_out3, demultiplexer_2_out3, demultiplexer_3_out3);
  AND8_1 and8_1_28 (.in_1(MEM_ADDR_IN), .in_2(cu_1_mdr0_mem_in), .out_3(and8_1_28_out_3));
  AND8_1 and8_1_29 (.in_1(MDR0_out_8), .in_2(cu_1_mdr1_mem_in), .out_3(and8_1_29_out_3));
  AND8_1 and8_1_30 (.in_1(MDR1_out_8), .in_2(cu_1_mdr2_mem_in), .out_3(and8_1_30_out_3));
  AND8_1 and8_1_31 (.in_1(MDR0_out_8), .in_2(cu_1_mdr0_reg_in), .out_3(and8_1_31_out_3));
  AND8_1 and8_1_32 (.in_1(MDR1_out_8), .in_2(cu_1_mdr1_reg_in), .out_3(and8_1_32_out_3));
  AND8_1 and8_1_33 (.in_1(MDR2_out_8), .in_2(cu_1_mdr2_reg_in), .out_3(and8_1_33_out_3));
  AND8_1 and8_1_34 (.in_1(I0), .in_2(or_8_out), .out_3(and8_1_34_out_3));
  AND8_1 and8_1_35 (.in_1(I1), .in_2(or_9_out), .out_3(and8_1_35_out_3));
  AND8_1 and8_1_36 (.in_1(I2), .in_2(or_10_out), .out_3(and8_1_36_out_3));
  AND8_1 and8_1_37 (.in_1(I3), .in_2(or_11_out), .out_3(and8_1_37_out_3));
  AND8_1 and8_1_38 (.in_1(MEM_ADDR_IN), .in_2(cu_1_mar_reg_id), .out_3(and8_1_38_out_3));
  AND8_1 and8_1_39 (.in_1(MDR0_out_8), .in_2(cu_1_mdr0_reg_id), .out_3(and8_1_39_out_3));
  AND8_1 and8_1_40 (.in_1(MDR1_out_8), .in_2(cu_1_mdr1_reg_id), .out_3(and8_1_40_out_3));
  AND8_1 and8_1_41 (.in_1(MDR2_out_8), .in_2(cu_1_mdr2_reg_id), .out_3(and8_1_41_out_3));
  AND8_1 and8_1_42 (.in_1(MEM_ADDR_IN), .in_2(cu_1_mar_alu_in0), .out_3(and8_1_42_out_3));
  AND8_1 and8_1_43 (.in_1(MDR0_out_8), .in_2(cu_1_mdr0_alu_in0), .out_3(and8_1_43_out_3));
  AND8_1 and8_1_44 (.in_1(MDR1_out_8), .in_2(cu_1_mdr1_alu_in0), .out_3(and8_1_44_out_3));
  AND8_1 and8_1_45 (.in_1(MDR2_out_8), .in_2(cu_1_mdr2_alu_in0), .out_3(and8_1_45_out_3));
  AND8_1 and8_1_46 (.in_1(MEM_ADDR_IN), .in_2(cu_1_mar_alu_in1), .out_3(and8_1_46_out_3));
  AND8_1 and8_1_47 (.in_1(MDR0_out_8), .in_2(cu_1_mdr0_alu_in1), .out_3(and8_1_47_out_3));
  AND8_1 and8_1_48 (.in_1(MDR1_out_8), .in_2(cu_1_mdr1_alu_in1), .out_3(and8_1_48_out_3));
  AND8_1 and8_1_49 (.in_1(MDR2_out_8), .in_2(cu_1_mdr2_alu_in1), .out_3(and8_1_49_out_3));
  assign MEM_IN = and8_1_28_out_3 | and8_1_29_out_3 | and8_1_30_out_3;  // OR_Gate or_12, 8 bits wide
  assign or_13_out = and8_1_31_out_3 | and8_1_32_out_3 | and8_1_33_out_3 | and8_1_34_out_3 | and8_1_35_out_3 | and8_1_36_out_3 | and8_1_37_out_3;  // OR_Gate or_13, 8 bits wide
  assign or_14_out = and8_1_38_out_3 | and8_1_39_out_3 | and8_1_40_out_3 | and8_1_41_out_3;  // OR_Gate or_14, 8 bits wide
  assign or_15_out = and8_1_42_out_3 | and8_1_43_out_3 | and8_1_44_out_3 | and8_1_45_out_3;  // OR_Gate or_15, 8 bits wide
  assign or_16_out = and8_1_46_out_3 | and8_1_47_out_3 | and8_1_48_out_3 | and8_1_49_out_3;  // OR_Gate or_16, 8 bits wide
  or or_17 (or_17_out, and_1_out, not_1_out);
  not not_1 (not_1_out, and_1_out);
  ALU alu_1 (
    .A(or_15_out), .B(or_16_out), .Selector(cu_1_alu_select), .Write(cu_1_alu_write), .Read(cu_1_alu_read),
    .ReadFlags(cu_1_alu_readflags), .Clk(or_17_out), .out_8(alu_1_out_8), .Remainder(alu_1_remainder),
    .Flags(alu_1_flags));
  RegFile regfile_1 (
    .in_1(or_13_out), .RegSelect(or_14_out[3:0]), .Write(cu_1_reg_write), .Read(cu_1_reg_read),
    .Clk(and_1_out), .out_6(regfile_1_out_6), .p3(p3), .p2(p2), .p1(p1), .p0(p0));
endmodule

module CU (
  input  [7:0] Instruction,
  input  [7:0] Flags,
  input  Reset,
  input  Clk,
  output IP_inc,
  output IP_read,
  output IP_write,
  output SP_inc,
  output SP_dec,
  output SP_read,
  output SP_write,
  output MAR_read,
  output MAR_write,
  output MDR0_read,
  output MDR0_write,
  output MDR0_zero,
  output MDR1_read,
  output MDR1_write,
  output MDR1_zero,
  output MDR2_read,
  output MDR2_write,
  output MDR2_zero,
  output MEM_read,
  output MEM_read2,
  output MEM_write,
  output MDR0_MEM_IN,
  output MDR1_MEM_IN,
  output MDR2_MEM_IN,
  output MDR0_REG_IN,
  output MDR1_REG_IN,
  output MDR2_REG_IN,
  output MDR0_IN_REG_IN,
  output MDR1_IN_REG_IN,
  output MDR2_IN_REG_IN,
  output MAR_REG_ID,
  output MDR0_REG_ID,
  output MDR1_REG_ID,
  output MDR2_REG_ID,
  output REG_OUT_MAR,
  output REG_OUT_MDR0,
  output REG_OUT_MDR1,
  output REG_OUT_MDR2,
  output REG_read,
  output REG_write,
  output MAR_MDR0,
  output MAR_MDR1,
  output MAR_MDR2,
  output MDR0_MAR,
  output MDR0_MDR1,
  output MDR0_MDR2,
  output MDR1_MAR,
  output MDR1_MDR0,
  output MDR1_MDR2,
  output MDR2_MAR,
  output MDR2_MDR0,
  output MDR2_MDR1,
  output MAR_ALU_IN0,
  output MDR0_ALU_IN0,
  output MDR1_ALU_IN0,
  output MDR2_ALU_IN0,
  output MAR_ALU_IN1,
  output MDR0_ALU_IN1,
  output MDR1_ALU_IN1,
  output MDR2_ALU_IN1,
  output [7:0] ALU_SELECT,
  output ALU_read,
  output ALU_write,
  output ALU_readFlags,
  output ALU_OUT_MAR,
  output ALU_OUT_MDR0,
  output ALU_OUT_MDR1,
  output ALU_OUT_MDR2,
  output ALU_REMAINDER_MAR,
  output ALU_REMAINDER_MDR0,
  output ALU_REMAINDER_MDR1,
  output ALU_REMAINDER_MDR2,
  output PAGE_read,
  output PAGE_write,
  output CU_endInstruction,
  output hlt
);

  wire and_1_out, equal_1_out_3, ins_rom_1_alu_out_mar, ins_rom_1_alu_out_mdr0, ins_rom_1_alu_out_mdr1,
       ins_rom_1_alu_out_mdr2, ins_rom_1_alu_read, ins_rom_1_alu_readflags, ins_rom_1_alu_remainder_mar,
       ins_rom_1_alu_remainder_mdr0, ins_rom_1_alu_remainder_mdr1, ins_rom_1_alu_remainder_mdr2,
       ins_rom_1_alu_write, ins_rom_1_cu_endinstruction, ins_rom_1_ip_inc, ins_rom_1_ip_read,
       ins_rom_1_ip_write, ins_rom_1_mar_alu_in0, ins_rom_1_mar_alu_in1, ins_rom_1_mar_mdr0,
       ins_rom_1_mar_mdr1, ins_rom_1_mar_mdr2, ins_rom_1_mar_read, ins_rom_1_mar_reg_id, ins_rom_1_mar_write,
       ins_rom_1_mdr0_alu_in0, ins_rom_1_mdr0_alu_in1, ins_rom_1_mdr0_in_reg_in, ins_rom_1_mdr0_mar,
       ins_rom_1_mdr0_mdr1, ins_rom_1_mdr0_mdr2, ins_rom_1_mdr0_mem_in, ins_rom_1_mdr0_read,
       ins_rom_1_mdr0_reg_id, ins_rom_1_mdr0_reg_in, ins_rom_1_mdr0_write, ins_rom_1_mdr0_zero,
       ins_rom_1_mdr1_alu_in0, ins_rom_1_mdr1_alu_in1, ins_rom_1_mdr1_in_reg_in, ins_rom_1_mdr1_mar,
       ins_rom_1_mdr1_mdr0, ins_rom_1_mdr1_mdr2, ins_rom_1_mdr1_mem_in, ins_rom_1_mdr1_read,
       ins_rom_1_mdr1_reg_id, ins_rom_1_mdr1_reg_in, ins_rom_1_mdr1_write, ins_rom_1_mdr1_zero,
       ins_rom_1_mdr2_alu_in0, ins_rom_1_mdr2_alu_in1, ins_rom_1_mdr2_in_reg_in, ins_rom_1_mdr2_mar,
       ins_rom_1_mdr2_mdr0, ins_rom_1_mdr2_mdr1, ins_rom_1_mdr2_mem_in, ins_rom_1_mdr2_read,
       ins_rom_1_mdr2_reg_id, ins_rom_1_mdr2_reg_in, ins_rom_1_mdr2_write, ins_rom_1_mdr2_zero,
       ins_rom_1_mem_read, ins_rom_1_mem_read2, ins_rom_1_mem_write, ins_rom_1_page_read,
       ins_rom_1_page_write, ins_rom_1_reg_out_mar, ins_rom_1_reg_out_mdr0, ins_rom_1_reg_out_mdr1,
       ins_rom_1_reg_out_mdr2, ins_rom_1_reg_read, ins_rom_1_reg_write, ins_rom_1_sp_dec, ins_rom_1_sp_inc,
       ins_rom_1_sp_read, ins_rom_1_sp_write, ins_rom_reg_1_cu_endinstruction, ins_rom_reg_1_ip_write,
       ins_rom_reg_1_mar_read, ins_rom_reg_1_mem_read, nor_1_out, nor_2_out, not_1_out, or_1_out, or_2_out,
       s_r_ff_1_q;
  wire [7:0] cyclereg_1_out_3, ins_rom_1_alu_select, register_1_q;

  or or_1 (or_1_out, Reset, ins_rom_reg_1_cu_endinstruction);
  nor nor_1 (nor_1_out, Clk, s_r_ff_1_q);
  S_R_Flip_Flop #(.trigger("high")) s_r_ff_1 (
    .S(or_1_out), .R(Clk), .clk(1'b1), .Q(s_r_ff_1_q));  // open: reset, Qn, preset
  nor nor_2 (nor_2_out, Clk, Reset);
  CycleReg cyclereg_1 (.Inc(nor_1_out), .Zero(s_r_ff_1_q), .out_3(cyclereg_1_out_3));
  INS_ROM ins_rom_1 (
    .Instruction(register_1_q), .Cycle(cyclereg_1_out_3), .CLK(nor_2_out), .Flags(Flags),
    .IP_inc(ins_rom_1_ip_inc), .IP_read(ins_rom_1_ip_read), .IP_write(ins_rom_1_ip_write),
    .SP_inc(ins_rom_1_sp_inc), .SP_dec(ins_rom_1_sp_dec), .SP_read(ins_rom_1_sp_read),
    .SP_write(ins_rom_1_sp_write), .MAR_read(ins_rom_1_mar_read), .MAR_write(ins_rom_1_mar_write),
    .MDR0_read(ins_rom_1_mdr0_read), .MDR0_write(ins_rom_1_mdr0_write), .MDR0_zero(ins_rom_1_mdr0_zero),
    .MDR1_read(ins_rom_1_mdr1_read), .MDR1_write(ins_rom_1_mdr1_write), .MDR1_zero(ins_rom_1_mdr1_zero),
    .MDR2_read(ins_rom_1_mdr2_read), .MDR2_write(ins_rom_1_mdr2_write), .MDR2_zero(ins_rom_1_mdr2_zero),
    .MEM_read(ins_rom_1_mem_read), .MEM_read2(ins_rom_1_mem_read2), .MEM_write(ins_rom_1_mem_write),
    .MDR0_MEM_IN(ins_rom_1_mdr0_mem_in), .MDR1_MEM_IN(ins_rom_1_mdr1_mem_in),
    .MDR2_MEM_IN(ins_rom_1_mdr2_mem_in), .MDR0_REG_IN(ins_rom_1_mdr0_reg_in),
    .MDR1_REG_IN(ins_rom_1_mdr1_reg_in), .MDR2_REG_IN(ins_rom_1_mdr2_reg_in),
    .MDR0_IN_REG_IN(ins_rom_1_mdr0_in_reg_in), .MDR1_IN_REG_IN(ins_rom_1_mdr1_in_reg_in),
    .MDR2_IN_REG_IN(ins_rom_1_mdr2_in_reg_in), .MAR_REG_ID(ins_rom_1_mar_reg_id),
    .MDR0_REG_ID(ins_rom_1_mdr0_reg_id), .MDR1_REG_ID(ins_rom_1_mdr1_reg_id),
    .MDR2_REG_ID(ins_rom_1_mdr2_reg_id), .REG_OUT_MAR(ins_rom_1_reg_out_mar),
    .REG_OUT_MDR0(ins_rom_1_reg_out_mdr0), .REG_OUT_MDR1(ins_rom_1_reg_out_mdr1),
    .REG_OUT_MDR2(ins_rom_1_reg_out_mdr2), .REG_read(ins_rom_1_reg_read), .REG_write(ins_rom_1_reg_write),
    .MAR_MDR0(ins_rom_1_mar_mdr0), .MAR_MDR1(ins_rom_1_mar_mdr1), .MAR_MDR2(ins_rom_1_mar_mdr2),
    .MDR0_MAR(ins_rom_1_mdr0_mar), .MDR0_MDR1(ins_rom_1_mdr0_mdr1), .MDR0_MDR2(ins_rom_1_mdr0_mdr2),
    .MDR1_MAR(ins_rom_1_mdr1_mar), .MDR1_MDR0(ins_rom_1_mdr1_mdr0), .MDR1_MDR2(ins_rom_1_mdr1_mdr2),
    .MDR2_MAR(ins_rom_1_mdr2_mar), .MDR2_MDR0(ins_rom_1_mdr2_mdr0), .MDR2_MDR1(ins_rom_1_mdr2_mdr1),
    .MAR_ALU_IN0(ins_rom_1_mar_alu_in0), .MDR0_ALU_IN0(ins_rom_1_mdr0_alu_in0),
    .MDR1_ALU_IN0(ins_rom_1_mdr1_alu_in0), .MDR2_ALU_IN0(ins_rom_1_mdr2_alu_in0),
    .MAR_ALU_IN1(ins_rom_1_mar_alu_in1), .MDR0_ALU_IN1(ins_rom_1_mdr0_alu_in1),
    .MDR1_ALU_IN1(ins_rom_1_mdr1_alu_in1), .MDR2_ALU_IN1(ins_rom_1_mdr2_alu_in1),
    .ALU_SELECT(ins_rom_1_alu_select), .ALU_read(ins_rom_1_alu_read), .ALU_write(ins_rom_1_alu_write),
    .ALU_readFlags(ins_rom_1_alu_readflags), .ALU_OUT_MAR(ins_rom_1_alu_out_mar),
    .ALU_OUT_MDR0(ins_rom_1_alu_out_mdr0), .ALU_OUT_MDR1(ins_rom_1_alu_out_mdr1),
    .ALU_OUT_MDR2(ins_rom_1_alu_out_mdr2), .ALU_REMAINDER_MAR(ins_rom_1_alu_remainder_mar),
    .ALU_REMAINDER_MDR0(ins_rom_1_alu_remainder_mdr0), .ALU_REMAINDER_MDR1(ins_rom_1_alu_remainder_mdr1),
    .ALU_REMAINDER_MDR2(ins_rom_1_alu_remainder_mdr2), .PAGE_read(ins_rom_1_page_read),
    .PAGE_write(ins_rom_1_page_write), .CU_endInstruction(ins_rom_1_cu_endinstruction));  // open: hlt
  and and_1 (and_1_out, s_r_ff_1_q, not_1_out);
  not not_1 (not_1_out, Clk);
  or or_2 (or_2_out, and_1_out, Clk);
  Equal equal_1 (.in_1(register_1_q), .in_2({8{1'b1}}), .out_3(equal_1_out_3));
  Register #(.trigger("high")) register_1 (
    .D(Instruction), .en(s_r_ff_1_q), .clk(or_2_out), .Q(register_1_q));  // open: clr
  INS_ROM_REG ins_rom_reg_1 (
    .Write(not_1_out), .Read(Clk), .Clk(1'b1), .in_4(ins_rom_1_ip_inc), .in_5(ins_rom_1_ip_read),
    .in_6(ins_rom_1_ip_write), .in_7(ins_rom_1_sp_inc), .in_8(ins_rom_1_sp_dec), .in_9(ins_rom_1_sp_read),
    .in_10(ins_rom_1_sp_write), .in_11(ins_rom_1_mar_read), .in_12(ins_rom_1_mar_write),
    .in_13(ins_rom_1_mdr0_read), .in_14(ins_rom_1_mdr0_write), .in_15(ins_rom_1_mdr0_zero),
    .in_16(ins_rom_1_mdr1_read), .in_17(ins_rom_1_mdr1_write), .in_18(ins_rom_1_mdr1_zero),
    .in_19(ins_rom_1_mdr2_read), .in_20(ins_rom_1_mdr2_write), .in_21(ins_rom_1_mdr2_zero),
    .in_22(ins_rom_1_mem_read), .in_23(ins_rom_1_mem_read2), .in_24(ins_rom_1_mem_write),
    .in_25(ins_rom_1_mdr0_mem_in), .in_26(ins_rom_1_mdr1_mem_in), .in_27(ins_rom_1_mdr2_mem_in),
    .in_28(ins_rom_1_mdr0_reg_in), .in_29(ins_rom_1_mdr1_reg_in), .in_30(ins_rom_1_mdr2_reg_in),
    .in_31(ins_rom_1_mdr0_in_reg_in), .in_32(ins_rom_1_mdr1_in_reg_in), .in_33(ins_rom_1_mdr2_in_reg_in),
    .in_34(ins_rom_1_mar_reg_id), .in_35(ins_rom_1_mdr0_reg_id), .in_36(ins_rom_1_mdr1_reg_id),
    .in_37(ins_rom_1_mdr2_reg_id), .in_38(ins_rom_1_reg_out_mar), .in_39(ins_rom_1_reg_out_mdr0),
    .in_40(ins_rom_1_reg_out_mdr1), .in_41(ins_rom_1_reg_out_mdr2), .in_42(ins_rom_1_reg_read),
    .in_43(ins_rom_1_reg_write), .in_44(ins_rom_1_mar_mdr0), .in_45(ins_rom_1_mar_mdr1),
    .in_46(ins_rom_1_mar_mdr2), .in_47(ins_rom_1_mdr0_mar), .in_48(ins_rom_1_mdr0_mdr1),
    .in_49(ins_rom_1_mdr0_mdr2), .in_50(ins_rom_1_mdr1_mar), .in_51(ins_rom_1_mdr1_mdr0),
    .in_52(ins_rom_1_mdr1_mdr2), .in_53(ins_rom_1_mdr2_mar), .in_54(ins_rom_1_mdr2_mdr0),
    .in_55(ins_rom_1_mdr2_mdr1), .in_56(ins_rom_1_mar_alu_in0), .in_57(ins_rom_1_mdr0_alu_in0),
    .in_58(ins_rom_1_mdr1_alu_in0), .in_59(ins_rom_1_mdr2_alu_in0), .in_60(ins_rom_1_mar_alu_in1),
    .in_61(ins_rom_1_mdr0_alu_in1), .in_62(ins_rom_1_mdr1_alu_in1), .in_63(ins_rom_1_mdr2_alu_in1),
    .in_64(ins_rom_1_alu_select), .in_65(ins_rom_1_alu_read), .in_66(ins_rom_1_alu_write),
    .in_67(ins_rom_1_alu_readflags), .in_68(ins_rom_1_alu_out_mar), .in_69(ins_rom_1_alu_out_mdr0),
    .in_70(ins_rom_1_alu_out_mdr1), .in_71(ins_rom_1_alu_out_mdr2), .in_72(ins_rom_1_alu_remainder_mar),
    .in_73(ins_rom_1_alu_remainder_mdr0), .in_74(ins_rom_1_alu_remainder_mdr1),
    .in_75(ins_rom_1_alu_remainder_mdr2), .in_76(ins_rom_1_page_read), .in_77(ins_rom_1_page_write),
    .in_78(ins_rom_1_cu_endinstruction), .in_79(equal_1_out_3), .IP_inc(IP_inc), .IP_read(IP_read),
    .IP_write(ins_rom_reg_1_ip_write), .SP_inc(SP_inc), .SP_dec(SP_dec), .SP_read(SP_read),
    .SP_write(SP_write), .MAR_read(ins_rom_reg_1_mar_read), .MAR_write(MAR_write), .MDR0_read(MDR0_read),
    .MDR0_write(MDR0_write), .MDR0_zero(MDR0_zero), .MDR1_read(MDR1_read), .MDR1_write(MDR1_write),
    .MDR1_zero(MDR1_zero), .MDR2_read(MDR2_read), .MDR2_write(MDR2_write), .MDR2_zero(MDR2_zero),
    .MEM_read(ins_rom_reg_1_mem_read), .MEM_read2(MEM_read2), .MEM_write(MEM_write),
    .MDR0_MEM_IN(MDR0_MEM_IN), .MDR1_MEM_IN(MDR1_MEM_IN), .MDR2_MEM_IN(MDR2_MEM_IN),
    .MDR0_REG_IN(MDR0_REG_IN), .MDR1_REG_IN(MDR1_REG_IN), .MDR2_REG_IN(MDR2_REG_IN),
    .MDR0_IN_REG_IN(MDR0_IN_REG_IN), .MDR1_IN_REG_IN(MDR1_IN_REG_IN), .MDR2_IN_REG_IN(MDR2_IN_REG_IN),
    .MAR_REG_ID(MAR_REG_ID), .MDR0_REG_ID(MDR0_REG_ID), .MDR1_REG_ID(MDR1_REG_ID), .MDR2_REG_ID(MDR2_REG_ID),
    .REG_OUT_MAR(REG_OUT_MAR), .REG_OUT_MDR0(REG_OUT_MDR0), .REG_OUT_MDR1(REG_OUT_MDR1),
    .REG_OUT_MDR2(REG_OUT_MDR2), .REG_read(REG_read), .REG_write(REG_write), .MAR_MDR0(MAR_MDR0),
    .MAR_MDR1(MAR_MDR1), .MAR_MDR2(MAR_MDR2), .MDR0_MAR(MDR0_MAR), .MDR0_MDR1(MDR0_MDR1),
    .MDR0_MDR2(MDR0_MDR2), .MDR1_MAR(MDR1_MAR), .MDR1_MDR0(MDR1_MDR0), .MDR1_MDR2(MDR1_MDR2),
    .MDR2_MAR(MDR2_MAR), .MDR2_MDR0(MDR2_MDR0), .MDR2_MDR1(MDR2_MDR1), .MAR_ALU_IN0(MAR_ALU_IN0),
    .MDR0_ALU_IN0(MDR0_ALU_IN0), .MDR1_ALU_IN0(MDR1_ALU_IN0), .MDR2_ALU_IN0(MDR2_ALU_IN0),
    .MAR_ALU_IN1(MAR_ALU_IN1), .MDR0_ALU_IN1(MDR0_ALU_IN1), .MDR1_ALU_IN1(MDR1_ALU_IN1),
    .MDR2_ALU_IN1(MDR2_ALU_IN1), .ALU_SELECT(ALU_SELECT), .ALU_read(ALU_read), .ALU_write(ALU_write),
    .ALU_readFlags(ALU_readFlags), .ALU_OUT_MAR(ALU_OUT_MAR), .ALU_OUT_MDR0(ALU_OUT_MDR0),
    .ALU_OUT_MDR1(ALU_OUT_MDR1), .ALU_OUT_MDR2(ALU_OUT_MDR2), .ALU_REMAINDER_MAR(ALU_REMAINDER_MAR),
    .ALU_REMAINDER_MDR0(ALU_REMAINDER_MDR0), .ALU_REMAINDER_MDR1(ALU_REMAINDER_MDR1),
    .ALU_REMAINDER_MDR2(ALU_REMAINDER_MDR2), .PAGE_read(PAGE_read), .PAGE_write(PAGE_write),
    .CU_endInstruction(ins_rom_reg_1_cu_endinstruction), .hlt(hlt));
  or or_3 (IP_write, Reset, ins_rom_reg_1_ip_write);
  or or_4 (MAR_read, and_1_out, ins_rom_reg_1_mar_read);
  or or_5 (MEM_read, and_1_out, ins_rom_reg_1_mem_read);
  or or_6 (CU_endInstruction, and_1_out, ins_rom_reg_1_cu_endinstruction);

  // Notes on the sheet:
  //   Fetch next Instruction
endmodule

module ALU (
  input  [7:0] A,
  input  [7:0] B,
  input  [7:0] Selector,
  input  Write,
  input  Read,
  input  ReadFlags,
  input  Clk,
  output [7:0] out_8,
  output [7:0] Remainder,
  output [7:0] Flags
);

  wire adder_1_cout, and_1_out, and_2_out, and_4_out, and_5_out, and_6_out, and_7_out, and_8_out,
       demultiplexer_1_out0, demultiplexer_1_out1, demultiplexer_1_out2, demultiplexer_1_out3,
       demultiplexer_1_out4, demultiplexer_1_out5, demultiplexer_1_out6, demultiplexer_1_out7,
       demultiplexer_1_out8, demultiplexer_1_out9, demultiplexer_1_out10, demultiplexer_1_out11, not_1_out,
       not_2_out, or5_1_out_2, or5_2_out_2, or8_1_out_2, subtractor_1_bout, xnor_1_out, xor_2_out, xor_3_out,
       ZF_out_2;
  wire [4:0] not_4_out;
  wire [6:0] and8_1_2_out_3;
  wire [7:0] adder_1_out, and8_1_1_out_3, and8_1_3_out_3, and8_1_4_out_3, and8_1_5_out_3, and8_1_6_out_3,
       and8_1_7_out_3, and8_1_8_out_3, and8_1_9_out_3, and8_1_10_out_3, and8_1_11_out_3, and_3_out,
       divider_1_out, divider_1_rem, multiplier_1_cout, multiplier_1_out, not_3_out, or_1_out, or_2_out,
       register_1_q, register_2_q, shifter_1_out, shifter_2_out, subtractor_1_out, xor_1_out;

  Demultiplexer #(.select(4)) demultiplexer_1 (
    .out0(demultiplexer_1_out0), .out1(demultiplexer_1_out1), .out2(demultiplexer_1_out2),
    .out3(demultiplexer_1_out3), .out4(demultiplexer_1_out4), .out5(demultiplexer_1_out5),
    .out6(demultiplexer_1_out6), .out7(demultiplexer_1_out7), .out8(demultiplexer_1_out8),
    .out9(demultiplexer_1_out9), .out10(demultiplexer_1_out10), .out11(demultiplexer_1_out11), .in(1'b1),
    .sel(Selector[3:0]));  // open: out12, out13, out14, out15
  OR5 or5_1 (.in_1(A[7:3]), .out_2(or5_1_out_2));
  OR5 or5_2 (.in_1(A[7:3]), .out_2(or5_2_out_2));
  Adder adder_1 (.a(A), .b(B), .out(adder_1_out), .cin(demultiplexer_1_out10), .cout(adder_1_cout));
  Subtractor subtractor_1 (.a(A), .b(B), .out(subtractor_1_out), .bin(demultiplexer_1_out11), .bout(subtractor_1_bout));
  Multiplier multiplier_1 (.a(A), .b(B), .out(multiplier_1_out), .cout(multiplier_1_cout));  // open: cin
  Divider divider_1 (.a(A), .b(B), .out(divider_1_out), .rem(divider_1_rem));  // open: upper
  Shifter shifter_1 (.in(A), .\dist (A[2:0]), .out(shifter_1_out));
  not not_1 (not_1_out, or5_1_out_2);
  and and_1 (and_1_out, not_1_out, demultiplexer_1_out4);
  Shifter #(.shift("lr")) shifter_2 (.in(A), .\dist (A[2:0]), .out(shifter_2_out));
  not not_2 (not_2_out, or5_2_out_2);
  and and_2 (and_2_out, not_2_out, demultiplexer_1_out5);
  assign and_3_out = A & B;  // AND_Gate and_3, 8 bits wide
  assign not_3_out = ~A;  // NOT_Gate not_3, 8 bits wide
  assign or_1_out = A | B;  // OR_Gate or_1, 8 bits wide
  assign xor_1_out = A ^ B;  // XOR_Gate xor_1, 8 bits wide
  AND8_1 and8_1_1 (.in_1(adder_1_out), .in_2(demultiplexer_1_out0), .out_3(and8_1_1_out_3));
  AND8_1 and8_1_2 (.in_1(subtractor_1_out), .in_2(demultiplexer_1_out1), .out_3({not_4_out[2], and8_1_2_out_3}));
  AND8_1 and8_1_3 (.in_1(multiplier_1_out), .in_2(demultiplexer_1_out2), .out_3(and8_1_3_out_3));
  AND8_1 and8_1_4 (.in_1(divider_1_out), .in_2(demultiplexer_1_out3), .out_3(and8_1_4_out_3));
  AND8_1 and8_1_5 (.in_1(shifter_1_out), .in_2(and_1_out), .out_3(and8_1_5_out_3));
  AND8_1 and8_1_6 (.in_1(shifter_2_out), .in_2(and_2_out), .out_3(and8_1_6_out_3));
  AND8_1 and8_1_7 (.in_1(and_3_out), .in_2(demultiplexer_1_out6), .out_3(and8_1_7_out_3));
  AND8_1 and8_1_8 (.in_1(not_3_out), .in_2(demultiplexer_1_out7), .out_3(and8_1_8_out_3));
  AND8_1 and8_1_9 (.in_1(or_1_out), .in_2(demultiplexer_1_out8), .out_3(and8_1_9_out_3));
  AND8_1 and8_1_10 (.in_1(xor_1_out), .in_2(demultiplexer_1_out9), .out_3(and8_1_10_out_3));
  OR8 or8_1 (.in_1(multiplier_1_cout), .out_2(or8_1_out_2));
  and and_4 (and_4_out, demultiplexer_1_out0, adder_1_cout);
  and and_5 (and_5_out, demultiplexer_1_out1, subtractor_1_bout);
  and and_6 (and_6_out, or8_1_out_2, demultiplexer_1_out2);
  AND8_1 and8_1_11 (.in_1(divider_1_rem), .in_2(demultiplexer_1_out3), .out_3(and8_1_11_out_3));
  xnor xnor_1 (xnor_1_out, A[7], B[7]);
  xor xor_2 (xor_2_out, A[7], not_4_out[2]);
  xor xor_3 (xor_3_out, A[7], B[7]);
  or CF (not_4_out[1], and_4_out, and_5_out, and_6_out);
  assign or_2_out = and8_1_1_out_3 | {not_4_out[2], and8_1_2_out_3} | and8_1_3_out_3 | and8_1_4_out_3 | and8_1_5_out_3 | and8_1_6_out_3 | and8_1_7_out_3 | and8_1_8_out_3 | and8_1_9_out_3 | and8_1_10_out_3;  // OR_Gate or_2, 8 bits wide
  and and_7 (and_7_out, demultiplexer_1_out1, xnor_1_out, xor_2_out);
  or OFlag (not_4_out[3], and_7_out, and_8_out);
  and and_8 (and_8_out, demultiplexer_1_out0, xor_3_out, xor_2_out);
  OR8 ZF (.in_1(or_2_out), .out_2(ZF_out_2));
  not not_4 (not_4_out[0], ZF_out_2);
  PF pf_1 (.in_1(or_2_out), .out_2(not_4_out[4]));
  Register #(.trigger("high")) register_1 (.D(or_2_out), .en(Write), .clk(Clk), .Q(register_1_q));  // open: clr
  Register #(.trigger("high")) register_2 (.D(and8_1_11_out_3), .en(Write), .clk(Clk), .Q(register_2_q));  // open: clr
  Register #(.trigger("high")) register_3 (.D({3'b000, not_4_out}), .en(Write), .clk(Clk), .Q(Flags));  // open: clr
  AND8_1 and8_1_12 (.in_1(register_1_q), .in_2(Read), .out_3(out_8));
  AND8_1 and8_1_13 (.in_1(register_2_q), .in_2(Read), .out_3(Remainder));
endmodule

module PF (
  input  [7:0] in_1,
  output out_2
);

  wire [1:0] xnor_2_out;
  wire [3:0] xnor_1_out;

  assign xnor_1_out = ~(in_1[3:0] ^ in_1[7:4]);  // XNOR_Gate xnor_1, 4 bits wide
  assign xnor_2_out = ~(xnor_1_out[1:0] ^ xnor_1_out[3:2]);  // XNOR_Gate xnor_2, 2 bits wide
  xnor xnor_3 (out_2, xnor_2_out[0], xnor_2_out[1]);
endmodule

module RegFile (
  input  [7:0] in_1,
  input  [3:0] RegSelect,
  input  Write,
  input  Read,
  input  Clk,
  output [7:0] out_6,
  output [7:0] p3,
  output [7:0] p2,
  output [7:0] p1,
  output [7:0] p0
);

  wire and_1_out, and_2_out, and_3_out, and_4_out, and_5_out, and_6_out, and_7_out, and_8_out, and_9_out,
       and_10_out, and_11_out, and_12_out, and_13_out, and_14_out, and_15_out, and_16_out, and_17_out,
       and_18_out, and_19_out, and_20_out, and_21_out, and_22_out, and_23_out, and_24_out, and_25_out,
       and_26_out, and_27_out, and_28_out, and_29_out, and_30_out, and_31_out, and_32_out, and_33_out,
       demultiplexer_1_out0, demultiplexer_1_out1, demultiplexer_1_out2, demultiplexer_1_out3,
       demultiplexer_1_out4, demultiplexer_1_out5, demultiplexer_1_out6, demultiplexer_1_out7,
       demultiplexer_1_out8, demultiplexer_1_out9, demultiplexer_1_out10, demultiplexer_1_out11,
       demultiplexer_1_out12, demultiplexer_1_out13, demultiplexer_1_out14, demultiplexer_1_out15, nor_1_out,
       nor_2_out, nor_3_out, nor_4_out, nor_5_out, nor_6_out, nor_7_out, nor_8_out, nor_9_out, nor_10_out,
       nor_11_out, not_1_out, not_2_out, not_3_out, not_4_out, not_5_out, not_6_out, not_7_out, not_8_out,
       not_9_out, not_10_out, not_11_out, not_12_out, not_13_out, not_14_out, not_15_out, not_16_out,
       not_17_out, not_18_out, not_19_out, not_20_out, not_21_out, not_22_out, or_1_out, or_2_out, or_3_out,
       or_4_out, or_5_out, or_6_out, or_7_out, or_8_out, or_9_out, or_10_out, or_11_out;
  wire [7:0] multiplexer_1_out, multiplexer_2_out, multiplexer_3_out, multiplexer_4_out, multiplexer_5_out,
       multiplexer_6_out, multiplexer_7_out, multiplexer_8_out, multiplexer_9_out, multiplexer_10_out,
       multiplexer_11_out, multiplexer_12_out, multiplexer_13_out, multiplexer_14_out, multiplexer_15_out,
       multiplexer_16_out, multiplexer_17_out, multiplexer_18_out, Reg0_q, Reg1_q, Reg2_q, Reg3_q, Reg4_q,
       Reg5_q, Reg6_q, register_1_q, register_2_q, register_3_q, register_4_q, register_5_q, register_6_q,
       register_7_q, register_8_q, register_9_q, register_10_q, register_11_q, register_12_q, register_13_q,
       register_14_q, register_15_q;

  Demultiplexer #(.select(4)) demultiplexer_1 (
    .out0(demultiplexer_1_out0), .out1(demultiplexer_1_out1), .out2(demultiplexer_1_out2),
    .out3(demultiplexer_1_out3), .out4(demultiplexer_1_out4), .out5(demultiplexer_1_out5),
    .out6(demultiplexer_1_out6), .out7(demultiplexer_1_out7), .out8(demultiplexer_1_out8),
    .out9(demultiplexer_1_out9), .out10(demultiplexer_1_out10), .out11(demultiplexer_1_out11),
    .out12(demultiplexer_1_out12), .out13(demultiplexer_1_out13), .out14(demultiplexer_1_out14),
    .out15(demultiplexer_1_out15), .in(1'b1), .sel(RegSelect));
  and and_1 (and_1_out, demultiplexer_1_out0, Write);
  and and_2 (and_2_out, demultiplexer_1_out1, Write);
  and and_3 (and_3_out, demultiplexer_1_out2, Write);
  and and_4 (and_4_out, demultiplexer_1_out3, Write);
  and and_5 (and_5_out, demultiplexer_1_out4, Write);
  and and_6 (and_6_out, demultiplexer_1_out5, Write);
  and and_7 (and_7_out, demultiplexer_1_out6, Write);
  and and_8 (and_8_out, demultiplexer_1_out12, Write);
  and and_9 (and_9_out, demultiplexer_1_out13, Write);
  and and_10 (and_10_out, demultiplexer_1_out14, Write);
  and and_11 (and_11_out, demultiplexer_1_out15, Write);
  Multiplexer #(.width(8)) multiplexer_1 (.in0(register_5_q), .in1(in_1), .out(multiplexer_1_out), .sel(and_1_out));
  Multiplexer #(.width(8)) multiplexer_2 (.in0(register_6_q), .in1(in_1), .out(multiplexer_2_out), .sel(and_2_out));
  Multiplexer #(.width(8)) multiplexer_3 (.in0(register_7_q), .in1(in_1), .out(multiplexer_3_out), .sel(and_3_out));
  Multiplexer #(.width(8)) multiplexer_4 (.in0(register_8_q), .in1(in_1), .out(multiplexer_4_out), .sel(and_4_out));
  Multiplexer #(.width(8)) multiplexer_5 (.in0(register_9_q), .in1(in_1), .out(multiplexer_5_out), .sel(and_5_out));
  Multiplexer #(.width(8)) multiplexer_6 (.in0(register_10_q), .in1(in_1), .out(multiplexer_6_out), .sel(and_6_out));
  Multiplexer #(.width(8)) multiplexer_7 (.in0(register_11_q), .in1(in_1), .out(multiplexer_7_out), .sel(and_7_out));
  Multiplexer #(.width(8)) multiplexer_8 (.in0(register_12_q), .in1(in_1), .out(multiplexer_8_out), .sel(and_8_out));
  Multiplexer #(.width(8)) multiplexer_9 (.in0(register_13_q), .in1(in_1), .out(multiplexer_9_out), .sel(and_9_out));
  Multiplexer #(.width(8)) multiplexer_10 (.in0(register_14_q), .in1(in_1), .out(multiplexer_10_out), .sel(and_10_out));
  Multiplexer #(.width(8)) multiplexer_11 (.in0(register_15_q), .in1(in_1), .out(multiplexer_11_out), .sel(and_11_out));
  Register #(.trigger("high")) Reg0 (.D(multiplexer_1_out), .en(or_1_out), .clk(1'b1), .Q(Reg0_q));  // open: clr
  nor nor_1 (nor_1_out, Clk, and_1_out);
  or or_1 (or_1_out, nor_1_out, and_12_out);
  and and_12 (and_12_out, and_1_out, Clk);
  Register #(.trigger("high")) Reg1 (.D(multiplexer_2_out), .en(or_2_out), .clk(1'b1), .Q(Reg1_q));  // open: clr
  nor nor_2 (nor_2_out, Clk, and_2_out);
  or or_2 (or_2_out, nor_2_out, and_13_out);
  and and_13 (and_13_out, and_2_out, Clk);
  Register #(.trigger("high")) Reg2 (.D(multiplexer_3_out), .en(or_3_out), .clk(1'b1), .Q(Reg2_q));  // open: clr
  nor nor_3 (nor_3_out, Clk, and_3_out);
  or or_3 (or_3_out, nor_3_out, and_14_out);
  and and_14 (and_14_out, and_3_out, Clk);
  Register #(.trigger("high")) Reg3 (.D(multiplexer_4_out), .en(or_4_out), .clk(1'b1), .Q(Reg3_q));  // open: clr
  nor nor_4 (nor_4_out, Clk, and_4_out);
  or or_4 (or_4_out, nor_4_out, and_15_out);
  and and_15 (and_15_out, and_4_out, Clk);
  Register #(.trigger("high")) Reg4 (.D(multiplexer_5_out), .en(or_5_out), .clk(1'b1), .Q(Reg4_q));  // open: clr
  nor nor_5 (nor_5_out, Clk, and_5_out);
  or or_5 (or_5_out, nor_5_out, and_16_out);
  and and_16 (and_16_out, and_5_out, Clk);
  Register #(.trigger("high")) Reg5 (.D(multiplexer_6_out), .en(or_6_out), .clk(1'b1), .Q(Reg5_q));  // open: clr
  nor nor_6 (nor_6_out, Clk, and_6_out);
  or or_6 (or_6_out, nor_6_out, and_17_out);
  and and_17 (and_17_out, and_6_out, Clk);
  Register #(.trigger("high")) Reg6 (.D(multiplexer_7_out), .en(or_7_out), .clk(1'b1), .Q(Reg6_q));  // open: clr
  nor nor_7 (nor_7_out, Clk, and_7_out);
  or or_7 (or_7_out, nor_7_out, and_18_out);
  and and_18 (and_18_out, and_7_out, Clk);
  Register #(.trigger("high")) register_1 (
    .D(multiplexer_8_out), .en(or_8_out), .clk(1'b1), .Q(register_1_q));  // open: clr
  nor nor_8 (nor_8_out, Clk, and_8_out);
  or or_8 (or_8_out, nor_8_out, and_19_out);
  and and_19 (and_19_out, and_8_out, Clk);
  Register #(.trigger("high")) register_2 (
    .D(multiplexer_9_out), .en(or_9_out), .clk(1'b1), .Q(register_2_q));  // open: clr
  nor nor_9 (nor_9_out, Clk, and_9_out);
  or or_9 (or_9_out, nor_9_out, and_20_out);
  and and_20 (and_20_out, and_9_out, Clk);
  Register #(.trigger("high")) register_3 (
    .D(multiplexer_10_out), .en(or_10_out), .clk(1'b1), .Q(register_3_q));  // open: clr
  nor nor_10 (nor_10_out, Clk, and_10_out);
  or or_10 (or_10_out, nor_10_out, and_21_out);
  and and_21 (and_21_out, and_10_out, Clk);
  Register #(.trigger("high")) register_4 (
    .D(multiplexer_11_out), .en(or_11_out), .clk(1'b1), .Q(register_4_q));  // open: clr
  nor nor_11 (nor_11_out, Clk, and_11_out);
  or or_11 (or_11_out, nor_11_out, and_22_out);
  and and_22 (and_22_out, and_11_out, Clk);
  Register #(.trigger("high")) register_5 (.D(Reg0_q), .en(and_23_out), .clk(1'b1), .Q(register_5_q));  // open: clr
  not not_1 (not_1_out, Clk);
  and and_23 (and_23_out, not_1_out, and_1_out);
  Register #(.trigger("high")) register_6 (.D(Reg1_q), .en(and_24_out), .clk(1'b1), .Q(register_6_q));  // open: clr
  not not_2 (not_2_out, Clk);
  and and_24 (and_24_out, not_2_out, and_2_out);
  Register #(.trigger("high")) register_7 (.D(Reg2_q), .en(and_25_out), .clk(1'b1), .Q(register_7_q));  // open: clr
  not not_3 (not_3_out, Clk);
  and and_25 (and_25_out, not_3_out, and_3_out);
  Register #(.trigger("high")) register_8 (.D(Reg3_q), .en(and_26_out), .clk(1'b1), .Q(register_8_q));  // open: clr
  not not_4 (not_4_out, Clk);
  and and_26 (and_26_out, not_4_out, and_4_out);
  Register #(.trigger("high")) register_9 (.D(Reg4_q), .en(and_27_out), .clk(1'b1), .Q(register_9_q));  // open: clr
  not not_5 (not_5_out, Clk);
  and and_27 (and_27_out, not_5_out, and_5_out);
  Register #(.trigger("high")) register_10 (.D(Reg5_q), .en(and_28_out), .clk(1'b1), .Q(register_10_q));  // open: clr
  not not_6 (not_6_out, Clk);
  and and_28 (and_28_out, not_6_out, and_6_out);
  Register #(.trigger("high")) register_11 (.D(Reg6_q), .en(and_29_out), .clk(1'b1), .Q(register_11_q));  // open: clr
  not not_7 (not_7_out, Clk);
  and and_29 (and_29_out, not_7_out, and_7_out);
  Register #(.trigger("high")) register_12 (
    .D(register_1_q), .en(and_30_out), .clk(1'b1), .Q(register_12_q));  // open: clr
  not not_8 (not_8_out, Clk);
  and and_30 (and_30_out, not_8_out, and_8_out);
  Register #(.trigger("high")) register_13 (
    .D(register_2_q), .en(and_31_out), .clk(1'b1), .Q(register_13_q));  // open: clr
  not not_9 (not_9_out, Clk);
  and and_31 (and_31_out, not_9_out, and_9_out);
  Register #(.trigger("high")) register_14 (
    .D(register_3_q), .en(and_32_out), .clk(1'b1), .Q(register_14_q));  // open: clr
  not not_10 (not_10_out, Clk);
  and and_32 (and_32_out, not_10_out, and_10_out);
  Register #(.trigger("high")) register_15 (
    .D(register_4_q), .en(and_33_out), .clk(1'b1), .Q(register_15_q));  // open: clr
  not not_11 (not_11_out, Clk);
  and and_33 (and_33_out, not_11_out, and_11_out);
  not not_12 (not_12_out, and_1_out);
  not not_13 (not_13_out, and_2_out);
  not not_14 (not_14_out, and_3_out);
  not not_15 (not_15_out, and_4_out);
  not not_16 (not_16_out, and_5_out);
  not not_17 (not_17_out, and_6_out);
  not not_18 (not_18_out, and_7_out);
  not not_19 (not_19_out, and_8_out);
  not not_20 (not_20_out, and_9_out);
  not not_21 (not_21_out, and_10_out);
  not not_22 (not_22_out, and_11_out);
  Multiplexer #(.enable("true"), .width(8)) multiplexer_12 (
    .in0(Reg0_q), .in1(register_5_q), .out(multiplexer_12_out), .sel(not_12_out), .en(Clk));
  Multiplexer #(.enable("true"), .width(8)) multiplexer_13 (
    .in0(Reg1_q), .in1(register_6_q), .out(multiplexer_13_out), .sel(not_13_out), .en(Clk));
  Multiplexer #(.enable("true"), .width(8)) multiplexer_14 (
    .in0(Reg2_q), .in1(register_7_q), .out(multiplexer_14_out), .sel(not_14_out), .en(Clk));
  Multiplexer #(.enable("true"), .width(8)) multiplexer_15 (
    .in0(Reg3_q), .in1(register_8_q), .out(multiplexer_15_out), .sel(not_15_out), .en(Clk));
  Multiplexer #(.enable("true"), .width(8)) multiplexer_16 (
    .in0(Reg4_q), .in1(register_9_q), .out(multiplexer_16_out), .sel(not_16_out), .en(Clk));
  Multiplexer #(.enable("true"), .width(8)) multiplexer_17 (
    .in0(Reg5_q), .in1(register_10_q), .out(multiplexer_17_out), .sel(not_17_out), .en(Clk));
  Multiplexer #(.enable("true"), .width(8)) multiplexer_18 (
    .in0(Reg6_q), .in1(register_11_q), .out(multiplexer_18_out), .sel(not_18_out), .en(Clk));
  Multiplexer #(.width(8)) multiplexer_19 (.in0(register_1_q), .in1(register_12_q), .out(p3), .sel(not_19_out));
  Multiplexer #(.width(8)) multiplexer_20 (.in0(register_2_q), .in1(register_13_q), .out(p2), .sel(not_20_out));
  Multiplexer #(.width(8)) multiplexer_21 (.in0(register_3_q), .in1(register_14_q), .out(p1), .sel(not_21_out));
  Multiplexer #(.width(8)) multiplexer_22 (.in0(register_4_q), .in1(register_15_q), .out(p0), .sel(not_22_out));
  Multiplexer #(.enable("true"), .select(4), .width(8)) multiplexer_23 (
    .in0(multiplexer_12_out), .in1(multiplexer_13_out), .in2(multiplexer_14_out), .in3(multiplexer_15_out),
    .in4(multiplexer_16_out), .in5(multiplexer_17_out), .in6(multiplexer_18_out), .out(out_6),
    .sel(RegSelect), .en(Read));  // open: in7, in8, in9, in10, in11, in12, in13, in14, in15
endmodule

module Reg8Ext (
  input  [7:0] in_1,
  input  Inc,
  input  Dec,
  input  Zero,
  input  Write,
  input  Read,
  input  Clk,
  output [7:0] out_8
);

  wire and_1_out, and_2_out, not_1_out, not_2_out, not_3_out, or_3_out;
  wire [1:0] or_1_out;
  wire [7:0] adder_1_out, multiplexer_1_out, multiplexer_2_out, register_1_q, register_2_q, subtractor_1_out;

  Adder adder_1 (.a(register_2_q), .b(8'h1), .out(adder_1_out));  // open: cin, cout
  Subtractor subtractor_1 (.a(register_2_q), .b(8'h1), .out(subtractor_1_out));  // open: bin, bout
  Multiplexer #(.select(2), .width(8)) multiplexer_1 (
    .in0({8{1'b0}}), .in1(adder_1_out), .in2(subtractor_1_out), .in3(in_1), .out(multiplexer_1_out),
    .sel(or_1_out));
  or or_1 (or_1_out[0], Inc, Write);
  or or_2 (or_1_out[1], Dec, Write);
  or or_3 (or_3_out, Inc, Dec, Zero, Write);
  not not_1 (not_1_out, Clk);
  Register #(.trigger("high")) register_1 (
    .D(multiplexer_2_out), .en(or_3_out), .clk(Clk), .Q(register_1_q), .clr(1'b0));
  Multiplexer #(.enable("true"), .width(8)) multiplexer_2 (
    .in0(register_2_q), .in1(multiplexer_1_out), .out(multiplexer_2_out), .sel(Clk), .en(not_2_out));
  not not_2 (not_2_out, Zero);
  and and_1 (and_1_out, Read, Clk);
  not not_3 (not_3_out, or_3_out);
  Register #(.trigger("high")) register_2 (.D(register_1_q), .en(and_2_out), .clk(1'b1), .Q(register_2_q), .clr(1'b0));
  and and_2 (and_2_out, or_3_out, not_1_out);
  Multiplexer #(.enable("true"), .width(8)) multiplexer_3 (
    .in0(multiplexer_1_out), .in1(register_1_q), .out(out_8), .sel(not_3_out), .en(and_1_out));
endmodule

module CycleReg (
  input  Inc,
  input  Zero,
  output [7:0] out_3
);

  wire not_1_out, or_1_out;
  wire [7:0] adder_1_out, and8_1_1_out_3, register_2_q;

  Adder adder_1 (.a(register_2_q), .b(8'h1), .out(adder_1_out));  // open: cin, cout
  AND8_1 and8_1_1 (.in_1(adder_1_out), .in_2(Inc), .out_3(and8_1_1_out_3));
  not not_1 (not_1_out, or_1_out);
  Register #(.trigger("high")) register_1 (.D(and8_1_1_out_3), .en(or_1_out), .clk(1'b1), .Q(out_3));  // open: clr
  or or_1 (or_1_out, Inc, Zero);
  Register #(.trigger("high")) register_2 (.D(out_3), .en(not_1_out), .clk(1'b1), .Q(register_2_q));  // open: clr
endmodule

module OR5 (
  input  [4:0] in_1,
  output out_2
);

  or or_1 (out_2, in_1[0], in_1[1], in_1[2], in_1[3], in_1[4]);
endmodule

module OR8 (
  input  [7:0] in_1,
  output out_2
);

  or or_1 (out_2, in_1[0], in_1[1], in_1[2], in_1[3], in_1[4], in_1[5], in_1[6], in_1[7]);
endmodule

module AND8_1 (
  input  [7:0] in_1,
  input  in_2,
  output [7:0] out_3
);

  wire [7:0] bit_extender_1_out;

  assign bit_extender_1_out = {{7{in_2}}, in_2};  // Bit_Extender bit_extender_1
  assign out_3 = in_1 & bit_extender_1_out;  // AND_Gate and_1, 8 bits wide
endmodule

module SafeReg (
  input  [7:0] Data,
  input  Write,
  input  Clk,
  output [7:0] out_4
);

  wire and_1_out, and_2_out, nor_1_out, not_1_out, not_2_out, or_1_out;
  wire [7:0] GPReg_q, multiplexer_1_out, register_1_q;

  Multiplexer #(.width(8)) multiplexer_1 (.in0(register_1_q), .in1(Data), .out(multiplexer_1_out), .sel(Write));
  nor nor_1 (nor_1_out, Clk, Write);
  and and_1 (and_1_out, Write, Clk);
  Register #(.trigger("high")) GPReg (.D(multiplexer_1_out), .en(or_1_out), .clk(1'b1), .Q(GPReg_q));  // open: clr
  or or_1 (or_1_out, nor_1_out, and_1_out);
  Register #(.trigger("high")) register_1 (.D(GPReg_q), .en(and_2_out), .clk(1'b1), .Q(register_1_q));  // open: clr
  not not_1 (not_1_out, Clk);
  and and_2 (and_2_out, not_1_out, Write);
  Multiplexer #(.enable("true"), .width(8)) multiplexer_2 (
    .in0(GPReg_q), .in1(register_1_q), .out(out_4), .sel(not_2_out), .en(Clk));
  not not_2 (not_2_out, Write);
endmodule

module Equal (
  input  [7:0] in_1,
  input  [7:0] in_2,
  output out_3
);

  wire [7:0] xnor_1_out;

  assign xnor_1_out = ~(in_1 ^ in_2);  // XNOR_Gate xnor_1, 8 bits wide
  and and_1 (out_3, xnor_1_out[0], xnor_1_out[1], xnor_1_out[2], xnor_1_out[3], xnor_1_out[4], xnor_1_out[5], xnor_1_out[6], xnor_1_out[7]);
endmodule
